// Logisim project LedControl.circ as structural Verilog: 1 circuit, main circuit LedControl
module LedControl (
  input  [7:0] data,
  input  clean,
  input  clk,
  output [7:0] out_4,
  output [7:0] out_5,
  output [7:0] out_6,
  output [7:0] out_7,
  output [7:0] out_8,
  output [7:0] out_9,
  output [7:0] out_10,
  output [7:0] out_11,
  output [7:0] out_12,
  output [7:0] out_13,
  output [7:0] out_14,
  output [7:0] out_15,
  output [7:0] out_16,
  output [7:0] out_17,
  output [7:0] out_18,
  output [7:0] out_19
);

  wire and_1_out, comparator_1_eq, CPU_io_write_31, decoder_1_out0, decoder_1_out1, decoder_1_out2,
       decoder_1_out3, decoder_1_out4, decoder_1_out5, decoder_1_out6, decoder_1_out7, decoder_1_out8,
       decoder_1_out9, decoder_1_out10, decoder_1_out11, decoder_1_out12, decoder_1_out13, decoder_1_out14,
       decoder_1_out15, or_1_out, undriven;
  wire [3:0] bit_extender_1_out, counter_1_q;
  wire [7:0] bit_extender_2_out;
  wire [15:0] CPU_io_addr_28, CPU_io_write_data_29;

  assign bit_extender_1_out = {{3{1'b1}}, clean};  // Bit_Extender bit_extender_1
  or or_1 (or_1_out, clean, clk);
  Counter #(.max('hf), .width(4)) counter_1 (
    .load(clean), .up(clk), .count(clk), .clk(or_1_out), .D(bit_extender_1_out), .Q(counter_1_q));  // open: clr, carry
  Comparator #(.width(16)) comparator_1 (.a(CPU_io_addr_28), .b(16'hf000), .eq(comparator_1_eq));  // open: gt, lt
  Bit_Extender #(.in_width(16), .out_width(8), .\type ("input")) bit_extender_2 (
    .in(CPU_io_write_data_29), .out(bit_extender_2_out));  // open: extend
  and and_1 (and_1_out, CPU_io_write_31, undriven, comparator_1_eq);
  Decoder #(.select(4)) decoder_1 (
    .out0(decoder_1_out0), .out1(decoder_1_out1), .out2(decoder_1_out2), .out3(decoder_1_out3),
    .out4(decoder_1_out4), .out5(decoder_1_out5), .out6(decoder_1_out6), .out7(decoder_1_out7),
    .out8(decoder_1_out8), .out9(decoder_1_out9), .out10(decoder_1_out10), .out11(decoder_1_out11),
    .out12(decoder_1_out12), .out13(decoder_1_out13), .out14(decoder_1_out14), .out15(decoder_1_out15),
    .sel(counter_1_q), .en(clk));
  DotMatrix #(.matrixcols(16), .matrixrows(8)) dotmatrix_1 ();  // open: col0, col1, col2, col3, col4, col5, col6, col7, col8, col9, col10, col11, col12, col13, col14, col15
  Register register_1 (.D(data), .en(decoder_1_out0), .clk(decoder_1_out0), .Q(out_4));  // open: clr
  Register register_2 (.D(data), .en(decoder_1_out1), .clk(decoder_1_out1), .Q(out_7));  // open: clr
  Register register_3 (.D(data), .en(decoder_1_out2), .clk(decoder_1_out2), .Q(out_8));  // open: clr
  Register register_4 (.D(data), .en(decoder_1_out3), .clk(decoder_1_out3), .Q(out_11));  // open: clr
  Register register_5 (.D(data), .en(decoder_1_out8), .clk(decoder_1_out8), .Q(out_12));  // open: clr
  Register register_6 (.D(data), .en(decoder_1_out9), .clk(decoder_1_out9), .Q(out_14));  // open: clr
  Register register_7 (.D(data), .en(decoder_1_out10), .clk(decoder_1_out10), .Q(out_16));  // open: clr
  Register register_8 (.D(data), .en(decoder_1_out11), .clk(decoder_1_out11), .Q(out_18));  // open: clr
  Register register_9 (.D(data), .en(decoder_1_out4), .clk(decoder_1_out4), .Q(out_5));  // open: clr
  Register register_10 (.D(data), .en(decoder_1_out5), .clk(decoder_1_out5), .Q(out_6));  // open: clr
  Register register_11 (.D(data), .en(decoder_1_out6), .clk(decoder_1_out6), .Q(out_9));  // open: clr
  Register register_12 (.D(data), .en(decoder_1_out7), .clk(decoder_1_out7), .Q(out_10));  // open: clr
  Register register_13 (.D(data), .en(decoder_1_out12), .clk(decoder_1_out12), .Q(out_13));  // open: clr
  Register register_14 (.D(data), .en(decoder_1_out13), .clk(decoder_1_out13), .Q(out_15));  // open: clr
  Register register_15 (.D(data), .en(decoder_1_out14), .clk(decoder_1_out14), .Q(out_17));  // open: clr
  Register register_16 (.D(data), .en(decoder_1_out15), .clk(decoder_1_out15), .Q(out_19));  // open: clr
endmodule
