// Logisim project LedControl_fixed.circ as structural Verilog: 1 circuit, main circuit LedControl
module LedControl (
  input  [7:0] data,
  input  clk,
  input  reset,
  input  write_enable,
  output [7:0] column0,
  output [7:0] column1,
  output [7:0] column2,
  output [7:0] column3,
  output [7:0] column4,
  output [7:0] column5,
  output [7:0] column6,
  output [7:0] column7,
  output [7:0] column8,
  output [7:0] column9,
  output [7:0] column10,
  output [7:0] column11,
  output [7:0] column12,
  output [7:0] column13,
  output [7:0] column14,
  output [7:0] column15
);

  wire and_6, and_8, and_10, and_12, and_14, and_16, and_18, and_20, and_22, and_24, and_26, and_28, and_30,
       and_32, and_34, and_36, selected_column0_5, selected_column1_7, selected_column2_9,
       selected_column3_11, selected_column4_13, selected_column5_15, selected_column6_17,
       selected_column7_19, selected_column8_21, selected_column9_23, selected_column10_25,
       selected_column11_27, selected_column12_29, selected_column13_31, selected_column14_33,
       selected_column15_35;
  wire [3:0] adder_2, column_index;

  Decoder #(.select(4)) decoder_1 (
    .out0(selected_column0_5), .out1(selected_column1_7), .out2(selected_column2_9),
    .out3(selected_column3_11), .out4(selected_column4_13), .out5(selected_column5_15),
    .out6(selected_column6_17), .out7(selected_column7_19), .out8(selected_column8_21),
    .out9(selected_column9_23), .out10(selected_column10_25), .out11(selected_column11_27),
    .out12(selected_column12_29), .out13(selected_column13_31), .out14(selected_column14_33),
    .out15(selected_column15_35), .sel(column_index), .en(1'b1));
  and and_1 (and_10, write_enable, selected_column2_9);
  and and_2 (and_18, write_enable, selected_column6_17);
  and and_3 (and_26, write_enable, selected_column10_25);
  and and_4 (and_34, write_enable, selected_column14_33);
  Register #(.width(8)) reg_column2 (.D(data), .en(and_10), .Q(column2), .clk(clk), .clr(reset));
  Register #(.width(8)) reg_column6 (.D(data), .en(and_18), .Q(column6), .clk(clk), .clr(reset));
  Register #(.width(8)) reg_column10 (.D(data), .en(and_26), .Q(column10), .clk(clk), .clr(reset));
  Register #(.width(8)) reg_column14 (.D(data), .en(and_34), .Q(column14), .clk(clk), .clr(reset));
  Adder #(.width(4)) adder_1 (.a(column_index), .b(4'b0001), .out(adder_2), .cin(1'b0));  // open: cout
  and and_5 (and_12, write_enable, selected_column3_11);
  and u_and_6 (and_20, write_enable, selected_column7_19);
  and and_7 (and_28, write_enable, selected_column11_27);
  and u_and_8 (and_36, write_enable, selected_column15_35);
  Register #(.width(8)) reg_column3 (.D(data), .en(and_12), .Q(column3), .clk(clk), .clr(reset));
  Register #(.width(8)) reg_column7 (.D(data), .en(and_20), .Q(column7), .clk(clk), .clr(reset));
  Register #(.width(8)) reg_column11 (.D(data), .en(and_28), .Q(column11), .clk(clk), .clr(reset));
  Register #(.width(8)) reg_column15 (.D(data), .en(and_36), .Q(column15), .clk(clk), .clr(reset));
  and and_9 (and_6, write_enable, selected_column0_5);
  and u_and_10 (and_14, write_enable, selected_column4_13);
  and and_11 (and_22, write_enable, selected_column8_21);
  and u_and_12 (and_30, write_enable, selected_column12_29);
  Register #(.width(8)) reg_column0 (.D(data), .en(and_6), .Q(column0), .clk(clk), .clr(reset));
  Register #(.width(8)) reg_column4 (.D(data), .en(and_14), .Q(column4), .clk(clk), .clr(reset));
  Register #(.width(8)) reg_column8 (.D(data), .en(and_22), .Q(column8), .clk(clk), .clr(reset));
  Register #(.width(8)) reg_column12 (.D(data), .en(and_30), .Q(column12), .clk(clk), .clr(reset));
  Register #(.width(4)) reg_column_index (.D(adder_2), .en(write_enable), .Q(column_index), .clk(clk), .clr(reset));
  and and_13 (and_8, write_enable, selected_column1_7);
  and u_and_14 (and_16, write_enable, selected_column5_15);
  and and_15 (and_24, write_enable, selected_column9_23);
  and u_and_16 (and_32, write_enable, selected_column13_31);
  Register #(.width(8)) reg_column1 (.D(data), .en(and_8), .Q(column1), .clk(clk), .clr(reset));
  Register #(.width(8)) reg_column5 (.D(data), .en(and_16), .Q(column5), .clk(clk), .clr(reset));
  Register #(.width(8)) reg_column9 (.D(data), .en(and_24), .Q(column9), .clk(clk), .clr(reset));
  Register #(.width(8)) reg_column13 (.D(data), .en(and_32), .Q(column13), .clk(clk), .clr(reset));

  // Notes on the sheet:
  //   Synchronous 16 x 8 LED column buffer
endmodule
