// Logisim project Superscalar16_io.circ as structural Verilog
module Superscalar16 (
  input  reset,
  input  pause,
  input  [15:0] io_read_data,
  output [15:0] r0,
  output [31:0] cycles,
  output [15:0] r1,
  output [31:0] committed,
  output [15:0] r2,
  output [31:0] dual_issue,
  output [15:0] r3,
  output [31:0] dual_cdb,
  output [15:0] r4,
  output [31:0] recoveries,
  output [15:0] r5,
  output [15:0] pc,
  output [15:0] r6,
  output halted,
  output [15:0] r7,
  output [15:0] memory_debug,
  output [15:0] io_addr,
  output [4:0] rs0_count,
  output [4:0] rob0_count,
  output [15:0] io_write_data,
  output [4:0] rs1_count,
  output [4:0] rob1_count,
  output io_read,
  output [4:0] rs2_count,
  output [4:0] rob2_count,
  output io_write,
  output [3:0] sb_count,
  output io_valid,
  output io_clk,
  output io_reset
);

  wire CPU_cdb0_valid_17, CPU_cdb1_valid_18, CPU_commit_valid_9, CPU_flush_14, CPU_forward_hit_25,
       CPU_stall_15, CPU_store_commit_22, run_enable;
  wire [1:0] CPU_issue_count_16;
  wire [3:0] CPU_commit_op_12, CPU_fifo_count_21;
  wire [7:0] CPU_cdb0_sn_19, CPU_cdb1_sn_20, CPU_commit_sn_10;
  wire [15:0] CPU_commit_pc_11, CPU_commit_result_13, CPU_store_addr_23, CPU_store_data_24;
  wire [31:0] CPU_dispatched_3;

  Clock #(.highDuration(1), .lowDuration(1)) SystemClock (.out(io_clk));
  not not_1 (run_enable, pause);
  CPU_Core CPU (
    .clk(io_clk), .rst(reset), .run(run_enable), .debug_addr({16{1'b0}}), .io_read_data(io_read_data),
    .cycles(cycles), .committed(committed), .dispatched(CPU_dispatched_3), .dual_issue(dual_issue),
    .recoveries(recoveries), .dual_cdb(dual_cdb), .halted(halted), .pc(pc),
    .commit_valid(CPU_commit_valid_9), .commit_sn(CPU_commit_sn_10), .commit_pc(CPU_commit_pc_11),
    .commit_op(CPU_commit_op_12), .commit_result(CPU_commit_result_13), .flush(CPU_flush_14),
    .stall(CPU_stall_15), .issue_count(CPU_issue_count_16), .cdb0_valid(CPU_cdb0_valid_17),
    .cdb1_valid(CPU_cdb1_valid_18), .cdb0_sn(CPU_cdb0_sn_19), .cdb1_sn(CPU_cdb1_sn_20),
    .fifo_count(CPU_fifo_count_21), .store_commit(CPU_store_commit_22), .store_addr(CPU_store_addr_23),
    .store_data(CPU_store_data_24), .forward_hit(CPU_forward_hit_25), .sb_count(sb_count),
    .memory_debug(memory_debug), .io_addr(io_addr), .io_write_data(io_write_data), .io_read(io_read),
    .io_write(io_write), .io_valid(io_valid), .r0(r0), .r1(r1), .r2(r2), .r3(r3), .r4(r4), .r5(r5), .r6(r6),
    .r7(r7), .rs0_count(rs0_count), .rob0_count(rob0_count), .rs1_count(rs1_count), .rob1_count(rob1_count),
    .rs2_count(rs2_count), .rob2_count(rob2_count));

  assign io_reset = reset;

  // Other names for the same wires on the sheet: clock = io_clk; CPU_committed_2[31:0] = committed;
  //   CPU_cycles_1[31:0] = cycles; CPU_dual_cdb_6[31:0] = dual_cdb; CPU_dual_issue_4[31:0] = dual_issue;
  //   CPU_halted_7 = halted; CPU_io_addr_28[15:0] = io_addr; CPU_io_read_30 = io_read; CPU_io_valid_32 = io_valid;
  //   CPU_io_write_31 = io_write; CPU_io_write_data_29[15:0] = io_write_data;
  //   CPU_memory_debug_27[15:0] = memory_debug; CPU_pc_8[15:0] = pc; CPU_r0_33[15:0] = r0; CPU_r1_34[15:0] = r1;
  //   CPU_r2_35[15:0] = r2; CPU_r3_36[15:0] = r3; CPU_r4_37[15:0] = r4; CPU_r5_38[15:0] = r5; CPU_r6_39[15:0] = r6;
  //   CPU_r7_40[15:0] = r7; CPU_recoveries_5[31:0] = recoveries; CPU_rob0_count_42[4:0] = rob0_count;
  //   CPU_rob1_count_44[4:0] = rob1_count; CPU_rob2_count_46[4:0] = rob2_count; CPU_rs0_count_41[4:0] = rs0_count;
  //   CPU_rs1_count_43[4:0] = rs1_count; CPU_rs2_count_45[4:0] = rs2_count; CPU_sb_count_26[3:0] = sb_count

  // Notes on the sheet:
  //   SUPERSCALAR16 | native Logisim circuit | demo program
  //   CONTROL
  //   MEMORY-MAPPED I/O  F000-F0FF
  //   PROCESSOR
  //   ARCHITECTURAL REGISTERS
  //   RESERVATION STATIONS
  //   COUNTERS
  //   STATE / MEMORY
  //   REORDER BUFFERS
endmodule

module CPU_Core (
  input  clk,
  input  rst,
  input  run,
  input  [15:0] debug_addr,
  input  [15:0] io_read_data,
  output [31:0] cycles,
  output [31:0] committed,
  output [31:0] dispatched,
  output [31:0] dual_issue,
  output [31:0] recoveries,
  output [31:0] dual_cdb,
  output halted,
  output [15:0] pc,
  output commit_valid,
  output [7:0] commit_sn,
  output [15:0] commit_pc,
  output [3:0] commit_op,
  output [15:0] commit_result,
  output flush,
  output stall,
  output [1:0] issue_count,
  output cdb0_valid,
  output cdb1_valid,
  output [7:0] cdb0_sn,
  output [7:0] cdb1_sn,
  output [3:0] fifo_count,
  output store_commit,
  output [15:0] store_addr,
  output [15:0] store_data,
  output forward_hit,
  output [3:0] sb_count,
  output [15:0] memory_debug,
  output [15:0] io_addr,
  output [15:0] io_write_data,
  output io_read,
  output io_write,
  output io_valid,
  output [15:0] r0,
  output [15:0] r1,
  output [15:0] r2,
  output [15:0] r3,
  output [15:0] r4,
  output [15:0] r5,
  output [15:0] r6,
  output [15:0] r7,
  output [4:0] rs0_count,
  output [4:0] rob0_count,
  output [4:0] rs1_count,
  output [4:0] rob1_count,
  output [4:0] rs2_count,
  output [4:0] rob2_count
);

  wire accept0, accept1, ALU0_taken_275, ALU1_taken_280, and_4, and_5, and_6, and_48, and_65, and_232,
       and_233, and_238, and_240, and_244, and_246, and_250, and_252, and_257, and_258, and_263, and_267,
       and_271, and_282, and_284, and_285, and_298, and_315, and_316, and_317, and_328, and_330, and_342,
       and_343, and_344, and_348, and_349, and_350, and_354, and_355, and_356, and_406, and_407, and_412,
       and_417, c0_taken, decode0_branch_39, decode0_halt_41, decode0_jump_40, decode0_mem_37, decode0_rw_36,
       decode0_store_38, decode1_branch_57, decode1_halt_59, decode1_jump_58, decode1_mem_55, decode1_rw_54,
       decode1_store_56, eq_45, eq_62, eq_236, eq_242, eq_248, eq_261, eq_265, eq_269, eq_296, eq_309,
       eq_312, eq_340, eq_346, eq_352, eq_385, eq_389, eq_393, eq_397, eq_403, eq_410, eq_414,
       fetch_pred0_23, fetch_pred1_24, fetch_valid0_27, fetch_valid1_28, gt_44, gt_61, gt_235, gt_241,
       gt_247, gt_260, gt_264, gt_268, gt_295, gt_308, gt_311, gt_339, gt_345, gt_351, gt_384, gt_388,
       gt_392, gt_396, gt_402, gt_409, gt_413, lt_46, lt_63, lt_237, lt_243, lt_249, lt_262, lt_266, lt_270,
       lt_297, lt_310, lt_313, lt_341, lt_347, lt_353, lt_386, lt_390, lt_394, lt_398, lt_404, lt_411,
       lt_415, mux_101, mux_102, mux_107, mux_143, mux_144, mux_149, mux_185, mux_186, mux_191, mux_231,
       mux_256, mux_329, mux_367, mux_368, mux_379, mux_380, not_1, not_2, not_3, not_47, not_64, not_220,
       not_222, not_224, not_239, not_245, not_251, not_283, not_314, not_324, not_325, not_326, not_405,
       not_426, or_7, or_18, or_93, or_135, or_177, or_219, or_221, or_223, or_230, or_255, or_327, or_357,
       or_399, or_400, or_401, rename_available0_66, rename_available1_67, rename_vj0_74, rename_vj1_80,
       rename_vk0_77, rename_vk1_83, ROB0_full_119, ROB0_head_done_122, ROB0_head_rw_127,
       ROB0_head_taken_133, ROB0_head_valid_121, ROB1_full_161, ROB1_head_done_164, ROB1_head_rw_169,
       ROB1_head_taken_175, ROB1_head_valid_163, ROB2_full_203, ROB2_head_done_206, ROB2_head_rw_211,
       ROB2_head_taken_217, ROB2_head_valid_205, RS0_ex_valid_111, RS0_full_109, RS1_ex_valid_153,
       RS1_full_151, RS2_ex_valid_195, RS2_full_193, stores_commit_found_303, stores_forward_301,
       stores_full_299;
  wire [1:0] ext_12, ext_13, mux_227, mux_229, mux_253, mux_254;
  wire [2:0] decode0_rd_32, decode0_rs1_33, decode0_rs2_34, decode1_rd_50, decode1_rs1_51, decode1_rs2_52,
       mux_106, mux_148, mux_190, mux_365, mux_366, ROB0_head_rd_logic_126, ROB1_head_rd_logic_168,
       ROB2_head_rd_logic_210;
  wire [3:0] decode0_opcode_31, decode1_opcode_49, mux_94, mux_136, mux_178, mux_359, ROB0_head_op_123,
       ROB1_head_op_165, ROB2_head_op_207, RS0_ex_op_112, RS1_ex_op_154, RS2_ex_op_196;
  wire [5:0] c0_rd, c1_rd, mux_95, mux_96, mux_97, mux_105, mux_137, mux_138, mux_139, mux_147, mux_179,
       mux_180, mux_181, mux_189, mux_361, mux_362, mux_363, mux_364, rename_new0_68, rename_new1_69,
       rename_old0_70, rename_old1_71, rename_qj0_72, rename_qj1_78, rename_qk0_75, rename_qk1_81,
       ROB0_head_rd_new_124, ROB0_head_rd_old_125, ROB1_head_rd_new_166, ROB1_head_rd_old_167,
       ROB2_head_rd_new_208, ROB2_head_rd_old_209, RS0_ex_rd_113, RS1_ex_rd_155, RS2_ex_rd_197;
  wire [7:0] adder_10, adder_16, adder_92, ext_15, global_sn, mux_17, mux_100, mux_142, mux_184, mux_371,
       mux_372, ROB0_head_sn_129, ROB1_head_sn_171, ROB2_head_sn_213, RS0_ex_sn_116, RS1_ex_sn_158;
  wire [15:0] adder_293, adder_337, adder_338, ALU0_addr_276, ALU0_next_273, ALU0_result_272,
       ALU0_target_274, ALU1_addr_281, ALU1_next_278, ALU1_result_277, ALU1_target_279, c0_next, c0_result,
       c0_target, c1_result, decode0_imm_35, decode1_imm_53, fetch_instr0_19, fetch_instr1_20,
       fetch_next0_25, fetch_next1_26, fetch_pc0_21, fetch_pc1_22, memory_data_322, mux_98, mux_99, mux_103,
       mux_104, mux_108, mux_140, mux_141, mux_145, mux_146, mux_150, mux_182, mux_183, mux_187, mux_188,
       mux_192, mux_334, mux_369, mux_373, mux_374, mux_375, mux_377, mux_378, mux_381, mux_382, recovery_pc,
       rename_dj0_73, rename_dj1_79, rename_dk0_76, rename_dk1_82, ROB0_head_next_132, ROB0_head_pc_128,
       ROB0_head_pred_next_130, ROB0_head_result_131, ROB0_head_target_134, ROB1_head_next_174,
       ROB1_head_pc_170, ROB1_head_pred_next_172, ROB1_head_result_173, ROB1_head_target_176,
       ROB2_head_next_216, ROB2_head_pc_212, ROB2_head_pred_next_214, ROB2_head_result_215,
       ROB2_head_target_218, RS0_ex_a_117, RS0_ex_b_118, RS0_ex_imm_114, RS0_ex_pc_115, RS1_ex_a_159,
       RS1_ex_b_160, RS1_ex_imm_156, RS1_ex_pc_157, RS2_ex_a_201, RS2_ex_b_202, RS2_ex_imm_198,
       RS2_ex_pc_199, stores_forward_data_302;
  wire [31:0] adder_419, adder_420, adder_422, adder_423, adder_424, adder_425, ext_421;
  wire [56:0] decode0_packet_42, decode1_packet_60;

  not u_not_1 (not_1, halted);
  and and_1 (and_5, and_4, not_2);
  Register #(.width(1)) reg_halted (.D(1'b1), .en(and_412), .Q(halted), .clk(clk), .clr(rst));
  Adder #(.width(8)) adder_1 (.a(commit_sn), .b(8'h1), .out(adder_10), .cin(1'b0));  // open: cout
  assign ext_13 = {{1{1'b0}}, accept1};  // Bit_Extender bit_extender_1
  Multiplexer #(.width(8), .select(1), .enable("false")) multiplexer_1 (
    .in0(adder_16), .in1(commit_sn), .out(mux_17), .sel(flush));
  DecodeOne decode0 (
    .instr(fetch_instr0_19), .pc(fetch_pc0_21), .pred(fetch_pred0_23), .opcode(decode0_opcode_31),
    .rd(decode0_rd_32), .rs1(decode0_rs1_33), .rs2(decode0_rs2_34), .imm(decode0_imm_35), .rw(decode0_rw_36),
    .mem(decode0_mem_37), .store(decode0_store_38), .branch(decode0_branch_39), .jump(decode0_jump_40),
    .halt(decode0_halt_41), .packet(decode0_packet_42));
  and and_2 (and_48, decode0_rw_36, not_47);
  and and_3 (and_65, decode1_rw_54, not_64);
  Multiplexer #(.width(4), .select(1), .enable("false")) multiplexer_2 (
    .in0(decode0_opcode_31), .in1(decode1_opcode_49), .out(mux_94), .sel(and_263));
  Multiplexer #(.width(16), .select(1), .enable("false")) multiplexer_3 (
    .in0(decode0_imm_35), .in1(decode1_imm_53), .out(mux_98), .sel(and_263));
  Multiplexer #(.width(1), .select(1), .enable("false")) multiplexer_4 (
    .in0(rename_vk0_77), .in1(rename_vk1_83), .out(mux_102), .sel(and_263));
  Multiplexer #(.width(3), .select(1), .enable("false")) multiplexer_5 (
    .in0(decode0_rd_32), .in1(decode1_rd_50), .out(mux_106), .sel(and_263));
  ROB ROB0 (
    .clk(clk), .rst(rst), .clear(or_7), .enable(and_6), .wr(or_93), .pop(and_344), .op(mux_94),
    .rd_new(mux_95), .rd_old(mux_105), .rd_logic(mux_106), .rw(mux_107), .pc(mux_99), .sn(mux_100),
    .pred_next(mux_108), .c0_valid(cdb0_valid), .c0_sn(cdb0_sn), .c0_result(c0_result), .c0_next(c0_next),
    .c0_taken(c0_taken), .c0_target(c0_target), .c1_valid(cdb1_valid), .c1_sn(cdb1_sn),
    .c1_result(c1_result), .c1_next(adder_337), .c1_taken(1'b0), .c1_target(adder_338), .full(ROB0_full_119),
    .count(rob0_count), .head_valid(ROB0_head_valid_121), .head_done(ROB0_head_done_122),
    .head_op(ROB0_head_op_123), .head_rd_new(ROB0_head_rd_new_124), .head_rd_old(ROB0_head_rd_old_125),
    .head_rd_logic(ROB0_head_rd_logic_126), .head_rw(ROB0_head_rw_127), .head_pc(ROB0_head_pc_128),
    .head_sn(ROB0_head_sn_129), .head_pred_next(ROB0_head_pred_next_130), .head_result(ROB0_head_result_131),
    .head_next(ROB0_head_next_132), .head_taken(ROB0_head_taken_133), .head_target(ROB0_head_target_134));
  Multiplexer #(.width(6), .select(1), .enable("false")) multiplexer_6 (
    .in0(rename_qj0_72), .in1(rename_qj1_78), .out(mux_138), .sel(and_267));
  Multiplexer #(.width(8), .select(1), .enable("false")) multiplexer_7 (
    .in0(global_sn), .in1(adder_92), .out(mux_142), .sel(and_267));
  Multiplexer #(.width(16), .select(1), .enable("false")) multiplexer_8 (
    .in0(rename_dk0_76), .in1(rename_dk1_82), .out(mux_146), .sel(and_267));
  Multiplexer #(.width(16), .select(1), .enable("false")) multiplexer_9 (
    .in0(fetch_next0_25), .in1(fetch_next1_26), .out(mux_150), .sel(and_267));
  Multiplexer #(.width(4), .select(1), .enable("false")) multiplexer_10 (
    .in0(decode0_opcode_31), .in1(decode1_opcode_49), .out(mux_178), .sel(and_271));
  Multiplexer #(.width(16), .select(1), .enable("false")) multiplexer_11 (
    .in0(decode0_imm_35), .in1(decode1_imm_53), .out(mux_182), .sel(and_271));
  Multiplexer #(.width(1), .select(1), .enable("false")) multiplexer_12 (
    .in0(rename_vk0_77), .in1(rename_vk1_83), .out(mux_186), .sel(and_271));
  Multiplexer #(.width(3), .select(1), .enable("false")) multiplexer_13 (
    .in0(decode0_rd_32), .in1(decode1_rd_50), .out(mux_190), .sel(and_271));
  ROB ROB2 (
    .clk(clk), .rst(rst), .clear(or_7), .enable(and_6), .wr(or_177), .pop(and_356), .op(mux_178),
    .rd_new(mux_179), .rd_old(mux_189), .rd_logic(mux_190), .rw(mux_191), .pc(mux_183), .sn(mux_184),
    .pred_next(mux_192), .c0_valid(cdb0_valid), .c0_sn(cdb0_sn), .c0_result(c0_result), .c0_next(c0_next),
    .c0_taken(c0_taken), .c0_target(c0_target), .c1_valid(cdb1_valid), .c1_sn(cdb1_sn),
    .c1_result(c1_result), .c1_next(adder_337), .c1_taken(1'b0), .c1_target(adder_338), .full(ROB2_full_203),
    .count(rob2_count), .head_valid(ROB2_head_valid_205), .head_done(ROB2_head_done_206),
    .head_op(ROB2_head_op_207), .head_rd_new(ROB2_head_rd_new_208), .head_rd_old(ROB2_head_rd_old_209),
    .head_rd_logic(ROB2_head_rd_logic_210), .head_rw(ROB2_head_rw_211), .head_pc(ROB2_head_pc_212),
    .head_sn(ROB2_head_sn_213), .head_pred_next(ROB2_head_pred_next_214), .head_result(ROB2_head_result_215),
    .head_next(ROB2_head_next_216), .head_taken(ROB2_head_taken_217), .head_target(ROB2_head_target_218));
  not u_not_2 (not_222, or_221);
  or or_1 (or_230, not_220, not_222);
  and u_and_4 (accept0, and_233, mux_231);
  not u_not_3 (not_239, and_238);
  not not_4 (not_245, and_244);
  not not_5 (not_251, and_250);
  or or_2 (or_255, and_240, and_246);
  and u_and_5 (accept1, and_258, mux_256);
  and u_and_6 (and_263, accept1, eq_261);
  and and_7 (and_267, accept1, eq_265);
  and and_8 (and_271, accept1, eq_269);
  and and_9 (and_282, and_6, RS0_ex_valid_111);
  and and_10 (and_285, and_284, not_283);
  Multiplexer #(.width(6), .select(1), .enable("false")) multiplexer_14 (
    .in0(RS1_ex_rd_155), .in1(RS0_ex_rd_113), .out(c0_rd), .sel(and_282));
  Multiplexer #(.width(16), .select(1), .enable("false")) multiplexer_15 (
    .in0(ALU1_result_277), .in1(ALU0_result_272), .out(c0_result), .sel(and_282));
  Multiplexer #(.width(1), .select(1), .enable("false")) multiplexer_16 (
    .in0(ALU1_taken_280), .in1(ALU0_taken_275), .out(c0_taken), .sel(and_282));
  Adder #(.width(16)) adder_2 (.a(RS2_ex_a_201), .b(RS2_ex_imm_198), .out(adder_293), .cin(1'b0));  // open: cout
  StoreBuffer stores (
    .clk(clk), .rst(rst), .enable(and_6), .clear(or_7), .push(and_298), .addr(adder_293),
    .data(RS2_ex_b_202), .sn(cdb1_sn), .load_addr(adder_293), .load_sn(cdb1_sn), .commit(store_commit),
    .commit_sn(commit_sn), .full(stores_full_299), .count(sb_count), .forward(stores_forward_301),
    .forward_data(stores_forward_data_302), .commit_found(stores_commit_found_303), .commit_addr(store_addr),
    .commit_data(store_data));
  Comparator #(.width(8), .mode("unsigned")) comparator_1 (
    .a(cdb1_sn), .b(commit_sn), .gt(gt_311), .eq(eq_312), .lt(lt_313));
  and and_11 (and_317, and_316, eq_312);
  not not_6 (not_326, eq_309);
  and and_12 (and_330, and_6, RS2_ex_valid_195);
  Multiplexer #(.width(16), .select(1), .enable("false")) multiplexer_17 (
    .in0(memory_data_322), .in1(stores_forward_data_302), .out(mux_334), .sel(stores_forward_301));
  Adder #(.width(16)) adder_3 (.a(RS2_ex_pc_199), .b(16'h1), .out(adder_337), .cin(1'b0));  // open: cout
  and and_13 (and_344, and_343, eq_340);
  and and_14 (and_349, and_348, ROB1_head_done_164);
  and and_15 (and_354, and_6, ROB2_head_valid_205);
  or or_3 (or_357, and_344, and_350);
  Multiplexer #(.width(4), .select(1), .enable("false")) multiplexer_18 (
    .in0(mux_359), .in1(ROB0_head_op_123), .out(commit_op), .sel(and_344));
  Multiplexer #(.width(3), .select(1), .enable("false")) multiplexer_19 (
    .in0(ROB2_head_rd_logic_210), .in1(ROB1_head_rd_logic_168), .out(mux_365), .sel(and_350));
  Multiplexer #(.width(1), .select(1), .enable("false")) multiplexer_20 (
    .in0(mux_367), .in1(ROB0_head_rw_127), .out(mux_368), .sel(and_344));
  Multiplexer #(.width(16), .select(1), .enable("false")) multiplexer_21 (
    .in0(ROB2_head_pred_next_214), .in1(ROB1_head_pred_next_172), .out(mux_373), .sel(and_350));
  Multiplexer #(.width(16), .select(1), .enable("false")) multiplexer_22 (
    .in0(mux_375), .in1(ROB0_head_result_131), .out(commit_result), .sel(and_344));
  Multiplexer #(.width(16), .select(1), .enable("false")) multiplexer_23 (
    .in0(ROB2_head_target_218), .in1(ROB1_head_target_176), .out(mux_381), .sel(and_350));
  Comparator #(.width(4), .mode("unsigned")) comparator_2 (
    .a(commit_op), .b(4'b1010), .gt(gt_384), .eq(eq_385), .lt(lt_386));
  Comparator #(.width(4), .mode("unsigned")) comparator_3 (
    .a(commit_op), .b(4'b1100), .gt(gt_392), .eq(eq_393), .lt(lt_394));
  or or_4 (or_400, or_399, eq_393);
  and and_16 (and_406, commit_valid, or_401);
  Comparator #(.width(4), .mode("unsigned")) comparator_4 (
    .a(commit_op), .b(4'b1001), .gt(gt_413), .eq(eq_414), .lt(lt_415));
  Register #(.width(32)) reg_committed (.D(adder_420), .en(commit_valid), .Q(committed), .clk(clk), .clr(rst));
  Adder #(.width(32)) adder_4 (.a(dual_issue), .b(32'h1), .out(adder_423), .cin(1'b0));  // open: cout
  Adder #(.width(32)) adder_5 (.a(dual_cdb), .b(32'h1), .out(adder_425), .cin(1'b0));  // open: cout
  and and_17 (forward_hit, and_315, stores_forward_301);
  not not_7 (not_2, flush);
  and and_18 (and_6, and_5, not_3);
  Register #(.width(1)) reg_recovery (.D(and_407), .en(1'b1), .Q(flush), .clk(clk), .clr(rst));
  Adder #(.width(2)) adder_6 (.a(ext_12), .b(ext_13), .out(issue_count), .cin(1'b0));  // open: cout
  or or_5 (or_18, and_6, flush);
  DecodeOne decode1 (
    .instr(fetch_instr1_20), .pc(fetch_pc1_22), .pred(fetch_pred1_24), .opcode(decode1_opcode_49),
    .rd(decode1_rd_50), .rs1(decode1_rs1_51), .rs2(decode1_rs2_52), .imm(decode1_imm_53), .rw(decode1_rw_54),
    .mem(decode1_mem_55), .store(decode1_store_56), .branch(decode1_branch_57), .jump(decode1_jump_58),
    .halt(decode1_halt_59), .packet(decode1_packet_60));
  Rename_PRF rename (
    .clk(clk), .rst(rst), .enable(and_6), .clear(flush), .accept0(accept0), .accept1(accept1),
    .commit_v(commit_valid), .commit_rw(mux_368), .commit_rd(mux_366), .commit_new(mux_362),
    .commit_old(mux_364), .commit_data(commit_result), .c0_v(cdb0_valid), .c0_tag(c0_rd),
    .c0_data(c0_result), .c1_v(cdb1_valid), .c1_tag(c1_rd), .c1_data(c1_result), .rd0(decode0_rd_32),
    .rs10(decode0_rs1_33), .rs20(decode0_rs2_34), .rw0(and_48), .rd1(decode1_rd_50), .rs11(decode1_rs1_51),
    .rs21(decode1_rs2_52), .rw1(and_65), .available0(rename_available0_66),
    .available1(rename_available1_67), .new0(rename_new0_68), .new1(rename_new1_69), .old0(rename_old0_70),
    .old1(rename_old1_71), .qj0(rename_qj0_72), .dj0(rename_dj0_73), .vj0(rename_vj0_74),
    .qk0(rename_qk0_75), .dk0(rename_dk0_76), .vk0(rename_vk0_77), .qj1(rename_qj1_78), .dj1(rename_dj1_79),
    .vj1(rename_vj1_80), .qk1(rename_qk1_81), .dk1(rename_dk1_82), .vk1(rename_vk1_83), .r0(r0), .r1(r1),
    .r2(r2), .r3(r3), .r4(r4), .r5(r5), .r6(r6), .r7(r7));
  Multiplexer #(.width(6), .select(1), .enable("false")) multiplexer_24 (
    .in0(rename_new0_68), .in1(rename_new1_69), .out(mux_95), .sel(and_263));
  Multiplexer #(.width(16), .select(1), .enable("false")) multiplexer_25 (
    .in0(fetch_pc0_21), .in1(fetch_pc1_22), .out(mux_99), .sel(and_263));
  Multiplexer #(.width(16), .select(1), .enable("false")) multiplexer_26 (
    .in0(rename_dj0_73), .in1(rename_dj1_79), .out(mux_103), .sel(and_263));
  Multiplexer #(.width(1), .select(1), .enable("false")) multiplexer_27 (
    .in0(and_48), .in1(and_65), .out(mux_107), .sel(and_263));
  or or_6 (or_135, and_244, and_267);
  Multiplexer #(.width(6), .select(1), .enable("false")) multiplexer_28 (
    .in0(rename_qk0_75), .in1(rename_qk1_81), .out(mux_139), .sel(and_267));
  Multiplexer #(.width(1), .select(1), .enable("false")) multiplexer_29 (
    .in0(rename_vj0_74), .in1(rename_vj1_80), .out(mux_143), .sel(and_267));
  Multiplexer #(.width(6), .select(1), .enable("false")) multiplexer_30 (
    .in0(rename_old0_70), .in1(rename_old1_71), .out(mux_147), .sel(and_267));
  ALU_RS RS1 (
    .clk(clk), .rst(rst), .clear(or_7), .enable(and_6), .wr(or_135), .take(and_285), .op(mux_136),
    .rd(mux_137), .qj(mux_138), .qk(mux_139), .imm(mux_140), .pc(mux_141), .sn(mux_142), .vj(mux_143),
    .vk(mux_144), .dj(mux_145), .dk(mux_146), .c0_valid(cdb0_valid), .c0_rd(c0_rd), .c0_data(c0_result),
    .c1_valid(cdb1_valid), .c1_rd(c1_rd), .c1_data(c1_result), .full(RS1_full_151), .count(rs1_count),
    .ex_valid(RS1_ex_valid_153), .ex_op(RS1_ex_op_154), .ex_rd(RS1_ex_rd_155), .ex_imm(RS1_ex_imm_156),
    .ex_pc(RS1_ex_pc_157), .ex_sn(RS1_ex_sn_158), .ex_a(RS1_ex_a_159), .ex_b(RS1_ex_b_160));
  Multiplexer #(.width(6), .select(1), .enable("false")) multiplexer_31 (
    .in0(rename_new0_68), .in1(rename_new1_69), .out(mux_179), .sel(and_271));
  Multiplexer #(.width(16), .select(1), .enable("false")) multiplexer_32 (
    .in0(fetch_pc0_21), .in1(fetch_pc1_22), .out(mux_183), .sel(and_271));
  Multiplexer #(.width(16), .select(1), .enable("false")) multiplexer_33 (
    .in0(rename_dj0_73), .in1(rename_dj1_79), .out(mux_187), .sel(and_271));
  Multiplexer #(.width(1), .select(1), .enable("false")) multiplexer_34 (
    .in0(and_48), .in1(and_65), .out(mux_191), .sel(and_271));
  or u_or_7 (or_219, RS0_full_109, ROB0_full_119);
  or or_8 (or_223, RS2_full_193, ROB2_full_203);
  Multiplexer #(.width(2), .select(1), .enable("false")) multiplexer_35 (
    .in0(2'b01), .in1(2'b00), .out(mux_227), .sel(not_220));
  Multiplexer #(.width(1), .select(1), .enable("false")) multiplexer_36 (
    .in0(or_230), .in1(not_224), .out(mux_231), .sel(decode0_mem_37));
  and and_19 (and_240, not_220, not_239);
  and and_20 (and_246, not_222, not_245);
  and and_21 (and_252, not_224, not_251);
  Multiplexer #(.width(1), .select(1), .enable("false")) multiplexer_37 (
    .in0(or_255), .in1(and_252), .out(mux_256), .sel(decode1_mem_55));
  not not_8 (not_314, eq_296);
  DataMemory memory (
    .clk(clk), .rst(rst), .read_addr(adder_293), .commit(store_commit), .write_addr(store_addr),
    .write_data(store_data), .debug_addr(debug_addr), .read_enable(and_317), .io_read_data(io_read_data),
    .io_addr(io_addr), .io_write_data(io_write_data), .io_read(io_read), .io_write(io_write),
    .data(memory_data_322), .debug_data(memory_debug));
  or or_9 (or_327, not_326, eq_312);
  and and_22 (cdb1_valid, and_330, mux_329);
  Multiplexer #(.width(6), .select(1), .enable("false")) multiplexer_38 (
    .in0(RS2_ex_rd_197), .in1({6{1'b0}}), .out(c1_rd), .sel(eq_296));
  Multiplexer #(.width(16), .select(1), .enable("false")) multiplexer_39 (
    .in0(io_read_data), .in1(mux_334), .out(c1_result), .sel(and_317));
  Comparator #(.width(8), .mode("unsigned")) comparator_5 (
    .a(ROB0_head_sn_129), .b(commit_sn), .gt(gt_339), .eq(eq_340), .lt(lt_341));
  and and_23 (and_350, and_349, eq_346);
  and and_24 (and_355, and_354, ROB2_head_done_206);
  or or_10 (commit_valid, or_357, and_356);
  Multiplexer #(.width(6), .select(1), .enable("false")) multiplexer_40 (
    .in0(ROB2_head_rd_old_209), .in1(ROB1_head_rd_old_167), .out(mux_363), .sel(and_350));
  Multiplexer #(.width(3), .select(1), .enable("false")) multiplexer_41 (
    .in0(mux_365), .in1(ROB0_head_rd_logic_126), .out(mux_366), .sel(and_344));
  Multiplexer #(.width(8), .select(1), .enable("false")) multiplexer_42 (
    .in0(ROB2_head_sn_213), .in1(ROB1_head_sn_171), .out(mux_371), .sel(and_350));
  Multiplexer #(.width(16), .select(1), .enable("false")) multiplexer_43 (
    .in0(mux_373), .in1(ROB0_head_pred_next_130), .out(mux_374), .sel(and_344));
  Multiplexer #(.width(1), .select(1), .enable("false")) multiplexer_44 (
    .in0(ROB2_head_taken_217), .in1(ROB1_head_taken_175), .out(mux_379), .sel(and_350));
  Multiplexer #(.width(16), .select(1), .enable("false")) multiplexer_45 (
    .in0(mux_381), .in1(ROB0_head_target_134), .out(mux_382), .sel(and_344));
  or or_11 (or_401, or_400, eq_397);
  and and_25 (and_407, and_406, not_405);
  Comparator #(.width(4), .mode("unsigned")) comparator_6 (
    .a(commit_op), .b(4'b1111), .gt(gt_409), .eq(eq_410), .lt(lt_411));
  and and_26 (store_commit, commit_valid, eq_414);
  Adder #(.width(32)) adder_7 (.a(cycles), .b(32'h1), .out(adder_419), .cin(1'b0));  // open: cout
  assign ext_421 = {{30{1'b0}}, issue_count};  // Bit_Extender bit_extender_2
  Register #(.width(32)) reg_dual_issue (.D(adder_423), .en(accept1), .Q(dual_issue), .clk(clk), .clr(rst));
  Register #(.width(32)) reg_dual_cdb (.D(adder_425), .en(and_417), .Q(dual_cdb), .clk(clk), .clr(rst));
  or or_12 (io_valid, io_read, io_write);
  not not_9 (not_3, rst);
  or or_13 (or_7, flush, halted);
  Register #(.width(16)) reg_recovery_pc (.D(mux_378), .en(and_407), .Q(recovery_pc), .clk(clk), .clr(rst));
  Register #(.width(8)) reg_retirement_sn (.D(adder_10), .en(commit_valid), .Q(commit_sn), .clk(clk), .clr(rst));
  assign ext_15 = {{6{1'b0}}, issue_count};  // Bit_Extender bit_extender_3
  Register #(.width(8)) reg_global_sn (.D(mux_17), .en(or_18), .Q(global_sn), .clk(clk), .clr(rst));
  Comparator #(.width(3), .mode("unsigned")) comparator_7 (
    .a(decode0_rd_32), .b(3'b000), .gt(gt_44), .eq(eq_45), .lt(lt_46));
  Comparator #(.width(3), .mode("unsigned")) comparator_8 (
    .a(decode1_rd_50), .b(3'b000), .gt(gt_61), .eq(eq_62), .lt(lt_63));
  Adder #(.width(8)) adder_8 (.a(global_sn), .b(8'h1), .out(adder_92), .cin(1'b0));  // open: cout
  Multiplexer #(.width(6), .select(1), .enable("false")) multiplexer_46 (
    .in0(rename_qj0_72), .in1(rename_qj1_78), .out(mux_96), .sel(and_263));
  Multiplexer #(.width(8), .select(1), .enable("false")) multiplexer_47 (
    .in0(global_sn), .in1(adder_92), .out(mux_100), .sel(and_263));
  Multiplexer #(.width(16), .select(1), .enable("false")) multiplexer_48 (
    .in0(rename_dk0_76), .in1(rename_dk1_82), .out(mux_104), .sel(and_263));
  Multiplexer #(.width(16), .select(1), .enable("false")) multiplexer_49 (
    .in0(fetch_next0_25), .in1(fetch_next1_26), .out(mux_108), .sel(and_263));
  Multiplexer #(.width(4), .select(1), .enable("false")) multiplexer_50 (
    .in0(decode0_opcode_31), .in1(decode1_opcode_49), .out(mux_136), .sel(and_267));
  Multiplexer #(.width(16), .select(1), .enable("false")) multiplexer_51 (
    .in0(decode0_imm_35), .in1(decode1_imm_53), .out(mux_140), .sel(and_267));
  Multiplexer #(.width(1), .select(1), .enable("false")) multiplexer_52 (
    .in0(rename_vk0_77), .in1(rename_vk1_83), .out(mux_144), .sel(and_267));
  Multiplexer #(.width(3), .select(1), .enable("false")) multiplexer_53 (
    .in0(decode0_rd_32), .in1(decode1_rd_50), .out(mux_148), .sel(and_267));
  ROB ROB1 (
    .clk(clk), .rst(rst), .clear(or_7), .enable(and_6), .wr(or_135), .pop(and_350), .op(mux_136),
    .rd_new(mux_137), .rd_old(mux_147), .rd_logic(mux_148), .rw(mux_149), .pc(mux_141), .sn(mux_142),
    .pred_next(mux_150), .c0_valid(cdb0_valid), .c0_sn(cdb0_sn), .c0_result(c0_result), .c0_next(c0_next),
    .c0_taken(c0_taken), .c0_target(c0_target), .c1_valid(cdb1_valid), .c1_sn(cdb1_sn),
    .c1_result(c1_result), .c1_next(adder_337), .c1_taken(1'b0), .c1_target(adder_338), .full(ROB1_full_161),
    .count(rob1_count), .head_valid(ROB1_head_valid_163), .head_done(ROB1_head_done_164),
    .head_op(ROB1_head_op_165), .head_rd_new(ROB1_head_rd_new_166), .head_rd_old(ROB1_head_rd_old_167),
    .head_rd_logic(ROB1_head_rd_logic_168), .head_rw(ROB1_head_rw_169), .head_pc(ROB1_head_pc_170),
    .head_sn(ROB1_head_sn_171), .head_pred_next(ROB1_head_pred_next_172), .head_result(ROB1_head_result_173),
    .head_next(ROB1_head_next_174), .head_taken(ROB1_head_taken_175), .head_target(ROB1_head_target_176));
  Multiplexer #(.width(6), .select(1), .enable("false")) multiplexer_54 (
    .in0(rename_qj0_72), .in1(rename_qj1_78), .out(mux_180), .sel(and_271));
  Multiplexer #(.width(8), .select(1), .enable("false")) multiplexer_55 (
    .in0(global_sn), .in1(adder_92), .out(mux_184), .sel(and_271));
  Multiplexer #(.width(16), .select(1), .enable("false")) multiplexer_56 (
    .in0(rename_dk0_76), .in1(rename_dk1_82), .out(mux_188), .sel(and_271));
  Multiplexer #(.width(16), .select(1), .enable("false")) multiplexer_57 (
    .in0(fetch_next0_25), .in1(fetch_next1_26), .out(mux_192), .sel(and_271));
  not not_10 (not_220, or_219);
  not not_11 (not_224, or_223);
  and and_27 (and_232, and_6, fetch_valid0_27);
  Comparator #(.width(2), .mode("unsigned")) comparator_9 (
    .a(mux_229), .b(2'b00), .gt(gt_235), .eq(eq_236), .lt(lt_237));
  Comparator #(.width(2), .mode("unsigned")) comparator_10 (
    .a(mux_229), .b(2'b01), .gt(gt_241), .eq(eq_242), .lt(lt_243));
  Comparator #(.width(2), .mode("unsigned")) comparator_11 (
    .a(mux_229), .b(2'b10), .gt(gt_247), .eq(eq_248), .lt(lt_249));
  Multiplexer #(.width(2), .select(1), .enable("false")) multiplexer_58 (
    .in0(2'b00), .in1(2'b01), .out(mux_253), .sel(and_246));
  and and_28 (and_257, accept0, fetch_valid1_28);
  ALU ALU0 (
    .op(RS0_ex_op_112), .a(RS0_ex_a_117), .b(RS0_ex_b_118), .imm(RS0_ex_imm_114), .pc(RS0_ex_pc_115),
    .result(ALU0_result_272), .next(ALU0_next_273), .target(ALU0_target_274), .taken(ALU0_taken_275),
    .addr(ALU0_addr_276));
  not not_12 (not_283, and_282);
  or or_14 (cdb0_valid, and_282, and_285);
  Multiplexer #(.width(8), .select(1), .enable("false")) multiplexer_59 (
    .in0(RS1_ex_sn_158), .in1(RS0_ex_sn_116), .out(cdb0_sn), .sel(and_282));
  Multiplexer #(.width(16), .select(1), .enable("false")) multiplexer_60 (
    .in0(ALU1_next_278), .in1(ALU0_next_273), .out(c0_next), .sel(and_282));
  Multiplexer #(.width(16), .select(1), .enable("false")) multiplexer_61 (
    .in0(ALU1_target_279), .in1(ALU0_target_274), .out(c0_target), .sel(and_282));
  Comparator #(.width(4), .mode("unsigned")) comparator_12 (
    .a(RS2_ex_op_196), .b(4'b1001), .gt(gt_295), .eq(eq_296), .lt(lt_297));
  and and_29 (and_315, cdb1_valid, not_314);
  not not_13 (not_324, store_commit);
  and and_30 (and_328, not_325, or_327);
  Adder #(.width(16)) adder_9 (.a(RS2_ex_pc_199), .b(16'h1), .out(adder_338), .cin(1'b0));  // open: cout
  and and_31 (and_342, and_6, ROB0_head_valid_121);
  Comparator #(.width(8), .mode("unsigned")) comparator_13 (
    .a(ROB1_head_sn_171), .b(commit_sn), .gt(gt_345), .eq(eq_346), .lt(lt_347));
  and and_32 (and_356, and_355, eq_352);
  Multiplexer #(.width(6), .select(1), .enable("false")) multiplexer_62 (
    .in0(ROB2_head_rd_new_208), .in1(ROB1_head_rd_new_166), .out(mux_361), .sel(and_350));
  Multiplexer #(.width(6), .select(1), .enable("false")) multiplexer_63 (
    .in0(mux_363), .in1(ROB0_head_rd_old_125), .out(mux_364), .sel(and_344));
  Multiplexer #(.width(16), .select(1), .enable("false")) multiplexer_64 (
    .in0(ROB2_head_pc_212), .in1(ROB1_head_pc_170), .out(mux_369), .sel(and_350));
  Multiplexer #(.width(8), .select(1), .enable("false")) multiplexer_65 (
    .in0(mux_371), .in1(ROB0_head_sn_129), .out(mux_372), .sel(and_344));
  Multiplexer #(.width(16), .select(1), .enable("false")) multiplexer_66 (
    .in0(ROB2_head_next_216), .in1(ROB1_head_next_174), .out(mux_377), .sel(and_350));
  Multiplexer #(.width(1), .select(1), .enable("false")) multiplexer_67 (
    .in0(mux_379), .in1(ROB0_head_taken_133), .out(mux_380), .sel(and_344));
  Comparator #(.width(4), .mode("unsigned")) comparator_14 (
    .a(commit_op), .b(4'b1011), .gt(gt_388), .eq(eq_389), .lt(lt_390));
  Comparator #(.width(4), .mode("unsigned")) comparator_15 (
    .a(commit_op), .b(4'b1101), .gt(gt_396), .eq(eq_397), .lt(lt_398));
  Comparator #(.width(16), .mode("unsigned")) comparator_16 (
    .a(mux_374), .b(mux_378), .gt(gt_402), .eq(eq_403), .lt(lt_404));
  and and_33 (and_412, commit_valid, eq_410);
  Register #(.width(32)) reg_cycles (.D(adder_419), .en(and_4), .Q(cycles), .clk(clk), .clr(rst));
  Adder #(.width(32)) u_adder_10 (.a(dispatched), .b(ext_421), .out(adder_422), .cin(1'b0));  // open: cout
  Adder #(.width(32)) adder_11 (.a(recoveries), .b(32'h1), .out(adder_424), .cin(1'b0));  // open: cout
  not not_14 (not_426, accept0);
  and and_34 (and_4, run, not_1);
  assign ext_12 = {{1{1'b0}}, accept0};  // Bit_Extender bit_extender_4
  Adder #(.width(8)) adder_12 (.a(global_sn), .b(ext_15), .out(adder_16), .cin(1'b0));  // open: cout
  FetchUnit fetch (
    .clk(clk), .rst(rst), .enable(and_6), .flush(flush), .recover_pc(recovery_pc), .consume(issue_count),
    .bp_we(and_406), .bp_pc(commit_pc), .bp_target(mux_382), .bp_taken(mux_380), .instr0(fetch_instr0_19),
    .instr1(fetch_instr1_20), .pc0(fetch_pc0_21), .pc1(fetch_pc1_22), .pred0(fetch_pred0_23),
    .pred1(fetch_pred1_24), .next0(fetch_next0_25), .next1(fetch_next1_26), .valid0(fetch_valid0_27),
    .valid1(fetch_valid1_28), .fetch_pc(pc), .fifo_count(fifo_count));
  not not_15 (not_47, eq_45);
  not not_16 (not_64, eq_62);
  or or_15 (or_93, and_238, and_263);
  Multiplexer #(.width(6), .select(1), .enable("false")) multiplexer_68 (
    .in0(rename_qk0_75), .in1(rename_qk1_81), .out(mux_97), .sel(and_263));
  Multiplexer #(.width(1), .select(1), .enable("false")) multiplexer_69 (
    .in0(rename_vj0_74), .in1(rename_vj1_80), .out(mux_101), .sel(and_263));
  Multiplexer #(.width(6), .select(1), .enable("false")) multiplexer_70 (
    .in0(rename_old0_70), .in1(rename_old1_71), .out(mux_105), .sel(and_263));
  ALU_RS RS0 (
    .clk(clk), .rst(rst), .clear(or_7), .enable(and_6), .wr(or_93), .take(and_282), .op(mux_94), .rd(mux_95),
    .qj(mux_96), .qk(mux_97), .imm(mux_98), .pc(mux_99), .sn(mux_100), .vj(mux_101), .vk(mux_102),
    .dj(mux_103), .dk(mux_104), .c0_valid(cdb0_valid), .c0_rd(c0_rd), .c0_data(c0_result),
    .c1_valid(cdb1_valid), .c1_rd(c1_rd), .c1_data(c1_result), .full(RS0_full_109), .count(rs0_count),
    .ex_valid(RS0_ex_valid_111), .ex_op(RS0_ex_op_112), .ex_rd(RS0_ex_rd_113), .ex_imm(RS0_ex_imm_114),
    .ex_pc(RS0_ex_pc_115), .ex_sn(RS0_ex_sn_116), .ex_a(RS0_ex_a_117), .ex_b(RS0_ex_b_118));
  Multiplexer #(.width(6), .select(1), .enable("false")) multiplexer_71 (
    .in0(rename_new0_68), .in1(rename_new1_69), .out(mux_137), .sel(and_267));
  Multiplexer #(.width(16), .select(1), .enable("false")) multiplexer_72 (
    .in0(fetch_pc0_21), .in1(fetch_pc1_22), .out(mux_141), .sel(and_267));
  Multiplexer #(.width(16), .select(1), .enable("false")) multiplexer_73 (
    .in0(rename_dj0_73), .in1(rename_dj1_79), .out(mux_145), .sel(and_267));
  Multiplexer #(.width(1), .select(1), .enable("false")) multiplexer_74 (
    .in0(and_48), .in1(and_65), .out(mux_149), .sel(and_267));
  or or_16 (or_177, and_250, and_271);
  Multiplexer #(.width(6), .select(1), .enable("false")) multiplexer_75 (
    .in0(rename_qk0_75), .in1(rename_qk1_81), .out(mux_181), .sel(and_271));
  Multiplexer #(.width(1), .select(1), .enable("false")) multiplexer_76 (
    .in0(rename_vj0_74), .in1(rename_vj1_80), .out(mux_185), .sel(and_271));
  Multiplexer #(.width(6), .select(1), .enable("false")) multiplexer_77 (
    .in0(rename_old0_70), .in1(rename_old1_71), .out(mux_189), .sel(and_271));
  LS_RS RS2 (
    .clk(clk), .rst(rst), .clear(or_7), .enable(and_6), .wr(or_177), .take(cdb1_valid), .op(mux_178),
    .rd(mux_179), .qj(mux_180), .qk(mux_181), .imm(mux_182), .pc(mux_183), .sn(mux_184), .vj(mux_185),
    .vk(mux_186), .dj(mux_187), .dk(mux_188), .c0_valid(cdb0_valid), .c0_rd(c0_rd), .c0_data(c0_result),
    .c1_valid(cdb1_valid), .c1_rd(c1_rd), .c1_data(c1_result), .full(RS2_full_193), .count(rs2_count),
    .ex_valid(RS2_ex_valid_195), .ex_op(RS2_ex_op_196), .ex_rd(RS2_ex_rd_197), .ex_imm(RS2_ex_imm_198),
    .ex_pc(RS2_ex_pc_199), .ex_sn(cdb1_sn), .ex_a(RS2_ex_a_201), .ex_b(RS2_ex_b_202));
  or or_17 (or_221, RS1_full_151, ROB1_full_161);
  Multiplexer #(.width(2), .select(1), .enable("false")) multiplexer_78 (
    .in0(mux_227), .in1(2'b10), .out(mux_229), .sel(decode0_mem_37));
  and and_35 (and_233, and_232, rename_available0_66);
  and and_36 (and_238, accept0, eq_236);
  and and_37 (and_244, accept0, eq_242);
  and and_38 (and_250, accept0, eq_248);
  Multiplexer #(.width(2), .select(1), .enable("false")) multiplexer_79 (
    .in0(mux_253), .in1(2'b10), .out(mux_254), .sel(decode1_mem_55));
  and and_39 (and_258, and_257, rename_available1_67);
  Comparator #(.width(2), .mode("unsigned")) comparator_17 (
    .a(mux_254), .b(2'b00), .gt(gt_260), .eq(eq_261), .lt(lt_262));
  Comparator #(.width(2), .mode("unsigned")) comparator_18 (
    .a(mux_254), .b(2'b01), .gt(gt_264), .eq(eq_265), .lt(lt_266));
  Comparator #(.width(2), .mode("unsigned")) comparator_19 (
    .a(mux_254), .b(2'b10), .gt(gt_268), .eq(eq_269), .lt(lt_270));
  ALU ALU1 (
    .op(RS1_ex_op_154), .a(RS1_ex_a_159), .b(RS1_ex_b_160), .imm(RS1_ex_imm_156), .pc(RS1_ex_pc_157),
    .result(ALU1_result_277), .next(ALU1_next_278), .target(ALU1_target_279), .taken(ALU1_taken_280),
    .addr(ALU1_addr_281));
  and and_40 (and_284, and_6, RS1_ex_valid_153);
  and and_41 (and_298, cdb1_valid, eq_296);
  Comparator #(.width(8), .mode("unsigned")) comparator_20 (
    .a(adder_293[15:8]), .b(8'hf0), .gt(gt_308), .eq(eq_309), .lt(lt_310));
  and and_42 (and_316, and_315, eq_309);
  not not_17 (not_325, stores_full_299);
  Multiplexer #(.width(1), .select(1), .enable("false")) multiplexer_80 (
    .in0(not_324), .in1(and_328), .out(mux_329), .sel(eq_296));
  and and_43 (and_343, and_342, ROB0_head_done_122);
  and and_44 (and_348, and_6, ROB1_head_valid_163);
  Comparator #(.width(8), .mode("unsigned")) comparator_21 (
    .a(ROB2_head_sn_213), .b(commit_sn), .gt(gt_351), .eq(eq_352), .lt(lt_353));
  Multiplexer #(.width(4), .select(1), .enable("false")) multiplexer_81 (
    .in0(ROB2_head_op_207), .in1(ROB1_head_op_165), .out(mux_359), .sel(and_350));
  Multiplexer #(.width(6), .select(1), .enable("false")) multiplexer_82 (
    .in0(mux_361), .in1(ROB0_head_rd_new_124), .out(mux_362), .sel(and_344));
  Multiplexer #(.width(1), .select(1), .enable("false")) multiplexer_83 (
    .in0(ROB2_head_rw_211), .in1(ROB1_head_rw_169), .out(mux_367), .sel(and_350));
  Multiplexer #(.width(16), .select(1), .enable("false")) multiplexer_84 (
    .in0(mux_369), .in1(ROB0_head_pc_128), .out(commit_pc), .sel(and_344));
  Multiplexer #(.width(16), .select(1), .enable("false")) multiplexer_85 (
    .in0(ROB2_head_result_215), .in1(ROB1_head_result_173), .out(mux_375), .sel(and_350));
  Multiplexer #(.width(16), .select(1), .enable("false")) multiplexer_86 (
    .in0(mux_377), .in1(ROB0_head_next_132), .out(mux_378), .sel(and_344));
  or u_or_18 (or_399, eq_385, eq_389);
  not not_18 (not_405, eq_403);
  and and_45 (and_417, cdb0_valid, cdb1_valid);
  Adder #(.width(32)) adder_13 (.a(committed), .b(32'h1), .out(adder_420), .cin(1'b0));  // open: cout
  Register #(.width(32)) reg_dispatched (.D(adder_422), .en(and_6), .Q(dispatched), .clk(clk), .clr(rst));
  Register #(.width(32)) reg_recoveries (.D(adder_424), .en(and_407), .Q(recoveries), .clk(clk), .clr(rst));
  and and_46 (stall, fetch_valid0_27, not_426);

  // Other names for the same wires on the sheet: adder_14[1:0] = issue_count; slice_306[7:0] = adder_293[15:8];
  //   and_234 = accept0; and_259 = accept1; and_427 = stall; and_428 = forward_hit; bp_we = and_406;
  //   branch_miss = and_407; c1_next[15:0] = adder_337; c1_sn[7:0] = cdb1_sn; RS2_ex_sn_200[7:0] = cdb1_sn;
  //   c1_target[15:0] = adder_338; and_416 = store_commit; commit_store = store_commit; fetch_fetch_pc_29[15:0] = pc;
  //   fetch_fifo_count_30[3:0] = fifo_count; halt_commit = and_412; memory_debug_data_323[15:0] = memory_debug;
  //   memory_io_addr_318[15:0] = io_addr; memory_io_read_320 = io_read; memory_io_write_321 = io_write;
  //   memory_io_write_data_319[15:0] = io_write_data; mux_287[5:0] = c0_rd; c0_sn[7:0] = cdb0_sn;
  //   mux_288[7:0] = cdb0_sn; mux_289[15:0] = c0_result; mux_290[15:0] = c0_next; mux_291 = c0_taken;
  //   mux_292[15:0] = c0_target; mux_333[5:0] = c1_rd; mux_335[15:0] = c1_result; c0_valid = cdb0_valid;
  //   or_286 = cdb0_valid; or_429 = io_valid; pop0 = and_344; pop1 = and_350; pop2 = and_356; recovery = flush;
  //   rename_r0_84[15:0] = r0; rename_r1_85[15:0] = r1; rename_r2_86[15:0] = r2; rename_r3_87[15:0] = r3;
  //   rename_r4_88[15:0] = r4; rename_r5_89[15:0] = r5; rename_r6_90[15:0] = r6; rename_r7_91[15:0] = r7;
  //   or_358 = commit_valid; retire = commit_valid; retire_next[15:0] = mux_378; mux_360[3:0] = commit_op;
  //   retire_op[3:0] = commit_op; mux_370[15:0] = commit_pc; retire_pc[15:0] = commit_pc;
  //   retire_pred_next[15:0] = mux_374; retire_rd_logic[2:0] = mux_366; retire_rd_new[5:0] = mux_362;
  //   retire_rd_old[5:0] = mux_364; mux_376[15:0] = commit_result; retire_result[15:0] = commit_result;
  //   retire_rw = mux_368; retire_sn[7:0] = mux_372; retire_taken = mux_380; retire_target[15:0] = mux_382;
  //   retirement_sn[7:0] = commit_sn; ROB0_count_120[4:0] = rob0_count; ROB1_count_162[4:0] = rob1_count;
  //   ROB2_count_204[4:0] = rob2_count; RS0_count_110[4:0] = rs0_count; RS1_count_152[4:0] = rs1_count;
  //   RS2_count_194[4:0] = rs2_count; stores_commit_addr_304[15:0] = store_addr;
  //   stores_commit_data_305[15:0] = store_data; stores_count_300[3:0] = sb_count; take0 = and_282; take1 = and_285;
  //   and_331 = cdb1_valid; c1_valid = cdb1_valid; take2 = cdb1_valid; unit0_lane0 = and_238; unit0_lane1 = and_263;
  //   unit1_lane0 = and_244; unit1_lane1 = and_267; unit2_lane0 = and_250; unit2_lane1 = and_271

  // Notes on the sheet:
  //   Dual issue / out-of-order execute / precise ordered retirement
endmodule

module DecodeOne (
  input  [15:0] instr,
  input  [15:0] pc,
  input  pred,
  output [3:0] opcode,
  output [2:0] rd,
  output [2:0] rs1,
  output [2:0] rs2,
  output [15:0] imm,
  output rw,
  output mem,
  output store,
  output branch,
  output jump,
  output halt,
  output [56:0] packet
);

  wire eq_4, eq_8, eq_12, eq_16, eq_20, eq_24, eq_33, eq_37, eq_42, eq_46, eq_64, eq_68, gt_3, gt_7, gt_11,
       gt_15, gt_19, gt_23, gt_32, gt_36, gt_41, gt_45, gt_50, gt_54, gt_59, gt_63, gt_67, lt_5, lt_9, lt_13,
       lt_17, lt_21, lt_25, lt_34, lt_38, lt_43, lt_47, lt_52, lt_56, lt_61, lt_65, lt_69, or_26, or_27,
       or_28, or_29, or_30, or_70, or_71, or_72, or_73, or_75, or_76, or_77, or_87, or_88, or_89, or_90,
       or_91, or_92;
  wire [2:0] mux_82, mux_85, mux_111, mux_112, mux_113, mux_114, mux_115, mux_116, mux_117, mux_118, mux_119;
  wire [15:0] ext_95, ext_98, mux_96;

  Comparator #(.width(4), .mode("unsigned")) comparator_1 (
    .a(instr[15:12]), .b(4'b0010), .gt(gt_7), .eq(eq_8), .lt(lt_9));
  Comparator #(.width(4), .mode("unsigned")) comparator_2 (
    .a(instr[15:12]), .b(4'b0100), .gt(gt_15), .eq(eq_16), .lt(lt_17));
  Comparator #(.width(4), .mode("unsigned")) comparator_3 (
    .a(instr[15:12]), .b(4'b0110), .gt(gt_23), .eq(eq_24), .lt(lt_25));
  or or_1 (or_29, or_28, eq_20);
  Comparator #(.width(4), .mode("unsigned")) comparator_4 (
    .a(instr[15:12]), .b(4'b1100), .gt(gt_41), .eq(eq_42), .lt(lt_43));
  or or_2 (mem, packet[38], packet[31]);
  Comparator #(.width(4), .mode("unsigned")) comparator_5 (
    .a(instr[15:12]), .b(4'b0111), .gt(gt_63), .eq(eq_64), .lt(lt_65));
  or or_3 (or_71, or_70, packet[38]);
  or or_4 (or_75, branch, packet[31]);
  Multiplexer #(.width(3), .select(1), .enable("false")) multiplexer_1 (
    .in0(mux_82), .in1(instr[11:9]), .out(packet[9:7]), .sel(or_75));
  or or_5 (or_87, eq_64, packet[38]);
  or or_6 (or_91, or_90, eq_46);
  assign ext_95 = {{10{instr[5]}}, instr[5:0]};  // Bit_Extender bit_extender_1
  Multiplexer #(.width(16), .select(1), .enable("false")) multiplexer_2 (
    .in0(mux_96), .in1(ext_98), .out(imm), .sel(eq_42));
  Multiplexer #(.width(3), .select(1), .enable("false")) multiplexer_3 (
    .in0(3'b001), .in1(3'b010), .out(mux_111), .sel(instr[12]));
  Multiplexer #(.width(3), .select(1), .enable("false")) multiplexer_4 (
    .in0(mux_113), .in1(mux_114), .out(mux_115), .sel(instr[13]));
  Multiplexer #(.width(3), .select(1), .enable("false")) multiplexer_5 (
    .in0(mux_117), .in1(mux_118), .out(mux_119), .sel(instr[14]));
  or or_7 (or_26, eq_4, eq_8);
  or or_8 (or_30, or_29, eq_24);
  Comparator #(.width(4), .mode("unsigned")) comparator_6 (
    .a(instr[15:12]), .b(4'b1011), .gt(gt_36), .eq(eq_37), .lt(lt_38));
  Comparator #(.width(4), .mode("unsigned")) comparator_7 (
    .a(instr[15:12]), .b(4'b1001), .gt(gt_50), .eq(packet[31]), .lt(lt_52));
  or or_9 (or_72, or_71, eq_42);
  or or_10 (or_76, or_71, eq_46);
  Multiplexer #(.width(3), .select(1), .enable("false")) multiplexer_6 (
    .in0(3'b000), .in1(instr[11:9]), .out(packet[6:4]), .sel(packet[29]));
  or or_11 (or_88, or_87, packet[31]);
  or or_12 (or_92, or_91, eq_68);
  Multiplexer #(.width(16), .select(1), .enable("false")) multiplexer_7 (
    .in0({16{1'b0}}), .in1(ext_95), .out(mux_96), .sel(or_92));
  Multiplexer #(.width(3), .select(1), .enable("false")) multiplexer_8 (
    .in0(3'b000), .in1(mux_111), .out(mux_112), .sel(instr[13]));
  Multiplexer #(.width(3), .select(1), .enable("false")) multiplexer_9 (
    .in0(mux_112), .in1(mux_115), .out(mux_116), .sel(instr[14]));
  Multiplexer #(.width(3), .select(1), .enable("false")) multiplexer_10 (
    .in0(mux_116), .in1(mux_119), .out(packet[36:34]), .sel(instr[15]));
  Comparator #(.width(4), .mode("unsigned")) comparator_8 (
    .a(instr[15:12]), .b(4'b0001), .gt(gt_3), .eq(eq_4), .lt(lt_5));
  Comparator #(.width(4), .mode("unsigned")) comparator_9 (
    .a(instr[15:12]), .b(4'b0011), .gt(gt_11), .eq(eq_12), .lt(lt_13));
  Comparator #(.width(4), .mode("unsigned")) comparator_10 (
    .a(instr[15:12]), .b(4'b0101), .gt(gt_19), .eq(eq_20), .lt(lt_21));
  or or_13 (or_27, or_26, eq_12);
  or or_14 (branch, eq_33, eq_37);
  Comparator #(.width(4), .mode("unsigned")) comparator_11 (
    .a(instr[15:12]), .b(4'b1101), .gt(gt_45), .eq(eq_46), .lt(lt_47));
  Comparator #(.width(4), .mode("unsigned")) comparator_12 (
    .a(instr[15:12]), .b(4'b1111), .gt(gt_59), .eq(halt), .lt(lt_61));
  Comparator #(.width(4), .mode("unsigned")) comparator_13 (
    .a(instr[15:12]), .b(4'b1110), .gt(gt_67), .eq(eq_68), .lt(lt_69));
  or or_15 (or_73, or_72, eq_46);
  or or_16 (or_77, or_76, eq_68);
  Multiplexer #(.width(3), .select(1), .enable("false")) multiplexer_11 (
    .in0(3'b000), .in1(instr[5:3]), .out(mux_85), .sel(or_30));
  or or_17 (or_89, or_88, eq_33);
  Multiplexer #(.width(3), .select(1), .enable("false")) multiplexer_12 (
    .in0(3'b011), .in1(3'b100), .out(mux_113), .sel(instr[12]));
  Multiplexer #(.width(3), .select(1), .enable("false")) multiplexer_13 (
    .in0(3'b000), .in1(3'b001), .out(mux_117), .sel(instr[13]));
  or or_18 (packet[37], or_88, eq_68);
  or or_19 (or_28, or_27, eq_16);
  Comparator #(.width(4), .mode("unsigned")) comparator_14 (
    .a(instr[15:12]), .b(4'b1010), .gt(gt_32), .eq(eq_33), .lt(lt_34));
  or or_20 (jump, eq_42, eq_46);
  Comparator #(.width(4), .mode("unsigned")) comparator_15 (
    .a(instr[15:12]), .b(4'b1000), .gt(gt_54), .eq(packet[38]), .lt(lt_56));
  or or_21 (or_70, or_30, eq_64);
  or or_22 (packet[29], or_73, eq_68);
  Multiplexer #(.width(3), .select(1), .enable("false")) multiplexer_14 (
    .in0(3'b000), .in1(instr[8:6]), .out(mux_82), .sel(or_77));
  Multiplexer #(.width(3), .select(1), .enable("false")) multiplexer_15 (
    .in0(mux_85), .in1(instr[8:6]), .out(packet[12:10]), .sel(or_75));
  or or_23 (or_90, or_89, eq_37);
  assign ext_98 = {{7{instr[8]}}, instr[8:0]};  // Bit_Extender bit_extender_2
  Multiplexer #(.width(3), .select(1), .enable("false")) multiplexer_16 (
    .in0(3'b101), .in1(3'b000), .out(mux_114), .sel(instr[12]));
  Multiplexer #(.width(3), .select(1), .enable("false")) multiplexer_17 (
    .in0(3'b000), .in1(mux_114), .out(mux_118), .sel(instr[13]));

  assign opcode = instr[15:12];
  assign {packet[56:39], packet[33:32], packet[30], packet[28:13], packet[3:0]} = {pred, pc, halt, jump, branch, packet[38], imm, instr[15:12]};
  assign rd = packet[6:4];
  assign rs1 = packet[9:7];
  assign rs2 = packet[12:10];
  assign rw = packet[29];
  assign store = packet[31];

  // Other names for the same wires on the sheet: slice_94[5:0] = instr[5:0]; slice_97[8:0] = instr[8:0];
  //   slice_84[2:0] = instr[5:3]; slice_81[2:0] = instr[8:6]; slice_79[2:0] = instr[11:9]; or_57 = mem;
  //   pack_122[56:0] = {pred, pc, halt, packet[38:34], jump, branch, packet[31], packet[38], packet[29], imm, packet[12:4], instr[15:12]};
  //   slice_1[3:0] = instr[15:12]; slice_105[2:0] = instr[14:12]; slice_107[1:0] = instr[13:12];
  //   slice_109 = instr[12]; slice_110 = instr[13]; slice_108 = instr[14]; slice_106 = instr[15];
  //   mux_80[2:0] = packet[6:4]; mux_83[2:0] = packet[9:7]; mux_86[2:0] = packet[12:10]; mux_99[15:0] = imm;
  //   or_74 = packet[29]; eq_51 = packet[31]; or_39 = branch; or_48 = jump; mux_120[2:0] = packet[36:34];
  //   or_121 = packet[37]; eq_55 = packet[38]; eq_60 = halt

  // Notes on the sheet:
  //   16-bit ISA decode / 57-bit control packet
endmodule
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module ROB (
  input  clk,
  input  rst,
  input  clear,
  input  enable,
  input  wr,
  input  pop,
  input  [3:0] op,
  input  [5:0] rd_new,
  input  [5:0] rd_old,
  input  [2:0] rd_logic,
  input  rw,
  input  [15:0] pc,
  input  [7:0] sn,
  input  [15:0] pred_next,
  input  c0_valid,
  input  [7:0] c0_sn,
  input  [15:0] c0_result,
  input  [15:0] c0_next,
  input  c0_taken,
  input  [15:0] c0_target,
  input  c1_valid,
  input  [7:0] c1_sn,
  input  [15:0] c1_result,
  input  [15:0] c1_next,
  input  c1_taken,
  input  [15:0] c1_target,
  output full,
  output [4:0] count,
  output head_valid,
  output head_done,
  output [3:0] head_op,
  output [5:0] head_rd_new,
  output [5:0] head_rd_old,
  output [2:0] head_rd_logic,
  output head_rw,
  output [15:0] head_pc,
  output [7:0] head_sn,
  output [15:0] head_pred_next,
  output [15:0] head_result,
  output [15:0] head_next,
  output head_taken,
  output [15:0] head_target
);

  wire and_12, and_13, and_14, and_15, and_30, and_34, and_52, and_56, and_75, and_79, and_98, and_102,
       and_121, and_125, and_144, and_148, and_167, and_171, and_190, and_194, and_213, and_217, and_236,
       and_240, and_259, and_263, and_282, and_286, and_305, and_309, and_328, and_332, and_351, and_355,
       and_374, and_378, entry00_done_36, entry00_rw_41, entry00_taken_47, entry00_valid_35, entry01_done_58,
       entry01_rw_63, entry01_taken_69, entry01_valid_57, entry02_done_81, entry02_rw_86, entry02_taken_92,
       entry02_valid_80, entry03_done_104, entry03_rw_109, entry03_taken_115, entry03_valid_103,
       entry04_done_127, entry04_rw_132, entry04_taken_138, entry04_valid_126, entry05_done_150,
       entry05_rw_155, entry05_taken_161, entry05_valid_149, entry06_done_173, entry06_rw_178,
       entry06_taken_184, entry06_valid_172, entry07_done_196, entry07_rw_201, entry07_taken_207,
       entry07_valid_195, entry08_done_219, entry08_rw_224, entry08_taken_230, entry08_valid_218,
       entry09_done_242, entry09_rw_247, entry09_taken_253, entry09_valid_241, entry10_done_265,
       entry10_rw_270, entry10_taken_276, entry10_valid_264, entry11_done_288, entry11_rw_293,
       entry11_taken_299, entry11_valid_287, entry12_done_311, entry12_rw_316, entry12_taken_322,
       entry12_valid_310, entry13_done_334, entry13_rw_339, entry13_taken_345, entry13_valid_333,
       entry14_done_357, entry14_rw_362, entry14_taken_368, entry14_valid_356, entry15_done_380,
       entry15_rw_385, entry15_taken_391, entry15_valid_379, eq_8, eq_28, eq_32, eq_50, eq_54, eq_73, eq_77,
       eq_96, eq_100, eq_119, eq_123, eq_142, eq_146, eq_165, eq_169, eq_188, eq_192, eq_211, eq_215, eq_234,
       eq_238, eq_257, eq_261, eq_280, eq_284, eq_303, eq_307, eq_326, eq_330, eq_349, eq_353, eq_372,
       eq_376, gt_3, gt_7, gt_27, gt_31, gt_49, gt_53, gt_72, gt_76, gt_95, gt_99, gt_118, gt_122, gt_141,
       gt_145, gt_164, gt_168, gt_187, gt_191, gt_210, gt_214, gt_233, gt_237, gt_256, gt_260, gt_279,
       gt_283, gt_302, gt_306, gt_325, gt_329, gt_348, gt_352, gt_371, gt_375, lt_5, lt_9, lt_29, lt_33,
       lt_51, lt_55, lt_74, lt_78, lt_97, lt_101, lt_120, lt_124, lt_143, lt_147, lt_166, lt_170, lt_189,
       lt_193, lt_212, lt_216, lt_235, lt_239, lt_258, lt_262, lt_281, lt_285, lt_304, lt_308, lt_327,
       lt_331, lt_350, lt_354, lt_373, lt_377, mux_399, mux_400, mux_401, mux_402, mux_403, mux_404, mux_405,
       mux_406, mux_407, mux_408, mux_409, mux_410, mux_411, mux_412, mux_413, mux_415, mux_416, mux_417,
       mux_418, mux_419, mux_420, mux_421, mux_422, mux_423, mux_424, mux_425, mux_426, mux_427, mux_428,
       mux_490, mux_491, mux_492, mux_493, mux_494, mux_495, mux_496, mux_497, mux_498, mux_499, mux_500,
       mux_501, mux_502, mux_503, mux_580, mux_581, mux_582, mux_583, mux_584, mux_585, mux_586, mux_587,
       mux_588, mux_589, mux_590, mux_591, mux_592, mux_593, not_10, not_11, or_1, xor_25;
  wire [2:0] entry00_rd_logic_40, entry01_rd_logic_62, entry02_rd_logic_85, entry03_rd_logic_108,
       entry04_rd_logic_131, entry05_rd_logic_154, entry06_rd_logic_177, entry07_rd_logic_200,
       entry08_rd_logic_223, entry09_rd_logic_246, entry10_rd_logic_269, entry11_rd_logic_292,
       entry12_rd_logic_315, entry13_rd_logic_338, entry14_rd_logic_361, entry15_rd_logic_384, mux_475,
       mux_476, mux_477, mux_478, mux_479, mux_480, mux_481, mux_482, mux_483, mux_484, mux_485, mux_486,
       mux_487, mux_488;
  wire [3:0] adder_17, adder_19, entry00_op_37, entry01_op_59, entry02_op_82, entry03_op_105, entry04_op_128,
       entry05_op_151, entry06_op_174, entry07_op_197, entry08_op_220, entry09_op_243, entry10_op_266,
       entry11_op_289, entry12_op_312, entry13_op_335, entry14_op_358, entry15_op_381, mux_430, mux_431,
       mux_432, mux_433, mux_434, mux_435, mux_436, mux_437, mux_438, mux_439, mux_440, mux_441, mux_442,
       mux_443, Q_head, Q_tail;
  wire [4:0] adder_21, adder_23, mux_24;
  wire [5:0] entry00_rd_new_38, entry00_rd_old_39, entry01_rd_new_60, entry01_rd_old_61, entry02_rd_new_83,
       entry02_rd_old_84, entry03_rd_new_106, entry03_rd_old_107, entry04_rd_new_129, entry04_rd_old_130,
       entry05_rd_new_152, entry05_rd_old_153, entry06_rd_new_175, entry06_rd_old_176, entry07_rd_new_198,
       entry07_rd_old_199, entry08_rd_new_221, entry08_rd_old_222, entry09_rd_new_244, entry09_rd_old_245,
       entry10_rd_new_267, entry10_rd_old_268, entry11_rd_new_290, entry11_rd_old_291, entry12_rd_new_313,
       entry12_rd_old_314, entry13_rd_new_336, entry13_rd_old_337, entry14_rd_new_359, entry14_rd_old_360,
       entry15_rd_new_382, entry15_rd_old_383, mux_445, mux_446, mux_447, mux_448, mux_449, mux_450, mux_451,
       mux_452, mux_453, mux_454, mux_455, mux_456, mux_457, mux_458, mux_460, mux_461, mux_462, mux_463,
       mux_464, mux_465, mux_466, mux_467, mux_468, mux_469, mux_470, mux_471, mux_472, mux_473;
  wire [7:0] entry00_sn_43, entry01_sn_65, entry02_sn_88, entry03_sn_111, entry04_sn_134, entry05_sn_157,
       entry06_sn_180, entry07_sn_203, entry08_sn_226, entry09_sn_249, entry10_sn_272, entry11_sn_295,
       entry12_sn_318, entry13_sn_341, entry14_sn_364, entry15_sn_387, mux_520, mux_521, mux_522, mux_523,
       mux_524, mux_525, mux_526, mux_527, mux_528, mux_529, mux_530, mux_531, mux_532, mux_533;
  wire [15:0] entry00_next_46, entry00_pc_42, entry00_pred_next_44, entry00_result_45, entry00_target_48,
       entry01_next_68, entry01_pc_64, entry01_pred_next_66, entry01_result_67, entry01_target_70,
       entry02_next_91, entry02_pc_87, entry02_pred_next_89, entry02_result_90, entry02_target_93,
       entry03_next_114, entry03_pc_110, entry03_pred_next_112, entry03_result_113, entry03_target_116,
       entry04_next_137, entry04_pc_133, entry04_pred_next_135, entry04_result_136, entry04_target_139,
       entry05_next_160, entry05_pc_156, entry05_pred_next_158, entry05_result_159, entry05_target_162,
       entry06_next_183, entry06_pc_179, entry06_pred_next_181, entry06_result_182, entry06_target_185,
       entry07_next_206, entry07_pc_202, entry07_pred_next_204, entry07_result_205, entry07_target_208,
       entry08_next_229, entry08_pc_225, entry08_pred_next_227, entry08_result_228, entry08_target_231,
       entry09_next_252, entry09_pc_248, entry09_pred_next_250, entry09_result_251, entry09_target_254,
       entry10_next_275, entry10_pc_271, entry10_pred_next_273, entry10_result_274, entry10_target_277,
       entry11_next_298, entry11_pc_294, entry11_pred_next_296, entry11_result_297, entry11_target_300,
       entry12_next_321, entry12_pc_317, entry12_pred_next_319, entry12_result_320, entry12_target_323,
       entry13_next_344, entry13_pc_340, entry13_pred_next_342, entry13_result_343, entry13_target_346,
       entry14_next_367, entry14_pc_363, entry14_pred_next_365, entry14_result_366, entry14_target_369,
       entry15_next_390, entry15_pc_386, entry15_pred_next_388, entry15_result_389, entry15_target_392,
       mux_505, mux_506, mux_507, mux_508, mux_509, mux_510, mux_511, mux_512, mux_513, mux_514, mux_515,
       mux_516, mux_517, mux_518, mux_535, mux_536, mux_537, mux_538, mux_539, mux_540, mux_541, mux_542,
       mux_543, mux_544, mux_545, mux_546, mux_547, mux_548, mux_550, mux_551, mux_552, mux_553, mux_554,
       mux_555, mux_556, mux_557, mux_558, mux_559, mux_560, mux_561, mux_562, mux_563, mux_565, mux_566,
       mux_567, mux_568, mux_569, mux_570, mux_571, mux_572, mux_573, mux_574, mux_575, mux_576, mux_577,
       mux_578, mux_595, mux_596, mux_597, mux_598, mux_599, mux_600, mux_601, mux_602, mux_603, mux_604,
       mux_605, mux_606, mux_607, mux_608;

  or u_or_1 (or_1, rst, clear);
  Comparator #(.width(5), .mode("unsigned")) comparator_1 (.a(count), .b({5{1'b0}}), .gt(gt_7), .eq(eq_8), .lt(lt_9));
  and and_1 (and_13, and_12, not_11);
  Adder #(.width(4)) adder_1 (.a(Q_head), .b(4'b0001), .out(adder_17), .cin(1'b0));  // open: cout
  Register #(.width(4)) reg_Q_tail (.D(adder_19), .en(and_13), .Q(Q_tail), .clk(clk), .clr(or_1));
  Adder #(.width(5)) adder_2 (.a(count), .b(5'b00001), .out(adder_23), .cin(1'b0));  // open: cout
  and and_2 (and_34, and_15, eq_32);
  Comparator #(.width(4), .mode("unsigned")) comparator_2 (.a(Q_head), .b(4'b0001), .gt(gt_53), .eq(eq_54), .lt(lt_55));
  Comparator #(.width(4), .mode("unsigned")) comparator_3 (.a(Q_tail), .b(4'b0010), .gt(gt_72), .eq(eq_73), .lt(lt_74));
  ROB_Entry entry02 (
    .clk(clk), .rst(rst), .clear(clear), .enable(enable), .wr(and_75), .erase(and_79), .op(op),
    .rd_new(rd_new), .rd_old(rd_old), .rd_logic(rd_logic), .rw(rw), .pc(pc), .sn(sn), .pred_next(pred_next),
    .c0_valid(c0_valid), .c0_sn(c0_sn), .c0_result(c0_result), .c0_next(c0_next), .c0_taken(c0_taken),
    .c0_target(c0_target), .c1_valid(c1_valid), .c1_sn(c1_sn), .c1_result(c1_result), .c1_next(c1_next),
    .c1_taken(c1_taken), .c1_target(c1_target), .valid(entry02_valid_80), .done(entry02_done_81),
    .op_2(entry02_op_82), .rd_new_2(entry02_rd_new_83), .rd_old_2(entry02_rd_old_84),
    .rd_logic_2(entry02_rd_logic_85), .rw_2(entry02_rw_86), .pc_2(entry02_pc_87), .sn_2(entry02_sn_88),
    .pred_next_2(entry02_pred_next_89), .result(entry02_result_90), .next(entry02_next_91),
    .taken(entry02_taken_92), .target(entry02_target_93));
  Comparator #(.width(4), .mode("unsigned")) comparator_4 (
    .a(Q_head), .b(4'b0011), .gt(gt_99), .eq(eq_100), .lt(lt_101));
  Comparator #(.width(4), .mode("unsigned")) comparator_5 (
    .a(Q_tail), .b(4'b0100), .gt(gt_118), .eq(eq_119), .lt(lt_120));
  ROB_Entry entry04 (
    .clk(clk), .rst(rst), .clear(clear), .enable(enable), .wr(and_121), .erase(and_125), .op(op),
    .rd_new(rd_new), .rd_old(rd_old), .rd_logic(rd_logic), .rw(rw), .pc(pc), .sn(sn), .pred_next(pred_next),
    .c0_valid(c0_valid), .c0_sn(c0_sn), .c0_result(c0_result), .c0_next(c0_next), .c0_taken(c0_taken),
    .c0_target(c0_target), .c1_valid(c1_valid), .c1_sn(c1_sn), .c1_result(c1_result), .c1_next(c1_next),
    .c1_taken(c1_taken), .c1_target(c1_target), .valid(entry04_valid_126), .done(entry04_done_127),
    .op_2(entry04_op_128), .rd_new_2(entry04_rd_new_129), .rd_old_2(entry04_rd_old_130),
    .rd_logic_2(entry04_rd_logic_131), .rw_2(entry04_rw_132), .pc_2(entry04_pc_133), .sn_2(entry04_sn_134),
    .pred_next_2(entry04_pred_next_135), .result(entry04_result_136), .next(entry04_next_137),
    .taken(entry04_taken_138), .target(entry04_target_139));
  Comparator #(.width(4), .mode("unsigned")) comparator_6 (
    .a(Q_head), .b(4'b0101), .gt(gt_145), .eq(eq_146), .lt(lt_147));
  Comparator #(.width(4), .mode("unsigned")) comparator_7 (
    .a(Q_tail), .b(4'b0110), .gt(gt_164), .eq(eq_165), .lt(lt_166));
  ROB_Entry entry06 (
    .clk(clk), .rst(rst), .clear(clear), .enable(enable), .wr(and_167), .erase(and_171), .op(op),
    .rd_new(rd_new), .rd_old(rd_old), .rd_logic(rd_logic), .rw(rw), .pc(pc), .sn(sn), .pred_next(pred_next),
    .c0_valid(c0_valid), .c0_sn(c0_sn), .c0_result(c0_result), .c0_next(c0_next), .c0_taken(c0_taken),
    .c0_target(c0_target), .c1_valid(c1_valid), .c1_sn(c1_sn), .c1_result(c1_result), .c1_next(c1_next),
    .c1_taken(c1_taken), .c1_target(c1_target), .valid(entry06_valid_172), .done(entry06_done_173),
    .op_2(entry06_op_174), .rd_new_2(entry06_rd_new_175), .rd_old_2(entry06_rd_old_176),
    .rd_logic_2(entry06_rd_logic_177), .rw_2(entry06_rw_178), .pc_2(entry06_pc_179), .sn_2(entry06_sn_180),
    .pred_next_2(entry06_pred_next_181), .result(entry06_result_182), .next(entry06_next_183),
    .taken(entry06_taken_184), .target(entry06_target_185));
  Comparator #(.width(4), .mode("unsigned")) comparator_8 (
    .a(Q_head), .b(4'b0111), .gt(gt_191), .eq(eq_192), .lt(lt_193));
  Comparator #(.width(4), .mode("unsigned")) comparator_9 (
    .a(Q_tail), .b(4'b1000), .gt(gt_210), .eq(eq_211), .lt(lt_212));
  ROB_Entry entry08 (
    .clk(clk), .rst(rst), .clear(clear), .enable(enable), .wr(and_213), .erase(and_217), .op(op),
    .rd_new(rd_new), .rd_old(rd_old), .rd_logic(rd_logic), .rw(rw), .pc(pc), .sn(sn), .pred_next(pred_next),
    .c0_valid(c0_valid), .c0_sn(c0_sn), .c0_result(c0_result), .c0_next(c0_next), .c0_taken(c0_taken),
    .c0_target(c0_target), .c1_valid(c1_valid), .c1_sn(c1_sn), .c1_result(c1_result), .c1_next(c1_next),
    .c1_taken(c1_taken), .c1_target(c1_target), .valid(entry08_valid_218), .done(entry08_done_219),
    .op_2(entry08_op_220), .rd_new_2(entry08_rd_new_221), .rd_old_2(entry08_rd_old_222),
    .rd_logic_2(entry08_rd_logic_223), .rw_2(entry08_rw_224), .pc_2(entry08_pc_225), .sn_2(entry08_sn_226),
    .pred_next_2(entry08_pred_next_227), .result(entry08_result_228), .next(entry08_next_229),
    .taken(entry08_taken_230), .target(entry08_target_231));
  Comparator #(.width(4), .mode("unsigned")) comparator_10 (
    .a(Q_head), .b(4'b1001), .gt(gt_237), .eq(eq_238), .lt(lt_239));
  Comparator #(.width(4), .mode("unsigned")) comparator_11 (
    .a(Q_tail), .b(4'b1010), .gt(gt_256), .eq(eq_257), .lt(lt_258));
  ROB_Entry entry10 (
    .clk(clk), .rst(rst), .clear(clear), .enable(enable), .wr(and_259), .erase(and_263), .op(op),
    .rd_new(rd_new), .rd_old(rd_old), .rd_logic(rd_logic), .rw(rw), .pc(pc), .sn(sn), .pred_next(pred_next),
    .c0_valid(c0_valid), .c0_sn(c0_sn), .c0_result(c0_result), .c0_next(c0_next), .c0_taken(c0_taken),
    .c0_target(c0_target), .c1_valid(c1_valid), .c1_sn(c1_sn), .c1_result(c1_result), .c1_next(c1_next),
    .c1_taken(c1_taken), .c1_target(c1_target), .valid(entry10_valid_264), .done(entry10_done_265),
    .op_2(entry10_op_266), .rd_new_2(entry10_rd_new_267), .rd_old_2(entry10_rd_old_268),
    .rd_logic_2(entry10_rd_logic_269), .rw_2(entry10_rw_270), .pc_2(entry10_pc_271), .sn_2(entry10_sn_272),
    .pred_next_2(entry10_pred_next_273), .result(entry10_result_274), .next(entry10_next_275),
    .taken(entry10_taken_276), .target(entry10_target_277));
  Comparator #(.width(4), .mode("unsigned")) comparator_12 (
    .a(Q_head), .b(4'b1011), .gt(gt_283), .eq(eq_284), .lt(lt_285));
  Comparator #(.width(4), .mode("unsigned")) comparator_13 (
    .a(Q_tail), .b(4'b1100), .gt(gt_302), .eq(eq_303), .lt(lt_304));
  ROB_Entry entry12 (
    .clk(clk), .rst(rst), .clear(clear), .enable(enable), .wr(and_305), .erase(and_309), .op(op),
    .rd_new(rd_new), .rd_old(rd_old), .rd_logic(rd_logic), .rw(rw), .pc(pc), .sn(sn), .pred_next(pred_next),
    .c0_valid(c0_valid), .c0_sn(c0_sn), .c0_result(c0_result), .c0_next(c0_next), .c0_taken(c0_taken),
    .c0_target(c0_target), .c1_valid(c1_valid), .c1_sn(c1_sn), .c1_result(c1_result), .c1_next(c1_next),
    .c1_taken(c1_taken), .c1_target(c1_target), .valid(entry12_valid_310), .done(entry12_done_311),
    .op_2(entry12_op_312), .rd_new_2(entry12_rd_new_313), .rd_old_2(entry12_rd_old_314),
    .rd_logic_2(entry12_rd_logic_315), .rw_2(entry12_rw_316), .pc_2(entry12_pc_317), .sn_2(entry12_sn_318),
    .pred_next_2(entry12_pred_next_319), .result(entry12_result_320), .next(entry12_next_321),
    .taken(entry12_taken_322), .target(entry12_target_323));
  Comparator #(.width(4), .mode("unsigned")) comparator_14 (
    .a(Q_head), .b(4'b1101), .gt(gt_329), .eq(eq_330), .lt(lt_331));
  Comparator #(.width(4), .mode("unsigned")) comparator_15 (
    .a(Q_tail), .b(4'b1110), .gt(gt_348), .eq(eq_349), .lt(lt_350));
  ROB_Entry entry14 (
    .clk(clk), .rst(rst), .clear(clear), .enable(enable), .wr(and_351), .erase(and_355), .op(op),
    .rd_new(rd_new), .rd_old(rd_old), .rd_logic(rd_logic), .rw(rw), .pc(pc), .sn(sn), .pred_next(pred_next),
    .c0_valid(c0_valid), .c0_sn(c0_sn), .c0_result(c0_result), .c0_next(c0_next), .c0_taken(c0_taken),
    .c0_target(c0_target), .c1_valid(c1_valid), .c1_sn(c1_sn), .c1_result(c1_result), .c1_next(c1_next),
    .c1_taken(c1_taken), .c1_target(c1_target), .valid(entry14_valid_356), .done(entry14_done_357),
    .op_2(entry14_op_358), .rd_new_2(entry14_rd_new_359), .rd_old_2(entry14_rd_old_360),
    .rd_logic_2(entry14_rd_logic_361), .rw_2(entry14_rw_362), .pc_2(entry14_pc_363), .sn_2(entry14_sn_364),
    .pred_next_2(entry14_pred_next_365), .result(entry14_result_366), .next(entry14_next_367),
    .taken(entry14_taken_368), .target(entry14_target_369));
  Comparator #(.width(4), .mode("unsigned")) comparator_16 (
    .a(Q_head), .b(4'b1111), .gt(gt_375), .eq(eq_376), .lt(lt_377));
  Multiplexer #(.width(1), .select(1), .enable("false")) multiplexer_1 (
    .in0(entry04_valid_126), .in1(entry05_valid_149), .out(mux_402), .sel(Q_head[0]));
  Multiplexer #(.width(1), .select(1), .enable("false")) multiplexer_2 (
    .in0(entry08_valid_218), .in1(entry09_valid_241), .out(mux_406), .sel(Q_head[0]));
  Multiplexer #(.width(1), .select(1), .enable("false")) multiplexer_3 (
    .in0(entry14_valid_356), .in1(entry15_valid_379), .out(mux_410), .sel(Q_head[0]));
  and and_3 (head_valid, not_10, mux_413);
  Multiplexer #(.width(1), .select(1), .enable("false")) multiplexer_4 (
    .in0(entry04_done_127), .in1(entry05_done_150), .out(mux_418), .sel(Q_head[0]));
  Multiplexer #(.width(1), .select(1), .enable("false")) multiplexer_5 (
    .in0(entry08_done_219), .in1(entry09_done_242), .out(mux_422), .sel(Q_head[0]));
  Multiplexer #(.width(1), .select(1), .enable("false")) multiplexer_6 (
    .in0(entry14_done_357), .in1(entry15_done_380), .out(mux_426), .sel(Q_head[0]));
  Multiplexer #(.width(4), .select(1), .enable("false")) multiplexer_7 (
    .in0(entry00_op_37), .in1(entry01_op_59), .out(mux_430), .sel(Q_head[0]));
  Multiplexer #(.width(4), .select(1), .enable("false")) multiplexer_8 (
    .in0(entry06_op_174), .in1(entry07_op_197), .out(mux_434), .sel(Q_head[0]));
  Multiplexer #(.width(4), .select(1), .enable("false")) multiplexer_9 (
    .in0(entry10_op_266), .in1(entry11_op_289), .out(mux_438), .sel(Q_head[0]));
  Multiplexer #(.width(4), .select(1), .enable("false")) multiplexer_10 (
    .in0(mux_440), .in1(mux_441), .out(mux_442), .sel(Q_head[1]));
  Multiplexer #(.width(6), .select(1), .enable("false")) multiplexer_11 (
    .in0(entry02_rd_new_83), .in1(entry03_rd_new_106), .out(mux_446), .sel(Q_head[0]));
  Multiplexer #(.width(6), .select(1), .enable("false")) multiplexer_12 (
    .in0(mux_448), .in1(mux_449), .out(mux_450), .sel(Q_head[1]));
  Multiplexer #(.width(6), .select(1), .enable("false")) multiplexer_13 (
    .in0(mux_452), .in1(mux_453), .out(mux_454), .sel(Q_head[1]));
  Multiplexer #(.width(6), .select(1), .enable("false")) multiplexer_14 (
    .in0(mux_454), .in1(mux_457), .out(mux_458), .sel(Q_head[2]));
  Multiplexer #(.width(6), .select(1), .enable("false")) multiplexer_15 (
    .in0(mux_460), .in1(mux_461), .out(mux_462), .sel(Q_head[1]));
  Multiplexer #(.width(6), .select(1), .enable("false")) multiplexer_16 (
    .in0(mux_462), .in1(mux_465), .out(mux_466), .sel(Q_head[2]));
  Multiplexer #(.width(6), .select(1), .enable("false")) multiplexer_17 (
    .in0(entry12_rd_old_314), .in1(entry13_rd_old_337), .out(mux_470), .sel(Q_head[0]));
  Multiplexer #(.width(6), .select(1), .enable("false")) multiplexer_18 (
    .in0(mux_466), .in1(mux_473), .out(head_rd_old), .sel(Q_head[3]));
  Multiplexer #(.width(3), .select(1), .enable("false")) multiplexer_19 (
    .in0(entry04_rd_logic_131), .in1(entry05_rd_logic_154), .out(mux_478), .sel(Q_head[0]));
  Multiplexer #(.width(3), .select(1), .enable("false")) multiplexer_20 (
    .in0(entry08_rd_logic_223), .in1(entry09_rd_logic_246), .out(mux_482), .sel(Q_head[0]));
  Multiplexer #(.width(3), .select(1), .enable("false")) multiplexer_21 (
    .in0(entry14_rd_logic_361), .in1(entry15_rd_logic_384), .out(mux_486), .sel(Q_head[0]));
  Multiplexer #(.width(1), .select(1), .enable("false")) multiplexer_22 (
    .in0(entry00_rw_41), .in1(entry01_rw_63), .out(mux_490), .sel(Q_head[0]));
  Multiplexer #(.width(1), .select(1), .enable("false")) multiplexer_23 (
    .in0(entry06_rw_178), .in1(entry07_rw_201), .out(mux_494), .sel(Q_head[0]));
  Multiplexer #(.width(1), .select(1), .enable("false")) multiplexer_24 (
    .in0(entry10_rw_270), .in1(entry11_rw_293), .out(mux_498), .sel(Q_head[0]));
  Multiplexer #(.width(1), .select(1), .enable("false")) multiplexer_25 (
    .in0(mux_500), .in1(mux_501), .out(mux_502), .sel(Q_head[1]));
  Multiplexer #(.width(16), .select(1), .enable("false")) multiplexer_26 (
    .in0(entry02_pc_87), .in1(entry03_pc_110), .out(mux_506), .sel(Q_head[0]));
  Multiplexer #(.width(16), .select(1), .enable("false")) multiplexer_27 (
    .in0(mux_508), .in1(mux_509), .out(mux_510), .sel(Q_head[1]));
  Multiplexer #(.width(16), .select(1), .enable("false")) multiplexer_28 (
    .in0(mux_512), .in1(mux_513), .out(mux_514), .sel(Q_head[1]));
  Multiplexer #(.width(16), .select(1), .enable("false")) multiplexer_29 (
    .in0(mux_514), .in1(mux_517), .out(mux_518), .sel(Q_head[2]));
  Multiplexer #(.width(8), .select(1), .enable("false")) multiplexer_30 (
    .in0(mux_520), .in1(mux_521), .out(mux_522), .sel(Q_head[1]));
  Multiplexer #(.width(8), .select(1), .enable("false")) multiplexer_31 (
    .in0(mux_522), .in1(mux_525), .out(mux_526), .sel(Q_head[2]));
  Multiplexer #(.width(8), .select(1), .enable("false")) multiplexer_32 (
    .in0(entry12_sn_318), .in1(entry13_sn_341), .out(mux_530), .sel(Q_head[0]));
  Multiplexer #(.width(8), .select(1), .enable("false")) multiplexer_33 (
    .in0(mux_526), .in1(mux_533), .out(head_sn), .sel(Q_head[3]));
  Multiplexer #(.width(16), .select(1), .enable("false")) multiplexer_34 (
    .in0(entry04_pred_next_135), .in1(entry05_pred_next_158), .out(mux_538), .sel(Q_head[0]));
  Multiplexer #(.width(16), .select(1), .enable("false")) multiplexer_35 (
    .in0(entry08_pred_next_227), .in1(entry09_pred_next_250), .out(mux_542), .sel(Q_head[0]));
  Multiplexer #(.width(16), .select(1), .enable("false")) multiplexer_36 (
    .in0(entry14_pred_next_365), .in1(entry15_pred_next_388), .out(mux_546), .sel(Q_head[0]));
  Multiplexer #(.width(16), .select(1), .enable("false")) multiplexer_37 (
    .in0(entry00_result_45), .in1(entry01_result_67), .out(mux_550), .sel(Q_head[0]));
  Multiplexer #(.width(16), .select(1), .enable("false")) multiplexer_38 (
    .in0(entry06_result_182), .in1(entry07_result_205), .out(mux_554), .sel(Q_head[0]));
  Multiplexer #(.width(16), .select(1), .enable("false")) multiplexer_39 (
    .in0(entry10_result_274), .in1(entry11_result_297), .out(mux_558), .sel(Q_head[0]));
  Multiplexer #(.width(16), .select(1), .enable("false")) multiplexer_40 (
    .in0(mux_560), .in1(mux_561), .out(mux_562), .sel(Q_head[1]));
  Multiplexer #(.width(16), .select(1), .enable("false")) multiplexer_41 (
    .in0(entry02_next_91), .in1(entry03_next_114), .out(mux_566), .sel(Q_head[0]));
  Multiplexer #(.width(16), .select(1), .enable("false")) multiplexer_42 (
    .in0(mux_568), .in1(mux_569), .out(mux_570), .sel(Q_head[1]));
  Multiplexer #(.width(16), .select(1), .enable("false")) multiplexer_43 (
    .in0(mux_572), .in1(mux_573), .out(mux_574), .sel(Q_head[1]));
  Multiplexer #(.width(16), .select(1), .enable("false")) multiplexer_44 (
    .in0(mux_574), .in1(mux_577), .out(mux_578), .sel(Q_head[2]));
  Multiplexer #(.width(1), .select(1), .enable("false")) multiplexer_45 (
    .in0(mux_580), .in1(mux_581), .out(mux_582), .sel(Q_head[1]));
  Multiplexer #(.width(1), .select(1), .enable("false")) multiplexer_46 (
    .in0(mux_582), .in1(mux_585), .out(mux_586), .sel(Q_head[2]));
  Multiplexer #(.width(1), .select(1), .enable("false")) multiplexer_47 (
    .in0(entry12_taken_322), .in1(entry13_taken_345), .out(mux_590), .sel(Q_head[0]));
  Multiplexer #(.width(1), .select(1), .enable("false")) multiplexer_48 (
    .in0(mux_586), .in1(mux_593), .out(head_taken), .sel(Q_head[3]));
  Multiplexer #(.width(16), .select(1), .enable("false")) multiplexer_49 (
    .in0(entry04_target_139), .in1(entry05_target_162), .out(mux_598), .sel(Q_head[0]));
  Multiplexer #(.width(16), .select(1), .enable("false")) multiplexer_50 (
    .in0(entry08_target_231), .in1(entry09_target_254), .out(mux_602), .sel(Q_head[0]));
  Multiplexer #(.width(16), .select(1), .enable("false")) multiplexer_51 (
    .in0(entry14_target_369), .in1(entry15_target_392), .out(mux_606), .sel(Q_head[0]));
  not not_1 (not_10, eq_8);
  and and_4 (and_14, enable, pop);
  Multiplexer #(.width(5), .select(1), .enable("false")) multiplexer_52 (
    .in0(adder_21), .in1(adder_23), .out(mux_24), .sel(and_13));
  Comparator #(.width(4), .mode("unsigned")) comparator_17 (
    .a(Q_tail), .b(4'b0000), .gt(gt_27), .eq(eq_28), .lt(lt_29));
  ROB_Entry entry00 (
    .clk(clk), .rst(rst), .clear(clear), .enable(enable), .wr(and_30), .erase(and_34), .op(op),
    .rd_new(rd_new), .rd_old(rd_old), .rd_logic(rd_logic), .rw(rw), .pc(pc), .sn(sn), .pred_next(pred_next),
    .c0_valid(c0_valid), .c0_sn(c0_sn), .c0_result(c0_result), .c0_next(c0_next), .c0_taken(c0_taken),
    .c0_target(c0_target), .c1_valid(c1_valid), .c1_sn(c1_sn), .c1_result(c1_result), .c1_next(c1_next),
    .c1_taken(c1_taken), .c1_target(c1_target), .valid(entry00_valid_35), .done(entry00_done_36),
    .op_2(entry00_op_37), .rd_new_2(entry00_rd_new_38), .rd_old_2(entry00_rd_old_39),
    .rd_logic_2(entry00_rd_logic_40), .rw_2(entry00_rw_41), .pc_2(entry00_pc_42), .sn_2(entry00_sn_43),
    .pred_next_2(entry00_pred_next_44), .result(entry00_result_45), .next(entry00_next_46),
    .taken(entry00_taken_47), .target(entry00_target_48));
  and and_5 (and_56, and_15, eq_54);
  and and_6 (and_75, and_13, eq_73);
  and and_7 (and_102, and_15, eq_100);
  and and_8 (and_121, and_13, eq_119);
  and and_9 (and_148, and_15, eq_146);
  and and_10 (and_167, and_13, eq_165);
  and and_11 (and_194, and_15, eq_192);
  and u_and_12 (and_213, and_13, eq_211);
  and u_and_13 (and_240, and_15, eq_238);
  and u_and_14 (and_259, and_13, eq_257);
  and u_and_15 (and_286, and_15, eq_284);
  and and_16 (and_305, and_13, eq_303);
  and and_17 (and_332, and_15, eq_330);
  and and_18 (and_351, and_13, eq_349);
  and and_19 (and_378, and_15, eq_376);
  Multiplexer #(.width(1), .select(1), .enable("false")) multiplexer_53 (
    .in0(entry00_valid_35), .in1(entry01_valid_57), .out(mux_399), .sel(Q_head[0]));
  Multiplexer #(.width(1), .select(1), .enable("false")) multiplexer_54 (
    .in0(entry06_valid_172), .in1(entry07_valid_195), .out(mux_403), .sel(Q_head[0]));
  Multiplexer #(.width(1), .select(1), .enable("false")) multiplexer_55 (
    .in0(entry10_valid_264), .in1(entry11_valid_287), .out(mux_407), .sel(Q_head[0]));
  Multiplexer #(.width(1), .select(1), .enable("false")) multiplexer_56 (
    .in0(mux_409), .in1(mux_410), .out(mux_411), .sel(Q_head[1]));
  Multiplexer #(.width(1), .select(1), .enable("false")) multiplexer_57 (
    .in0(entry00_done_36), .in1(entry01_done_58), .out(mux_415), .sel(Q_head[0]));
  Multiplexer #(.width(1), .select(1), .enable("false")) multiplexer_58 (
    .in0(entry06_done_173), .in1(entry07_done_196), .out(mux_419), .sel(Q_head[0]));
  Multiplexer #(.width(1), .select(1), .enable("false")) multiplexer_59 (
    .in0(entry10_done_265), .in1(entry11_done_288), .out(mux_423), .sel(Q_head[0]));
  Multiplexer #(.width(1), .select(1), .enable("false")) multiplexer_60 (
    .in0(mux_425), .in1(mux_426), .out(mux_427), .sel(Q_head[1]));
  Multiplexer #(.width(4), .select(1), .enable("false")) multiplexer_61 (
    .in0(entry02_op_82), .in1(entry03_op_105), .out(mux_431), .sel(Q_head[0]));
  Multiplexer #(.width(4), .select(1), .enable("false")) multiplexer_62 (
    .in0(mux_433), .in1(mux_434), .out(mux_435), .sel(Q_head[1]));
  Multiplexer #(.width(4), .select(1), .enable("false")) multiplexer_63 (
    .in0(mux_437), .in1(mux_438), .out(mux_439), .sel(Q_head[1]));
  Multiplexer #(.width(4), .select(1), .enable("false")) multiplexer_64 (
    .in0(mux_439), .in1(mux_442), .out(mux_443), .sel(Q_head[2]));
  Multiplexer #(.width(6), .select(1), .enable("false")) multiplexer_65 (
    .in0(mux_445), .in1(mux_446), .out(mux_447), .sel(Q_head[1]));
  Multiplexer #(.width(6), .select(1), .enable("false")) multiplexer_66 (
    .in0(mux_447), .in1(mux_450), .out(mux_451), .sel(Q_head[2]));
  Multiplexer #(.width(6), .select(1), .enable("false")) multiplexer_67 (
    .in0(entry12_rd_new_313), .in1(entry13_rd_new_336), .out(mux_455), .sel(Q_head[0]));
  Multiplexer #(.width(6), .select(1), .enable("false")) multiplexer_68 (
    .in0(mux_451), .in1(mux_458), .out(head_rd_new), .sel(Q_head[3]));
  Multiplexer #(.width(6), .select(1), .enable("false")) multiplexer_69 (
    .in0(entry04_rd_old_130), .in1(entry05_rd_old_153), .out(mux_463), .sel(Q_head[0]));
  Multiplexer #(.width(6), .select(1), .enable("false")) multiplexer_70 (
    .in0(entry08_rd_old_222), .in1(entry09_rd_old_245), .out(mux_467), .sel(Q_head[0]));
  Multiplexer #(.width(6), .select(1), .enable("false")) multiplexer_71 (
    .in0(entry14_rd_old_360), .in1(entry15_rd_old_383), .out(mux_471), .sel(Q_head[0]));
  Multiplexer #(.width(3), .select(1), .enable("false")) multiplexer_72 (
    .in0(entry00_rd_logic_40), .in1(entry01_rd_logic_62), .out(mux_475), .sel(Q_head[0]));
  Multiplexer #(.width(3), .select(1), .enable("false")) multiplexer_73 (
    .in0(entry06_rd_logic_177), .in1(entry07_rd_logic_200), .out(mux_479), .sel(Q_head[0]));
  Multiplexer #(.width(3), .select(1), .enable("false")) multiplexer_74 (
    .in0(entry10_rd_logic_269), .in1(entry11_rd_logic_292), .out(mux_483), .sel(Q_head[0]));
  Multiplexer #(.width(3), .select(1), .enable("false")) multiplexer_75 (
    .in0(mux_485), .in1(mux_486), .out(mux_487), .sel(Q_head[1]));
  Multiplexer #(.width(1), .select(1), .enable("false")) multiplexer_76 (
    .in0(entry02_rw_86), .in1(entry03_rw_109), .out(mux_491), .sel(Q_head[0]));
  Multiplexer #(.width(1), .select(1), .enable("false")) multiplexer_77 (
    .in0(mux_493), .in1(mux_494), .out(mux_495), .sel(Q_head[1]));
  Multiplexer #(.width(1), .select(1), .enable("false")) multiplexer_78 (
    .in0(mux_497), .in1(mux_498), .out(mux_499), .sel(Q_head[1]));
  Multiplexer #(.width(1), .select(1), .enable("false")) multiplexer_79 (
    .in0(mux_499), .in1(mux_502), .out(mux_503), .sel(Q_head[2]));
  Multiplexer #(.width(16), .select(1), .enable("false")) multiplexer_80 (
    .in0(mux_505), .in1(mux_506), .out(mux_507), .sel(Q_head[1]));
  Multiplexer #(.width(16), .select(1), .enable("false")) multiplexer_81 (
    .in0(mux_507), .in1(mux_510), .out(mux_511), .sel(Q_head[2]));
  Multiplexer #(.width(16), .select(1), .enable("false")) multiplexer_82 (
    .in0(entry12_pc_317), .in1(entry13_pc_340), .out(mux_515), .sel(Q_head[0]));
  Multiplexer #(.width(16), .select(1), .enable("false")) multiplexer_83 (
    .in0(mux_511), .in1(mux_518), .out(head_pc), .sel(Q_head[3]));
  Multiplexer #(.width(8), .select(1), .enable("false")) multiplexer_84 (
    .in0(entry04_sn_134), .in1(entry05_sn_157), .out(mux_523), .sel(Q_head[0]));
  Multiplexer #(.width(8), .select(1), .enable("false")) multiplexer_85 (
    .in0(entry08_sn_226), .in1(entry09_sn_249), .out(mux_527), .sel(Q_head[0]));
  Multiplexer #(.width(8), .select(1), .enable("false")) multiplexer_86 (
    .in0(entry14_sn_364), .in1(entry15_sn_387), .out(mux_531), .sel(Q_head[0]));
  Multiplexer #(.width(16), .select(1), .enable("false")) multiplexer_87 (
    .in0(entry00_pred_next_44), .in1(entry01_pred_next_66), .out(mux_535), .sel(Q_head[0]));
  Multiplexer #(.width(16), .select(1), .enable("false")) multiplexer_88 (
    .in0(entry06_pred_next_181), .in1(entry07_pred_next_204), .out(mux_539), .sel(Q_head[0]));
  Multiplexer #(.width(16), .select(1), .enable("false")) multiplexer_89 (
    .in0(entry10_pred_next_273), .in1(entry11_pred_next_296), .out(mux_543), .sel(Q_head[0]));
  Multiplexer #(.width(16), .select(1), .enable("false")) multiplexer_90 (
    .in0(mux_545), .in1(mux_546), .out(mux_547), .sel(Q_head[1]));
  Multiplexer #(.width(16), .select(1), .enable("false")) multiplexer_91 (
    .in0(entry02_result_90), .in1(entry03_result_113), .out(mux_551), .sel(Q_head[0]));
  Multiplexer #(.width(16), .select(1), .enable("false")) multiplexer_92 (
    .in0(mux_553), .in1(mux_554), .out(mux_555), .sel(Q_head[1]));
  Multiplexer #(.width(16), .select(1), .enable("false")) multiplexer_93 (
    .in0(mux_557), .in1(mux_558), .out(mux_559), .sel(Q_head[1]));
  Multiplexer #(.width(16), .select(1), .enable("false")) multiplexer_94 (
    .in0(mux_559), .in1(mux_562), .out(mux_563), .sel(Q_head[2]));
  Multiplexer #(.width(16), .select(1), .enable("false")) multiplexer_95 (
    .in0(mux_565), .in1(mux_566), .out(mux_567), .sel(Q_head[1]));
  Multiplexer #(.width(16), .select(1), .enable("false")) multiplexer_96 (
    .in0(mux_567), .in1(mux_570), .out(mux_571), .sel(Q_head[2]));
  Multiplexer #(.width(16), .select(1), .enable("false")) multiplexer_97 (
    .in0(entry12_next_321), .in1(entry13_next_344), .out(mux_575), .sel(Q_head[0]));
  Multiplexer #(.width(16), .select(1), .enable("false")) multiplexer_98 (
    .in0(mux_571), .in1(mux_578), .out(head_next), .sel(Q_head[3]));
  Multiplexer #(.width(1), .select(1), .enable("false")) multiplexer_99 (
    .in0(entry04_taken_138), .in1(entry05_taken_161), .out(mux_583), .sel(Q_head[0]));
  Multiplexer #(.width(1), .select(1), .enable("false")) multiplexer_100 (
    .in0(entry08_taken_230), .in1(entry09_taken_253), .out(mux_587), .sel(Q_head[0]));
  Multiplexer #(.width(1), .select(1), .enable("false")) multiplexer_101 (
    .in0(entry14_taken_368), .in1(entry15_taken_391), .out(mux_591), .sel(Q_head[0]));
  Multiplexer #(.width(16), .select(1), .enable("false")) multiplexer_102 (
    .in0(entry00_target_48), .in1(entry01_target_70), .out(mux_595), .sel(Q_head[0]));
  Multiplexer #(.width(16), .select(1), .enable("false")) multiplexer_103 (
    .in0(entry06_target_185), .in1(entry07_target_208), .out(mux_599), .sel(Q_head[0]));
  Multiplexer #(.width(16), .select(1), .enable("false")) multiplexer_104 (
    .in0(entry10_target_277), .in1(entry11_target_300), .out(mux_603), .sel(Q_head[0]));
  Multiplexer #(.width(16), .select(1), .enable("false")) multiplexer_105 (
    .in0(mux_605), .in1(mux_606), .out(mux_607), .sel(Q_head[1]));
  Comparator #(.width(5), .mode("unsigned")) comparator_18 (.a(count), .b(5'b10000), .gt(gt_3), .eq(full), .lt(lt_5));
  not not_2 (not_11, full);
  and and_20 (and_15, and_14, not_10);
  Register #(.width(4)) reg_Q_head (.D(adder_17), .en(and_15), .Q(Q_head), .clk(clk), .clr(or_1));
  Adder #(.width(5)) adder_3 (.a(count), .b({5{1'b1}}), .out(adder_21), .cin(1'b0));  // open: cout
  // XOR_Gate #(.width(1)) xor_1: pin names not known; wires that end beside it: and_13, and_15, xor_25
  and and_21 (and_30, and_13, eq_28);
  Comparator #(.width(4), .mode("unsigned")) comparator_19 (
    .a(Q_tail), .b(4'b0001), .gt(gt_49), .eq(eq_50), .lt(lt_51));
  ROB_Entry entry01 (
    .clk(clk), .rst(rst), .clear(clear), .enable(enable), .wr(and_52), .erase(and_56), .op(op),
    .rd_new(rd_new), .rd_old(rd_old), .rd_logic(rd_logic), .rw(rw), .pc(pc), .sn(sn), .pred_next(pred_next),
    .c0_valid(c0_valid), .c0_sn(c0_sn), .c0_result(c0_result), .c0_next(c0_next), .c0_taken(c0_taken),
    .c0_target(c0_target), .c1_valid(c1_valid), .c1_sn(c1_sn), .c1_result(c1_result), .c1_next(c1_next),
    .c1_taken(c1_taken), .c1_target(c1_target), .valid(entry01_valid_57), .done(entry01_done_58),
    .op_2(entry01_op_59), .rd_new_2(entry01_rd_new_60), .rd_old_2(entry01_rd_old_61),
    .rd_logic_2(entry01_rd_logic_62), .rw_2(entry01_rw_63), .pc_2(entry01_pc_64), .sn_2(entry01_sn_65),
    .pred_next_2(entry01_pred_next_66), .result(entry01_result_67), .next(entry01_next_68),
    .taken(entry01_taken_69), .target(entry01_target_70));
  Comparator #(.width(4), .mode("unsigned")) comparator_20 (
    .a(Q_head), .b(4'b0010), .gt(gt_76), .eq(eq_77), .lt(lt_78));
  Comparator #(.width(4), .mode("unsigned")) comparator_21 (
    .a(Q_tail), .b(4'b0011), .gt(gt_95), .eq(eq_96), .lt(lt_97));
  ROB_Entry entry03 (
    .clk(clk), .rst(rst), .clear(clear), .enable(enable), .wr(and_98), .erase(and_102), .op(op),
    .rd_new(rd_new), .rd_old(rd_old), .rd_logic(rd_logic), .rw(rw), .pc(pc), .sn(sn), .pred_next(pred_next),
    .c0_valid(c0_valid), .c0_sn(c0_sn), .c0_result(c0_result), .c0_next(c0_next), .c0_taken(c0_taken),
    .c0_target(c0_target), .c1_valid(c1_valid), .c1_sn(c1_sn), .c1_result(c1_result), .c1_next(c1_next),
    .c1_taken(c1_taken), .c1_target(c1_target), .valid(entry03_valid_103), .done(entry03_done_104),
    .op_2(entry03_op_105), .rd_new_2(entry03_rd_new_106), .rd_old_2(entry03_rd_old_107),
    .rd_logic_2(entry03_rd_logic_108), .rw_2(entry03_rw_109), .pc_2(entry03_pc_110), .sn_2(entry03_sn_111),
    .pred_next_2(entry03_pred_next_112), .result(entry03_result_113), .next(entry03_next_114),
    .taken(entry03_taken_115), .target(entry03_target_116));
  Comparator #(.width(4), .mode("unsigned")) comparator_22 (
    .a(Q_head), .b(4'b0100), .gt(gt_122), .eq(eq_123), .lt(lt_124));
  Comparator #(.width(4), .mode("unsigned")) comparator_23 (
    .a(Q_tail), .b(4'b0101), .gt(gt_141), .eq(eq_142), .lt(lt_143));
  ROB_Entry entry05 (
    .clk(clk), .rst(rst), .clear(clear), .enable(enable), .wr(and_144), .erase(and_148), .op(op),
    .rd_new(rd_new), .rd_old(rd_old), .rd_logic(rd_logic), .rw(rw), .pc(pc), .sn(sn), .pred_next(pred_next),
    .c0_valid(c0_valid), .c0_sn(c0_sn), .c0_result(c0_result), .c0_next(c0_next), .c0_taken(c0_taken),
    .c0_target(c0_target), .c1_valid(c1_valid), .c1_sn(c1_sn), .c1_result(c1_result), .c1_next(c1_next),
    .c1_taken(c1_taken), .c1_target(c1_target), .valid(entry05_valid_149), .done(entry05_done_150),
    .op_2(entry05_op_151), .rd_new_2(entry05_rd_new_152), .rd_old_2(entry05_rd_old_153),
    .rd_logic_2(entry05_rd_logic_154), .rw_2(entry05_rw_155), .pc_2(entry05_pc_156), .sn_2(entry05_sn_157),
    .pred_next_2(entry05_pred_next_158), .result(entry05_result_159), .next(entry05_next_160),
    .taken(entry05_taken_161), .target(entry05_target_162));
  Comparator #(.width(4), .mode("unsigned")) comparator_24 (
    .a(Q_head), .b(4'b0110), .gt(gt_168), .eq(eq_169), .lt(lt_170));
  Comparator #(.width(4), .mode("unsigned")) comparator_25 (
    .a(Q_tail), .b(4'b0111), .gt(gt_187), .eq(eq_188), .lt(lt_189));
  ROB_Entry entry07 (
    .clk(clk), .rst(rst), .clear(clear), .enable(enable), .wr(and_190), .erase(and_194), .op(op),
    .rd_new(rd_new), .rd_old(rd_old), .rd_logic(rd_logic), .rw(rw), .pc(pc), .sn(sn), .pred_next(pred_next),
    .c0_valid(c0_valid), .c0_sn(c0_sn), .c0_result(c0_result), .c0_next(c0_next), .c0_taken(c0_taken),
    .c0_target(c0_target), .c1_valid(c1_valid), .c1_sn(c1_sn), .c1_result(c1_result), .c1_next(c1_next),
    .c1_taken(c1_taken), .c1_target(c1_target), .valid(entry07_valid_195), .done(entry07_done_196),
    .op_2(entry07_op_197), .rd_new_2(entry07_rd_new_198), .rd_old_2(entry07_rd_old_199),
    .rd_logic_2(entry07_rd_logic_200), .rw_2(entry07_rw_201), .pc_2(entry07_pc_202), .sn_2(entry07_sn_203),
    .pred_next_2(entry07_pred_next_204), .result(entry07_result_205), .next(entry07_next_206),
    .taken(entry07_taken_207), .target(entry07_target_208));
  Comparator #(.width(4), .mode("unsigned")) comparator_26 (
    .a(Q_head), .b(4'b1000), .gt(gt_214), .eq(eq_215), .lt(lt_216));
  Comparator #(.width(4), .mode("unsigned")) comparator_27 (
    .a(Q_tail), .b(4'b1001), .gt(gt_233), .eq(eq_234), .lt(lt_235));
  ROB_Entry entry09 (
    .clk(clk), .rst(rst), .clear(clear), .enable(enable), .wr(and_236), .erase(and_240), .op(op),
    .rd_new(rd_new), .rd_old(rd_old), .rd_logic(rd_logic), .rw(rw), .pc(pc), .sn(sn), .pred_next(pred_next),
    .c0_valid(c0_valid), .c0_sn(c0_sn), .c0_result(c0_result), .c0_next(c0_next), .c0_taken(c0_taken),
    .c0_target(c0_target), .c1_valid(c1_valid), .c1_sn(c1_sn), .c1_result(c1_result), .c1_next(c1_next),
    .c1_taken(c1_taken), .c1_target(c1_target), .valid(entry09_valid_241), .done(entry09_done_242),
    .op_2(entry09_op_243), .rd_new_2(entry09_rd_new_244), .rd_old_2(entry09_rd_old_245),
    .rd_logic_2(entry09_rd_logic_246), .rw_2(entry09_rw_247), .pc_2(entry09_pc_248), .sn_2(entry09_sn_249),
    .pred_next_2(entry09_pred_next_250), .result(entry09_result_251), .next(entry09_next_252),
    .taken(entry09_taken_253), .target(entry09_target_254));
  Comparator #(.width(4), .mode("unsigned")) comparator_28 (
    .a(Q_head), .b(4'b1010), .gt(gt_260), .eq(eq_261), .lt(lt_262));
  Comparator #(.width(4), .mode("unsigned")) comparator_29 (
    .a(Q_tail), .b(4'b1011), .gt(gt_279), .eq(eq_280), .lt(lt_281));
  ROB_Entry entry11 (
    .clk(clk), .rst(rst), .clear(clear), .enable(enable), .wr(and_282), .erase(and_286), .op(op),
    .rd_new(rd_new), .rd_old(rd_old), .rd_logic(rd_logic), .rw(rw), .pc(pc), .sn(sn), .pred_next(pred_next),
    .c0_valid(c0_valid), .c0_sn(c0_sn), .c0_result(c0_result), .c0_next(c0_next), .c0_taken(c0_taken),
    .c0_target(c0_target), .c1_valid(c1_valid), .c1_sn(c1_sn), .c1_result(c1_result), .c1_next(c1_next),
    .c1_taken(c1_taken), .c1_target(c1_target), .valid(entry11_valid_287), .done(entry11_done_288),
    .op_2(entry11_op_289), .rd_new_2(entry11_rd_new_290), .rd_old_2(entry11_rd_old_291),
    .rd_logic_2(entry11_rd_logic_292), .rw_2(entry11_rw_293), .pc_2(entry11_pc_294), .sn_2(entry11_sn_295),
    .pred_next_2(entry11_pred_next_296), .result(entry11_result_297), .next(entry11_next_298),
    .taken(entry11_taken_299), .target(entry11_target_300));
  Comparator #(.width(4), .mode("unsigned")) comparator_30 (
    .a(Q_head), .b(4'b1100), .gt(gt_306), .eq(eq_307), .lt(lt_308));
  Comparator #(.width(4), .mode("unsigned")) comparator_31 (
    .a(Q_tail), .b(4'b1101), .gt(gt_325), .eq(eq_326), .lt(lt_327));
  ROB_Entry entry13 (
    .clk(clk), .rst(rst), .clear(clear), .enable(enable), .wr(and_328), .erase(and_332), .op(op),
    .rd_new(rd_new), .rd_old(rd_old), .rd_logic(rd_logic), .rw(rw), .pc(pc), .sn(sn), .pred_next(pred_next),
    .c0_valid(c0_valid), .c0_sn(c0_sn), .c0_result(c0_result), .c0_next(c0_next), .c0_taken(c0_taken),
    .c0_target(c0_target), .c1_valid(c1_valid), .c1_sn(c1_sn), .c1_result(c1_result), .c1_next(c1_next),
    .c1_taken(c1_taken), .c1_target(c1_target), .valid(entry13_valid_333), .done(entry13_done_334),
    .op_2(entry13_op_335), .rd_new_2(entry13_rd_new_336), .rd_old_2(entry13_rd_old_337),
    .rd_logic_2(entry13_rd_logic_338), .rw_2(entry13_rw_339), .pc_2(entry13_pc_340), .sn_2(entry13_sn_341),
    .pred_next_2(entry13_pred_next_342), .result(entry13_result_343), .next(entry13_next_344),
    .taken(entry13_taken_345), .target(entry13_target_346));
  Comparator #(.width(4), .mode("unsigned")) comparator_32 (
    .a(Q_head), .b(4'b1110), .gt(gt_352), .eq(eq_353), .lt(lt_354));
  Comparator #(.width(4), .mode("unsigned")) comparator_33 (
    .a(Q_tail), .b(4'b1111), .gt(gt_371), .eq(eq_372), .lt(lt_373));
  ROB_Entry entry15 (
    .clk(clk), .rst(rst), .clear(clear), .enable(enable), .wr(and_374), .erase(and_378), .op(op),
    .rd_new(rd_new), .rd_old(rd_old), .rd_logic(rd_logic), .rw(rw), .pc(pc), .sn(sn), .pred_next(pred_next),
    .c0_valid(c0_valid), .c0_sn(c0_sn), .c0_result(c0_result), .c0_next(c0_next), .c0_taken(c0_taken),
    .c0_target(c0_target), .c1_valid(c1_valid), .c1_sn(c1_sn), .c1_result(c1_result), .c1_next(c1_next),
    .c1_taken(c1_taken), .c1_target(c1_target), .valid(entry15_valid_379), .done(entry15_done_380),
    .op_2(entry15_op_381), .rd_new_2(entry15_rd_new_382), .rd_old_2(entry15_rd_old_383),
    .rd_logic_2(entry15_rd_logic_384), .rw_2(entry15_rw_385), .pc_2(entry15_pc_386), .sn_2(entry15_sn_387),
    .pred_next_2(entry15_pred_next_388), .result(entry15_result_389), .next(entry15_next_390),
    .taken(entry15_taken_391), .target(entry15_target_392));
  Multiplexer #(.width(1), .select(1), .enable("false")) multiplexer_106 (
    .in0(entry02_valid_80), .in1(entry03_valid_103), .out(mux_400), .sel(Q_head[0]));
  Multiplexer #(.width(1), .select(1), .enable("false")) multiplexer_107 (
    .in0(mux_402), .in1(mux_403), .out(mux_404), .sel(Q_head[1]));
  Multiplexer #(.width(1), .select(1), .enable("false")) multiplexer_108 (
    .in0(mux_406), .in1(mux_407), .out(mux_408), .sel(Q_head[1]));
  Multiplexer #(.width(1), .select(1), .enable("false")) multiplexer_109 (
    .in0(mux_408), .in1(mux_411), .out(mux_412), .sel(Q_head[2]));
  Multiplexer #(.width(1), .select(1), .enable("false")) multiplexer_110 (
    .in0(entry02_done_81), .in1(entry03_done_104), .out(mux_416), .sel(Q_head[0]));
  Multiplexer #(.width(1), .select(1), .enable("false")) multiplexer_111 (
    .in0(mux_418), .in1(mux_419), .out(mux_420), .sel(Q_head[1]));
  Multiplexer #(.width(1), .select(1), .enable("false")) multiplexer_112 (
    .in0(mux_422), .in1(mux_423), .out(mux_424), .sel(Q_head[1]));
  Multiplexer #(.width(1), .select(1), .enable("false")) multiplexer_113 (
    .in0(mux_424), .in1(mux_427), .out(mux_428), .sel(Q_head[2]));
  Multiplexer #(.width(4), .select(1), .enable("false")) multiplexer_114 (
    .in0(mux_430), .in1(mux_431), .out(mux_432), .sel(Q_head[1]));
  Multiplexer #(.width(4), .select(1), .enable("false")) multiplexer_115 (
    .in0(mux_432), .in1(mux_435), .out(mux_436), .sel(Q_head[2]));
  Multiplexer #(.width(4), .select(1), .enable("false")) multiplexer_116 (
    .in0(entry12_op_312), .in1(entry13_op_335), .out(mux_440), .sel(Q_head[0]));
  Multiplexer #(.width(4), .select(1), .enable("false")) multiplexer_117 (
    .in0(mux_436), .in1(mux_443), .out(head_op), .sel(Q_head[3]));
  Multiplexer #(.width(6), .select(1), .enable("false")) multiplexer_118 (
    .in0(entry04_rd_new_129), .in1(entry05_rd_new_152), .out(mux_448), .sel(Q_head[0]));
  Multiplexer #(.width(6), .select(1), .enable("false")) multiplexer_119 (
    .in0(entry08_rd_new_221), .in1(entry09_rd_new_244), .out(mux_452), .sel(Q_head[0]));
  Multiplexer #(.width(6), .select(1), .enable("false")) multiplexer_120 (
    .in0(entry14_rd_new_359), .in1(entry15_rd_new_382), .out(mux_456), .sel(Q_head[0]));
  Multiplexer #(.width(6), .select(1), .enable("false")) multiplexer_121 (
    .in0(entry00_rd_old_39), .in1(entry01_rd_old_61), .out(mux_460), .sel(Q_head[0]));
  Multiplexer #(.width(6), .select(1), .enable("false")) multiplexer_122 (
    .in0(entry06_rd_old_176), .in1(entry07_rd_old_199), .out(mux_464), .sel(Q_head[0]));
  Multiplexer #(.width(6), .select(1), .enable("false")) multiplexer_123 (
    .in0(entry10_rd_old_268), .in1(entry11_rd_old_291), .out(mux_468), .sel(Q_head[0]));
  Multiplexer #(.width(6), .select(1), .enable("false")) multiplexer_124 (
    .in0(mux_470), .in1(mux_471), .out(mux_472), .sel(Q_head[1]));
  Multiplexer #(.width(3), .select(1), .enable("false")) multiplexer_125 (
    .in0(entry02_rd_logic_85), .in1(entry03_rd_logic_108), .out(mux_476), .sel(Q_head[0]));
  Multiplexer #(.width(3), .select(1), .enable("false")) multiplexer_126 (
    .in0(mux_478), .in1(mux_479), .out(mux_480), .sel(Q_head[1]));
  Multiplexer #(.width(3), .select(1), .enable("false")) multiplexer_127 (
    .in0(mux_482), .in1(mux_483), .out(mux_484), .sel(Q_head[1]));
  Multiplexer #(.width(3), .select(1), .enable("false")) multiplexer_128 (
    .in0(mux_484), .in1(mux_487), .out(mux_488), .sel(Q_head[2]));
  Multiplexer #(.width(1), .select(1), .enable("false")) multiplexer_129 (
    .in0(mux_490), .in1(mux_491), .out(mux_492), .sel(Q_head[1]));
  Multiplexer #(.width(1), .select(1), .enable("false")) multiplexer_130 (
    .in0(mux_492), .in1(mux_495), .out(mux_496), .sel(Q_head[2]));
  Multiplexer #(.width(1), .select(1), .enable("false")) multiplexer_131 (
    .in0(entry12_rw_316), .in1(entry13_rw_339), .out(mux_500), .sel(Q_head[0]));
  Multiplexer #(.width(1), .select(1), .enable("false")) multiplexer_132 (
    .in0(mux_496), .in1(mux_503), .out(head_rw), .sel(Q_head[3]));
  Multiplexer #(.width(16), .select(1), .enable("false")) multiplexer_133 (
    .in0(entry04_pc_133), .in1(entry05_pc_156), .out(mux_508), .sel(Q_head[0]));
  Multiplexer #(.width(16), .select(1), .enable("false")) multiplexer_134 (
    .in0(entry08_pc_225), .in1(entry09_pc_248), .out(mux_512), .sel(Q_head[0]));
  Multiplexer #(.width(16), .select(1), .enable("false")) multiplexer_135 (
    .in0(entry14_pc_363), .in1(entry15_pc_386), .out(mux_516), .sel(Q_head[0]));
  Multiplexer #(.width(8), .select(1), .enable("false")) multiplexer_136 (
    .in0(entry00_sn_43), .in1(entry01_sn_65), .out(mux_520), .sel(Q_head[0]));
  Multiplexer #(.width(8), .select(1), .enable("false")) multiplexer_137 (
    .in0(entry06_sn_180), .in1(entry07_sn_203), .out(mux_524), .sel(Q_head[0]));
  Multiplexer #(.width(8), .select(1), .enable("false")) multiplexer_138 (
    .in0(entry10_sn_272), .in1(entry11_sn_295), .out(mux_528), .sel(Q_head[0]));
  Multiplexer #(.width(8), .select(1), .enable("false")) multiplexer_139 (
    .in0(mux_530), .in1(mux_531), .out(mux_532), .sel(Q_head[1]));
  Multiplexer #(.width(16), .select(1), .enable("false")) multiplexer_140 (
    .in0(entry02_pred_next_89), .in1(entry03_pred_next_112), .out(mux_536), .sel(Q_head[0]));
  Multiplexer #(.width(16), .select(1), .enable("false")) multiplexer_141 (
    .in0(mux_538), .in1(mux_539), .out(mux_540), .sel(Q_head[1]));
  Multiplexer #(.width(16), .select(1), .enable("false")) multiplexer_142 (
    .in0(mux_542), .in1(mux_543), .out(mux_544), .sel(Q_head[1]));
  Multiplexer #(.width(16), .select(1), .enable("false")) multiplexer_143 (
    .in0(mux_544), .in1(mux_547), .out(mux_548), .sel(Q_head[2]));
  Multiplexer #(.width(16), .select(1), .enable("false")) multiplexer_144 (
    .in0(mux_550), .in1(mux_551), .out(mux_552), .sel(Q_head[1]));
  Multiplexer #(.width(16), .select(1), .enable("false")) multiplexer_145 (
    .in0(mux_552), .in1(mux_555), .out(mux_556), .sel(Q_head[2]));
  Multiplexer #(.width(16), .select(1), .enable("false")) multiplexer_146 (
    .in0(entry12_result_320), .in1(entry13_result_343), .out(mux_560), .sel(Q_head[0]));
  Multiplexer #(.width(16), .select(1), .enable("false")) multiplexer_147 (
    .in0(mux_556), .in1(mux_563), .out(head_result), .sel(Q_head[3]));
  Multiplexer #(.width(16), .select(1), .enable("false")) multiplexer_148 (
    .in0(entry04_next_137), .in1(entry05_next_160), .out(mux_568), .sel(Q_head[0]));
  Multiplexer #(.width(16), .select(1), .enable("false")) multiplexer_149 (
    .in0(entry08_next_229), .in1(entry09_next_252), .out(mux_572), .sel(Q_head[0]));
  Multiplexer #(.width(16), .select(1), .enable("false")) multiplexer_150 (
    .in0(entry14_next_367), .in1(entry15_next_390), .out(mux_576), .sel(Q_head[0]));
  Multiplexer #(.width(1), .select(1), .enable("false")) multiplexer_151 (
    .in0(entry00_taken_47), .in1(entry01_taken_69), .out(mux_580), .sel(Q_head[0]));
  Multiplexer #(.width(1), .select(1), .enable("false")) multiplexer_152 (
    .in0(entry06_taken_184), .in1(entry07_taken_207), .out(mux_584), .sel(Q_head[0]));
  Multiplexer #(.width(1), .select(1), .enable("false")) multiplexer_153 (
    .in0(entry10_taken_276), .in1(entry11_taken_299), .out(mux_588), .sel(Q_head[0]));
  Multiplexer #(.width(1), .select(1), .enable("false")) multiplexer_154 (
    .in0(mux_590), .in1(mux_591), .out(mux_592), .sel(Q_head[1]));
  Multiplexer #(.width(16), .select(1), .enable("false")) multiplexer_155 (
    .in0(entry02_target_93), .in1(entry03_target_116), .out(mux_596), .sel(Q_head[0]));
  Multiplexer #(.width(16), .select(1), .enable("false")) multiplexer_156 (
    .in0(mux_598), .in1(mux_599), .out(mux_600), .sel(Q_head[1]));
  Multiplexer #(.width(16), .select(1), .enable("false")) multiplexer_157 (
    .in0(mux_602), .in1(mux_603), .out(mux_604), .sel(Q_head[1]));
  Multiplexer #(.width(16), .select(1), .enable("false")) multiplexer_158 (
    .in0(mux_604), .in1(mux_607), .out(mux_608), .sel(Q_head[2]));
  and and_22 (and_12, enable, wr);
  Adder #(.width(4)) adder_4 (.a(Q_tail), .b(4'b0001), .out(adder_19), .cin(1'b0));  // open: cout
  Register #(.width(5)) reg_Q_count (.D(mux_24), .en(xor_25), .Q(count), .clk(clk), .clr(or_1));
  Comparator #(.width(4), .mode("unsigned")) comparator_34 (
    .a(Q_head), .b(4'b0000), .gt(gt_31), .eq(eq_32), .lt(lt_33));
  and and_23 (and_52, and_13, eq_50);
  and and_24 (and_79, and_15, eq_77);
  and and_25 (and_98, and_13, eq_96);
  and and_26 (and_125, and_15, eq_123);
  and and_27 (and_144, and_13, eq_142);
  and and_28 (and_171, and_15, eq_169);
  and and_29 (and_190, and_13, eq_188);
  and u_and_30 (and_217, and_15, eq_215);
  and and_31 (and_236, and_13, eq_234);
  and and_32 (and_263, and_15, eq_261);
  and and_33 (and_282, and_13, eq_280);
  and u_and_34 (and_309, and_15, eq_307);
  and and_35 (and_328, and_13, eq_326);
  and and_36 (and_355, and_15, eq_353);
  and and_37 (and_374, and_13, eq_372);
  Multiplexer #(.width(1), .select(1), .enable("false")) multiplexer_159 (
    .in0(mux_399), .in1(mux_400), .out(mux_401), .sel(Q_head[1]));
  Multiplexer #(.width(1), .select(1), .enable("false")) multiplexer_160 (
    .in0(mux_401), .in1(mux_404), .out(mux_405), .sel(Q_head[2]));
  Multiplexer #(.width(1), .select(1), .enable("false")) multiplexer_161 (
    .in0(entry12_valid_310), .in1(entry13_valid_333), .out(mux_409), .sel(Q_head[0]));
  Multiplexer #(.width(1), .select(1), .enable("false")) multiplexer_162 (
    .in0(mux_405), .in1(mux_412), .out(mux_413), .sel(Q_head[3]));
  Multiplexer #(.width(1), .select(1), .enable("false")) multiplexer_163 (
    .in0(mux_415), .in1(mux_416), .out(mux_417), .sel(Q_head[1]));
  Multiplexer #(.width(1), .select(1), .enable("false")) multiplexer_164 (
    .in0(mux_417), .in1(mux_420), .out(mux_421), .sel(Q_head[2]));
  Multiplexer #(.width(1), .select(1), .enable("false")) multiplexer_165 (
    .in0(entry12_done_311), .in1(entry13_done_334), .out(mux_425), .sel(Q_head[0]));
  Multiplexer #(.width(1), .select(1), .enable("false")) multiplexer_166 (
    .in0(mux_421), .in1(mux_428), .out(head_done), .sel(Q_head[3]));
  Multiplexer #(.width(4), .select(1), .enable("false")) multiplexer_167 (
    .in0(entry04_op_128), .in1(entry05_op_151), .out(mux_433), .sel(Q_head[0]));
  Multiplexer #(.width(4), .select(1), .enable("false")) multiplexer_168 (
    .in0(entry08_op_220), .in1(entry09_op_243), .out(mux_437), .sel(Q_head[0]));
  Multiplexer #(.width(4), .select(1), .enable("false")) multiplexer_169 (
    .in0(entry14_op_358), .in1(entry15_op_381), .out(mux_441), .sel(Q_head[0]));
  Multiplexer #(.width(6), .select(1), .enable("false")) multiplexer_170 (
    .in0(entry00_rd_new_38), .in1(entry01_rd_new_60), .out(mux_445), .sel(Q_head[0]));
  Multiplexer #(.width(6), .select(1), .enable("false")) multiplexer_171 (
    .in0(entry06_rd_new_175), .in1(entry07_rd_new_198), .out(mux_449), .sel(Q_head[0]));
  Multiplexer #(.width(6), .select(1), .enable("false")) multiplexer_172 (
    .in0(entry10_rd_new_267), .in1(entry11_rd_new_290), .out(mux_453), .sel(Q_head[0]));
  Multiplexer #(.width(6), .select(1), .enable("false")) multiplexer_173 (
    .in0(mux_455), .in1(mux_456), .out(mux_457), .sel(Q_head[1]));
  Multiplexer #(.width(6), .select(1), .enable("false")) multiplexer_174 (
    .in0(entry02_rd_old_84), .in1(entry03_rd_old_107), .out(mux_461), .sel(Q_head[0]));
  Multiplexer #(.width(6), .select(1), .enable("false")) multiplexer_175 (
    .in0(mux_463), .in1(mux_464), .out(mux_465), .sel(Q_head[1]));
  Multiplexer #(.width(6), .select(1), .enable("false")) multiplexer_176 (
    .in0(mux_467), .in1(mux_468), .out(mux_469), .sel(Q_head[1]));
  Multiplexer #(.width(6), .select(1), .enable("false")) multiplexer_177 (
    .in0(mux_469), .in1(mux_472), .out(mux_473), .sel(Q_head[2]));
  Multiplexer #(.width(3), .select(1), .enable("false")) multiplexer_178 (
    .in0(mux_475), .in1(mux_476), .out(mux_477), .sel(Q_head[1]));
  Multiplexer #(.width(3), .select(1), .enable("false")) multiplexer_179 (
    .in0(mux_477), .in1(mux_480), .out(mux_481), .sel(Q_head[2]));
  Multiplexer #(.width(3), .select(1), .enable("false")) multiplexer_180 (
    .in0(entry12_rd_logic_315), .in1(entry13_rd_logic_338), .out(mux_485), .sel(Q_head[0]));
  Multiplexer #(.width(3), .select(1), .enable("false")) multiplexer_181 (
    .in0(mux_481), .in1(mux_488), .out(head_rd_logic), .sel(Q_head[3]));
  Multiplexer #(.width(1), .select(1), .enable("false")) multiplexer_182 (
    .in0(entry04_rw_132), .in1(entry05_rw_155), .out(mux_493), .sel(Q_head[0]));
  Multiplexer #(.width(1), .select(1), .enable("false")) multiplexer_183 (
    .in0(entry08_rw_224), .in1(entry09_rw_247), .out(mux_497), .sel(Q_head[0]));
  Multiplexer #(.width(1), .select(1), .enable("false")) multiplexer_184 (
    .in0(entry14_rw_362), .in1(entry15_rw_385), .out(mux_501), .sel(Q_head[0]));
  Multiplexer #(.width(16), .select(1), .enable("false")) multiplexer_185 (
    .in0(entry00_pc_42), .in1(entry01_pc_64), .out(mux_505), .sel(Q_head[0]));
  Multiplexer #(.width(16), .select(1), .enable("false")) multiplexer_186 (
    .in0(entry06_pc_179), .in1(entry07_pc_202), .out(mux_509), .sel(Q_head[0]));
  Multiplexer #(.width(16), .select(1), .enable("false")) multiplexer_187 (
    .in0(entry10_pc_271), .in1(entry11_pc_294), .out(mux_513), .sel(Q_head[0]));
  Multiplexer #(.width(16), .select(1), .enable("false")) multiplexer_188 (
    .in0(mux_515), .in1(mux_516), .out(mux_517), .sel(Q_head[1]));
  Multiplexer #(.width(8), .select(1), .enable("false")) multiplexer_189 (
    .in0(entry02_sn_88), .in1(entry03_sn_111), .out(mux_521), .sel(Q_head[0]));
  Multiplexer #(.width(8), .select(1), .enable("false")) multiplexer_190 (
    .in0(mux_523), .in1(mux_524), .out(mux_525), .sel(Q_head[1]));
  Multiplexer #(.width(8), .select(1), .enable("false")) multiplexer_191 (
    .in0(mux_527), .in1(mux_528), .out(mux_529), .sel(Q_head[1]));
  Multiplexer #(.width(8), .select(1), .enable("false")) multiplexer_192 (
    .in0(mux_529), .in1(mux_532), .out(mux_533), .sel(Q_head[2]));
  Multiplexer #(.width(16), .select(1), .enable("false")) multiplexer_193 (
    .in0(mux_535), .in1(mux_536), .out(mux_537), .sel(Q_head[1]));
  Multiplexer #(.width(16), .select(1), .enable("false")) multiplexer_194 (
    .in0(mux_537), .in1(mux_540), .out(mux_541), .sel(Q_head[2]));
  Multiplexer #(.width(16), .select(1), .enable("false")) multiplexer_195 (
    .in0(entry12_pred_next_319), .in1(entry13_pred_next_342), .out(mux_545), .sel(Q_head[0]));
  Multiplexer #(.width(16), .select(1), .enable("false")) multiplexer_196 (
    .in0(mux_541), .in1(mux_548), .out(head_pred_next), .sel(Q_head[3]));
  Multiplexer #(.width(16), .select(1), .enable("false")) multiplexer_197 (
    .in0(entry04_result_136), .in1(entry05_result_159), .out(mux_553), .sel(Q_head[0]));
  Multiplexer #(.width(16), .select(1), .enable("false")) multiplexer_198 (
    .in0(entry08_result_228), .in1(entry09_result_251), .out(mux_557), .sel(Q_head[0]));
  Multiplexer #(.width(16), .select(1), .enable("false")) multiplexer_199 (
    .in0(entry14_result_366), .in1(entry15_result_389), .out(mux_561), .sel(Q_head[0]));
  Multiplexer #(.width(16), .select(1), .enable("false")) multiplexer_200 (
    .in0(entry00_next_46), .in1(entry01_next_68), .out(mux_565), .sel(Q_head[0]));
  Multiplexer #(.width(16), .select(1), .enable("false")) multiplexer_201 (
    .in0(entry06_next_183), .in1(entry07_next_206), .out(mux_569), .sel(Q_head[0]));
  Multiplexer #(.width(16), .select(1), .enable("false")) multiplexer_202 (
    .in0(entry10_next_275), .in1(entry11_next_298), .out(mux_573), .sel(Q_head[0]));
  Multiplexer #(.width(16), .select(1), .enable("false")) multiplexer_203 (
    .in0(mux_575), .in1(mux_576), .out(mux_577), .sel(Q_head[1]));
  Multiplexer #(.width(1), .select(1), .enable("false")) multiplexer_204 (
    .in0(entry02_taken_92), .in1(entry03_taken_115), .out(mux_581), .sel(Q_head[0]));
  Multiplexer #(.width(1), .select(1), .enable("false")) multiplexer_205 (
    .in0(mux_583), .in1(mux_584), .out(mux_585), .sel(Q_head[1]));
  Multiplexer #(.width(1), .select(1), .enable("false")) multiplexer_206 (
    .in0(mux_587), .in1(mux_588), .out(mux_589), .sel(Q_head[1]));
  Multiplexer #(.width(1), .select(1), .enable("false")) multiplexer_207 (
    .in0(mux_589), .in1(mux_592), .out(mux_593), .sel(Q_head[2]));
  Multiplexer #(.width(16), .select(1), .enable("false")) multiplexer_208 (
    .in0(mux_595), .in1(mux_596), .out(mux_597), .sel(Q_head[1]));
  Multiplexer #(.width(16), .select(1), .enable("false")) multiplexer_209 (
    .in0(mux_597), .in1(mux_600), .out(mux_601), .sel(Q_head[2]));
  Multiplexer #(.width(16), .select(1), .enable("false")) multiplexer_210 (
    .in0(entry12_target_323), .in1(entry13_target_346), .out(mux_605), .sel(Q_head[0]));
  Multiplexer #(.width(16), .select(1), .enable("false")) multiplexer_211 (
    .in0(mux_601), .in1(mux_608), .out(head_target), .sel(Q_head[3]));

  // Other names for the same wires on the sheet: and_414 = head_valid; eq_4 = full; mux_429 = head_done;
  //   mux_444[3:0] = head_op; mux_459[5:0] = head_rd_new; mux_474[5:0] = head_rd_old; mux_489[2:0] = head_rd_logic;
  //   mux_504 = head_rw; mux_519[15:0] = head_pc; mux_534[7:0] = head_sn; mux_549[15:0] = head_pred_next;
  //   mux_564[15:0] = head_result; mux_579[15:0] = head_next; mux_594 = head_taken; mux_609[15:0] = head_target;
  //   Q_count[4:0] = count; slice_393[2:0] = Q_head[2:0]; slice_395[1:0] = Q_head[1:0]; slice_397 = Q_head[0];
  //   slice_398 = Q_head[1]; slice_396 = Q_head[2]; slice_394 = Q_head[3]

  // Notes on the sheet:
  //   16-entry distributed ROB | stable head, single retire
endmodule
module ALU_RS (
  input  clk,
  input  rst,
  input  clear,
  input  enable,
  input  wr,
  input  take,
  input  [3:0] op,
  input  [5:0] rd,
  input  [5:0] qj,
  input  [5:0] qk,
  input  [15:0] imm,
  input  [15:0] pc,
  input  [7:0] sn,
  input  vj,
  input  vk,
  input  [15:0] dj,
  input  [15:0] dk,
  input  c0_valid,
  input  [5:0] c0_rd,
  input  [15:0] c0_data,
  input  c1_valid,
  input  [5:0] c1_rd,
  input  [15:0] c1_data,
  output full,
  output [4:0] count,
  output ex_valid,
  output [3:0] ex_op,
  output [5:0] ex_rd,
  output [15:0] ex_imm,
  output [15:0] ex_pc,
  output [7:0] ex_sn,
  output [15:0] ex_a,
  output [15:0] ex_b
);

  wire allocate_0, allocate_1, allocate_2, allocate_3, allocate_4, allocate_5, allocate_6, allocate_7,
       allocate_8, allocate_9, allocate_10, allocate_11, allocate_12, allocate_13, allocate_14, allocate_15,
       and_147, and_149, and_151, and_153, and_155, and_157, and_159, and_161, and_163, and_165, and_167,
       and_169, and_171, and_173, and_175, and_177, and_179, and_181, and_183, and_185, and_187, and_189,
       and_191, and_193, and_195, and_197, and_199, and_201, and_203, and_205, and_207, and_262, and_270,
       and_278, and_286, and_294, and_302, and_310, and_318, and_326, and_334, and_342, and_350, and_358,
       and_366, and_374, and_400, and_401, and_405, and_409, and_413, and_417, and_421, and_425, and_429,
       and_433, and_437, and_441, and_445, and_449, and_453, and_457, and_461, and_465, entry00_busy_1,
       entry00_ready_2, entry01_busy_10, entry01_ready_11, entry02_busy_19, entry02_ready_20,
       entry03_busy_28, entry03_ready_29, entry04_busy_37, entry04_ready_38, entry05_busy_46,
       entry05_ready_47, entry06_busy_55, entry06_ready_56, entry07_busy_64, entry07_ready_65,
       entry08_busy_73, entry08_ready_74, entry09_busy_82, entry09_ready_83, entry10_busy_91,
       entry10_ready_92, entry11_busy_100, entry11_ready_101, entry12_busy_109, entry12_ready_110,
       entry13_busy_118, entry13_ready_119, entry14_busy_127, entry14_ready_128, entry15_busy_136,
       entry15_ready_137, eq_403, eq_407, eq_411, eq_415, eq_419, eq_423, eq_427, eq_431, eq_435, eq_439,
       eq_443, eq_447, eq_451, eq_455, eq_459, eq_463, gt_402, gt_406, gt_410, gt_414, gt_418, gt_422,
       gt_426, gt_430, gt_434, gt_438, gt_442, gt_446, gt_450, gt_454, gt_458, gt_462, lt_404, lt_408,
       lt_412, lt_416, lt_420, lt_424, lt_428, lt_432, lt_436, lt_440, lt_444, lt_448, lt_452, lt_456,
       lt_460, lt_464, mux_384, mux_385, mux_386, mux_387, mux_388, mux_389, mux_390, mux_391, mux_392,
       mux_393, mux_394, mux_395, mux_396, mux_397, mux_398, not_146, not_150, not_154, not_158, not_162,
       not_166, not_170, not_174, not_178, not_182, not_186, not_190, not_194, not_198, not_202, not_206,
       not_260, not_268, not_276, not_284, not_292, not_300, not_308, not_316, not_324, not_332, not_340,
       not_348, not_356, not_364, not_372, or_261, or_263, or_269, or_271, or_277, or_279, or_285, or_287,
       or_293, or_295, or_301, or_303, or_309, or_311, or_317, or_319, or_325, or_327, or_333, or_335,
       or_341, or_343, or_349, or_351, or_357, or_359, or_365, or_367, or_373, or_375, slice_259, slice_267,
       slice_275, slice_283, slice_291, slice_299, slice_307, slice_315, slice_323, slice_331, slice_339,
       slice_347, slice_355, slice_363, slice_371;
  wire [3:0] entry00_op_3, entry01_op_12, entry02_op_21, entry03_op_30, entry04_op_39, entry05_op_48,
       entry06_op_57, entry07_op_66, entry08_op_75, entry09_op_84, entry10_op_93, entry11_op_102,
       entry12_op_111, entry13_op_120, entry14_op_129, entry15_op_138, mux_265, mux_273, mux_281, mux_289,
       mux_297, mux_305, mux_313, mux_321, mux_329, mux_337, mux_345, mux_353, mux_361, mux_369, mux_377,
       mux_466, mux_467, mux_468, mux_469, mux_470, mux_471, mux_472, mux_473, mux_474, mux_475, mux_476,
       mux_477, mux_478, mux_479;
  wire [4:0] adder_226, adder_228, adder_229, adder_230, adder_231, adder_232, adder_233, adder_234,
       adder_235, adder_236, adder_237, adder_238, adder_239, adder_240, ext_210, ext_211, ext_212, ext_213,
       ext_214, ext_215, ext_216, ext_217, ext_218, ext_219, ext_220, ext_221, ext_222, ext_223, ext_224,
       ext_225;
  wire [5:0] entry00_rd_4, entry01_rd_13, entry02_rd_22, entry03_rd_31, entry04_rd_40, entry05_rd_49,
       entry06_rd_58, entry07_rd_67, entry08_rd_76, entry09_rd_85, entry10_rd_94, entry11_rd_103,
       entry12_rd_112, entry13_rd_121, entry14_rd_130, entry15_rd_139, mux_481, mux_482, mux_483, mux_484,
       mux_485, mux_486, mux_487, mux_488, mux_489, mux_490, mux_491, mux_492, mux_493, mux_494;
  wire [6:0] subtractor_258, subtractor_266, subtractor_274, subtractor_282, subtractor_290, subtractor_298,
       subtractor_306, subtractor_314, subtractor_322, subtractor_330, subtractor_338, subtractor_346,
       subtractor_354, subtractor_362, subtractor_370;
  wire [7:0] entry00_sn_7, entry01_sn_16, entry02_sn_25, entry03_sn_34, entry04_sn_43, entry05_sn_52,
       entry06_sn_61, entry07_sn_70, entry08_sn_79, entry09_sn_88, entry10_sn_97, entry11_sn_106,
       entry12_sn_115, entry13_sn_124, entry14_sn_133, entry15_sn_142, mux_264, mux_272, mux_280, mux_288,
       mux_296, mux_304, mux_312, mux_320, mux_328, mux_336, mux_344, mux_352, mux_360, mux_368, mux_376,
       mux_526, mux_527, mux_528, mux_529, mux_530, mux_531, mux_532, mux_533, mux_534, mux_535, mux_536,
       mux_537, mux_538, mux_539;
  wire [15:0] entry00_a_8, entry00_b_9, entry00_imm_5, entry00_pc_6, entry01_a_17, entry01_b_18,
       entry01_imm_14, entry01_pc_15, entry02_a_26, entry02_b_27, entry02_imm_23, entry02_pc_24,
       entry03_a_35, entry03_b_36, entry03_imm_32, entry03_pc_33, entry04_a_44, entry04_b_45, entry04_imm_41,
       entry04_pc_42, entry05_a_53, entry05_b_54, entry05_imm_50, entry05_pc_51, entry06_a_62, entry06_b_63,
       entry06_imm_59, entry06_pc_60, entry07_a_71, entry07_b_72, entry07_imm_68, entry07_pc_69,
       entry08_a_80, entry08_b_81, entry08_imm_77, entry08_pc_78, entry09_a_89, entry09_b_90, entry09_imm_86,
       entry09_pc_87, entry10_a_98, entry10_b_99, entry10_imm_95, entry10_pc_96, entry11_a_107,
       entry11_b_108, entry11_imm_104, entry11_pc_105, entry12_a_116, entry12_b_117, entry12_imm_113,
       entry12_pc_114, entry13_a_125, entry13_b_126, entry13_imm_122, entry13_pc_123, entry14_a_134,
       entry14_b_135, entry14_imm_131, entry14_pc_132, entry15_a_143, entry15_b_144, entry15_imm_140,
       entry15_pc_141, mux_496, mux_497, mux_498, mux_499, mux_500, mux_501, mux_502, mux_503, mux_504,
       mux_505, mux_506, mux_507, mux_508, mux_509, mux_511, mux_512, mux_513, mux_514, mux_515, mux_516,
       mux_517, mux_518, mux_519, mux_520, mux_521, mux_522, mux_523, mux_524, mux_541, mux_542, mux_543,
       mux_544, mux_545, mux_546, mux_547, mux_548, mux_549, mux_550, mux_551, mux_552, mux_553, mux_554,
       mux_556, mux_557, mux_558, mux_559, mux_560, mux_561, mux_562, mux_563, mux_564, mux_565, mux_566,
       mux_567, mux_568, mux_569;

  RS_Entry entry00 (
    .clk(clk), .rst(rst), .clear(clear), .enable(enable), .wr(allocate_0), .erase(and_405), .op(op), .rd(rd),
    .qj(qj), .qk(qk), .imm(imm), .pc(pc), .sn(sn), .vj(vj), .vk(vk), .dj(dj), .dk(dk), .c0_valid(c0_valid),
    .c0_rd(c0_rd), .c0_data(c0_data), .c1_valid(c1_valid), .c1_rd(c1_rd), .c1_data(c1_data),
    .busy(entry00_busy_1), .ready(entry00_ready_2), .op_2(entry00_op_3), .rd_2(entry00_rd_4),
    .imm_2(entry00_imm_5), .pc_2(entry00_pc_6), .sn_2(entry00_sn_7), .a(entry00_a_8), .b(entry00_b_9));
  RS_Entry entry04 (
    .clk(clk), .rst(rst), .clear(clear), .enable(enable), .wr(allocate_4), .erase(and_421), .op(op), .rd(rd),
    .qj(qj), .qk(qk), .imm(imm), .pc(pc), .sn(sn), .vj(vj), .vk(vk), .dj(dj), .dk(dk), .c0_valid(c0_valid),
    .c0_rd(c0_rd), .c0_data(c0_data), .c1_valid(c1_valid), .c1_rd(c1_rd), .c1_data(c1_data),
    .busy(entry04_busy_37), .ready(entry04_ready_38), .op_2(entry04_op_39), .rd_2(entry04_rd_40),
    .imm_2(entry04_imm_41), .pc_2(entry04_pc_42), .sn_2(entry04_sn_43), .a(entry04_a_44), .b(entry04_b_45));
  RS_Entry entry08 (
    .clk(clk), .rst(rst), .clear(clear), .enable(enable), .wr(allocate_8), .erase(and_437), .op(op), .rd(rd),
    .qj(qj), .qk(qk), .imm(imm), .pc(pc), .sn(sn), .vj(vj), .vk(vk), .dj(dj), .dk(dk), .c0_valid(c0_valid),
    .c0_rd(c0_rd), .c0_data(c0_data), .c1_valid(c1_valid), .c1_rd(c1_rd), .c1_data(c1_data),
    .busy(entry08_busy_73), .ready(entry08_ready_74), .op_2(entry08_op_75), .rd_2(entry08_rd_76),
    .imm_2(entry08_imm_77), .pc_2(entry08_pc_78), .sn_2(entry08_sn_79), .a(entry08_a_80), .b(entry08_b_81));
  RS_Entry entry12 (
    .clk(clk), .rst(rst), .clear(clear), .enable(enable), .wr(allocate_12), .erase(and_453), .op(op),
    .rd(rd), .qj(qj), .qk(qk), .imm(imm), .pc(pc), .sn(sn), .vj(vj), .vk(vk), .dj(dj), .dk(dk),
    .c0_valid(c0_valid), .c0_rd(c0_rd), .c0_data(c0_data), .c1_valid(c1_valid), .c1_rd(c1_rd),
    .c1_data(c1_data), .busy(entry12_busy_109), .ready(entry12_ready_110), .op_2(entry12_op_111),
    .rd_2(entry12_rd_112), .imm_2(entry12_imm_113), .pc_2(entry12_pc_114), .sn_2(entry12_sn_115),
    .a(entry12_a_116), .b(entry12_b_117));
  and and_1 (allocate_1, and_151, not_150);
  and and_2 (and_155, wr, and_153);
  not not_1 (not_158, entry03_busy_28);
  and and_3 (and_161, and_157, entry03_busy_28);
  and and_4 (allocate_5, and_167, not_166);
  and and_5 (and_171, wr, and_169);
  not not_2 (not_174, entry07_busy_64);
  and and_6 (and_177, and_173, entry07_busy_64);
  and and_7 (allocate_9, and_183, not_182);
  and and_8 (and_187, wr, and_185);
  not not_3 (not_190, entry11_busy_100);
  and and_9 (and_193, and_189, entry11_busy_100);
  and and_10 (allocate_13, and_199, not_198);
  and and_11 (and_203, wr, and_201);
  not not_4 (not_206, entry15_busy_136);
  and and_12 (full, and_205, entry15_busy_136);
  assign ext_213 = {{4{1'b0}}, entry03_busy_28};  // Bit_Extender bit_extender_1
  assign ext_217 = {{4{1'b0}}, entry07_busy_64};  // Bit_Extender bit_extender_2
  assign ext_221 = {{4{1'b0}}, entry11_busy_100};  // Bit_Extender bit_extender_3
  assign ext_225 = {{4{1'b0}}, entry15_busy_136};  // Bit_Extender bit_extender_4
  Adder #(.width(5)) adder_1 (.a(ext_214), .b(ext_215), .out(adder_229), .cin(1'b0));  // open: cout
  Adder #(.width(5)) adder_2 (.a(ext_222), .b(ext_223), .out(adder_233), .cin(1'b0));  // open: cout
  Adder #(.width(5)) adder_3 (.a(adder_231), .b(adder_232), .out(adder_237), .cin(1'b0));  // open: cout
  Adder #(.width(5)) adder_4 (.a(adder_239), .b(adder_240), .out(count), .cin(1'b0));  // open: cout
  or or_1 (or_261, not_260, slice_259);
  Multiplexer #(.width(4), .select(1), .enable("false")) multiplexer_1 (
    .in0(4'b0000), .in1(4'b0001), .out(mux_265), .sel(and_262));
  or or_2 (or_269, not_268, slice_267);
  Multiplexer #(.width(4), .select(1), .enable("false")) multiplexer_2 (
    .in0(4'b0010), .in1(4'b0011), .out(mux_273), .sel(and_270));
  or or_3 (or_277, not_276, slice_275);
  Multiplexer #(.width(4), .select(1), .enable("false")) multiplexer_3 (
    .in0(4'b0100), .in1(4'b0101), .out(mux_281), .sel(and_278));
  or or_4 (or_285, not_284, slice_283);
  Multiplexer #(.width(4), .select(1), .enable("false")) multiplexer_4 (
    .in0(4'b0110), .in1(4'b0111), .out(mux_289), .sel(and_286));
  or or_5 (or_293, not_292, slice_291);
  Multiplexer #(.width(4), .select(1), .enable("false")) multiplexer_5 (
    .in0(4'b1000), .in1(4'b1001), .out(mux_297), .sel(and_294));
  or or_6 (or_301, not_300, slice_299);
  Multiplexer #(.width(4), .select(1), .enable("false")) multiplexer_6 (
    .in0(4'b1010), .in1(4'b1011), .out(mux_305), .sel(and_302));
  or or_7 (or_309, not_308, slice_307);
  Multiplexer #(.width(4), .select(1), .enable("false")) multiplexer_7 (
    .in0(4'b1100), .in1(4'b1101), .out(mux_313), .sel(and_310));
  or or_8 (or_317, not_316, slice_315);
  Multiplexer #(.width(4), .select(1), .enable("false")) multiplexer_8 (
    .in0(4'b1110), .in1(4'b1111), .out(mux_321), .sel(and_318));
  or or_9 (or_325, not_324, slice_323);
  Multiplexer #(.width(4), .select(1), .enable("false")) multiplexer_9 (
    .in0(mux_265), .in1(mux_273), .out(mux_329), .sel(and_326));
  or or_10 (or_333, not_332, slice_331);
  Multiplexer #(.width(4), .select(1), .enable("false")) multiplexer_10 (
    .in0(mux_281), .in1(mux_289), .out(mux_337), .sel(and_334));
  or or_11 (or_341, not_340, slice_339);
  Multiplexer #(.width(4), .select(1), .enable("false")) multiplexer_11 (
    .in0(mux_297), .in1(mux_305), .out(mux_345), .sel(and_342));
  or or_12 (or_349, not_348, slice_347);
  Multiplexer #(.width(4), .select(1), .enable("false")) multiplexer_12 (
    .in0(mux_313), .in1(mux_321), .out(mux_353), .sel(and_350));
  or or_13 (or_357, not_356, slice_355);
  Multiplexer #(.width(4), .select(1), .enable("false")) multiplexer_13 (
    .in0(mux_329), .in1(mux_337), .out(mux_361), .sel(and_358));
  or or_14 (or_365, not_364, slice_363);
  Multiplexer #(.width(4), .select(1), .enable("false")) multiplexer_14 (
    .in0(mux_345), .in1(mux_353), .out(mux_369), .sel(and_366));
  or or_15 (or_373, not_372, slice_371);
  Multiplexer #(.width(4), .select(1), .enable("false")) multiplexer_15 (
    .in0(mux_361), .in1(mux_369), .out(mux_377), .sel(and_374));
  Multiplexer #(.width(1), .select(1), .enable("false")) multiplexer_16 (
    .in0(entry02_ready_20), .in1(entry03_ready_29), .out(mux_385), .sel(mux_377[0]));
  Multiplexer #(.width(1), .select(1), .enable("false")) multiplexer_17 (
    .in0(mux_387), .in1(mux_388), .out(mux_389), .sel(mux_377[1]));
  Multiplexer #(.width(1), .select(1), .enable("false")) multiplexer_18 (
    .in0(mux_391), .in1(mux_392), .out(mux_393), .sel(mux_377[1]));
  Multiplexer #(.width(1), .select(1), .enable("false")) multiplexer_19 (
    .in0(mux_393), .in1(mux_396), .out(mux_397), .sel(mux_377[2]));
  and and_13 (and_401, and_400, ex_valid);
  Comparator #(.width(4), .mode("unsigned")) comparator_1 (
    .a(mux_377), .b(4'b0001), .gt(gt_406), .eq(eq_407), .lt(lt_408));
  and and_14 (and_413, and_401, eq_411);
  Comparator #(.width(4), .mode("unsigned")) comparator_2 (
    .a(mux_377), .b(4'b0101), .gt(gt_422), .eq(eq_423), .lt(lt_424));
  and and_15 (and_429, and_401, eq_427);
  Comparator #(.width(4), .mode("unsigned")) comparator_3 (
    .a(mux_377), .b(4'b1001), .gt(gt_438), .eq(eq_439), .lt(lt_440));
  and and_16 (and_445, and_401, eq_443);
  Comparator #(.width(4), .mode("unsigned")) comparator_4 (
    .a(mux_377), .b(4'b1101), .gt(gt_454), .eq(eq_455), .lt(lt_456));
  and and_17 (and_461, and_401, eq_459);
  Multiplexer #(.width(4), .select(1), .enable("false")) multiplexer_20 (
    .in0(entry04_op_39), .in1(entry05_op_48), .out(mux_469), .sel(mux_377[0]));
  Multiplexer #(.width(4), .select(1), .enable("false")) multiplexer_21 (
    .in0(entry08_op_75), .in1(entry09_op_84), .out(mux_473), .sel(mux_377[0]));
  Multiplexer #(.width(4), .select(1), .enable("false")) multiplexer_22 (
    .in0(entry14_op_129), .in1(entry15_op_138), .out(mux_477), .sel(mux_377[0]));
  Multiplexer #(.width(6), .select(1), .enable("false")) multiplexer_23 (
    .in0(entry00_rd_4), .in1(entry01_rd_13), .out(mux_481), .sel(mux_377[0]));
  Multiplexer #(.width(6), .select(1), .enable("false")) multiplexer_24 (
    .in0(entry06_rd_58), .in1(entry07_rd_67), .out(mux_485), .sel(mux_377[0]));
  Multiplexer #(.width(6), .select(1), .enable("false")) multiplexer_25 (
    .in0(entry10_rd_94), .in1(entry11_rd_103), .out(mux_489), .sel(mux_377[0]));
  Multiplexer #(.width(6), .select(1), .enable("false")) multiplexer_26 (
    .in0(mux_491), .in1(mux_492), .out(mux_493), .sel(mux_377[1]));
  Multiplexer #(.width(16), .select(1), .enable("false")) multiplexer_27 (
    .in0(entry02_imm_23), .in1(entry03_imm_32), .out(mux_497), .sel(mux_377[0]));
  Multiplexer #(.width(16), .select(1), .enable("false")) multiplexer_28 (
    .in0(mux_499), .in1(mux_500), .out(mux_501), .sel(mux_377[1]));
  Multiplexer #(.width(16), .select(1), .enable("false")) multiplexer_29 (
    .in0(mux_503), .in1(mux_504), .out(mux_505), .sel(mux_377[1]));
  Multiplexer #(.width(16), .select(1), .enable("false")) multiplexer_30 (
    .in0(mux_505), .in1(mux_508), .out(mux_509), .sel(mux_377[2]));
  Multiplexer #(.width(16), .select(1), .enable("false")) multiplexer_31 (
    .in0(mux_511), .in1(mux_512), .out(mux_513), .sel(mux_377[1]));
  Multiplexer #(.width(16), .select(1), .enable("false")) multiplexer_32 (
    .in0(mux_513), .in1(mux_516), .out(mux_517), .sel(mux_377[2]));
  Multiplexer #(.width(16), .select(1), .enable("false")) multiplexer_33 (
    .in0(entry12_pc_114), .in1(entry13_pc_123), .out(mux_521), .sel(mux_377[0]));
  Multiplexer #(.width(16), .select(1), .enable("false")) multiplexer_34 (
    .in0(mux_517), .in1(mux_524), .out(ex_pc), .sel(mux_377[3]));
  Multiplexer #(.width(8), .select(1), .enable("false")) multiplexer_35 (
    .in0(entry04_sn_43), .in1(entry05_sn_52), .out(mux_529), .sel(mux_377[0]));
  Multiplexer #(.width(8), .select(1), .enable("false")) multiplexer_36 (
    .in0(entry08_sn_79), .in1(entry09_sn_88), .out(mux_533), .sel(mux_377[0]));
  Multiplexer #(.width(8), .select(1), .enable("false")) multiplexer_37 (
    .in0(entry14_sn_133), .in1(entry15_sn_142), .out(mux_537), .sel(mux_377[0]));
  Multiplexer #(.width(16), .select(1), .enable("false")) multiplexer_38 (
    .in0(entry00_a_8), .in1(entry01_a_17), .out(mux_541), .sel(mux_377[0]));
  Multiplexer #(.width(16), .select(1), .enable("false")) multiplexer_39 (
    .in0(entry06_a_62), .in1(entry07_a_71), .out(mux_545), .sel(mux_377[0]));
  Multiplexer #(.width(16), .select(1), .enable("false")) multiplexer_40 (
    .in0(entry10_a_98), .in1(entry11_a_107), .out(mux_549), .sel(mux_377[0]));
  Multiplexer #(.width(16), .select(1), .enable("false")) multiplexer_41 (
    .in0(mux_551), .in1(mux_552), .out(mux_553), .sel(mux_377[1]));
  Multiplexer #(.width(16), .select(1), .enable("false")) multiplexer_42 (
    .in0(entry02_b_27), .in1(entry03_b_36), .out(mux_557), .sel(mux_377[0]));
  Multiplexer #(.width(16), .select(1), .enable("false")) multiplexer_43 (
    .in0(mux_559), .in1(mux_560), .out(mux_561), .sel(mux_377[1]));
  Multiplexer #(.width(16), .select(1), .enable("false")) multiplexer_44 (
    .in0(mux_563), .in1(mux_564), .out(mux_565), .sel(mux_377[1]));
  Multiplexer #(.width(16), .select(1), .enable("false")) multiplexer_45 (
    .in0(mux_565), .in1(mux_568), .out(mux_569), .sel(mux_377[2]));
  RS_Entry entry01 (
    .clk(clk), .rst(rst), .clear(clear), .enable(enable), .wr(allocate_1), .erase(and_409), .op(op), .rd(rd),
    .qj(qj), .qk(qk), .imm(imm), .pc(pc), .sn(sn), .vj(vj), .vk(vk), .dj(dj), .dk(dk), .c0_valid(c0_valid),
    .c0_rd(c0_rd), .c0_data(c0_data), .c1_valid(c1_valid), .c1_rd(c1_rd), .c1_data(c1_data),
    .busy(entry01_busy_10), .ready(entry01_ready_11), .op_2(entry01_op_12), .rd_2(entry01_rd_13),
    .imm_2(entry01_imm_14), .pc_2(entry01_pc_15), .sn_2(entry01_sn_16), .a(entry01_a_17), .b(entry01_b_18));
  RS_Entry entry05 (
    .clk(clk), .rst(rst), .clear(clear), .enable(enable), .wr(allocate_5), .erase(and_425), .op(op), .rd(rd),
    .qj(qj), .qk(qk), .imm(imm), .pc(pc), .sn(sn), .vj(vj), .vk(vk), .dj(dj), .dk(dk), .c0_valid(c0_valid),
    .c0_rd(c0_rd), .c0_data(c0_data), .c1_valid(c1_valid), .c1_rd(c1_rd), .c1_data(c1_data),
    .busy(entry05_busy_46), .ready(entry05_ready_47), .op_2(entry05_op_48), .rd_2(entry05_rd_49),
    .imm_2(entry05_imm_50), .pc_2(entry05_pc_51), .sn_2(entry05_sn_52), .a(entry05_a_53), .b(entry05_b_54));
  RS_Entry entry09 (
    .clk(clk), .rst(rst), .clear(clear), .enable(enable), .wr(allocate_9), .erase(and_441), .op(op), .rd(rd),
    .qj(qj), .qk(qk), .imm(imm), .pc(pc), .sn(sn), .vj(vj), .vk(vk), .dj(dj), .dk(dk), .c0_valid(c0_valid),
    .c0_rd(c0_rd), .c0_data(c0_data), .c1_valid(c1_valid), .c1_rd(c1_rd), .c1_data(c1_data),
    .busy(entry09_busy_82), .ready(entry09_ready_83), .op_2(entry09_op_84), .rd_2(entry09_rd_85),
    .imm_2(entry09_imm_86), .pc_2(entry09_pc_87), .sn_2(entry09_sn_88), .a(entry09_a_89), .b(entry09_b_90));
  RS_Entry entry13 (
    .clk(clk), .rst(rst), .clear(clear), .enable(enable), .wr(allocate_13), .erase(and_457), .op(op),
    .rd(rd), .qj(qj), .qk(qk), .imm(imm), .pc(pc), .sn(sn), .vj(vj), .vk(vk), .dj(dj), .dk(dk),
    .c0_valid(c0_valid), .c0_rd(c0_rd), .c0_data(c0_data), .c1_valid(c1_valid), .c1_rd(c1_rd),
    .c1_data(c1_data), .busy(entry13_busy_118), .ready(entry13_ready_119), .op_2(entry13_op_120),
    .rd_2(entry13_rd_121), .imm_2(entry13_imm_122), .pc_2(entry13_pc_123), .sn_2(entry13_sn_124),
    .a(entry13_a_125), .b(entry13_b_126));
  not not_5 (not_146, entry00_busy_1);
  and and_18 (and_149, 1'b1, entry00_busy_1);
  and and_19 (allocate_2, and_155, not_154);
  and and_20 (and_159, wr, and_157);
  not not_6 (not_162, entry04_busy_37);
  and and_21 (and_165, and_161, entry04_busy_37);
  and and_22 (allocate_6, and_171, not_170);
  and and_23 (and_175, wr, and_173);
  not not_7 (not_178, entry08_busy_73);
  and and_24 (and_181, and_177, entry08_busy_73);
  and and_25 (allocate_10, and_187, not_186);
  and and_26 (and_191, wr, and_189);
  not not_8 (not_194, entry12_busy_109);
  and and_27 (and_197, and_193, entry12_busy_109);
  and and_28 (allocate_14, and_203, not_202);
  and and_29 (and_207, wr, and_205);
  assign ext_210 = {{4{1'b0}}, entry00_busy_1};  // Bit_Extender bit_extender_5
  assign ext_214 = {{4{1'b0}}, entry04_busy_37};  // Bit_Extender bit_extender_6
  assign ext_218 = {{4{1'b0}}, entry08_busy_73};  // Bit_Extender bit_extender_7
  assign ext_222 = {{4{1'b0}}, entry12_busy_109};  // Bit_Extender bit_extender_8
  Adder #(.width(5)) adder_5 (.a(ext_210), .b(ext_211), .out(adder_226), .cin(1'b0));  // open: cout
  Adder #(.width(5)) adder_6 (.a(ext_216), .b(ext_217), .out(adder_230), .cin(1'b0));  // open: cout
  Adder #(.width(5)) adder_7 (.a(ext_224), .b(ext_225), .out(adder_234), .cin(1'b0));  // open: cout
  Adder #(.width(5)) adder_8 (.a(adder_233), .b(adder_234), .out(adder_238), .cin(1'b0));  // open: cout
  Subtractor #(.width(8)) subtractor_1 (
    .a(entry01_sn_16), .b(entry00_sn_7), .out({slice_259, subtractor_258}), .bin(1'b0));  // open: bout
  and and_30 (and_262, entry01_ready_11, or_261);
  Subtractor #(.width(8)) subtractor_2 (
    .a(entry03_sn_34), .b(entry02_sn_25), .out({slice_267, subtractor_266}), .bin(1'b0));  // open: bout
  and and_31 (and_270, entry03_ready_29, or_269);
  Subtractor #(.width(8)) subtractor_3 (
    .a(entry05_sn_52), .b(entry04_sn_43), .out({slice_275, subtractor_274}), .bin(1'b0));  // open: bout
  and and_32 (and_278, entry05_ready_47, or_277);
  Subtractor #(.width(8)) subtractor_4 (
    .a(entry07_sn_70), .b(entry06_sn_61), .out({slice_283, subtractor_282}), .bin(1'b0));  // open: bout
  and and_33 (and_286, entry07_ready_65, or_285);
  Subtractor #(.width(8)) subtractor_5 (
    .a(entry09_sn_88), .b(entry08_sn_79), .out({slice_291, subtractor_290}), .bin(1'b0));  // open: bout
  and and_34 (and_294, entry09_ready_83, or_293);
  Subtractor #(.width(8)) subtractor_6 (
    .a(entry11_sn_106), .b(entry10_sn_97), .out({slice_299, subtractor_298}), .bin(1'b0));  // open: bout
  and and_35 (and_302, entry11_ready_101, or_301);
  Subtractor #(.width(8)) subtractor_7 (
    .a(entry13_sn_124), .b(entry12_sn_115), .out({slice_307, subtractor_306}), .bin(1'b0));  // open: bout
  and and_36 (and_310, entry13_ready_119, or_309);
  Subtractor #(.width(8)) subtractor_8 (
    .a(entry15_sn_142), .b(entry14_sn_133), .out({slice_315, subtractor_314}), .bin(1'b0));  // open: bout
  and and_37 (and_318, entry15_ready_137, or_317);
  Subtractor #(.width(8)) subtractor_9 (
    .a(mux_272), .b(mux_264), .out({slice_323, subtractor_322}), .bin(1'b0));  // open: bout
  and and_38 (and_326, or_271, or_325);
  Subtractor #(.width(8)) subtractor_10 (
    .a(mux_288), .b(mux_280), .out({slice_331, subtractor_330}), .bin(1'b0));  // open: bout
  and and_39 (and_334, or_287, or_333);
  Subtractor #(.width(8)) subtractor_11 (
    .a(mux_304), .b(mux_296), .out({slice_339, subtractor_338}), .bin(1'b0));  // open: bout
  and and_40 (and_342, or_303, or_341);
  Subtractor #(.width(8)) subtractor_12 (
    .a(mux_320), .b(mux_312), .out({slice_347, subtractor_346}), .bin(1'b0));  // open: bout
  and and_41 (and_350, or_319, or_349);
  Subtractor #(.width(8)) subtractor_13 (
    .a(mux_336), .b(mux_328), .out({slice_355, subtractor_354}), .bin(1'b0));  // open: bout
  and and_42 (and_358, or_335, or_357);
  Subtractor #(.width(8)) subtractor_14 (
    .a(mux_352), .b(mux_344), .out({slice_363, subtractor_362}), .bin(1'b0));  // open: bout
  and and_43 (and_366, or_351, or_365);
  Subtractor #(.width(8)) subtractor_15 (
    .a(mux_368), .b(mux_360), .out({slice_371, subtractor_370}), .bin(1'b0));  // open: bout
  and and_44 (and_374, or_367, or_373);
  Multiplexer #(.width(1), .select(1), .enable("false")) multiplexer_46 (
    .in0(mux_384), .in1(mux_385), .out(mux_386), .sel(mux_377[1]));
  Multiplexer #(.width(1), .select(1), .enable("false")) multiplexer_47 (
    .in0(mux_386), .in1(mux_389), .out(mux_390), .sel(mux_377[2]));
  Multiplexer #(.width(1), .select(1), .enable("false")) multiplexer_48 (
    .in0(entry12_ready_110), .in1(entry13_ready_119), .out(mux_394), .sel(mux_377[0]));
  Multiplexer #(.width(1), .select(1), .enable("false")) multiplexer_49 (
    .in0(mux_390), .in1(mux_397), .out(mux_398), .sel(mux_377[3]));
  Comparator #(.width(4), .mode("unsigned")) comparator_5 (
    .a(mux_377), .b(4'b0000), .gt(gt_402), .eq(eq_403), .lt(lt_404));
  and and_45 (and_409, and_401, eq_407);
  Comparator #(.width(4), .mode("unsigned")) comparator_6 (
    .a(mux_377), .b(4'b0100), .gt(gt_418), .eq(eq_419), .lt(lt_420));
  and and_46 (and_425, and_401, eq_423);
  Comparator #(.width(4), .mode("unsigned")) comparator_7 (
    .a(mux_377), .b(4'b1000), .gt(gt_434), .eq(eq_435), .lt(lt_436));
  and and_47 (and_441, and_401, eq_439);
  Comparator #(.width(4), .mode("unsigned")) comparator_8 (
    .a(mux_377), .b(4'b1100), .gt(gt_450), .eq(eq_451), .lt(lt_452));
  and and_48 (and_457, and_401, eq_455);
  Multiplexer #(.width(4), .select(1), .enable("false")) multiplexer_50 (
    .in0(entry00_op_3), .in1(entry01_op_12), .out(mux_466), .sel(mux_377[0]));
  Multiplexer #(.width(4), .select(1), .enable("false")) multiplexer_51 (
    .in0(entry06_op_57), .in1(entry07_op_66), .out(mux_470), .sel(mux_377[0]));
  Multiplexer #(.width(4), .select(1), .enable("false")) multiplexer_52 (
    .in0(entry10_op_93), .in1(entry11_op_102), .out(mux_474), .sel(mux_377[0]));
  Multiplexer #(.width(4), .select(1), .enable("false")) multiplexer_53 (
    .in0(mux_476), .in1(mux_477), .out(mux_478), .sel(mux_377[1]));
  Multiplexer #(.width(6), .select(1), .enable("false")) multiplexer_54 (
    .in0(entry02_rd_22), .in1(entry03_rd_31), .out(mux_482), .sel(mux_377[0]));
  Multiplexer #(.width(6), .select(1), .enable("false")) multiplexer_55 (
    .in0(mux_484), .in1(mux_485), .out(mux_486), .sel(mux_377[1]));
  Multiplexer #(.width(6), .select(1), .enable("false")) multiplexer_56 (
    .in0(mux_488), .in1(mux_489), .out(mux_490), .sel(mux_377[1]));
  Multiplexer #(.width(6), .select(1), .enable("false")) multiplexer_57 (
    .in0(mux_490), .in1(mux_493), .out(mux_494), .sel(mux_377[2]));
  Multiplexer #(.width(16), .select(1), .enable("false")) multiplexer_58 (
    .in0(mux_496), .in1(mux_497), .out(mux_498), .sel(mux_377[1]));
  Multiplexer #(.width(16), .select(1), .enable("false")) multiplexer_59 (
    .in0(mux_498), .in1(mux_501), .out(mux_502), .sel(mux_377[2]));
  Multiplexer #(.width(16), .select(1), .enable("false")) multiplexer_60 (
    .in0(entry12_imm_113), .in1(entry13_imm_122), .out(mux_506), .sel(mux_377[0]));
  Multiplexer #(.width(16), .select(1), .enable("false")) multiplexer_61 (
    .in0(mux_502), .in1(mux_509), .out(ex_imm), .sel(mux_377[3]));
  Multiplexer #(.width(16), .select(1), .enable("false")) multiplexer_62 (
    .in0(entry04_pc_42), .in1(entry05_pc_51), .out(mux_514), .sel(mux_377[0]));
  Multiplexer #(.width(16), .select(1), .enable("false")) multiplexer_63 (
    .in0(entry08_pc_78), .in1(entry09_pc_87), .out(mux_518), .sel(mux_377[0]));
  Multiplexer #(.width(16), .select(1), .enable("false")) multiplexer_64 (
    .in0(entry14_pc_132), .in1(entry15_pc_141), .out(mux_522), .sel(mux_377[0]));
  Multiplexer #(.width(8), .select(1), .enable("false")) multiplexer_65 (
    .in0(entry00_sn_7), .in1(entry01_sn_16), .out(mux_526), .sel(mux_377[0]));
  Multiplexer #(.width(8), .select(1), .enable("false")) multiplexer_66 (
    .in0(entry06_sn_61), .in1(entry07_sn_70), .out(mux_530), .sel(mux_377[0]));
  Multiplexer #(.width(8), .select(1), .enable("false")) multiplexer_67 (
    .in0(entry10_sn_97), .in1(entry11_sn_106), .out(mux_534), .sel(mux_377[0]));
  Multiplexer #(.width(8), .select(1), .enable("false")) multiplexer_68 (
    .in0(mux_536), .in1(mux_537), .out(mux_538), .sel(mux_377[1]));
  Multiplexer #(.width(16), .select(1), .enable("false")) multiplexer_69 (
    .in0(entry02_a_26), .in1(entry03_a_35), .out(mux_542), .sel(mux_377[0]));
  Multiplexer #(.width(16), .select(1), .enable("false")) multiplexer_70 (
    .in0(mux_544), .in1(mux_545), .out(mux_546), .sel(mux_377[1]));
  Multiplexer #(.width(16), .select(1), .enable("false")) multiplexer_71 (
    .in0(mux_548), .in1(mux_549), .out(mux_550), .sel(mux_377[1]));
  Multiplexer #(.width(16), .select(1), .enable("false")) multiplexer_72 (
    .in0(mux_550), .in1(mux_553), .out(mux_554), .sel(mux_377[2]));
  Multiplexer #(.width(16), .select(1), .enable("false")) multiplexer_73 (
    .in0(mux_556), .in1(mux_557), .out(mux_558), .sel(mux_377[1]));
  Multiplexer #(.width(16), .select(1), .enable("false")) multiplexer_74 (
    .in0(mux_558), .in1(mux_561), .out(mux_562), .sel(mux_377[2]));
  Multiplexer #(.width(16), .select(1), .enable("false")) multiplexer_75 (
    .in0(entry12_b_117), .in1(entry13_b_126), .out(mux_566), .sel(mux_377[0]));
  Multiplexer #(.width(16), .select(1), .enable("false")) multiplexer_76 (
    .in0(mux_562), .in1(mux_569), .out(ex_b), .sel(mux_377[3]));
  RS_Entry entry02 (
    .clk(clk), .rst(rst), .clear(clear), .enable(enable), .wr(allocate_2), .erase(and_413), .op(op), .rd(rd),
    .qj(qj), .qk(qk), .imm(imm), .pc(pc), .sn(sn), .vj(vj), .vk(vk), .dj(dj), .dk(dk), .c0_valid(c0_valid),
    .c0_rd(c0_rd), .c0_data(c0_data), .c1_valid(c1_valid), .c1_rd(c1_rd), .c1_data(c1_data),
    .busy(entry02_busy_19), .ready(entry02_ready_20), .op_2(entry02_op_21), .rd_2(entry02_rd_22),
    .imm_2(entry02_imm_23), .pc_2(entry02_pc_24), .sn_2(entry02_sn_25), .a(entry02_a_26), .b(entry02_b_27));
  RS_Entry entry06 (
    .clk(clk), .rst(rst), .clear(clear), .enable(enable), .wr(allocate_6), .erase(and_429), .op(op), .rd(rd),
    .qj(qj), .qk(qk), .imm(imm), .pc(pc), .sn(sn), .vj(vj), .vk(vk), .dj(dj), .dk(dk), .c0_valid(c0_valid),
    .c0_rd(c0_rd), .c0_data(c0_data), .c1_valid(c1_valid), .c1_rd(c1_rd), .c1_data(c1_data),
    .busy(entry06_busy_55), .ready(entry06_ready_56), .op_2(entry06_op_57), .rd_2(entry06_rd_58),
    .imm_2(entry06_imm_59), .pc_2(entry06_pc_60), .sn_2(entry06_sn_61), .a(entry06_a_62), .b(entry06_b_63));
  RS_Entry entry10 (
    .clk(clk), .rst(rst), .clear(clear), .enable(enable), .wr(allocate_10), .erase(and_445), .op(op),
    .rd(rd), .qj(qj), .qk(qk), .imm(imm), .pc(pc), .sn(sn), .vj(vj), .vk(vk), .dj(dj), .dk(dk),
    .c0_valid(c0_valid), .c0_rd(c0_rd), .c0_data(c0_data), .c1_valid(c1_valid), .c1_rd(c1_rd),
    .c1_data(c1_data), .busy(entry10_busy_91), .ready(entry10_ready_92), .op_2(entry10_op_93),
    .rd_2(entry10_rd_94), .imm_2(entry10_imm_95), .pc_2(entry10_pc_96), .sn_2(entry10_sn_97),
    .a(entry10_a_98), .b(entry10_b_99));
  RS_Entry entry14 (
    .clk(clk), .rst(rst), .clear(clear), .enable(enable), .wr(allocate_14), .erase(and_461), .op(op),
    .rd(rd), .qj(qj), .qk(qk), .imm(imm), .pc(pc), .sn(sn), .vj(vj), .vk(vk), .dj(dj), .dk(dk),
    .c0_valid(c0_valid), .c0_rd(c0_rd), .c0_data(c0_data), .c1_valid(c1_valid), .c1_rd(c1_rd),
    .c1_data(c1_data), .busy(entry14_busy_127), .ready(entry14_ready_128), .op_2(entry14_op_129),
    .rd_2(entry14_rd_130), .imm_2(entry14_imm_131), .pc_2(entry14_pc_132), .sn_2(entry14_sn_133),
    .a(entry14_a_134), .b(entry14_b_135));
  and and_49 (and_147, wr, 1'b1);
  not not_9 (not_150, entry01_busy_10);
  and and_50 (and_153, and_149, entry01_busy_10);
  and and_51 (allocate_3, and_159, not_158);
  and and_52 (and_163, wr, and_161);
  not not_10 (not_166, entry05_busy_46);
  and and_53 (and_169, and_165, entry05_busy_46);
  and and_54 (allocate_7, and_175, not_174);
  and and_55 (and_179, wr, and_177);
  not not_11 (not_182, entry09_busy_82);
  and and_56 (and_185, and_181, entry09_busy_82);
  and and_57 (allocate_11, and_191, not_190);
  and and_58 (and_195, wr, and_193);
  not not_12 (not_198, entry13_busy_118);
  and and_59 (and_201, and_197, entry13_busy_118);
  and and_60 (allocate_15, and_207, not_206);
  assign ext_211 = {{4{1'b0}}, entry01_busy_10};  // Bit_Extender bit_extender_9
  assign ext_215 = {{4{1'b0}}, entry05_busy_46};  // Bit_Extender bit_extender_10
  assign ext_219 = {{4{1'b0}}, entry09_busy_82};  // Bit_Extender bit_extender_11
  assign ext_223 = {{4{1'b0}}, entry13_busy_118};  // Bit_Extender bit_extender_12
  Adder #(.width(5)) adder_9 (.a(ext_218), .b(ext_219), .out(adder_231), .cin(1'b0));  // open: cout
  Adder #(.width(5)) adder_10 (.a(adder_226), .b(adder_228), .out(adder_235), .cin(1'b0));  // open: cout
  Adder #(.width(5)) adder_11 (.a(adder_235), .b(adder_236), .out(adder_239), .cin(1'b0));  // open: cout
  or or_16 (or_263, entry00_ready_2, entry01_ready_11);
  or or_17 (or_271, entry02_ready_20, entry03_ready_29);
  or or_18 (or_279, entry04_ready_38, entry05_ready_47);
  or or_19 (or_287, entry06_ready_56, entry07_ready_65);
  or or_20 (or_295, entry08_ready_74, entry09_ready_83);
  or or_21 (or_303, entry10_ready_92, entry11_ready_101);
  or or_22 (or_311, entry12_ready_110, entry13_ready_119);
  or or_23 (or_319, entry14_ready_128, entry15_ready_137);
  or or_24 (or_327, or_263, or_271);
  or or_25 (or_335, or_279, or_287);
  or or_26 (or_343, or_295, or_303);
  or or_27 (or_351, or_311, or_319);
  or or_28 (or_359, or_327, or_335);
  or or_29 (or_367, or_343, or_351);
  or or_30 (or_375, or_359, or_367);
  Multiplexer #(.width(1), .select(1), .enable("false")) multiplexer_77 (
    .in0(entry04_ready_38), .in1(entry05_ready_47), .out(mux_387), .sel(mux_377[0]));
  Multiplexer #(.width(1), .select(1), .enable("false")) multiplexer_78 (
    .in0(entry08_ready_74), .in1(entry09_ready_83), .out(mux_391), .sel(mux_377[0]));
  Multiplexer #(.width(1), .select(1), .enable("false")) multiplexer_79 (
    .in0(entry14_ready_128), .in1(entry15_ready_137), .out(mux_395), .sel(mux_377[0]));
  and and_61 (ex_valid, or_375, mux_398);
  and and_62 (and_405, and_401, eq_403);
  Comparator #(.width(4), .mode("unsigned")) comparator_9 (
    .a(mux_377), .b(4'b0011), .gt(gt_414), .eq(eq_415), .lt(lt_416));
  and and_63 (and_421, and_401, eq_419);
  Comparator #(.width(4), .mode("unsigned")) comparator_10 (
    .a(mux_377), .b(4'b0111), .gt(gt_430), .eq(eq_431), .lt(lt_432));
  and and_64 (and_437, and_401, eq_435);
  Comparator #(.width(4), .mode("unsigned")) comparator_11 (
    .a(mux_377), .b(4'b1011), .gt(gt_446), .eq(eq_447), .lt(lt_448));
  and and_65 (and_453, and_401, eq_451);
  Comparator #(.width(4), .mode("unsigned")) comparator_12 (
    .a(mux_377), .b(4'b1111), .gt(gt_462), .eq(eq_463), .lt(lt_464));
  Multiplexer #(.width(4), .select(1), .enable("false")) multiplexer_80 (
    .in0(entry02_op_21), .in1(entry03_op_30), .out(mux_467), .sel(mux_377[0]));
  Multiplexer #(.width(4), .select(1), .enable("false")) multiplexer_81 (
    .in0(mux_469), .in1(mux_470), .out(mux_471), .sel(mux_377[1]));
  Multiplexer #(.width(4), .select(1), .enable("false")) multiplexer_82 (
    .in0(mux_473), .in1(mux_474), .out(mux_475), .sel(mux_377[1]));
  Multiplexer #(.width(4), .select(1), .enable("false")) multiplexer_83 (
    .in0(mux_475), .in1(mux_478), .out(mux_479), .sel(mux_377[2]));
  Multiplexer #(.width(6), .select(1), .enable("false")) multiplexer_84 (
    .in0(mux_481), .in1(mux_482), .out(mux_483), .sel(mux_377[1]));
  Multiplexer #(.width(6), .select(1), .enable("false")) multiplexer_85 (
    .in0(mux_483), .in1(mux_486), .out(mux_487), .sel(mux_377[2]));
  Multiplexer #(.width(6), .select(1), .enable("false")) multiplexer_86 (
    .in0(entry12_rd_112), .in1(entry13_rd_121), .out(mux_491), .sel(mux_377[0]));
  Multiplexer #(.width(6), .select(1), .enable("false")) multiplexer_87 (
    .in0(mux_487), .in1(mux_494), .out(ex_rd), .sel(mux_377[3]));
  Multiplexer #(.width(16), .select(1), .enable("false")) multiplexer_88 (
    .in0(entry04_imm_41), .in1(entry05_imm_50), .out(mux_499), .sel(mux_377[0]));
  Multiplexer #(.width(16), .select(1), .enable("false")) multiplexer_89 (
    .in0(entry08_imm_77), .in1(entry09_imm_86), .out(mux_503), .sel(mux_377[0]));
  Multiplexer #(.width(16), .select(1), .enable("false")) multiplexer_90 (
    .in0(entry14_imm_131), .in1(entry15_imm_140), .out(mux_507), .sel(mux_377[0]));
  Multiplexer #(.width(16), .select(1), .enable("false")) multiplexer_91 (
    .in0(entry00_pc_6), .in1(entry01_pc_15), .out(mux_511), .sel(mux_377[0]));
  Multiplexer #(.width(16), .select(1), .enable("false")) multiplexer_92 (
    .in0(entry06_pc_60), .in1(entry07_pc_69), .out(mux_515), .sel(mux_377[0]));
  Multiplexer #(.width(16), .select(1), .enable("false")) multiplexer_93 (
    .in0(entry10_pc_96), .in1(entry11_pc_105), .out(mux_519), .sel(mux_377[0]));
  Multiplexer #(.width(16), .select(1), .enable("false")) multiplexer_94 (
    .in0(mux_521), .in1(mux_522), .out(mux_523), .sel(mux_377[1]));
  Multiplexer #(.width(8), .select(1), .enable("false")) multiplexer_95 (
    .in0(entry02_sn_25), .in1(entry03_sn_34), .out(mux_527), .sel(mux_377[0]));
  Multiplexer #(.width(8), .select(1), .enable("false")) multiplexer_96 (
    .in0(mux_529), .in1(mux_530), .out(mux_531), .sel(mux_377[1]));
  Multiplexer #(.width(8), .select(1), .enable("false")) multiplexer_97 (
    .in0(mux_533), .in1(mux_534), .out(mux_535), .sel(mux_377[1]));
  Multiplexer #(.width(8), .select(1), .enable("false")) multiplexer_98 (
    .in0(mux_535), .in1(mux_538), .out(mux_539), .sel(mux_377[2]));
  Multiplexer #(.width(16), .select(1), .enable("false")) multiplexer_99 (
    .in0(mux_541), .in1(mux_542), .out(mux_543), .sel(mux_377[1]));
  Multiplexer #(.width(16), .select(1), .enable("false")) multiplexer_100 (
    .in0(mux_543), .in1(mux_546), .out(mux_547), .sel(mux_377[2]));
  Multiplexer #(.width(16), .select(1), .enable("false")) multiplexer_101 (
    .in0(entry12_a_116), .in1(entry13_a_125), .out(mux_551), .sel(mux_377[0]));
  Multiplexer #(.width(16), .select(1), .enable("false")) multiplexer_102 (
    .in0(mux_547), .in1(mux_554), .out(ex_a), .sel(mux_377[3]));
  Multiplexer #(.width(16), .select(1), .enable("false")) multiplexer_103 (
    .in0(entry04_b_45), .in1(entry05_b_54), .out(mux_559), .sel(mux_377[0]));
  Multiplexer #(.width(16), .select(1), .enable("false")) multiplexer_104 (
    .in0(entry08_b_81), .in1(entry09_b_90), .out(mux_563), .sel(mux_377[0]));
  Multiplexer #(.width(16), .select(1), .enable("false")) multiplexer_105 (
    .in0(entry14_b_135), .in1(entry15_b_144), .out(mux_567), .sel(mux_377[0]));
  RS_Entry entry03 (
    .clk(clk), .rst(rst), .clear(clear), .enable(enable), .wr(allocate_3), .erase(and_417), .op(op), .rd(rd),
    .qj(qj), .qk(qk), .imm(imm), .pc(pc), .sn(sn), .vj(vj), .vk(vk), .dj(dj), .dk(dk), .c0_valid(c0_valid),
    .c0_rd(c0_rd), .c0_data(c0_data), .c1_valid(c1_valid), .c1_rd(c1_rd), .c1_data(c1_data),
    .busy(entry03_busy_28), .ready(entry03_ready_29), .op_2(entry03_op_30), .rd_2(entry03_rd_31),
    .imm_2(entry03_imm_32), .pc_2(entry03_pc_33), .sn_2(entry03_sn_34), .a(entry03_a_35), .b(entry03_b_36));
  RS_Entry entry07 (
    .clk(clk), .rst(rst), .clear(clear), .enable(enable), .wr(allocate_7), .erase(and_433), .op(op), .rd(rd),
    .qj(qj), .qk(qk), .imm(imm), .pc(pc), .sn(sn), .vj(vj), .vk(vk), .dj(dj), .dk(dk), .c0_valid(c0_valid),
    .c0_rd(c0_rd), .c0_data(c0_data), .c1_valid(c1_valid), .c1_rd(c1_rd), .c1_data(c1_data),
    .busy(entry07_busy_64), .ready(entry07_ready_65), .op_2(entry07_op_66), .rd_2(entry07_rd_67),
    .imm_2(entry07_imm_68), .pc_2(entry07_pc_69), .sn_2(entry07_sn_70), .a(entry07_a_71), .b(entry07_b_72));
  RS_Entry entry11 (
    .clk(clk), .rst(rst), .clear(clear), .enable(enable), .wr(allocate_11), .erase(and_449), .op(op),
    .rd(rd), .qj(qj), .qk(qk), .imm(imm), .pc(pc), .sn(sn), .vj(vj), .vk(vk), .dj(dj), .dk(dk),
    .c0_valid(c0_valid), .c0_rd(c0_rd), .c0_data(c0_data), .c1_valid(c1_valid), .c1_rd(c1_rd),
    .c1_data(c1_data), .busy(entry11_busy_100), .ready(entry11_ready_101), .op_2(entry11_op_102),
    .rd_2(entry11_rd_103), .imm_2(entry11_imm_104), .pc_2(entry11_pc_105), .sn_2(entry11_sn_106),
    .a(entry11_a_107), .b(entry11_b_108));
  RS_Entry entry15 (
    .clk(clk), .rst(rst), .clear(clear), .enable(enable), .wr(allocate_15), .erase(and_465), .op(op),
    .rd(rd), .qj(qj), .qk(qk), .imm(imm), .pc(pc), .sn(sn), .vj(vj), .vk(vk), .dj(dj), .dk(dk),
    .c0_valid(c0_valid), .c0_rd(c0_rd), .c0_data(c0_data), .c1_valid(c1_valid), .c1_rd(c1_rd),
    .c1_data(c1_data), .busy(entry15_busy_136), .ready(entry15_ready_137), .op_2(entry15_op_138),
    .rd_2(entry15_rd_139), .imm_2(entry15_imm_140), .pc_2(entry15_pc_141), .sn_2(entry15_sn_142),
    .a(entry15_a_143), .b(entry15_b_144));
  and and_66 (allocate_0, and_147, not_146);
  and and_67 (and_151, wr, and_149);
  not not_13 (not_154, entry02_busy_19);
  and and_68 (and_157, and_153, entry02_busy_19);
  and and_69 (allocate_4, and_163, not_162);
  and and_70 (and_167, wr, and_165);
  not not_14 (not_170, entry06_busy_55);
  and and_71 (and_173, and_169, entry06_busy_55);
  and and_72 (allocate_8, and_179, not_178);
  and and_73 (and_183, wr, and_181);
  not not_15 (not_186, entry10_busy_91);
  and and_74 (and_189, and_185, entry10_busy_91);
  and and_75 (allocate_12, and_195, not_194);
  and and_76 (and_199, wr, and_197);
  not not_16 (not_202, entry14_busy_127);
  and and_77 (and_205, and_201, entry14_busy_127);
  assign ext_212 = {{4{1'b0}}, entry02_busy_19};  // Bit_Extender bit_extender_13
  assign ext_216 = {{4{1'b0}}, entry06_busy_55};  // Bit_Extender bit_extender_14
  assign ext_220 = {{4{1'b0}}, entry10_busy_91};  // Bit_Extender bit_extender_15
  assign ext_224 = {{4{1'b0}}, entry14_busy_127};  // Bit_Extender bit_extender_16
  Adder #(.width(5)) adder_12 (.a(ext_212), .b(ext_213), .out(adder_228), .cin(1'b0));  // open: cout
  Adder #(.width(5)) adder_13 (.a(ext_220), .b(ext_221), .out(adder_232), .cin(1'b0));  // open: cout
  Adder #(.width(5)) adder_14 (.a(adder_229), .b(adder_230), .out(adder_236), .cin(1'b0));  // open: cout
  Adder #(.width(5)) adder_15 (.a(adder_237), .b(adder_238), .out(adder_240), .cin(1'b0));  // open: cout
  not not_17 (not_260, entry00_ready_2);
  Multiplexer #(.width(8), .select(1), .enable("false")) multiplexer_106 (
    .in0(entry00_sn_7), .in1(entry01_sn_16), .out(mux_264), .sel(and_262));
  not not_18 (not_268, entry02_ready_20);
  Multiplexer #(.width(8), .select(1), .enable("false")) multiplexer_107 (
    .in0(entry02_sn_25), .in1(entry03_sn_34), .out(mux_272), .sel(and_270));
  not not_19 (not_276, entry04_ready_38);
  Multiplexer #(.width(8), .select(1), .enable("false")) multiplexer_108 (
    .in0(entry04_sn_43), .in1(entry05_sn_52), .out(mux_280), .sel(and_278));
  not not_20 (not_284, entry06_ready_56);
  Multiplexer #(.width(8), .select(1), .enable("false")) multiplexer_109 (
    .in0(entry06_sn_61), .in1(entry07_sn_70), .out(mux_288), .sel(and_286));
  not not_21 (not_292, entry08_ready_74);
  Multiplexer #(.width(8), .select(1), .enable("false")) multiplexer_110 (
    .in0(entry08_sn_79), .in1(entry09_sn_88), .out(mux_296), .sel(and_294));
  not not_22 (not_300, entry10_ready_92);
  Multiplexer #(.width(8), .select(1), .enable("false")) multiplexer_111 (
    .in0(entry10_sn_97), .in1(entry11_sn_106), .out(mux_304), .sel(and_302));
  not not_23 (not_308, entry12_ready_110);
  Multiplexer #(.width(8), .select(1), .enable("false")) multiplexer_112 (
    .in0(entry12_sn_115), .in1(entry13_sn_124), .out(mux_312), .sel(and_310));
  not not_24 (not_316, entry14_ready_128);
  Multiplexer #(.width(8), .select(1), .enable("false")) multiplexer_113 (
    .in0(entry14_sn_133), .in1(entry15_sn_142), .out(mux_320), .sel(and_318));
  not not_25 (not_324, or_263);
  Multiplexer #(.width(8), .select(1), .enable("false")) multiplexer_114 (
    .in0(mux_264), .in1(mux_272), .out(mux_328), .sel(and_326));
  not not_26 (not_332, or_279);
  Multiplexer #(.width(8), .select(1), .enable("false")) multiplexer_115 (
    .in0(mux_280), .in1(mux_288), .out(mux_336), .sel(and_334));
  not not_27 (not_340, or_295);
  Multiplexer #(.width(8), .select(1), .enable("false")) multiplexer_116 (
    .in0(mux_296), .in1(mux_304), .out(mux_344), .sel(and_342));
  not not_28 (not_348, or_311);
  Multiplexer #(.width(8), .select(1), .enable("false")) multiplexer_117 (
    .in0(mux_312), .in1(mux_320), .out(mux_352), .sel(and_350));
  not not_29 (not_356, or_327);
  Multiplexer #(.width(8), .select(1), .enable("false")) multiplexer_118 (
    .in0(mux_328), .in1(mux_336), .out(mux_360), .sel(and_358));
  not not_30 (not_364, or_343);
  Multiplexer #(.width(8), .select(1), .enable("false")) multiplexer_119 (
    .in0(mux_344), .in1(mux_352), .out(mux_368), .sel(and_366));
  not not_31 (not_372, or_359);
  Multiplexer #(.width(8), .select(1), .enable("false")) multiplexer_120 (
    .in0(mux_360), .in1(mux_368), .out(mux_376), .sel(and_374));
  Multiplexer #(.width(1), .select(1), .enable("false")) multiplexer_121 (
    .in0(entry00_ready_2), .in1(entry01_ready_11), .out(mux_384), .sel(mux_377[0]));
  Multiplexer #(.width(1), .select(1), .enable("false")) multiplexer_122 (
    .in0(entry06_ready_56), .in1(entry07_ready_65), .out(mux_388), .sel(mux_377[0]));
  Multiplexer #(.width(1), .select(1), .enable("false")) multiplexer_123 (
    .in0(entry10_ready_92), .in1(entry11_ready_101), .out(mux_392), .sel(mux_377[0]));
  Multiplexer #(.width(1), .select(1), .enable("false")) multiplexer_124 (
    .in0(mux_394), .in1(mux_395), .out(mux_396), .sel(mux_377[1]));
  and and_78 (and_400, enable, take);
  Comparator #(.width(4), .mode("unsigned")) comparator_13 (
    .a(mux_377), .b(4'b0010), .gt(gt_410), .eq(eq_411), .lt(lt_412));
  and and_79 (and_417, and_401, eq_415);
  Comparator #(.width(4), .mode("unsigned")) comparator_14 (
    .a(mux_377), .b(4'b0110), .gt(gt_426), .eq(eq_427), .lt(lt_428));
  and and_80 (and_433, and_401, eq_431);
  Comparator #(.width(4), .mode("unsigned")) comparator_15 (
    .a(mux_377), .b(4'b1010), .gt(gt_442), .eq(eq_443), .lt(lt_444));
  and and_81 (and_449, and_401, eq_447);
  Comparator #(.width(4), .mode("unsigned")) comparator_16 (
    .a(mux_377), .b(4'b1110), .gt(gt_458), .eq(eq_459), .lt(lt_460));
  and and_82 (and_465, and_401, eq_463);
  Multiplexer #(.width(4), .select(1), .enable("false")) multiplexer_125 (
    .in0(mux_466), .in1(mux_467), .out(mux_468), .sel(mux_377[1]));
  Multiplexer #(.width(4), .select(1), .enable("false")) multiplexer_126 (
    .in0(mux_468), .in1(mux_471), .out(mux_472), .sel(mux_377[2]));
  Multiplexer #(.width(4), .select(1), .enable("false")) multiplexer_127 (
    .in0(entry12_op_111), .in1(entry13_op_120), .out(mux_476), .sel(mux_377[0]));
  Multiplexer #(.width(4), .select(1), .enable("false")) multiplexer_128 (
    .in0(mux_472), .in1(mux_479), .out(ex_op), .sel(mux_377[3]));
  Multiplexer #(.width(6), .select(1), .enable("false")) multiplexer_129 (
    .in0(entry04_rd_40), .in1(entry05_rd_49), .out(mux_484), .sel(mux_377[0]));
  Multiplexer #(.width(6), .select(1), .enable("false")) multiplexer_130 (
    .in0(entry08_rd_76), .in1(entry09_rd_85), .out(mux_488), .sel(mux_377[0]));
  Multiplexer #(.width(6), .select(1), .enable("false")) multiplexer_131 (
    .in0(entry14_rd_130), .in1(entry15_rd_139), .out(mux_492), .sel(mux_377[0]));
  Multiplexer #(.width(16), .select(1), .enable("false")) multiplexer_132 (
    .in0(entry00_imm_5), .in1(entry01_imm_14), .out(mux_496), .sel(mux_377[0]));
  Multiplexer #(.width(16), .select(1), .enable("false")) multiplexer_133 (
    .in0(entry06_imm_59), .in1(entry07_imm_68), .out(mux_500), .sel(mux_377[0]));
  Multiplexer #(.width(16), .select(1), .enable("false")) multiplexer_134 (
    .in0(entry10_imm_95), .in1(entry11_imm_104), .out(mux_504), .sel(mux_377[0]));
  Multiplexer #(.width(16), .select(1), .enable("false")) multiplexer_135 (
    .in0(mux_506), .in1(mux_507), .out(mux_508), .sel(mux_377[1]));
  Multiplexer #(.width(16), .select(1), .enable("false")) multiplexer_136 (
    .in0(entry02_pc_24), .in1(entry03_pc_33), .out(mux_512), .sel(mux_377[0]));
  Multiplexer #(.width(16), .select(1), .enable("false")) multiplexer_137 (
    .in0(mux_514), .in1(mux_515), .out(mux_516), .sel(mux_377[1]));
  Multiplexer #(.width(16), .select(1), .enable("false")) multiplexer_138 (
    .in0(mux_518), .in1(mux_519), .out(mux_520), .sel(mux_377[1]));
  Multiplexer #(.width(16), .select(1), .enable("false")) multiplexer_139 (
    .in0(mux_520), .in1(mux_523), .out(mux_524), .sel(mux_377[2]));
  Multiplexer #(.width(8), .select(1), .enable("false")) multiplexer_140 (
    .in0(mux_526), .in1(mux_527), .out(mux_528), .sel(mux_377[1]));
  Multiplexer #(.width(8), .select(1), .enable("false")) multiplexer_141 (
    .in0(mux_528), .in1(mux_531), .out(mux_532), .sel(mux_377[2]));
  Multiplexer #(.width(8), .select(1), .enable("false")) multiplexer_142 (
    .in0(entry12_sn_115), .in1(entry13_sn_124), .out(mux_536), .sel(mux_377[0]));
  Multiplexer #(.width(8), .select(1), .enable("false")) multiplexer_143 (
    .in0(mux_532), .in1(mux_539), .out(ex_sn), .sel(mux_377[3]));
  Multiplexer #(.width(16), .select(1), .enable("false")) multiplexer_144 (
    .in0(entry04_a_44), .in1(entry05_a_53), .out(mux_544), .sel(mux_377[0]));
  Multiplexer #(.width(16), .select(1), .enable("false")) multiplexer_145 (
    .in0(entry08_a_80), .in1(entry09_a_89), .out(mux_548), .sel(mux_377[0]));
  Multiplexer #(.width(16), .select(1), .enable("false")) multiplexer_146 (
    .in0(entry14_a_134), .in1(entry15_a_143), .out(mux_552), .sel(mux_377[0]));
  Multiplexer #(.width(16), .select(1), .enable("false")) multiplexer_147 (
    .in0(entry00_b_9), .in1(entry01_b_18), .out(mux_556), .sel(mux_377[0]));
  Multiplexer #(.width(16), .select(1), .enable("false")) multiplexer_148 (
    .in0(entry06_b_63), .in1(entry07_b_72), .out(mux_560), .sel(mux_377[0]));
  Multiplexer #(.width(16), .select(1), .enable("false")) multiplexer_149 (
    .in0(entry10_b_99), .in1(entry11_b_108), .out(mux_564), .sel(mux_377[0]));
  Multiplexer #(.width(16), .select(1), .enable("false")) multiplexer_150 (
    .in0(mux_566), .in1(mux_567), .out(mux_568), .sel(mux_377[1]));

  // Other names for the same wires on the sheet: adder_241[4:0] = count; and_148 = allocate_0; and_152 = allocate_1;
  //   and_156 = allocate_2; and_160 = allocate_3; and_164 = allocate_4; and_168 = allocate_5; and_172 = allocate_6;
  //   and_176 = allocate_7; and_180 = allocate_8; and_184 = allocate_9; and_188 = allocate_10; and_192 = allocate_11;
  //   and_196 = allocate_12; and_200 = allocate_13; and_204 = allocate_14; and_208 = allocate_15; and_209 = full;
  //   and_399 = ex_valid; slice_378[2:0] = mux_377[2:0]; slice_380[1:0] = mux_377[1:0]; slice_382 = mux_377[0];
  //   slice_383 = mux_377[1]; slice_381 = mux_377[2]; slice_379 = mux_377[3]; mux_480[3:0] = ex_op;
  //   mux_495[5:0] = ex_rd; mux_510[15:0] = ex_imm; mux_525[15:0] = ex_pc; mux_540[7:0] = ex_sn; mux_555[15:0] = ex_a;
  //   mux_570[15:0] = ex_b; remove_0 = and_405; remove_1 = and_409; remove_2 = and_413; remove_3 = and_417;
  //   remove_4 = and_421; remove_5 = and_425; remove_6 = and_429; remove_7 = and_433; remove_8 = and_437;
  //   remove_9 = and_441; remove_10 = and_445; remove_11 = and_449; remove_12 = and_453; remove_13 = and_457;
  //   remove_14 = and_461; remove_15 = and_465; subtractor_258[7] = slice_259; subtractor_266[7] = slice_267;
  //   subtractor_274[7] = slice_275; subtractor_282[7] = slice_283; subtractor_290[7] = slice_291;
  //   subtractor_298[7] = slice_299; subtractor_306[7] = slice_307; subtractor_314[7] = slice_315;
  //   subtractor_322[7] = slice_323; subtractor_330[7] = slice_331; subtractor_338[7] = slice_339;
  //   subtractor_346[7] = slice_347; subtractor_354[7] = slice_355; subtractor_362[7] = slice_363;
  //   subtractor_370[7] = slice_371

  // Notes on the sheet:
  //   16-entry oldest-ready reservation station
endmodule
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