// Logisim project frontend-tests.circ as structural Verilog: 5 circuits, main circuit FetchUnit
module DecodeOne (
  input  [15:0] instr,
  input  [15:0] pc,
  input  pred,
  output [3:0] opcode,
  output [2:0] rd,
  output [2:0] rs1,
  output [2:0] rs2,
  output [15:0] imm,
  output rw,
  output mem,
  output store,
  output branch,
  output jump,
  output halt,
  output [56:0] packet
);

  wire eq_4, eq_8, eq_12, eq_16, eq_20, eq_24, eq_33, eq_37, eq_42, eq_46, eq_64, eq_68, gt_3, gt_7, gt_11,
       gt_15, gt_19, gt_23, gt_32, gt_36, gt_41, gt_45, gt_50, gt_54, gt_59, gt_63, gt_67, lt_5, lt_9, lt_13,
       lt_17, lt_21, lt_25, lt_34, lt_38, lt_43, lt_47, lt_52, lt_56, lt_61, lt_65, lt_69, or_26, or_27,
       or_28, or_29, or_30, or_70, or_71, or_72, or_73, or_75, or_76, or_77, or_87, or_88, or_89, or_90,
       or_91, or_92;
  wire [2:0] mux_82, mux_85, mux_111, mux_112, mux_113, mux_114, mux_115, mux_116, mux_117, mux_118, mux_119;
  wire [15:0] ext_95, ext_98, mux_96;

  Comparator #(.width(4), .mode("unsigned")) comparator_1 (
    .a(instr[15:12]), .b(4'b0010), .gt(gt_7), .eq(eq_8), .lt(lt_9));
  Comparator #(.width(4), .mode("unsigned")) comparator_2 (
    .a(instr[15:12]), .b(4'b0100), .gt(gt_15), .eq(eq_16), .lt(lt_17));
  Comparator #(.width(4), .mode("unsigned")) comparator_3 (
    .a(instr[15:12]), .b(4'b0110), .gt(gt_23), .eq(eq_24), .lt(lt_25));
  or or_1 (or_29, or_28, eq_20);
  Comparator #(.width(4), .mode("unsigned")) comparator_4 (
    .a(instr[15:12]), .b(4'b1100), .gt(gt_41), .eq(eq_42), .lt(lt_43));
  or or_2 (mem, packet[38], packet[31]);
  Comparator #(.width(4), .mode("unsigned")) comparator_5 (
    .a(instr[15:12]), .b(4'b0111), .gt(gt_63), .eq(eq_64), .lt(lt_65));
  or or_3 (or_71, or_70, packet[38]);
  or or_4 (or_75, branch, packet[31]);
  Multiplexer #(.width(3), .select(1), .enable("false")) multiplexer_1 (
    .in0(mux_82), .in1(instr[11:9]), .out(packet[9:7]), .sel(or_75));
  or or_5 (or_87, eq_64, packet[38]);
  or or_6 (or_91, or_90, eq_46);
  assign ext_95 = {{10{instr[5]}}, instr[5:0]};  // Bit_Extender bit_extender_1
  Multiplexer #(.width(16), .select(1), .enable("false")) multiplexer_2 (
    .in0(mux_96), .in1(ext_98), .out(imm), .sel(eq_42));
  Multiplexer #(.width(3), .select(1), .enable("false")) multiplexer_3 (
    .in0(3'b001), .in1(3'b010), .out(mux_111), .sel(instr[12]));
  Multiplexer #(.width(3), .select(1), .enable("false")) multiplexer_4 (
    .in0(mux_113), .in1(mux_114), .out(mux_115), .sel(instr[13]));
  Multiplexer #(.width(3), .select(1), .enable("false")) multiplexer_5 (
    .in0(mux_117), .in1(mux_118), .out(mux_119), .sel(instr[14]));
  or or_7 (or_26, eq_4, eq_8);
  or or_8 (or_30, or_29, eq_24);
  Comparator #(.width(4), .mode("unsigned")) comparator_6 (
    .a(instr[15:12]), .b(4'b1011), .gt(gt_36), .eq(eq_37), .lt(lt_38));
  Comparator #(.width(4), .mode("unsigned")) comparator_7 (
    .a(instr[15:12]), .b(4'b1001), .gt(gt_50), .eq(packet[31]), .lt(lt_52));
  or or_9 (or_72, or_71, eq_42);
  or or_10 (or_76, or_71, eq_46);
  Multiplexer #(.width(3), .select(1), .enable("false")) multiplexer_6 (
    .in0(3'b000), .in1(instr[11:9]), .out(packet[6:4]), .sel(packet[29]));
  or or_11 (or_88, or_87, packet[31]);
  or or_12 (or_92, or_91, eq_68);
  Multiplexer #(.width(16), .select(1), .enable("false")) multiplexer_7 (
    .in0({16{1'b0}}), .in1(ext_95), .out(mux_96), .sel(or_92));
  Multiplexer #(.width(3), .select(1), .enable("false")) multiplexer_8 (
    .in0(3'b000), .in1(mux_111), .out(mux_112), .sel(instr[13]));
  Multiplexer #(.width(3), .select(1), .enable("false")) multiplexer_9 (
    .in0(mux_112), .in1(mux_115), .out(mux_116), .sel(instr[14]));
  Multiplexer #(.width(3), .select(1), .enable("false")) multiplexer_10 (
    .in0(mux_116), .in1(mux_119), .out(packet[36:34]), .sel(instr[15]));
  Comparator #(.width(4), .mode("unsigned")) comparator_8 (
    .a(instr[15:12]), .b(4'b0001), .gt(gt_3), .eq(eq_4), .lt(lt_5));
  Comparator #(.width(4), .mode("unsigned")) comparator_9 (
    .a(instr[15:12]), .b(4'b0011), .gt(gt_11), .eq(eq_12), .lt(lt_13));
  Comparator #(.width(4), .mode("unsigned")) comparator_10 (
    .a(instr[15:12]), .b(4'b0101), .gt(gt_19), .eq(eq_20), .lt(lt_21));
  or or_13 (or_27, or_26, eq_12);
  or or_14 (branch, eq_33, eq_37);
  Comparator #(.width(4), .mode("unsigned")) comparator_11 (
    .a(instr[15:12]), .b(4'b1101), .gt(gt_45), .eq(eq_46), .lt(lt_47));
  Comparator #(.width(4), .mode("unsigned")) comparator_12 (
    .a(instr[15:12]), .b(4'b1111), .gt(gt_59), .eq(halt), .lt(lt_61));
  Comparator #(.width(4), .mode("unsigned")) comparator_13 (
    .a(instr[15:12]), .b(4'b1110), .gt(gt_67), .eq(eq_68), .lt(lt_69));
  or or_15 (or_73, or_72, eq_46);
  or or_16 (or_77, or_76, eq_68);
  Multiplexer #(.width(3), .select(1), .enable("false")) multiplexer_11 (
    .in0(3'b000), .in1(instr[5:3]), .out(mux_85), .sel(or_30));
  or or_17 (or_89, or_88, eq_33);
  Multiplexer #(.width(3), .select(1), .enable("false")) multiplexer_12 (
    .in0(3'b011), .in1(3'b100), .out(mux_113), .sel(instr[12]));
  Multiplexer #(.width(3), .select(1), .enable("false")) multiplexer_13 (
    .in0(3'b000), .in1(3'b001), .out(mux_117), .sel(instr[13]));
  or or_18 (packet[37], or_88, eq_68);
  or or_19 (or_28, or_27, eq_16);
  Comparator #(.width(4), .mode("unsigned")) comparator_14 (
    .a(instr[15:12]), .b(4'b1010), .gt(gt_32), .eq(eq_33), .lt(lt_34));
  or or_20 (jump, eq_42, eq_46);
  Comparator #(.width(4), .mode("unsigned")) comparator_15 (
    .a(instr[15:12]), .b(4'b1000), .gt(gt_54), .eq(packet[38]), .lt(lt_56));
  or or_21 (or_70, or_30, eq_64);
  or or_22 (packet[29], or_73, eq_68);
  Multiplexer #(.width(3), .select(1), .enable("false")) multiplexer_14 (
    .in0(3'b000), .in1(instr[8:6]), .out(mux_82), .sel(or_77));
  Multiplexer #(.width(3), .select(1), .enable("false")) multiplexer_15 (
    .in0(mux_85), .in1(instr[8:6]), .out(packet[12:10]), .sel(or_75));
  or or_23 (or_90, or_89, eq_37);
  assign ext_98 = {{7{instr[8]}}, instr[8:0]};  // Bit_Extender bit_extender_2
  Multiplexer #(.width(3), .select(1), .enable("false")) multiplexer_16 (
    .in0(3'b101), .in1(3'b000), .out(mux_114), .sel(instr[12]));
  Multiplexer #(.width(3), .select(1), .enable("false")) multiplexer_17 (
    .in0(3'b000), .in1(mux_114), .out(mux_118), .sel(instr[13]));

  assign opcode = instr[15:12];
  assign {packet[56:39], packet[33:32], packet[30], packet[28:13], packet[3:0]} = {pred, pc, halt, jump, branch, packet[38], imm, instr[15:12]};
  assign rd = packet[6:4];
  assign rs1 = packet[9:7];
  assign rs2 = packet[12:10];
  assign rw = packet[29];
  assign store = packet[31];

  // Other names for the same wires on the sheet: slice_94[5:0] = instr[5:0]; slice_97[8:0] = instr[8:0];
  //   slice_84[2:0] = instr[5:3]; slice_81[2:0] = instr[8:6]; slice_79[2:0] = instr[11:9]; or_57 = mem;
  //   pack_122[56:0] = {pred, pc, halt, packet[38:34], jump, branch, packet[31], packet[38], packet[29], imm, packet[12:4], instr[15:12]};
  //   slice_1[3:0] = instr[15:12]; slice_105[2:0] = instr[14:12]; slice_107[1:0] = instr[13:12];
  //   slice_109 = instr[12]; slice_110 = instr[13]; slice_108 = instr[14]; slice_106 = instr[15];
  //   mux_80[2:0] = packet[6:4]; mux_83[2:0] = packet[9:7]; mux_86[2:0] = packet[12:10]; mux_99[15:0] = imm;
  //   or_74 = packet[29]; eq_51 = packet[31]; or_39 = branch; or_48 = jump; mux_120[2:0] = packet[36:34];
  //   or_121 = packet[37]; eq_55 = packet[38]; eq_60 = halt

  // Notes on the sheet:
  //   16-bit ISA decode / 57-bit control packet
endmodule

module BTB64 (
  input  clk,
  input  rst,
  input  [15:0] pc0,
  input  [15:0] pc1,
  input  we,
  input  [15:0] update_pc,
  input  [15:0] target,
  input  taken,
  output pred0,
  output [15:0] target0,
  output pred1,
  output [15:0] target1
);

  wire and_82, and_106, and_111, and_116, and_121, and_126, and_131, and_136, and_141, and_146, and_151,
       and_156, and_161, and_166, and_171, and_176, and_181, and_186, and_191, and_196, and_201, and_206,
       and_211, and_216, and_221, and_226, and_231, and_236, and_241, and_246, and_251, and_256, and_261,
       and_266, and_271, and_276, and_281, and_286, and_291, and_296, and_301, and_306, and_311, and_316,
       and_321, and_326, and_331, and_336, and_341, and_346, and_351, and_356, and_361, and_366, and_371,
       and_376, and_381, and_386, and_391, and_396, and_401, and_406, and_411, and_416, and_421, and_502,
       and_586, eq_80, eq_85, eq_93, eq_104, eq_109, eq_114, eq_119, eq_124, eq_129, eq_134, eq_139, eq_144,
       eq_149, eq_154, eq_159, eq_164, eq_169, eq_174, eq_179, eq_184, eq_189, eq_194, eq_199, eq_204,
       eq_209, eq_214, eq_219, eq_224, eq_229, eq_234, eq_239, eq_244, eq_249, eq_254, eq_259, eq_264,
       eq_269, eq_274, eq_279, eq_284, eq_289, eq_294, eq_299, eq_304, eq_309, eq_314, eq_319, eq_324,
       eq_329, eq_334, eq_339, eq_344, eq_349, eq_354, eq_359, eq_364, eq_369, eq_374, eq_379, eq_384,
       eq_389, eq_394, eq_399, eq_404, eq_409, eq_414, eq_419, eq_500, eq_584, gt_79, gt_84, gt_92, gt_103,
       gt_108, gt_113, gt_118, gt_123, gt_128, gt_133, gt_138, gt_143, gt_148, gt_153, gt_158, gt_163,
       gt_168, gt_173, gt_178, gt_183, gt_188, gt_193, gt_198, gt_203, gt_208, gt_213, gt_218, gt_223,
       gt_228, gt_233, gt_238, gt_243, gt_248, gt_253, gt_258, gt_263, gt_268, gt_273, gt_278, gt_283,
       gt_288, gt_293, gt_298, gt_303, gt_308, gt_313, gt_318, gt_323, gt_328, gt_333, gt_338, gt_343,
       gt_348, gt_353, gt_358, gt_363, gt_368, gt_373, gt_378, gt_383, gt_388, gt_393, gt_398, gt_403,
       gt_408, gt_413, gt_418, gt_499, gt_583, lt_81, lt_86, lt_94, lt_105, lt_110, lt_115, lt_120, lt_125,
       lt_130, lt_135, lt_140, lt_145, lt_150, lt_155, lt_160, lt_165, lt_170, lt_175, lt_180, lt_185,
       lt_190, lt_195, lt_200, lt_205, lt_210, lt_215, lt_220, lt_225, lt_230, lt_235, lt_240, lt_245,
       lt_250, lt_255, lt_260, lt_265, lt_270, lt_275, lt_280, lt_285, lt_290, lt_295, lt_300, lt_305,
       lt_310, lt_315, lt_320, lt_325, lt_330, lt_335, lt_340, lt_345, lt_350, lt_355, lt_360, lt_365,
       lt_370, lt_375, lt_380, lt_385, lt_390, lt_395, lt_400, lt_405, lt_410, lt_415, lt_420, lt_501, lt_585;
  wire [1:0] adder_88, adder_95, mux_90, mux_96, mux_98, mux_99;
  wire [28:0] entry00, entry01, entry02, entry03, entry04, entry05, entry06, entry07, entry08, entry09,
       entry10, entry11, entry12, entry13, entry14, entry15, entry16, entry17, entry18, entry19, entry20,
       entry21, entry22, entry23, entry24, entry25, entry26, entry27, entry28, entry29, entry30, entry31,
       entry32, entry33, entry34, entry35, entry36, entry37, entry38, entry39, entry40, entry41, entry42,
       entry43, entry44, entry45, entry46, entry47, entry48, entry49, entry50, entry51, entry52, entry53,
       entry54, entry55, entry56, entry57, entry58, entry59, entry60, entry61, entry62, entry63, mux_13,
       mux_14, mux_15, mux_16, mux_17, mux_18, mux_19, mux_20, mux_21, mux_22, mux_23, mux_24, mux_25,
       mux_26, mux_27, mux_28, mux_29, mux_30, mux_31, mux_32, mux_33, mux_34, mux_35, mux_36, mux_37,
       mux_38, mux_39, mux_40, mux_41, mux_42, mux_43, mux_44, mux_45, mux_46, mux_47, mux_48, mux_49,
       mux_50, mux_51, mux_52, mux_53, mux_54, mux_55, mux_56, mux_57, mux_58, mux_59, mux_60, mux_61,
       mux_62, mux_63, mux_64, mux_65, mux_66, mux_67, mux_68, mux_69, mux_70, mux_71, mux_72, mux_73,
       mux_74, mux_75, mux_433, mux_434, mux_435, mux_436, mux_437, mux_438, mux_439, mux_440, mux_441,
       mux_442, mux_443, mux_444, mux_445, mux_446, mux_447, mux_448, mux_449, mux_450, mux_451, mux_452,
       mux_453, mux_454, mux_455, mux_456, mux_457, mux_458, mux_459, mux_460, mux_461, mux_462, mux_463,
       mux_464, mux_465, mux_466, mux_467, mux_468, mux_469, mux_470, mux_471, mux_472, mux_473, mux_474,
       mux_475, mux_476, mux_477, mux_478, mux_479, mux_480, mux_481, mux_482, mux_483, mux_484, mux_485,
       mux_486, mux_487, mux_488, mux_489, mux_490, mux_491, mux_492, mux_493, mux_494, mux_495, mux_517,
       mux_518, mux_519, mux_520, mux_521, mux_522, mux_523, mux_524, mux_525, mux_526, mux_527, mux_528,
       mux_529, mux_530, mux_531, mux_532, mux_533, mux_534, mux_535, mux_536, mux_537, mux_538, mux_539,
       mux_540, mux_541, mux_542, mux_543, mux_544, mux_545, mux_546, mux_547, mux_548, mux_549, mux_550,
       mux_551, mux_552, mux_553, mux_554, mux_555, mux_556, mux_557, mux_558, mux_559, mux_560, mux_561,
       mux_562, mux_563, mux_564, mux_565, mux_566, mux_567, mux_568, mux_569, mux_570, mux_571, mux_572,
       mux_573, mux_574, mux_575, mux_576, mux_577, mux_578, mux_579;

  Multiplexer #(.width(29), .select(1), .enable("false")) multiplexer_1 (
    .in0(entry00), .in1(entry01), .out(mux_13), .sel(update_pc[0]));
  Multiplexer #(.width(29), .select(1), .enable("false")) multiplexer_2 (
    .in0(entry06), .in1(entry07), .out(mux_17), .sel(update_pc[0]));
  Multiplexer #(.width(29), .select(1), .enable("false")) multiplexer_3 (
    .in0(entry10), .in1(entry11), .out(mux_21), .sel(update_pc[0]));
  Multiplexer #(.width(29), .select(1), .enable("false")) multiplexer_4 (
    .in0(mux_23), .in1(mux_24), .out(mux_25), .sel(update_pc[1]));
  Multiplexer #(.width(29), .select(1), .enable("false")) multiplexer_5 (
    .in0(entry18), .in1(entry19), .out(mux_29), .sel(update_pc[0]));
  Multiplexer #(.width(29), .select(1), .enable("false")) multiplexer_6 (
    .in0(mux_31), .in1(mux_32), .out(mux_33), .sel(update_pc[1]));
  Multiplexer #(.width(29), .select(1), .enable("false")) multiplexer_7 (
    .in0(mux_35), .in1(mux_36), .out(mux_37), .sel(update_pc[1]));
  Multiplexer #(.width(29), .select(1), .enable("false")) multiplexer_8 (
    .in0(mux_37), .in1(mux_40), .out(mux_41), .sel(update_pc[2]));
  Multiplexer #(.width(29), .select(1), .enable("false")) multiplexer_9 (
    .in0(entry34), .in1(entry35), .out(mux_45), .sel(update_pc[0]));
  Multiplexer #(.width(29), .select(1), .enable("false")) multiplexer_10 (
    .in0(mux_47), .in1(mux_48), .out(mux_49), .sel(update_pc[1]));
  Multiplexer #(.width(29), .select(1), .enable("false")) multiplexer_11 (
    .in0(mux_51), .in1(mux_52), .out(mux_53), .sel(update_pc[1]));
  Multiplexer #(.width(29), .select(1), .enable("false")) multiplexer_12 (
    .in0(mux_53), .in1(mux_56), .out(mux_57), .sel(update_pc[2]));
  Multiplexer #(.width(29), .select(1), .enable("false")) multiplexer_13 (
    .in0(mux_59), .in1(mux_60), .out(mux_61), .sel(update_pc[1]));
  Multiplexer #(.width(29), .select(1), .enable("false")) multiplexer_14 (
    .in0(mux_61), .in1(mux_64), .out(mux_65), .sel(update_pc[2]));
  Multiplexer #(.width(29), .select(1), .enable("false")) multiplexer_15 (
    .in0(entry60), .in1(entry61), .out(mux_69), .sel(update_pc[0]));
  Multiplexer #(.width(29), .select(1), .enable("false")) multiplexer_16 (
    .in0(mux_65), .in1(mux_72), .out(mux_73), .sel(update_pc[3]));
  Adder #(.width(2)) adder_1 (.a(mux_75[27:26]), .b(2'b11), .out(adder_95), .cin(1'b0));  // open: cout
  Multiplexer #(.width(2), .select(1), .enable("false")) multiplexer_17 (
    .in0(2'b10), .in1(mux_98), .out(mux_99), .sel(and_82));
  Comparator #(.width(6), .mode("unsigned")) comparator_1 (
    .a(update_pc[5:0]), .b({6{1'b0}}), .gt(gt_103), .eq(eq_104), .lt(lt_105));
  Comparator #(.width(6), .mode("unsigned")) comparator_2 (
    .a(update_pc[5:0]), .b(6'b000001), .gt(gt_108), .eq(eq_109), .lt(lt_110));
  Comparator #(.width(6), .mode("unsigned")) comparator_3 (
    .a(update_pc[5:0]), .b(6'b000010), .gt(gt_113), .eq(eq_114), .lt(lt_115));
  Comparator #(.width(6), .mode("unsigned")) comparator_4 (
    .a(update_pc[5:0]), .b(6'b000011), .gt(gt_118), .eq(eq_119), .lt(lt_120));
  Comparator #(.width(6), .mode("unsigned")) comparator_5 (
    .a(update_pc[5:0]), .b(6'b000100), .gt(gt_123), .eq(eq_124), .lt(lt_125));
  Comparator #(.width(6), .mode("unsigned")) comparator_6 (
    .a(update_pc[5:0]), .b(6'b000101), .gt(gt_128), .eq(eq_129), .lt(lt_130));
  Comparator #(.width(6), .mode("unsigned")) comparator_7 (
    .a(update_pc[5:0]), .b(6'b000110), .gt(gt_133), .eq(eq_134), .lt(lt_135));
  Comparator #(.width(6), .mode("unsigned")) comparator_8 (
    .a(update_pc[5:0]), .b(6'b000111), .gt(gt_138), .eq(eq_139), .lt(lt_140));
  Comparator #(.width(6), .mode("unsigned")) comparator_9 (
    .a(update_pc[5:0]), .b(6'b001000), .gt(gt_143), .eq(eq_144), .lt(lt_145));
  Comparator #(.width(6), .mode("unsigned")) comparator_10 (
    .a(update_pc[5:0]), .b(6'b001001), .gt(gt_148), .eq(eq_149), .lt(lt_150));
  Comparator #(.width(6), .mode("unsigned")) comparator_11 (
    .a(update_pc[5:0]), .b(6'b001010), .gt(gt_153), .eq(eq_154), .lt(lt_155));
  Comparator #(.width(6), .mode("unsigned")) comparator_12 (
    .a(update_pc[5:0]), .b(6'b001011), .gt(gt_158), .eq(eq_159), .lt(lt_160));
  Comparator #(.width(6), .mode("unsigned")) comparator_13 (
    .a(update_pc[5:0]), .b(6'b001100), .gt(gt_163), .eq(eq_164), .lt(lt_165));
  Comparator #(.width(6), .mode("unsigned")) comparator_14 (
    .a(update_pc[5:0]), .b(6'b001101), .gt(gt_168), .eq(eq_169), .lt(lt_170));
  Comparator #(.width(6), .mode("unsigned")) comparator_15 (
    .a(update_pc[5:0]), .b(6'b001110), .gt(gt_173), .eq(eq_174), .lt(lt_175));
  Comparator #(.width(6), .mode("unsigned")) comparator_16 (
    .a(update_pc[5:0]), .b(6'b001111), .gt(gt_178), .eq(eq_179), .lt(lt_180));
  Comparator #(.width(6), .mode("unsigned")) comparator_17 (
    .a(update_pc[5:0]), .b(6'b010000), .gt(gt_183), .eq(eq_184), .lt(lt_185));
  Comparator #(.width(6), .mode("unsigned")) comparator_18 (
    .a(update_pc[5:0]), .b(6'b010001), .gt(gt_188), .eq(eq_189), .lt(lt_190));
  Comparator #(.width(6), .mode("unsigned")) comparator_19 (
    .a(update_pc[5:0]), .b(6'b010010), .gt(gt_193), .eq(eq_194), .lt(lt_195));
  Comparator #(.width(6), .mode("unsigned")) comparator_20 (
    .a(update_pc[5:0]), .b(6'b010011), .gt(gt_198), .eq(eq_199), .lt(lt_200));
  Comparator #(.width(6), .mode("unsigned")) comparator_21 (
    .a(update_pc[5:0]), .b(6'b010100), .gt(gt_203), .eq(eq_204), .lt(lt_205));
  Comparator #(.width(6), .mode("unsigned")) comparator_22 (
    .a(update_pc[5:0]), .b(6'b010101), .gt(gt_208), .eq(eq_209), .lt(lt_210));
  Comparator #(.width(6), .mode("unsigned")) comparator_23 (
    .a(update_pc[5:0]), .b(6'b010110), .gt(gt_213), .eq(eq_214), .lt(lt_215));
  Comparator #(.width(6), .mode("unsigned")) comparator_24 (
    .a(update_pc[5:0]), .b(6'b010111), .gt(gt_218), .eq(eq_219), .lt(lt_220));
  Comparator #(.width(6), .mode("unsigned")) comparator_25 (
    .a(update_pc[5:0]), .b(6'b011000), .gt(gt_223), .eq(eq_224), .lt(lt_225));
  Comparator #(.width(6), .mode("unsigned")) comparator_26 (
    .a(update_pc[5:0]), .b(6'b011001), .gt(gt_228), .eq(eq_229), .lt(lt_230));
  Comparator #(.width(6), .mode("unsigned")) comparator_27 (
    .a(update_pc[5:0]), .b(6'b011010), .gt(gt_233), .eq(eq_234), .lt(lt_235));
  Comparator #(.width(6), .mode("unsigned")) comparator_28 (
    .a(update_pc[5:0]), .b(6'b011011), .gt(gt_238), .eq(eq_239), .lt(lt_240));
  Comparator #(.width(6), .mode("unsigned")) comparator_29 (
    .a(update_pc[5:0]), .b(6'b011100), .gt(gt_243), .eq(eq_244), .lt(lt_245));
  Comparator #(.width(6), .mode("unsigned")) comparator_30 (
    .a(update_pc[5:0]), .b(6'b011101), .gt(gt_248), .eq(eq_249), .lt(lt_250));
  Comparator #(.width(6), .mode("unsigned")) comparator_31 (
    .a(update_pc[5:0]), .b(6'b011110), .gt(gt_253), .eq(eq_254), .lt(lt_255));
  Comparator #(.width(6), .mode("unsigned")) comparator_32 (
    .a(update_pc[5:0]), .b(6'b011111), .gt(gt_258), .eq(eq_259), .lt(lt_260));
  Comparator #(.width(6), .mode("unsigned")) comparator_33 (
    .a(update_pc[5:0]), .b(6'b100000), .gt(gt_263), .eq(eq_264), .lt(lt_265));
  Comparator #(.width(6), .mode("unsigned")) comparator_34 (
    .a(update_pc[5:0]), .b(6'b100001), .gt(gt_268), .eq(eq_269), .lt(lt_270));
  Comparator #(.width(6), .mode("unsigned")) comparator_35 (
    .a(update_pc[5:0]), .b(6'b100010), .gt(gt_273), .eq(eq_274), .lt(lt_275));
  Comparator #(.width(6), .mode("unsigned")) comparator_36 (
    .a(update_pc[5:0]), .b(6'b100011), .gt(gt_278), .eq(eq_279), .lt(lt_280));
  Comparator #(.width(6), .mode("unsigned")) comparator_37 (
    .a(update_pc[5:0]), .b(6'b100100), .gt(gt_283), .eq(eq_284), .lt(lt_285));
  Comparator #(.width(6), .mode("unsigned")) comparator_38 (
    .a(update_pc[5:0]), .b(6'b100101), .gt(gt_288), .eq(eq_289), .lt(lt_290));
  Comparator #(.width(6), .mode("unsigned")) comparator_39 (
    .a(update_pc[5:0]), .b(6'b100110), .gt(gt_293), .eq(eq_294), .lt(lt_295));
  Comparator #(.width(6), .mode("unsigned")) comparator_40 (
    .a(update_pc[5:0]), .b(6'b100111), .gt(gt_298), .eq(eq_299), .lt(lt_300));
  Comparator #(.width(6), .mode("unsigned")) comparator_41 (
    .a(update_pc[5:0]), .b(6'b101000), .gt(gt_303), .eq(eq_304), .lt(lt_305));
  Comparator #(.width(6), .mode("unsigned")) comparator_42 (
    .a(update_pc[5:0]), .b(6'b101001), .gt(gt_308), .eq(eq_309), .lt(lt_310));
  Comparator #(.width(6), .mode("unsigned")) comparator_43 (
    .a(update_pc[5:0]), .b(6'b101010), .gt(gt_313), .eq(eq_314), .lt(lt_315));
  Comparator #(.width(6), .mode("unsigned")) comparator_44 (
    .a(update_pc[5:0]), .b(6'b101011), .gt(gt_318), .eq(eq_319), .lt(lt_320));
  Comparator #(.width(6), .mode("unsigned")) comparator_45 (
    .a(update_pc[5:0]), .b(6'b101100), .gt(gt_323), .eq(eq_324), .lt(lt_325));
  Comparator #(.width(6), .mode("unsigned")) comparator_46 (
    .a(update_pc[5:0]), .b(6'b101101), .gt(gt_328), .eq(eq_329), .lt(lt_330));
  Comparator #(.width(6), .mode("unsigned")) comparator_47 (
    .a(update_pc[5:0]), .b(6'b101110), .gt(gt_333), .eq(eq_334), .lt(lt_335));
  Comparator #(.width(6), .mode("unsigned")) comparator_48 (
    .a(update_pc[5:0]), .b(6'b101111), .gt(gt_338), .eq(eq_339), .lt(lt_340));
  Comparator #(.width(6), .mode("unsigned")) comparator_49 (
    .a(update_pc[5:0]), .b(6'b110000), .gt(gt_343), .eq(eq_344), .lt(lt_345));
  Comparator #(.width(6), .mode("unsigned")) comparator_50 (
    .a(update_pc[5:0]), .b(6'b110001), .gt(gt_348), .eq(eq_349), .lt(lt_350));
  Comparator #(.width(6), .mode("unsigned")) comparator_51 (
    .a(update_pc[5:0]), .b(6'b110010), .gt(gt_353), .eq(eq_354), .lt(lt_355));
  Comparator #(.width(6), .mode("unsigned")) comparator_52 (
    .a(update_pc[5:0]), .b(6'b110011), .gt(gt_358), .eq(eq_359), .lt(lt_360));
  Comparator #(.width(6), .mode("unsigned")) comparator_53 (
    .a(update_pc[5:0]), .b(6'b110100), .gt(gt_363), .eq(eq_364), .lt(lt_365));
  Comparator #(.width(6), .mode("unsigned")) comparator_54 (
    .a(update_pc[5:0]), .b(6'b110101), .gt(gt_368), .eq(eq_369), .lt(lt_370));
  Comparator #(.width(6), .mode("unsigned")) comparator_55 (
    .a(update_pc[5:0]), .b(6'b110110), .gt(gt_373), .eq(eq_374), .lt(lt_375));
  Comparator #(.width(6), .mode("unsigned")) comparator_56 (
    .a(update_pc[5:0]), .b(6'b110111), .gt(gt_378), .eq(eq_379), .lt(lt_380));
  Comparator #(.width(6), .mode("unsigned")) comparator_57 (
    .a(update_pc[5:0]), .b(6'b111000), .gt(gt_383), .eq(eq_384), .lt(lt_385));
  Comparator #(.width(6), .mode("unsigned")) comparator_58 (
    .a(update_pc[5:0]), .b(6'b111001), .gt(gt_388), .eq(eq_389), .lt(lt_390));
  Comparator #(.width(6), .mode("unsigned")) comparator_59 (
    .a(update_pc[5:0]), .b(6'b111010), .gt(gt_393), .eq(eq_394), .lt(lt_395));
  Comparator #(.width(6), .mode("unsigned")) comparator_60 (
    .a(update_pc[5:0]), .b(6'b111011), .gt(gt_398), .eq(eq_399), .lt(lt_400));
  Comparator #(.width(6), .mode("unsigned")) comparator_61 (
    .a(update_pc[5:0]), .b(6'b111100), .gt(gt_403), .eq(eq_404), .lt(lt_405));
  Comparator #(.width(6), .mode("unsigned")) comparator_62 (
    .a(update_pc[5:0]), .b(6'b111101), .gt(gt_408), .eq(eq_409), .lt(lt_410));
  Comparator #(.width(6), .mode("unsigned")) comparator_63 (
    .a(update_pc[5:0]), .b(6'b111110), .gt(gt_413), .eq(eq_414), .lt(lt_415));
  Comparator #(.width(6), .mode("unsigned")) comparator_64 (
    .a(update_pc[5:0]), .b({6{1'b1}}), .gt(gt_418), .eq(eq_419), .lt(lt_420));
  Multiplexer #(.width(29), .select(1), .enable("false")) multiplexer_18 (
    .in0(mux_433), .in1(mux_434), .out(mux_435), .sel(pc0[1]));
  Multiplexer #(.width(29), .select(1), .enable("false")) multiplexer_19 (
    .in0(mux_435), .in1(mux_438), .out(mux_439), .sel(pc0[2]));
  Multiplexer #(.width(29), .select(1), .enable("false")) multiplexer_20 (
    .in0(entry12), .in1(entry13), .out(mux_443), .sel(pc0[0]));
  Multiplexer #(.width(29), .select(1), .enable("false")) multiplexer_21 (
    .in0(mux_439), .in1(mux_446), .out(mux_447), .sel(pc0[3]));
  Multiplexer #(.width(29), .select(1), .enable("false")) multiplexer_22 (
    .in0(entry20), .in1(entry21), .out(mux_451), .sel(pc0[0]));
  Multiplexer #(.width(29), .select(1), .enable("false")) multiplexer_23 (
    .in0(entry24), .in1(entry25), .out(mux_455), .sel(pc0[0]));
  Multiplexer #(.width(29), .select(1), .enable("false")) multiplexer_24 (
    .in0(entry30), .in1(entry31), .out(mux_459), .sel(pc0[0]));
  Multiplexer #(.width(29), .select(1), .enable("false")) multiplexer_25 (
    .in0(mux_447), .in1(mux_462), .out(mux_463), .sel(pc0[4]));
  Multiplexer #(.width(29), .select(1), .enable("false")) multiplexer_26 (
    .in0(entry36), .in1(entry37), .out(mux_467), .sel(pc0[0]));
  Multiplexer #(.width(29), .select(1), .enable("false")) multiplexer_27 (
    .in0(entry40), .in1(entry41), .out(mux_471), .sel(pc0[0]));
  Multiplexer #(.width(29), .select(1), .enable("false")) multiplexer_28 (
    .in0(entry46), .in1(entry47), .out(mux_475), .sel(pc0[0]));
  Multiplexer #(.width(29), .select(1), .enable("false")) multiplexer_29 (
    .in0(entry48), .in1(entry49), .out(mux_479), .sel(pc0[0]));
  Multiplexer #(.width(29), .select(1), .enable("false")) multiplexer_30 (
    .in0(entry54), .in1(entry55), .out(mux_483), .sel(pc0[0]));
  Multiplexer #(.width(29), .select(1), .enable("false")) multiplexer_31 (
    .in0(entry58), .in1(entry59), .out(mux_487), .sel(pc0[0]));
  Multiplexer #(.width(29), .select(1), .enable("false")) multiplexer_32 (
    .in0(mux_489), .in1(mux_490), .out(mux_491), .sel(pc0[1]));
  Multiplexer #(.width(29), .select(1), .enable("false")) multiplexer_33 (
    .in0(mux_463), .in1(mux_494), .out({mux_495[28:26], target0, mux_495[9:0]}), .sel(pc0[5]));
  Comparator #(.width(10), .mode("unsigned")) comparator_65 (
    .a(mux_495[9:0]), .b(pc0[15:6]), .gt(gt_499), .eq(eq_500), .lt(lt_501));
  Multiplexer #(.width(29), .select(1), .enable("false")) multiplexer_34 (
    .in0(entry00), .in1(entry01), .out(mux_517), .sel(pc1[0]));
  Multiplexer #(.width(29), .select(1), .enable("false")) multiplexer_35 (
    .in0(entry06), .in1(entry07), .out(mux_521), .sel(pc1[0]));
  Multiplexer #(.width(29), .select(1), .enable("false")) multiplexer_36 (
    .in0(entry10), .in1(entry11), .out(mux_525), .sel(pc1[0]));
  Multiplexer #(.width(29), .select(1), .enable("false")) multiplexer_37 (
    .in0(mux_527), .in1(mux_528), .out(mux_529), .sel(pc1[1]));
  Multiplexer #(.width(29), .select(1), .enable("false")) multiplexer_38 (
    .in0(entry18), .in1(entry19), .out(mux_533), .sel(pc1[0]));
  Multiplexer #(.width(29), .select(1), .enable("false")) multiplexer_39 (
    .in0(mux_535), .in1(mux_536), .out(mux_537), .sel(pc1[1]));
  Multiplexer #(.width(29), .select(1), .enable("false")) multiplexer_40 (
    .in0(mux_539), .in1(mux_540), .out(mux_541), .sel(pc1[1]));
  Multiplexer #(.width(29), .select(1), .enable("false")) multiplexer_41 (
    .in0(mux_541), .in1(mux_544), .out(mux_545), .sel(pc1[2]));
  Multiplexer #(.width(29), .select(1), .enable("false")) multiplexer_42 (
    .in0(entry34), .in1(entry35), .out(mux_549), .sel(pc1[0]));
  Multiplexer #(.width(29), .select(1), .enable("false")) multiplexer_43 (
    .in0(mux_551), .in1(mux_552), .out(mux_553), .sel(pc1[1]));
  Multiplexer #(.width(29), .select(1), .enable("false")) multiplexer_44 (
    .in0(mux_555), .in1(mux_556), .out(mux_557), .sel(pc1[1]));
  Multiplexer #(.width(29), .select(1), .enable("false")) multiplexer_45 (
    .in0(mux_557), .in1(mux_560), .out(mux_561), .sel(pc1[2]));
  Multiplexer #(.width(29), .select(1), .enable("false")) multiplexer_46 (
    .in0(mux_563), .in1(mux_564), .out(mux_565), .sel(pc1[1]));
  Multiplexer #(.width(29), .select(1), .enable("false")) multiplexer_47 (
    .in0(mux_565), .in1(mux_568), .out(mux_569), .sel(pc1[2]));
  Multiplexer #(.width(29), .select(1), .enable("false")) multiplexer_48 (
    .in0(entry60), .in1(entry61), .out(mux_573), .sel(pc1[0]));
  Multiplexer #(.width(29), .select(1), .enable("false")) multiplexer_49 (
    .in0(mux_569), .in1(mux_576), .out(mux_577), .sel(pc1[3]));
  Multiplexer #(.width(29), .select(1), .enable("false")) multiplexer_50 (
    .in0(entry02), .in1(entry03), .out(mux_14), .sel(update_pc[0]));
  Multiplexer #(.width(29), .select(1), .enable("false")) multiplexer_51 (
    .in0(mux_16), .in1(mux_17), .out(mux_18), .sel(update_pc[1]));
  Multiplexer #(.width(29), .select(1), .enable("false")) multiplexer_52 (
    .in0(mux_20), .in1(mux_21), .out(mux_22), .sel(update_pc[1]));
  Multiplexer #(.width(29), .select(1), .enable("false")) multiplexer_53 (
    .in0(mux_22), .in1(mux_25), .out(mux_26), .sel(update_pc[2]));
  Multiplexer #(.width(29), .select(1), .enable("false")) multiplexer_54 (
    .in0(mux_28), .in1(mux_29), .out(mux_30), .sel(update_pc[1]));
  Multiplexer #(.width(29), .select(1), .enable("false")) multiplexer_55 (
    .in0(mux_30), .in1(mux_33), .out(mux_34), .sel(update_pc[2]));
  Multiplexer #(.width(29), .select(1), .enable("false")) multiplexer_56 (
    .in0(entry28), .in1(entry29), .out(mux_38), .sel(update_pc[0]));
  Multiplexer #(.width(29), .select(1), .enable("false")) multiplexer_57 (
    .in0(mux_34), .in1(mux_41), .out(mux_42), .sel(update_pc[3]));
  Multiplexer #(.width(29), .select(1), .enable("false")) multiplexer_58 (
    .in0(mux_44), .in1(mux_45), .out(mux_46), .sel(update_pc[1]));
  Multiplexer #(.width(29), .select(1), .enable("false")) multiplexer_59 (
    .in0(mux_46), .in1(mux_49), .out(mux_50), .sel(update_pc[2]));
  Multiplexer #(.width(29), .select(1), .enable("false")) multiplexer_60 (
    .in0(entry44), .in1(entry45), .out(mux_54), .sel(update_pc[0]));
  Multiplexer #(.width(29), .select(1), .enable("false")) multiplexer_61 (
    .in0(mux_50), .in1(mux_57), .out(mux_58), .sel(update_pc[3]));
  Multiplexer #(.width(29), .select(1), .enable("false")) multiplexer_62 (
    .in0(entry52), .in1(entry53), .out(mux_62), .sel(update_pc[0]));
  Multiplexer #(.width(29), .select(1), .enable("false")) multiplexer_63 (
    .in0(entry56), .in1(entry57), .out(mux_66), .sel(update_pc[0]));
  Multiplexer #(.width(29), .select(1), .enable("false")) multiplexer_64 (
    .in0(entry62), .in1(entry63), .out(mux_70), .sel(update_pc[0]));
  Multiplexer #(.width(29), .select(1), .enable("false")) multiplexer_65 (
    .in0(mux_58), .in1(mux_73), .out(mux_74), .sel(update_pc[4]));
  Comparator #(.width(2), .mode("unsigned")) comparator_66 (
    .a(mux_75[27:26]), .b(2'b11), .gt(gt_84), .eq(eq_85), .lt(lt_86));
  Multiplexer #(.width(2), .select(1), .enable("false")) multiplexer_66 (
    .in0(adder_88), .in1(mux_75[27:26]), .out(mux_90), .sel(eq_85));
  Multiplexer #(.width(2), .select(1), .enable("false")) multiplexer_67 (
    .in0(adder_95), .in1(mux_75[27:26]), .out(mux_96), .sel(eq_93));
  and and_1 (and_106, we, eq_104);
  and and_2 (and_111, we, eq_109);
  and and_3 (and_116, we, eq_114);
  and and_4 (and_121, we, eq_119);
  and and_5 (and_126, we, eq_124);
  and and_6 (and_131, we, eq_129);
  and and_7 (and_136, we, eq_134);
  and and_8 (and_141, we, eq_139);
  and and_9 (and_146, we, eq_144);
  and and_10 (and_151, we, eq_149);
  and and_11 (and_156, we, eq_154);
  and and_12 (and_161, we, eq_159);
  and and_13 (and_166, we, eq_164);
  and and_14 (and_171, we, eq_169);
  and and_15 (and_176, we, eq_174);
  and and_16 (and_181, we, eq_179);
  and and_17 (and_186, we, eq_184);
  and and_18 (and_191, we, eq_189);
  and and_19 (and_196, we, eq_194);
  and and_20 (and_201, we, eq_199);
  and and_21 (and_206, we, eq_204);
  and and_22 (and_211, we, eq_209);
  and and_23 (and_216, we, eq_214);
  and and_24 (and_221, we, eq_219);
  and and_25 (and_226, we, eq_224);
  and and_26 (and_231, we, eq_229);
  and and_27 (and_236, we, eq_234);
  and and_28 (and_241, we, eq_239);
  and and_29 (and_246, we, eq_244);
  and and_30 (and_251, we, eq_249);
  and and_31 (and_256, we, eq_254);
  and and_32 (and_261, we, eq_259);
  and and_33 (and_266, we, eq_264);
  and and_34 (and_271, we, eq_269);
  and and_35 (and_276, we, eq_274);
  and and_36 (and_281, we, eq_279);
  and and_37 (and_286, we, eq_284);
  and and_38 (and_291, we, eq_289);
  and and_39 (and_296, we, eq_294);
  and and_40 (and_301, we, eq_299);
  and and_41 (and_306, we, eq_304);
  and and_42 (and_311, we, eq_309);
  and and_43 (and_316, we, eq_314);
  and and_44 (and_321, we, eq_319);
  and and_45 (and_326, we, eq_324);
  and and_46 (and_331, we, eq_329);
  and and_47 (and_336, we, eq_334);
  and and_48 (and_341, we, eq_339);
  and and_49 (and_346, we, eq_344);
  and and_50 (and_351, we, eq_349);
  and and_51 (and_356, we, eq_354);
  and and_52 (and_361, we, eq_359);
  and and_53 (and_366, we, eq_364);
  and and_54 (and_371, we, eq_369);
  and and_55 (and_376, we, eq_374);
  and and_56 (and_381, we, eq_379);
  and and_57 (and_386, we, eq_384);
  and and_58 (and_391, we, eq_389);
  and and_59 (and_396, we, eq_394);
  and and_60 (and_401, we, eq_399);
  and and_61 (and_406, we, eq_404);
  and and_62 (and_411, we, eq_409);
  and and_63 (and_416, we, eq_414);
  and and_64 (and_421, we, eq_419);
  Multiplexer #(.width(29), .select(1), .enable("false")) multiplexer_68 (
    .in0(entry04), .in1(entry05), .out(mux_436), .sel(pc0[0]));
  Multiplexer #(.width(29), .select(1), .enable("false")) multiplexer_69 (
    .in0(entry08), .in1(entry09), .out(mux_440), .sel(pc0[0]));
  Multiplexer #(.width(29), .select(1), .enable("false")) multiplexer_70 (
    .in0(entry14), .in1(entry15), .out(mux_444), .sel(pc0[0]));
  Multiplexer #(.width(29), .select(1), .enable("false")) multiplexer_71 (
    .in0(entry16), .in1(entry17), .out(mux_448), .sel(pc0[0]));
  Multiplexer #(.width(29), .select(1), .enable("false")) multiplexer_72 (
    .in0(entry22), .in1(entry23), .out(mux_452), .sel(pc0[0]));
  Multiplexer #(.width(29), .select(1), .enable("false")) multiplexer_73 (
    .in0(entry26), .in1(entry27), .out(mux_456), .sel(pc0[0]));
  Multiplexer #(.width(29), .select(1), .enable("false")) multiplexer_74 (
    .in0(mux_458), .in1(mux_459), .out(mux_460), .sel(pc0[1]));
  Multiplexer #(.width(29), .select(1), .enable("false")) multiplexer_75 (
    .in0(entry32), .in1(entry33), .out(mux_464), .sel(pc0[0]));
  Multiplexer #(.width(29), .select(1), .enable("false")) multiplexer_76 (
    .in0(entry38), .in1(entry39), .out(mux_468), .sel(pc0[0]));
  Multiplexer #(.width(29), .select(1), .enable("false")) multiplexer_77 (
    .in0(entry42), .in1(entry43), .out(mux_472), .sel(pc0[0]));
  Multiplexer #(.width(29), .select(1), .enable("false")) multiplexer_78 (
    .in0(mux_474), .in1(mux_475), .out(mux_476), .sel(pc0[1]));
  Multiplexer #(.width(29), .select(1), .enable("false")) multiplexer_79 (
    .in0(entry50), .in1(entry51), .out(mux_480), .sel(pc0[0]));
  Multiplexer #(.width(29), .select(1), .enable("false")) multiplexer_80 (
    .in0(mux_482), .in1(mux_483), .out(mux_484), .sel(pc0[1]));
  Multiplexer #(.width(29), .select(1), .enable("false")) multiplexer_81 (
    .in0(mux_486), .in1(mux_487), .out(mux_488), .sel(pc0[1]));
  Multiplexer #(.width(29), .select(1), .enable("false")) multiplexer_82 (
    .in0(mux_488), .in1(mux_491), .out(mux_492), .sel(pc0[2]));
  and and_65 (and_502, mux_495[28], eq_500);
  Multiplexer #(.width(29), .select(1), .enable("false")) multiplexer_83 (
    .in0(entry02), .in1(entry03), .out(mux_518), .sel(pc1[0]));
  Multiplexer #(.width(29), .select(1), .enable("false")) multiplexer_84 (
    .in0(mux_520), .in1(mux_521), .out(mux_522), .sel(pc1[1]));
  Multiplexer #(.width(29), .select(1), .enable("false")) multiplexer_85 (
    .in0(mux_524), .in1(mux_525), .out(mux_526), .sel(pc1[1]));
  Multiplexer #(.width(29), .select(1), .enable("false")) multiplexer_86 (
    .in0(mux_526), .in1(mux_529), .out(mux_530), .sel(pc1[2]));
  Multiplexer #(.width(29), .select(1), .enable("false")) multiplexer_87 (
    .in0(mux_532), .in1(mux_533), .out(mux_534), .sel(pc1[1]));
  Multiplexer #(.width(29), .select(1), .enable("false")) multiplexer_88 (
    .in0(mux_534), .in1(mux_537), .out(mux_538), .sel(pc1[2]));
  Multiplexer #(.width(29), .select(1), .enable("false")) multiplexer_89 (
    .in0(entry28), .in1(entry29), .out(mux_542), .sel(pc1[0]));
  Multiplexer #(.width(29), .select(1), .enable("false")) multiplexer_90 (
    .in0(mux_538), .in1(mux_545), .out(mux_546), .sel(pc1[3]));
  Multiplexer #(.width(29), .select(1), .enable("false")) multiplexer_91 (
    .in0(mux_548), .in1(mux_549), .out(mux_550), .sel(pc1[1]));
  Multiplexer #(.width(29), .select(1), .enable("false")) multiplexer_92 (
    .in0(mux_550), .in1(mux_553), .out(mux_554), .sel(pc1[2]));
  Multiplexer #(.width(29), .select(1), .enable("false")) multiplexer_93 (
    .in0(entry44), .in1(entry45), .out(mux_558), .sel(pc1[0]));
  Multiplexer #(.width(29), .select(1), .enable("false")) multiplexer_94 (
    .in0(mux_554), .in1(mux_561), .out(mux_562), .sel(pc1[3]));
  Multiplexer #(.width(29), .select(1), .enable("false")) multiplexer_95 (
    .in0(entry52), .in1(entry53), .out(mux_566), .sel(pc1[0]));
  Multiplexer #(.width(29), .select(1), .enable("false")) multiplexer_96 (
    .in0(entry56), .in1(entry57), .out(mux_570), .sel(pc1[0]));
  Multiplexer #(.width(29), .select(1), .enable("false")) multiplexer_97 (
    .in0(entry62), .in1(entry63), .out(mux_574), .sel(pc1[0]));
  Multiplexer #(.width(29), .select(1), .enable("false")) multiplexer_98 (
    .in0(mux_562), .in1(mux_577), .out(mux_578), .sel(pc1[4]));
  and and_66 (pred1, and_586, mux_579[27]);
  Multiplexer #(.width(29), .select(1), .enable("false")) multiplexer_99 (
    .in0(mux_13), .in1(mux_14), .out(mux_15), .sel(update_pc[1]));
  Multiplexer #(.width(29), .select(1), .enable("false")) multiplexer_100 (
    .in0(mux_15), .in1(mux_18), .out(mux_19), .sel(update_pc[2]));
  Multiplexer #(.width(29), .select(1), .enable("false")) multiplexer_101 (
    .in0(entry12), .in1(entry13), .out(mux_23), .sel(update_pc[0]));
  Multiplexer #(.width(29), .select(1), .enable("false")) multiplexer_102 (
    .in0(mux_19), .in1(mux_26), .out(mux_27), .sel(update_pc[3]));
  Multiplexer #(.width(29), .select(1), .enable("false")) multiplexer_103 (
    .in0(entry20), .in1(entry21), .out(mux_31), .sel(update_pc[0]));
  Multiplexer #(.width(29), .select(1), .enable("false")) multiplexer_104 (
    .in0(entry24), .in1(entry25), .out(mux_35), .sel(update_pc[0]));
  Multiplexer #(.width(29), .select(1), .enable("false")) multiplexer_105 (
    .in0(entry30), .in1(entry31), .out(mux_39), .sel(update_pc[0]));
  Multiplexer #(.width(29), .select(1), .enable("false")) multiplexer_106 (
    .in0(mux_27), .in1(mux_42), .out(mux_43), .sel(update_pc[4]));
  Multiplexer #(.width(29), .select(1), .enable("false")) multiplexer_107 (
    .in0(entry36), .in1(entry37), .out(mux_47), .sel(update_pc[0]));
  Multiplexer #(.width(29), .select(1), .enable("false")) multiplexer_108 (
    .in0(entry40), .in1(entry41), .out(mux_51), .sel(update_pc[0]));
  Multiplexer #(.width(29), .select(1), .enable("false")) multiplexer_109 (
    .in0(entry46), .in1(entry47), .out(mux_55), .sel(update_pc[0]));
  Multiplexer #(.width(29), .select(1), .enable("false")) multiplexer_110 (
    .in0(entry48), .in1(entry49), .out(mux_59), .sel(update_pc[0]));
  Multiplexer #(.width(29), .select(1), .enable("false")) multiplexer_111 (
    .in0(entry54), .in1(entry55), .out(mux_63), .sel(update_pc[0]));
  Multiplexer #(.width(29), .select(1), .enable("false")) multiplexer_112 (
    .in0(entry58), .in1(entry59), .out(mux_67), .sel(update_pc[0]));
  Multiplexer #(.width(29), .select(1), .enable("false")) multiplexer_113 (
    .in0(mux_69), .in1(mux_70), .out(mux_71), .sel(update_pc[1]));
  Multiplexer #(.width(29), .select(1), .enable("false")) multiplexer_114 (
    .in0(mux_43), .in1(mux_74), .out(mux_75), .sel(update_pc[5]));
  Comparator #(.width(10), .mode("unsigned")) comparator_67 (
    .a(mux_75[9:0]), .b(update_pc[15:6]), .gt(gt_79), .eq(eq_80), .lt(lt_81));
  Register #(.width(29)) reg_entry00 (
    .D({1'b1, mux_99, target, update_pc[15:6]}), .en(and_106), .Q(entry00), .clk(clk), .clr(rst));
  Register #(.width(29)) reg_entry01 (
    .D({1'b1, mux_99, target, update_pc[15:6]}), .en(and_111), .Q(entry01), .clk(clk), .clr(rst));
  Register #(.width(29)) reg_entry02 (
    .D({1'b1, mux_99, target, update_pc[15:6]}), .en(and_116), .Q(entry02), .clk(clk), .clr(rst));
  Register #(.width(29)) reg_entry03 (
    .D({1'b1, mux_99, target, update_pc[15:6]}), .en(and_121), .Q(entry03), .clk(clk), .clr(rst));
  Register #(.width(29)) reg_entry04 (
    .D({1'b1, mux_99, target, update_pc[15:6]}), .en(and_126), .Q(entry04), .clk(clk), .clr(rst));
  Register #(.width(29)) reg_entry05 (
    .D({1'b1, mux_99, target, update_pc[15:6]}), .en(and_131), .Q(entry05), .clk(clk), .clr(rst));
  Register #(.width(29)) reg_entry06 (
    .D({1'b1, mux_99, target, update_pc[15:6]}), .en(and_136), .Q(entry06), .clk(clk), .clr(rst));
  Register #(.width(29)) reg_entry07 (
    .D({1'b1, mux_99, target, update_pc[15:6]}), .en(and_141), .Q(entry07), .clk(clk), .clr(rst));
  Register #(.width(29)) reg_entry08 (
    .D({1'b1, mux_99, target, update_pc[15:6]}), .en(and_146), .Q(entry08), .clk(clk), .clr(rst));
  Register #(.width(29)) reg_entry09 (
    .D({1'b1, mux_99, target, update_pc[15:6]}), .en(and_151), .Q(entry09), .clk(clk), .clr(rst));
  Register #(.width(29)) reg_entry10 (
    .D({1'b1, mux_99, target, update_pc[15:6]}), .en(and_156), .Q(entry10), .clk(clk), .clr(rst));
  Register #(.width(29)) reg_entry11 (
    .D({1'b1, mux_99, target, update_pc[15:6]}), .en(and_161), .Q(entry11), .clk(clk), .clr(rst));
  Register #(.width(29)) reg_entry12 (
    .D({1'b1, mux_99, target, update_pc[15:6]}), .en(and_166), .Q(entry12), .clk(clk), .clr(rst));
  Register #(.width(29)) reg_entry13 (
    .D({1'b1, mux_99, target, update_pc[15:6]}), .en(and_171), .Q(entry13), .clk(clk), .clr(rst));
  Register #(.width(29)) reg_entry14 (
    .D({1'b1, mux_99, target, update_pc[15:6]}), .en(and_176), .Q(entry14), .clk(clk), .clr(rst));
  Register #(.width(29)) reg_entry15 (
    .D({1'b1, mux_99, target, update_pc[15:6]}), .en(and_181), .Q(entry15), .clk(clk), .clr(rst));
  Register #(.width(29)) reg_entry16 (
    .D({1'b1, mux_99, target, update_pc[15:6]}), .en(and_186), .Q(entry16), .clk(clk), .clr(rst));
  Register #(.width(29)) reg_entry17 (
    .D({1'b1, mux_99, target, update_pc[15:6]}), .en(and_191), .Q(entry17), .clk(clk), .clr(rst));
  Register #(.width(29)) reg_entry18 (
    .D({1'b1, mux_99, target, update_pc[15:6]}), .en(and_196), .Q(entry18), .clk(clk), .clr(rst));
  Register #(.width(29)) reg_entry19 (
    .D({1'b1, mux_99, target, update_pc[15:6]}), .en(and_201), .Q(entry19), .clk(clk), .clr(rst));
  Register #(.width(29)) reg_entry20 (
    .D({1'b1, mux_99, target, update_pc[15:6]}), .en(and_206), .Q(entry20), .clk(clk), .clr(rst));
  Register #(.width(29)) reg_entry21 (
    .D({1'b1, mux_99, target, update_pc[15:6]}), .en(and_211), .Q(entry21), .clk(clk), .clr(rst));
  Register #(.width(29)) reg_entry22 (
    .D({1'b1, mux_99, target, update_pc[15:6]}), .en(and_216), .Q(entry22), .clk(clk), .clr(rst));
  Register #(.width(29)) reg_entry23 (
    .D({1'b1, mux_99, target, update_pc[15:6]}), .en(and_221), .Q(entry23), .clk(clk), .clr(rst));
  Register #(.width(29)) reg_entry24 (
    .D({1'b1, mux_99, target, update_pc[15:6]}), .en(and_226), .Q(entry24), .clk(clk), .clr(rst));
  Register #(.width(29)) reg_entry25 (
    .D({1'b1, mux_99, target, update_pc[15:6]}), .en(and_231), .Q(entry25), .clk(clk), .clr(rst));
  Register #(.width(29)) reg_entry26 (
    .D({1'b1, mux_99, target, update_pc[15:6]}), .en(and_236), .Q(entry26), .clk(clk), .clr(rst));
  Register #(.width(29)) reg_entry27 (
    .D({1'b1, mux_99, target, update_pc[15:6]}), .en(and_241), .Q(entry27), .clk(clk), .clr(rst));
  Register #(.width(29)) reg_entry28 (
    .D({1'b1, mux_99, target, update_pc[15:6]}), .en(and_246), .Q(entry28), .clk(clk), .clr(rst));
  Register #(.width(29)) reg_entry29 (
    .D({1'b1, mux_99, target, update_pc[15:6]}), .en(and_251), .Q(entry29), .clk(clk), .clr(rst));
  Register #(.width(29)) reg_entry30 (
    .D({1'b1, mux_99, target, update_pc[15:6]}), .en(and_256), .Q(entry30), .clk(clk), .clr(rst));
  Register #(.width(29)) reg_entry31 (
    .D({1'b1, mux_99, target, update_pc[15:6]}), .en(and_261), .Q(entry31), .clk(clk), .clr(rst));
  Register #(.width(29)) reg_entry32 (
    .D({1'b1, mux_99, target, update_pc[15:6]}), .en(and_266), .Q(entry32), .clk(clk), .clr(rst));
  Register #(.width(29)) reg_entry33 (
    .D({1'b1, mux_99, target, update_pc[15:6]}), .en(and_271), .Q(entry33), .clk(clk), .clr(rst));
  Register #(.width(29)) reg_entry34 (
    .D({1'b1, mux_99, target, update_pc[15:6]}), .en(and_276), .Q(entry34), .clk(clk), .clr(rst));
  Register #(.width(29)) reg_entry35 (
    .D({1'b1, mux_99, target, update_pc[15:6]}), .en(and_281), .Q(entry35), .clk(clk), .clr(rst));
  Register #(.width(29)) reg_entry36 (
    .D({1'b1, mux_99, target, update_pc[15:6]}), .en(and_286), .Q(entry36), .clk(clk), .clr(rst));
  Register #(.width(29)) reg_entry37 (
    .D({1'b1, mux_99, target, update_pc[15:6]}), .en(and_291), .Q(entry37), .clk(clk), .clr(rst));
  Register #(.width(29)) reg_entry38 (
    .D({1'b1, mux_99, target, update_pc[15:6]}), .en(and_296), .Q(entry38), .clk(clk), .clr(rst));
  Register #(.width(29)) reg_entry39 (
    .D({1'b1, mux_99, target, update_pc[15:6]}), .en(and_301), .Q(entry39), .clk(clk), .clr(rst));
  Register #(.width(29)) reg_entry40 (
    .D({1'b1, mux_99, target, update_pc[15:6]}), .en(and_306), .Q(entry40), .clk(clk), .clr(rst));
  Register #(.width(29)) reg_entry41 (
    .D({1'b1, mux_99, target, update_pc[15:6]}), .en(and_311), .Q(entry41), .clk(clk), .clr(rst));
  Register #(.width(29)) reg_entry42 (
    .D({1'b1, mux_99, target, update_pc[15:6]}), .en(and_316), .Q(entry42), .clk(clk), .clr(rst));
  Register #(.width(29)) reg_entry43 (
    .D({1'b1, mux_99, target, update_pc[15:6]}), .en(and_321), .Q(entry43), .clk(clk), .clr(rst));
  Register #(.width(29)) reg_entry44 (
    .D({1'b1, mux_99, target, update_pc[15:6]}), .en(and_326), .Q(entry44), .clk(clk), .clr(rst));
  Register #(.width(29)) reg_entry45 (
    .D({1'b1, mux_99, target, update_pc[15:6]}), .en(and_331), .Q(entry45), .clk(clk), .clr(rst));
  Register #(.width(29)) reg_entry46 (
    .D({1'b1, mux_99, target, update_pc[15:6]}), .en(and_336), .Q(entry46), .clk(clk), .clr(rst));
  Register #(.width(29)) reg_entry47 (
    .D({1'b1, mux_99, target, update_pc[15:6]}), .en(and_341), .Q(entry47), .clk(clk), .clr(rst));
  Register #(.width(29)) reg_entry48 (
    .D({1'b1, mux_99, target, update_pc[15:6]}), .en(and_346), .Q(entry48), .clk(clk), .clr(rst));
  Register #(.width(29)) reg_entry49 (
    .D({1'b1, mux_99, target, update_pc[15:6]}), .en(and_351), .Q(entry49), .clk(clk), .clr(rst));
  Register #(.width(29)) reg_entry50 (
    .D({1'b1, mux_99, target, update_pc[15:6]}), .en(and_356), .Q(entry50), .clk(clk), .clr(rst));
  Register #(.width(29)) reg_entry51 (
    .D({1'b1, mux_99, target, update_pc[15:6]}), .en(and_361), .Q(entry51), .clk(clk), .clr(rst));
  Register #(.width(29)) reg_entry52 (
    .D({1'b1, mux_99, target, update_pc[15:6]}), .en(and_366), .Q(entry52), .clk(clk), .clr(rst));
  Register #(.width(29)) reg_entry53 (
    .D({1'b1, mux_99, target, update_pc[15:6]}), .en(and_371), .Q(entry53), .clk(clk), .clr(rst));
  Register #(.width(29)) reg_entry54 (
    .D({1'b1, mux_99, target, update_pc[15:6]}), .en(and_376), .Q(entry54), .clk(clk), .clr(rst));
  Register #(.width(29)) reg_entry55 (
    .D({1'b1, mux_99, target, update_pc[15:6]}), .en(and_381), .Q(entry55), .clk(clk), .clr(rst));
  Register #(.width(29)) reg_entry56 (
    .D({1'b1, mux_99, target, update_pc[15:6]}), .en(and_386), .Q(entry56), .clk(clk), .clr(rst));
  Register #(.width(29)) reg_entry57 (
    .D({1'b1, mux_99, target, update_pc[15:6]}), .en(and_391), .Q(entry57), .clk(clk), .clr(rst));
  Register #(.width(29)) reg_entry58 (
    .D({1'b1, mux_99, target, update_pc[15:6]}), .en(and_396), .Q(entry58), .clk(clk), .clr(rst));
  Register #(.width(29)) reg_entry59 (
    .D({1'b1, mux_99, target, update_pc[15:6]}), .en(and_401), .Q(entry59), .clk(clk), .clr(rst));
  Register #(.width(29)) reg_entry60 (
    .D({1'b1, mux_99, target, update_pc[15:6]}), .en(and_406), .Q(entry60), .clk(clk), .clr(rst));
  Register #(.width(29)) reg_entry61 (
    .D({1'b1, mux_99, target, update_pc[15:6]}), .en(and_411), .Q(entry61), .clk(clk), .clr(rst));
  Register #(.width(29)) reg_entry62 (
    .D({1'b1, mux_99, target, update_pc[15:6]}), .en(and_416), .Q(entry62), .clk(clk), .clr(rst));
  Register #(.width(29)) reg_entry63 (
    .D({1'b1, mux_99, target, update_pc[15:6]}), .en(and_421), .Q(entry63), .clk(clk), .clr(rst));
  Multiplexer #(.width(29), .select(1), .enable("false")) multiplexer_115 (
    .in0(entry00), .in1(entry01), .out(mux_433), .sel(pc0[0]));
  Multiplexer #(.width(29), .select(1), .enable("false")) multiplexer_116 (
    .in0(entry06), .in1(entry07), .out(mux_437), .sel(pc0[0]));
  Multiplexer #(.width(29), .select(1), .enable("false")) multiplexer_117 (
    .in0(entry10), .in1(entry11), .out(mux_441), .sel(pc0[0]));
  Multiplexer #(.width(29), .select(1), .enable("false")) multiplexer_118 (
    .in0(mux_443), .in1(mux_444), .out(mux_445), .sel(pc0[1]));
  Multiplexer #(.width(29), .select(1), .enable("false")) multiplexer_119 (
    .in0(entry18), .in1(entry19), .out(mux_449), .sel(pc0[0]));
  Multiplexer #(.width(29), .select(1), .enable("false")) multiplexer_120 (
    .in0(mux_451), .in1(mux_452), .out(mux_453), .sel(pc0[1]));
  Multiplexer #(.width(29), .select(1), .enable("false")) multiplexer_121 (
    .in0(mux_455), .in1(mux_456), .out(mux_457), .sel(pc0[1]));
  Multiplexer #(.width(29), .select(1), .enable("false")) multiplexer_122 (
    .in0(mux_457), .in1(mux_460), .out(mux_461), .sel(pc0[2]));
  Multiplexer #(.width(29), .select(1), .enable("false")) multiplexer_123 (
    .in0(entry34), .in1(entry35), .out(mux_465), .sel(pc0[0]));
  Multiplexer #(.width(29), .select(1), .enable("false")) multiplexer_124 (
    .in0(mux_467), .in1(mux_468), .out(mux_469), .sel(pc0[1]));
  Multiplexer #(.width(29), .select(1), .enable("false")) multiplexer_125 (
    .in0(mux_471), .in1(mux_472), .out(mux_473), .sel(pc0[1]));
  Multiplexer #(.width(29), .select(1), .enable("false")) multiplexer_126 (
    .in0(mux_473), .in1(mux_476), .out(mux_477), .sel(pc0[2]));
  Multiplexer #(.width(29), .select(1), .enable("false")) multiplexer_127 (
    .in0(mux_479), .in1(mux_480), .out(mux_481), .sel(pc0[1]));
  Multiplexer #(.width(29), .select(1), .enable("false")) multiplexer_128 (
    .in0(mux_481), .in1(mux_484), .out(mux_485), .sel(pc0[2]));
  Multiplexer #(.width(29), .select(1), .enable("false")) multiplexer_129 (
    .in0(entry60), .in1(entry61), .out(mux_489), .sel(pc0[0]));
  Multiplexer #(.width(29), .select(1), .enable("false")) multiplexer_130 (
    .in0(mux_485), .in1(mux_492), .out(mux_493), .sel(pc0[3]));
  Multiplexer #(.width(29), .select(1), .enable("false")) multiplexer_131 (
    .in0(mux_517), .in1(mux_518), .out(mux_519), .sel(pc1[1]));
  Multiplexer #(.width(29), .select(1), .enable("false")) multiplexer_132 (
    .in0(mux_519), .in1(mux_522), .out(mux_523), .sel(pc1[2]));
  Multiplexer #(.width(29), .select(1), .enable("false")) multiplexer_133 (
    .in0(entry12), .in1(entry13), .out(mux_527), .sel(pc1[0]));
  Multiplexer #(.width(29), .select(1), .enable("false")) multiplexer_134 (
    .in0(mux_523), .in1(mux_530), .out(mux_531), .sel(pc1[3]));
  Multiplexer #(.width(29), .select(1), .enable("false")) multiplexer_135 (
    .in0(entry20), .in1(entry21), .out(mux_535), .sel(pc1[0]));
  Multiplexer #(.width(29), .select(1), .enable("false")) multiplexer_136 (
    .in0(entry24), .in1(entry25), .out(mux_539), .sel(pc1[0]));
  Multiplexer #(.width(29), .select(1), .enable("false")) multiplexer_137 (
    .in0(entry30), .in1(entry31), .out(mux_543), .sel(pc1[0]));
  Multiplexer #(.width(29), .select(1), .enable("false")) multiplexer_138 (
    .in0(mux_531), .in1(mux_546), .out(mux_547), .sel(pc1[4]));
  Multiplexer #(.width(29), .select(1), .enable("false")) multiplexer_139 (
    .in0(entry36), .in1(entry37), .out(mux_551), .sel(pc1[0]));
  Multiplexer #(.width(29), .select(1), .enable("false")) multiplexer_140 (
    .in0(entry40), .in1(entry41), .out(mux_555), .sel(pc1[0]));
  Multiplexer #(.width(29), .select(1), .enable("false")) multiplexer_141 (
    .in0(entry46), .in1(entry47), .out(mux_559), .sel(pc1[0]));
  Multiplexer #(.width(29), .select(1), .enable("false")) multiplexer_142 (
    .in0(entry48), .in1(entry49), .out(mux_563), .sel(pc1[0]));
  Multiplexer #(.width(29), .select(1), .enable("false")) multiplexer_143 (
    .in0(entry54), .in1(entry55), .out(mux_567), .sel(pc1[0]));
  Multiplexer #(.width(29), .select(1), .enable("false")) multiplexer_144 (
    .in0(entry58), .in1(entry59), .out(mux_571), .sel(pc1[0]));
  Multiplexer #(.width(29), .select(1), .enable("false")) multiplexer_145 (
    .in0(mux_573), .in1(mux_574), .out(mux_575), .sel(pc1[1]));
  Multiplexer #(.width(29), .select(1), .enable("false")) multiplexer_146 (
    .in0(mux_547), .in1(mux_578), .out({mux_579[28:26], target1, mux_579[9:0]}), .sel(pc1[5]));
  Comparator #(.width(10), .mode("unsigned")) comparator_68 (
    .a(mux_579[9:0]), .b(pc1[15:6]), .gt(gt_583), .eq(eq_584), .lt(lt_585));
  Multiplexer #(.width(29), .select(1), .enable("false")) multiplexer_147 (
    .in0(entry04), .in1(entry05), .out(mux_16), .sel(update_pc[0]));
  Multiplexer #(.width(29), .select(1), .enable("false")) multiplexer_148 (
    .in0(entry08), .in1(entry09), .out(mux_20), .sel(update_pc[0]));
  Multiplexer #(.width(29), .select(1), .enable("false")) multiplexer_149 (
    .in0(entry14), .in1(entry15), .out(mux_24), .sel(update_pc[0]));
  Multiplexer #(.width(29), .select(1), .enable("false")) multiplexer_150 (
    .in0(entry16), .in1(entry17), .out(mux_28), .sel(update_pc[0]));
  Multiplexer #(.width(29), .select(1), .enable("false")) multiplexer_151 (
    .in0(entry22), .in1(entry23), .out(mux_32), .sel(update_pc[0]));
  Multiplexer #(.width(29), .select(1), .enable("false")) multiplexer_152 (
    .in0(entry26), .in1(entry27), .out(mux_36), .sel(update_pc[0]));
  Multiplexer #(.width(29), .select(1), .enable("false")) multiplexer_153 (
    .in0(mux_38), .in1(mux_39), .out(mux_40), .sel(update_pc[1]));
  Multiplexer #(.width(29), .select(1), .enable("false")) multiplexer_154 (
    .in0(entry32), .in1(entry33), .out(mux_44), .sel(update_pc[0]));
  Multiplexer #(.width(29), .select(1), .enable("false")) multiplexer_155 (
    .in0(entry38), .in1(entry39), .out(mux_48), .sel(update_pc[0]));
  Multiplexer #(.width(29), .select(1), .enable("false")) multiplexer_156 (
    .in0(entry42), .in1(entry43), .out(mux_52), .sel(update_pc[0]));
  Multiplexer #(.width(29), .select(1), .enable("false")) multiplexer_157 (
    .in0(mux_54), .in1(mux_55), .out(mux_56), .sel(update_pc[1]));
  Multiplexer #(.width(29), .select(1), .enable("false")) multiplexer_158 (
    .in0(entry50), .in1(entry51), .out(mux_60), .sel(update_pc[0]));
  Multiplexer #(.width(29), .select(1), .enable("false")) multiplexer_159 (
    .in0(mux_62), .in1(mux_63), .out(mux_64), .sel(update_pc[1]));
  Multiplexer #(.width(29), .select(1), .enable("false")) multiplexer_160 (
    .in0(mux_66), .in1(mux_67), .out(mux_68), .sel(update_pc[1]));
  Multiplexer #(.width(29), .select(1), .enable("false")) multiplexer_161 (
    .in0(mux_68), .in1(mux_71), .out(mux_72), .sel(update_pc[2]));
  and and_67 (and_82, mux_75[28], eq_80);
  Adder #(.width(2)) adder_2 (.a(mux_75[27:26]), .b(2'b01), .out(adder_88), .cin(1'b0));  // open: cout
  Comparator #(.width(2), .mode("unsigned")) comparator_69 (
    .a(mux_75[27:26]), .b(2'b00), .gt(gt_92), .eq(eq_93), .lt(lt_94));
  Multiplexer #(.width(2), .select(1), .enable("false")) multiplexer_162 (
    .in0(mux_96), .in1(mux_90), .out(mux_98), .sel(taken));
  Multiplexer #(.width(29), .select(1), .enable("false")) multiplexer_163 (
    .in0(entry02), .in1(entry03), .out(mux_434), .sel(pc0[0]));
  Multiplexer #(.width(29), .select(1), .enable("false")) multiplexer_164 (
    .in0(mux_436), .in1(mux_437), .out(mux_438), .sel(pc0[1]));
  Multiplexer #(.width(29), .select(1), .enable("false")) multiplexer_165 (
    .in0(mux_440), .in1(mux_441), .out(mux_442), .sel(pc0[1]));
  Multiplexer #(.width(29), .select(1), .enable("false")) multiplexer_166 (
    .in0(mux_442), .in1(mux_445), .out(mux_446), .sel(pc0[2]));
  Multiplexer #(.width(29), .select(1), .enable("false")) multiplexer_167 (
    .in0(mux_448), .in1(mux_449), .out(mux_450), .sel(pc0[1]));
  Multiplexer #(.width(29), .select(1), .enable("false")) multiplexer_168 (
    .in0(mux_450), .in1(mux_453), .out(mux_454), .sel(pc0[2]));
  Multiplexer #(.width(29), .select(1), .enable("false")) multiplexer_169 (
    .in0(entry28), .in1(entry29), .out(mux_458), .sel(pc0[0]));
  Multiplexer #(.width(29), .select(1), .enable("false")) multiplexer_170 (
    .in0(mux_454), .in1(mux_461), .out(mux_462), .sel(pc0[3]));
  Multiplexer #(.width(29), .select(1), .enable("false")) multiplexer_171 (
    .in0(mux_464), .in1(mux_465), .out(mux_466), .sel(pc0[1]));
  Multiplexer #(.width(29), .select(1), .enable("false")) multiplexer_172 (
    .in0(mux_466), .in1(mux_469), .out(mux_470), .sel(pc0[2]));
  Multiplexer #(.width(29), .select(1), .enable("false")) multiplexer_173 (
    .in0(entry44), .in1(entry45), .out(mux_474), .sel(pc0[0]));
  Multiplexer #(.width(29), .select(1), .enable("false")) multiplexer_174 (
    .in0(mux_470), .in1(mux_477), .out(mux_478), .sel(pc0[3]));
  Multiplexer #(.width(29), .select(1), .enable("false")) multiplexer_175 (
    .in0(entry52), .in1(entry53), .out(mux_482), .sel(pc0[0]));
  Multiplexer #(.width(29), .select(1), .enable("false")) multiplexer_176 (
    .in0(entry56), .in1(entry57), .out(mux_486), .sel(pc0[0]));
  Multiplexer #(.width(29), .select(1), .enable("false")) multiplexer_177 (
    .in0(entry62), .in1(entry63), .out(mux_490), .sel(pc0[0]));
  Multiplexer #(.width(29), .select(1), .enable("false")) multiplexer_178 (
    .in0(mux_478), .in1(mux_493), .out(mux_494), .sel(pc0[4]));
  and and_68 (pred0, and_502, mux_495[27]);
  Multiplexer #(.width(29), .select(1), .enable("false")) multiplexer_179 (
    .in0(entry04), .in1(entry05), .out(mux_520), .sel(pc1[0]));
  Multiplexer #(.width(29), .select(1), .enable("false")) multiplexer_180 (
    .in0(entry08), .in1(entry09), .out(mux_524), .sel(pc1[0]));
  Multiplexer #(.width(29), .select(1), .enable("false")) multiplexer_181 (
    .in0(entry14), .in1(entry15), .out(mux_528), .sel(pc1[0]));
  Multiplexer #(.width(29), .select(1), .enable("false")) multiplexer_182 (
    .in0(entry16), .in1(entry17), .out(mux_532), .sel(pc1[0]));
  Multiplexer #(.width(29), .select(1), .enable("false")) multiplexer_183 (
    .in0(entry22), .in1(entry23), .out(mux_536), .sel(pc1[0]));
  Multiplexer #(.width(29), .select(1), .enable("false")) multiplexer_184 (
    .in0(entry26), .in1(entry27), .out(mux_540), .sel(pc1[0]));
  Multiplexer #(.width(29), .select(1), .enable("false")) multiplexer_185 (
    .in0(mux_542), .in1(mux_543), .out(mux_544), .sel(pc1[1]));
  Multiplexer #(.width(29), .select(1), .enable("false")) multiplexer_186 (
    .in0(entry32), .in1(entry33), .out(mux_548), .sel(pc1[0]));
  Multiplexer #(.width(29), .select(1), .enable("false")) multiplexer_187 (
    .in0(entry38), .in1(entry39), .out(mux_552), .sel(pc1[0]));
  Multiplexer #(.width(29), .select(1), .enable("false")) multiplexer_188 (
    .in0(entry42), .in1(entry43), .out(mux_556), .sel(pc1[0]));
  Multiplexer #(.width(29), .select(1), .enable("false")) multiplexer_189 (
    .in0(mux_558), .in1(mux_559), .out(mux_560), .sel(pc1[1]));
  Multiplexer #(.width(29), .select(1), .enable("false")) multiplexer_190 (
    .in0(entry50), .in1(entry51), .out(mux_564), .sel(pc1[0]));
  Multiplexer #(.width(29), .select(1), .enable("false")) multiplexer_191 (
    .in0(mux_566), .in1(mux_567), .out(mux_568), .sel(pc1[1]));
  Multiplexer #(.width(29), .select(1), .enable("false")) multiplexer_192 (
    .in0(mux_570), .in1(mux_571), .out(mux_572), .sel(pc1[1]));
  Multiplexer #(.width(29), .select(1), .enable("false")) multiplexer_193 (
    .in0(mux_572), .in1(mux_575), .out(mux_576), .sel(pc1[2]));
  and and_69 (and_586, mux_579[28], eq_584);

  // Other names for the same wires on the sheet: and_504 = pred0; and_588 = pred1; slice_78[9:0] = mux_75[9:0];
  //   slice_76[1:0] = mux_75[27:26]; slice_77 = mux_75[28]; slice_497[9:0] = mux_495[9:0]; mux_495[25:10] = target0;
  //   slice_505[15:0] = target0; slice_503 = mux_495[27]; slice_496 = mux_495[28]; slice_581[9:0] = mux_579[9:0];
  //   mux_579[25:10] = target1; slice_589[15:0] = target1; slice_587 = mux_579[27]; slice_580 = mux_579[28];
  //   pack_101[27:0] = {mux_99, target, update_pc[15:6]}; slice_2[9:0] = update_pc[15:6]; slice_422[5:0] = pc0[5:0];
  //   slice_423[4:0] = pc0[4:0]; slice_425[3:0] = pc0[3:0]; slice_427[2:0] = pc0[2:0]; slice_429[1:0] = pc0[1:0];
  //   slice_431 = pc0[0]; slice_432 = pc0[1]; slice_430 = pc0[2]; slice_428 = pc0[3]; slice_426 = pc0[4];
  //   slice_424 = pc0[5]; slice_498[9:0] = pc0[15:6]; slice_506[5:0] = pc1[5:0]; slice_507[4:0] = pc1[4:0];
  //   slice_509[3:0] = pc1[3:0]; slice_511[2:0] = pc1[2:0]; slice_513[1:0] = pc1[1:0]; slice_515 = pc1[0];
  //   slice_516 = pc1[1]; slice_514 = pc1[2]; slice_512 = pc1[3]; slice_510 = pc1[4]; slice_508 = pc1[5];
  //   slice_582[9:0] = pc1[15:6]; slice_1[5:0] = update_pc[5:0]; slice_3[4:0] = update_pc[4:0];
  //   slice_5[3:0] = update_pc[3:0]; slice_7[2:0] = update_pc[2:0]; slice_9[1:0] = update_pc[1:0];
  //   slice_11 = update_pc[0]; slice_12 = update_pc[1]; slice_10 = update_pc[2]; slice_8 = update_pc[3];
  //   slice_6 = update_pc[4]; slice_4 = update_pc[5]

  // Notes on the sheet:
  //   64-entry direct-mapped BTB / two simultaneous queries
endmodule

module InstructionMemory (
  input  [15:0] pc,
  output [15:0] instr0,
  output [15:0] instr1
);

  wire [15:0] adder_2;

  ROM #(.addrWidth(16), .dataWidth(16)) IMEM1 (.addr(adder_2), .data(instr1));
  Adder #(.width(16)) adder_1 (.a(pc), .b(16'h1), .out(adder_2), .cin(1'b0));  // open: cout
  ROM #(.addrWidth(16), .dataWidth(16)) IMEM0 (.addr(pc), .data(instr0));

  // Other names for the same wires on the sheet: instruction0_4[15:0] = instr0; instruction1_5[15:0] = instr1

  // Notes on the sheet:
  //   64K x 16 instruction ROM / two read ports
  //   contents of IMEM1 (hex, n*v repeats v):
  //   7205 7443 1650 90c0 8800 f000
  //   contents of IMEM0 (hex, n*v repeats v):
  //   7205 7443 1650 90c0 8800 f000
endmodule

module FetchFIFO8 (
  input  clk,
  input  rst,
  input  enable,
  input  flush,
  input  [1:0] consume,
  input  write_en,
  input  [15:0] in_instr0,
  input  [15:0] in_instr1,
  input  [15:0] in_pc,
  input  in_pred0,
  input  in_pred1,
  input  [15:0] in_next0,
  input  [15:0] in_next1,
  output [15:0] instr0,
  output [15:0] instr1,
  output [15:0] pc0,
  output [15:0] pc1,
  output pred0,
  output pred1,
  output [15:0] next0,
  output [15:0] next1,
  output valid0,
  output valid1,
  output full,
  output [3:0] count
);

  wire and_21, and_22, and_32, and_43, and_47, and_52, and_54, and_55, and_75, and_79, and_84, and_89,
       and_94, and_99, and_104, and_109, eq_25, eq_40, eq_50, eq_73, eq_77, eq_82, eq_87, eq_92, eq_97,
       eq_102, eq_107, gt_24, gt_35, gt_39, gt_49, gt_72, gt_76, gt_81, gt_86, gt_91, gt_96, gt_101, gt_106,
       half, lt_26, lt_37, lt_41, lt_51, lt_74, lt_78, lt_83, lt_88, lt_93, lt_98, lt_103, lt_108, mux_67,
       not_19, not_20, not_27, not_29, not_31, not_42, not_44, not_53, or_46, or_56, or_65, or_68;
  wire [2:0] adder_58, adder_60, head, tail;
  wire [3:0] adder_62, ext_61, ext_63, subtractor_64;
  wire [15:0] mux_11;
  wire [31:0] instructions0, instructions1, instructions2, instructions3, instructions4, instructions5,
       instructions6, instructions7, mux_5, mux_6, mux_7, mux_8, mux_9, mux_10;
  wire [33:0] mux_18;
  wire [49:0] metadata0, metadata1, metadata2, metadata3, metadata4, metadata5, metadata6, metadata7, mux_12,
       mux_13, mux_14, mux_15, mux_16, mux_17;

  Multiplexer #(.width(32), .select(1), .enable("false")) multiplexer_1 (
    .in0(instructions0), .in1(instructions1), .out(mux_5), .sel(head[0]));
  Multiplexer #(.width(32), .select(1), .enable("false")) multiplexer_2 (
    .in0(instructions6), .in1(instructions7), .out(mux_9), .sel(head[0]));
  Multiplexer #(.width(50), .select(1), .enable("false")) multiplexer_3 (
    .in0(metadata2), .in1(metadata3), .out(mux_13), .sel(head[0]));
  Multiplexer #(.width(50), .select(1), .enable("false")) multiplexer_4 (
    .in0(mux_15), .in1(mux_16), .out(mux_17), .sel(head[1]));
  and and_1 (and_21, enable, not_19);
  not not_1 (not_27, eq_25);
  not not_2 (not_31, mux_18[16]);
  Comparator #(.width(4), .mode("unsigned")) comparator_1 (.a(count), .b(4'b1000), .gt(gt_35), .eq(full), .lt(lt_37));
  and and_2 (and_43, valid0, not_42);
  and and_3 (and_47, and_43, or_46);
  not not_3 (not_53, full);
  Adder #(.width(3)) adder_1 (.a(tail), .b(3'b001), .out(adder_60), .cin(1'b0));  // open: cout
  assign ext_63 = {{3{1'b0}}, and_47};  // Bit_Extender bit_extender_1
  and and_4 (and_75, and_55, eq_73);
  and and_5 (and_79, and_55, eq_77);
  Comparator #(.width(3), .mode("unsigned")) comparator_2 (.a(tail), .b(3'b010), .gt(gt_81), .eq(eq_82), .lt(lt_83));
  Register #(.width(50)) reg_metadata3 (
    .D({in_next1, in_next0, in_pred1, in_pred0, in_pc}), .en(and_89), .Q(metadata3), .clk(clk), .clr(rst));
  Register #(.width(32)) reg_instructions4 (
    .D({in_instr1, in_instr0}), .en(and_94), .Q(instructions4), .clk(clk), .clr(rst));
  and and_6 (and_99, and_55, eq_97);
  Comparator #(.width(3), .mode("unsigned")) comparator_3 (.a(tail), .b(3'b110), .gt(gt_101), .eq(eq_102), .lt(lt_103));
  Register #(.width(50)) reg_metadata7 (
    .D({in_next1, in_next0, in_pred1, in_pred0, in_pc}), .en(and_109), .Q(metadata7), .clk(clk), .clr(rst));
  Multiplexer #(.width(16), .select(1), .enable("false")) multiplexer_5 (
    .in0(mux_18[33:18]), .in1(next1), .out(next0), .sel(half));
  Multiplexer #(.width(32), .select(1), .enable("false")) multiplexer_6 (
    .in0(instructions2), .in1(instructions3), .out(mux_6), .sel(head[0]));
  Multiplexer #(.width(32), .select(1), .enable("false")) multiplexer_7 (
    .in0(mux_8), .in1(mux_9), .out(mux_10), .sel(head[1]));
  Multiplexer #(.width(50), .select(1), .enable("false")) multiplexer_8 (
    .in0(mux_12), .in1(mux_13), .out(mux_14), .sel(head[1]));
  Multiplexer #(.width(50), .select(1), .enable("false")) multiplexer_9 (
    .in0(mux_14), .in1(mux_17), .out({next1, mux_18[33:18], pred1, mux_18[16:0]}), .sel(head[2]));
  and and_7 (and_22, and_21, not_20);
  and and_8 (valid0, and_22, not_27);
  and and_9 (and_32, valid0, not_29);
  not not_4 (not_44, valid1);
  and and_10 (and_54, and_22, write_en);
  Adder #(.width(3)) adder_2 (.a(head), .b(3'b001), .out(adder_58), .cin(1'b0));  // open: cout
  Register #(.width(3)) reg_tail (.D(adder_60), .en(and_55), .Q(tail), .clk(clk), .clr(or_56));
  Subtractor #(.width(4)) subtractor_1 (.a(adder_62), .b(ext_63), .out(subtractor_64), .bin(1'b0));  // open: bout
  Multiplexer #(.width(1), .select(1), .enable("false")) multiplexer_10 (
    .in0(1'b1), .in1(1'b0), .out(mux_67), .sel(and_47));
  Register #(.width(32)) reg_instructions0 (
    .D({in_instr1, in_instr0}), .en(and_75), .Q(instructions0), .clk(clk), .clr(rst));
  Register #(.width(32)) reg_instructions1 (
    .D({in_instr1, in_instr0}), .en(and_79), .Q(instructions1), .clk(clk), .clr(rst));
  and and_11 (and_84, and_55, eq_82);
  Comparator #(.width(3), .mode("unsigned")) comparator_4 (.a(tail), .b(3'b011), .gt(gt_86), .eq(eq_87), .lt(lt_88));
  Register #(.width(50)) reg_metadata4 (
    .D({in_next1, in_next0, in_pred1, in_pred0, in_pc}), .en(and_94), .Q(metadata4), .clk(clk), .clr(rst));
  Register #(.width(32)) reg_instructions5 (
    .D({in_instr1, in_instr0}), .en(and_99), .Q(instructions5), .clk(clk), .clr(rst));
  and and_12 (and_104, and_55, eq_102);
  Comparator #(.width(3), .mode("unsigned")) comparator_5 (.a(tail), .b(3'b111), .gt(gt_106), .eq(eq_107), .lt(lt_108));
  Multiplexer #(.width(16), .select(1), .enable("false")) multiplexer_11 (
    .in0(mux_11), .in1(instr1), .out(instr0), .sel(half));
  Multiplexer #(.width(32), .select(1), .enable("false")) multiplexer_12 (
    .in0(mux_5), .in1(mux_6), .out(mux_7), .sel(head[1]));
  Multiplexer #(.width(32), .select(1), .enable("false")) multiplexer_13 (
    .in0(mux_7), .in1(mux_10), .out({instr1, mux_11}), .sel(head[2]));
  Multiplexer #(.width(50), .select(1), .enable("false")) multiplexer_14 (
    .in0(metadata4), .in1(metadata5), .out(mux_15), .sel(head[0]));
  not not_5 (not_19, rst);
  not not_6 (not_29, half);
  and and_13 (valid1, and_32, not_31);
  Comparator #(.width(2), .mode("unsigned")) comparator_6 (.a(consume), .b(2'b00), .gt(gt_39), .eq(eq_40), .lt(lt_41));
  Comparator #(.width(2), .mode("unsigned")) comparator_7 (.a(consume), .b(2'b01), .gt(gt_49), .eq(eq_50), .lt(lt_51));
  and and_14 (and_55, and_54, not_53);
  assign ext_61 = {{3{1'b0}}, and_55};  // Bit_Extender bit_extender_2
  or or_1 (or_65, and_55, and_47);
  or or_2 (or_68, and_47, and_52);
  Register #(.width(50)) reg_metadata0 (
    .D({in_next1, in_next0, in_pred1, in_pred0, in_pc}), .en(and_75), .Q(metadata0), .clk(clk), .clr(rst));
  Register #(.width(50)) reg_metadata1 (
    .D({in_next1, in_next0, in_pred1, in_pred0, in_pc}), .en(and_79), .Q(metadata1), .clk(clk), .clr(rst));
  Register #(.width(32)) reg_instructions2 (
    .D({in_instr1, in_instr0}), .en(and_84), .Q(instructions2), .clk(clk), .clr(rst));
  and and_15 (and_89, and_55, eq_87);
  Comparator #(.width(3), .mode("unsigned")) comparator_8 (.a(tail), .b(3'b100), .gt(gt_91), .eq(eq_92), .lt(lt_93));
  Register #(.width(50)) reg_metadata5 (
    .D({in_next1, in_next0, in_pred1, in_pred0, in_pc}), .en(and_99), .Q(metadata5), .clk(clk), .clr(rst));
  Register #(.width(32)) reg_instructions6 (
    .D({in_instr1, in_instr0}), .en(and_104), .Q(instructions6), .clk(clk), .clr(rst));
  and and_16 (and_109, and_55, eq_107);
  Multiplexer #(.width(16), .select(1), .enable("false")) multiplexer_15 (
    .in0(mux_18[15:0]), .in1(pc1), .out(pc0), .sel(half));
  Multiplexer #(.width(32), .select(1), .enable("false")) multiplexer_16 (
    .in0(instructions4), .in1(instructions5), .out(mux_8), .sel(head[0]));
  Multiplexer #(.width(50), .select(1), .enable("false")) multiplexer_17 (
    .in0(metadata0), .in1(metadata1), .out(mux_12), .sel(head[0]));
  Multiplexer #(.width(50), .select(1), .enable("false")) multiplexer_18 (
    .in0(metadata6), .in1(metadata7), .out(mux_16), .sel(head[0]));
  not not_7 (not_20, flush);
  Comparator #(.width(4), .mode("unsigned")) comparator_9 (.a(count), .b(4'b0000), .gt(gt_24), .eq(eq_25), .lt(lt_26));
  not not_8 (not_42, eq_40);
  or or_3 (or_46, not_44, consume[1]);
  and and_17 (and_52, valid1, eq_50);
  or or_4 (or_56, rst, flush);
  Register #(.width(3)) reg_head (.D(adder_58), .en(and_47), .Q(head), .clk(clk), .clr(or_56));
  Adder #(.width(4)) adder_3 (.a(count), .b(ext_61), .out(adder_62), .cin(1'b0));  // open: cout
  Register #(.width(4)) reg_pair_count (.D(subtractor_64), .en(or_65), .Q(count), .clk(clk), .clr(or_56));
  Register #(.width(1)) reg_half (.D(mux_67), .en(or_68), .Q(half), .clk(clk), .clr(or_56));
  Comparator #(.width(3), .mode("unsigned")) comparator_10 (.a(tail), .b(3'b000), .gt(gt_72), .eq(eq_73), .lt(lt_74));
  Comparator #(.width(3), .mode("unsigned")) comparator_11 (.a(tail), .b(3'b001), .gt(gt_76), .eq(eq_77), .lt(lt_78));
  Register #(.width(50)) reg_metadata2 (
    .D({in_next1, in_next0, in_pred1, in_pred0, in_pc}), .en(and_84), .Q(metadata2), .clk(clk), .clr(rst));
  Register #(.width(32)) reg_instructions3 (
    .D({in_instr1, in_instr0}), .en(and_89), .Q(instructions3), .clk(clk), .clr(rst));
  and and_18 (and_94, and_55, eq_92);
  Comparator #(.width(3), .mode("unsigned")) comparator_12 (.a(tail), .b(3'b101), .gt(gt_96), .eq(eq_97), .lt(lt_98));
  Register #(.width(50)) reg_metadata6 (
    .D({in_next1, in_next0, in_pred1, in_pred0, in_pc}), .en(and_104), .Q(metadata6), .clk(clk), .clr(rst));
  Register #(.width(32)) reg_instructions7 (
    .D({in_instr1, in_instr0}), .en(and_109), .Q(instructions7), .clk(clk), .clr(rst));
  Adder #(.width(16)) adder_4 (.a(mux_18[15:0]), .b(16'h1), .out(pc1), .cin(1'b0));  // open: cout
  Multiplexer #(.width(1), .select(1), .enable("false")) multiplexer_19 (
    .in0(mux_18[16]), .in1(pred1), .out(pred0), .sel(half));

  // Other names for the same wires on the sheet: adder_112[15:0] = pc1; and_28 = valid0; and_33 = valid1;
  //   slice_45 = consume[1]; eq_36 = full; slice_1[1:0] = head[1:0]; slice_3 = head[0]; slice_4 = head[1];
  //   slice_2 = head[2]; slice_113[15:0] = mux_11; mux_11[31:16] = instr1; slice_114[15:0] = instr1;
  //   slice_110[15:0] = mux_18[15:0]; slice_30 = mux_18[16]; mux_18 (some bits) = {next1, pred1}; slice_115 = pred1;
  //   slice_116[15:0] = mux_18[33:18]; slice_117[15:0] = next1; mux_118[15:0] = instr0; mux_119[15:0] = pc0;
  //   mux_120 = pred0; mux_121[15:0] = next0; pack_69[31:0] = {in_instr1, in_instr0};
  //   pack_70[49:0] = {in_next1, in_next0, in_pred1, in_pred0, in_pc}; pair_count[3:0] = count

  // Notes on the sheet:
  //   8-pair fetch FIFO / retains a partially accepted pair
endmodule

module FetchUnit (
  input  clk,
  input  rst,
  input  enable,
  input  flush,
  input  [15:0] recover_pc,
  input  [1:0] consume,
  input  bp_we,
  input  [15:0] bp_pc,
  input  [15:0] bp_target,
  input  bp_taken,
  output [15:0] instr0,
  output [15:0] instr1,
  output [15:0] pc0,
  output [15:0] pc1,
  output pred0,
  output pred1,
  output [15:0] next0,
  output [15:0] next1,
  output valid0,
  output valid1,
  output [15:0] fetch_pc,
  output [3:0] fifo_count
);

  wire and_31, and_32, and_33, BTB_pred0_6, BTB_pred1_8, FQ_full_26, not_28, not_29, not_30, or_35;
  wire [15:0] adder_2, adder_5, BTB_target0_7, BTB_target1_9, IMEM_instr0_10, IMEM_instr1_11, mux_12, mux_13,
       mux_14, mux_34;

  Adder #(.width(16)) adder_1 (.a(fetch_pc), .b(16'h2), .out(adder_5), .cin(1'b0));  // open: cout
  Multiplexer #(.width(16), .select(1), .enable("false")) multiplexer_1 (
    .in0(adder_5), .in1(BTB_target1_9), .out(mux_13), .sel(BTB_pred1_8));
  not not_1 (not_28, FQ_full_26);
  and and_1 (and_32, and_31, not_29);
  Register #(.width(16)) reg_fetch_pc_reg (.D(mux_34), .en(or_35), .Q(fetch_pc), .clk(clk), .clr(rst));
  Adder #(.width(16)) u_adder_2 (.a(fetch_pc), .b(16'h1), .out(adder_2), .cin(1'b0));  // open: cout
  BTB64 BTB (
    .clk(clk), .rst(rst), .pc0(fetch_pc), .pc1(adder_2), .we(bp_we), .update_pc(bp_pc), .target(bp_target),
    .taken(bp_taken), .pred0(BTB_pred0_6), .target0(BTB_target0_7), .pred1(BTB_pred1_8),
    .target1(BTB_target1_9));
  Multiplexer #(.width(16), .select(1), .enable("false")) multiplexer_2 (
    .in0(mux_13), .in1(BTB_target0_7), .out(mux_14), .sel(BTB_pred0_6));
  not not_2 (not_29, flush);
  and and_2 (and_33, and_32, not_30);
  InstructionMemory IMEM (.pc(fetch_pc), .instr0(IMEM_instr0_10), .instr1(IMEM_instr1_11));
  not not_3 (not_30, rst);
  Multiplexer #(.width(16), .select(1), .enable("false")) multiplexer_3 (
    .in0(mux_14), .in1(recover_pc), .out(mux_34), .sel(flush));
  Multiplexer #(.width(16), .select(1), .enable("false")) multiplexer_4 (
    .in0(adder_2), .in1(BTB_target0_7), .out(mux_12), .sel(BTB_pred0_6));
  FetchFIFO8 FQ (
    .clk(clk), .rst(rst), .enable(enable), .flush(flush), .consume(consume), .write_en(1'b1),
    .in_instr0(IMEM_instr0_10), .in_instr1(IMEM_instr1_11), .in_pc(fetch_pc), .in_pred0(BTB_pred0_6),
    .in_pred1(BTB_pred1_8), .in_next0(mux_12), .in_next1(mux_13), .instr0(instr0), .instr1(instr1),
    .pc0(pc0), .pc1(pc1), .pred0(pred0), .pred1(pred1), .next0(next0), .next1(next1), .valid0(valid0),
    .valid1(valid1), .full(FQ_full_26), .count(fifo_count));
  and and_3 (and_31, enable, not_28);
  or or_1 (or_35, flush, and_33);

  // Other names for the same wires on the sheet: fetch_pc_reg[15:0] = fetch_pc; FQ_count_27[3:0] = fifo_count;
  //   FQ_instr0_16[15:0] = instr0; FQ_instr1_17[15:0] = instr1; FQ_next0_22[15:0] = next0; FQ_next1_23[15:0] = next1;
  //   FQ_pc0_18[15:0] = pc0; FQ_pc1_19[15:0] = pc1; FQ_pred0_20 = pred0; FQ_pred1_21 = pred1; FQ_valid0_24 = valid0;
  //   FQ_valid1_25 = valid1

  // Notes on the sheet:
  //   Dual fetch / BTB64 / 8-pair FIFO
endmodule
