// Logisim project harness-cpu.circ as structural Verilog
module Superscalar16 (
  input  reset,
  input  pause,
  output [15:0] pc,
  output halted,
  output [31:0] cycles,
  output [31:0] committed,
  output [31:0] dual_issue,
  output [31:0] dual_cdb,
  output [31:0] recoveries,
  output [15:0] r0,
  output [15:0] r1,
  output [15:0] r2,
  output [15:0] r3,
  output [15:0] r4,
  output [15:0] r5,
  output [15:0] r6,
  output [15:0] r7,
  output [15:0] memory_debug,
  output [4:0] rs0_count,
  output [4:0] rs1_count,
  output [4:0] rs2_count,
  output [4:0] rob0_count,
  output [4:0] rob1_count,
  output [4:0] rob2_count,
  output [3:0] sb_count
);

  wire clock, not_1, Processor_cdb0_valid_19, Processor_cdb1_valid_20, Processor_commit_valid_11,
       Processor_flush_16, Processor_stall_17;
  wire [1:0] Processor_issue_count_18;
  wire [3:0] Processor_commit_op_14;
  wire [7:0] Processor_commit_sn_12;
  wire [15:0] Processor_commit_pc_13, Processor_commit_result_15;
  wire [31:0] Processor_dispatched_5;

  Clock #(.highDuration(1), .lowDuration(1)) u_Clock (.out(clock));
  not u_not_1 (not_1, pause);
  CPU_Core Processor (
    .clk(clock), .rst(reset), .run(not_1), .debug_addr({16{1'b0}}), .cycles(cycles), .committed(committed),
    .dispatched(Processor_dispatched_5), .dual_issue(dual_issue), .recoveries(recoveries),
    .dual_cdb(dual_cdb), .halted(halted), .pc(pc), .commit_valid(Processor_commit_valid_11),
    .commit_sn(Processor_commit_sn_12), .commit_pc(Processor_commit_pc_13),
    .commit_op(Processor_commit_op_14), .commit_result(Processor_commit_result_15),
    .flush(Processor_flush_16), .stall(Processor_stall_17), .issue_count(Processor_issue_count_18),
    .cdb0_valid(Processor_cdb0_valid_19), .cdb1_valid(Processor_cdb1_valid_20), .sb_count(sb_count),
    .memory_debug(memory_debug), .r0(r0), .r1(r1), .r2(r2), .r3(r3), .r4(r4), .r5(r5), .r6(r6), .r7(r7),
    .rs0_count(rs0_count), .rob0_count(rob0_count), .rs1_count(rs1_count), .rob1_count(rob1_count),
    .rs2_count(rs2_count), .rob2_count(rob2_count));

  // Other names for the same wires on the sheet: Processor_committed_4[31:0] = committed;
  //   Processor_cycles_3[31:0] = cycles; Processor_dual_cdb_8[31:0] = dual_cdb;
  //   Processor_dual_issue_6[31:0] = dual_issue; Processor_halted_9 = halted;
  //   Processor_memory_debug_22[15:0] = memory_debug; Processor_pc_10[15:0] = pc; Processor_r0_23[15:0] = r0;
  //   Processor_r1_24[15:0] = r1; Processor_r2_25[15:0] = r2; Processor_r3_26[15:0] = r3; Processor_r4_27[15:0] = r4;
  //   Processor_r5_28[15:0] = r5; Processor_r6_29[15:0] = r6; Processor_r7_30[15:0] = r7;
  //   Processor_recoveries_7[31:0] = recoveries; Processor_rob0_count_32[4:0] = rob0_count;
  //   Processor_rob1_count_34[4:0] = rob1_count; Processor_rob2_count_36[4:0] = rob2_count;
  //   Processor_rs0_count_31[4:0] = rs0_count; Processor_rs1_count_33[4:0] = rs1_count;
  //   Processor_rs2_count_35[4:0] = rs2_count; Processor_sb_count_21[3:0] = sb_count

  // Notes on the sheet:
  //   SUPERSCALAR16 | native Logisim circuit | demo program
endmodule

module CPU_Core (
  input  clk,
  input  rst,
  input  run,
  input  [15:0] debug_addr,
  output [31:0] cycles,
  output [31:0] committed,
  output [31:0] dispatched,
  output [31:0] dual_issue,
  output [31:0] recoveries,
  output [31:0] dual_cdb,
  output halted,
  output [15:0] pc,
  output commit_valid,
  output [7:0] commit_sn,
  output [15:0] commit_pc,
  output [3:0] commit_op,
  output [15:0] commit_result,
  output flush,
  output stall,
  output [1:0] issue_count,
  output cdb0_valid,
  output cdb1_valid,
  output [3:0] sb_count,
  output [15:0] memory_debug,
  output [15:0] r0,
  output [15:0] r1,
  output [15:0] r2,
  output [15:0] r3,
  output [15:0] r4,
  output [15:0] r5,
  output [15:0] r6,
  output [15:0] r7,
  output [4:0] rs0_count,
  output [4:0] rob0_count,
  output [4:0] rs1_count,
  output [4:0] rob1_count,
  output [4:0] rs2_count,
  output [4:0] rob2_count
);

  wire accept0, accept1, ALU0_taken_272, ALU1_taken_277, and_4, and_5, and_6, and_48, and_65, and_229,
       and_230, and_235, and_237, and_241, and_243, and_247, and_249, and_254, and_255, and_260, and_264,
       and_268, and_279, and_281, and_282, and_294, and_307, and_317, and_318, and_319, and_323, and_324,
       and_325, and_329, and_330, and_331, and_379, and_380, and_385, and_389, and_390, c0_taken,
       decode0_branch_39, decode0_halt_41, decode0_jump_40, decode0_mem_37, decode0_rw_36, decode0_store_38,
       decode1_branch_57, decode1_halt_59, decode1_jump_58, decode1_mem_55, decode1_rw_54, decode1_store_56,
       eq_45, eq_62, eq_233, eq_239, eq_245, eq_258, eq_262, eq_266, eq_292, eq_315, eq_321, eq_327, eq_358,
       eq_362, eq_366, eq_370, eq_376, eq_383, eq_387, fetch_pred0_23, fetch_pred1_24, fetch_valid0_27,
       fetch_valid1_28, gt_44, gt_61, gt_232, gt_238, gt_244, gt_257, gt_261, gt_265, gt_291, gt_314, gt_320,
       gt_326, gt_357, gt_361, gt_365, gt_369, gt_375, gt_382, gt_386, lt_46, lt_63, lt_234, lt_240, lt_246,
       lt_259, lt_263, lt_267, lt_293, lt_316, lt_322, lt_328, lt_359, lt_363, lt_367, lt_371, lt_377,
       lt_384, lt_388, mux_101, mux_102, mux_107, mux_142, mux_143, mux_148, mux_183, mux_184, mux_189,
       mux_228, mux_253, mux_306, mux_342, mux_343, mux_354, mux_355, not_1, not_2, not_3, not_47, not_64,
       not_217, not_219, not_221, not_236, not_242, not_248, not_280, not_304, not_305, not_378, not_399,
       or_7, or_18, or_93, or_134, or_175, or_216, or_218, or_220, or_227, or_252, or_332, or_372, or_373,
       or_374, rename_available0_66, rename_available1_67, rename_vj0_74, rename_vj1_80, rename_vk0_77,
       rename_vk1_83, ROB0_full_119, ROB0_head_done_122, ROB0_head_rw_127, ROB0_head_taken_133,
       ROB0_head_valid_121, ROB1_full_160, ROB1_head_done_163, ROB1_head_rw_168, ROB1_head_taken_174,
       ROB1_head_valid_162, ROB2_full_201, ROB2_head_done_204, ROB2_head_rw_209, ROB2_head_taken_215,
       ROB2_head_valid_203, RS0_ex_valid_111, RS0_full_109, RS1_ex_valid_152, RS1_full_150, RS2_ex_valid_193,
       RS2_full_191, stores_commit_found_299, stores_forward_297, stores_full_295;
  wire [1:0] ext_12, ext_13, mux_224, mux_226, mux_250, mux_251;
  wire [2:0] decode0_rd_32, decode0_rs1_33, decode0_rs2_34, decode1_rd_50, decode1_rs1_51, decode1_rs2_52,
       mux_106, mux_147, mux_188, mux_340, mux_341, ROB0_head_rd_logic_126, ROB1_head_rd_logic_167,
       ROB2_head_rd_logic_208;
  wire [3:0] decode0_opcode_31, decode1_opcode_49, fetch_fifo_count_30, mux_94, mux_135, mux_176, mux_334,
       ROB0_head_op_123, ROB1_head_op_164, ROB2_head_op_205, RS0_ex_op_112, RS1_ex_op_153, RS2_ex_op_194;
  wire [5:0] c0_rd, c1_rd, mux_95, mux_96, mux_97, mux_105, mux_136, mux_137, mux_138, mux_146, mux_177,
       mux_178, mux_179, mux_187, mux_336, mux_337, mux_338, mux_339, rename_new0_68, rename_new1_69,
       rename_old0_70, rename_old1_71, rename_qj0_72, rename_qj1_78, rename_qk0_75, rename_qk1_81,
       ROB0_head_rd_new_124, ROB0_head_rd_old_125, ROB1_head_rd_new_165, ROB1_head_rd_old_166,
       ROB2_head_rd_new_206, ROB2_head_rd_old_207, RS0_ex_rd_113, RS1_ex_rd_154, RS2_ex_rd_195;
  wire [7:0] adder_10, adder_16, adder_92, c0_sn, c1_sn, ext_15, global_sn, mux_17, mux_100, mux_141,
       mux_182, mux_346, mux_347, ROB0_head_sn_129, ROB1_head_sn_170, ROB2_head_sn_211, RS0_ex_sn_116,
       RS1_ex_sn_157;
  wire [15:0] adder_289, adder_313, ALU0_addr_273, ALU0_next_270, ALU0_result_269, ALU0_target_271,
       ALU1_addr_278, ALU1_next_275, ALU1_result_274, ALU1_target_276, c0_next, c0_result, c1_result,
       decode0_imm_35, decode1_imm_53, fetch_instr0_19, fetch_instr1_20, fetch_next0_25, fetch_next1_26,
       fetch_pc0_21, fetch_pc1_22, memory_data_302, mux_98, mux_99, mux_103, mux_104, mux_108, mux_139,
       mux_140, mux_144, mux_145, mux_149, mux_180, mux_181, mux_185, mux_186, mux_190, mux_344, mux_348,
       mux_349, mux_350, mux_352, mux_353, recovery_pc, rename_dj0_73, rename_dj1_79, rename_dk0_76,
       rename_dk1_82, ROB0_head_next_132, ROB0_head_pc_128, ROB0_head_pred_next_130, ROB0_head_result_131,
       ROB1_head_next_173, ROB1_head_pc_169, ROB1_head_pred_next_171, ROB1_head_result_172,
       ROB2_head_next_214, ROB2_head_pc_210, ROB2_head_pred_next_212, ROB2_head_result_213, RS0_ex_a_117,
       RS0_ex_b_118, RS0_ex_imm_114, RS0_ex_pc_115, RS1_ex_a_158, RS1_ex_b_159, RS1_ex_imm_155,
       RS1_ex_pc_156, RS2_ex_a_199, RS2_ex_b_200, RS2_ex_imm_196, RS2_ex_pc_197, stores_commit_addr_300,
       stores_commit_data_301, stores_forward_data_298;
  wire [31:0] adder_392, adder_393, adder_395, adder_396, adder_397, adder_398, ext_394;
  wire [56:0] decode0_packet_42, decode1_packet_60;

  not u_not_1 (not_1, halted);
  not u_not_2 (not_2, flush);
  not u_not_3 (not_3, rst);
  and and_1 (and_4, run, not_1);
  and and_2 (and_5, and_4, not_2);
  and and_3 (and_6, and_5, not_3);
  or or_1 (or_7, flush, halted);
  Register #(.width(1)) reg_halted (.D(1'b1), .en(and_385), .Q(halted), .clk(clk), .clr(rst));
  Register #(.width(1)) reg_recovery (.D(and_380), .en(1'b1), .Q(flush), .clk(clk), .clr(rst));
  Register #(.width(16)) reg_recovery_pc (.D(mux_353), .en(and_380), .Q(recovery_pc), .clk(clk), .clr(rst));
  Adder #(.width(8)) adder_1 (.a(commit_sn), .b(8'h1), .out(adder_10), .cin(1'b0));  // open: cout
  Register #(.width(8)) reg_retirement_sn (.D(adder_10), .en(commit_valid), .Q(commit_sn), .clk(clk), .clr(rst));
  assign ext_12 = {{1{1'b0}}, accept0};  // Bit_Extender bit_extender_1
  assign ext_13 = {{1{1'b0}}, accept1};  // Bit_Extender bit_extender_2
  Adder #(.width(2)) adder_2 (.a(ext_12), .b(ext_13), .out(issue_count), .cin(1'b0));  // open: cout
  assign ext_15 = {{6{1'b0}}, issue_count};  // Bit_Extender bit_extender_3
  Adder #(.width(8)) adder_3 (.a(global_sn), .b(ext_15), .out(adder_16), .cin(1'b0));  // open: cout
  Multiplexer #(.width(8), .select(1), .enable("false")) multiplexer_1 (
    .in0(adder_16), .in1(commit_sn), .out(mux_17), .sel(flush));
  or or_2 (or_18, and_6, flush);
  Register #(.width(8)) reg_global_sn (.D(mux_17), .en(or_18), .Q(global_sn), .clk(clk), .clr(rst));
  FetchUnit fetch (
    .clk(clk), .rst(rst), .enable(and_6), .flush(flush), .recover_pc(recovery_pc), .consume(issue_count),
    .bp_we(and_379), .bp_pc(commit_pc), .bp_target(mux_353), .bp_taken(mux_355), .instr0(fetch_instr0_19),
    .instr1(fetch_instr1_20), .pc0(fetch_pc0_21), .pc1(fetch_pc1_22), .pred0(fetch_pred0_23),
    .pred1(fetch_pred1_24), .next0(fetch_next0_25), .next1(fetch_next1_26), .valid0(fetch_valid0_27),
    .valid1(fetch_valid1_28), .fetch_pc(pc), .fifo_count(fetch_fifo_count_30));
  DecodeOne decode0 (
    .instr(fetch_instr0_19), .pc(fetch_pc0_21), .pred(fetch_pred0_23), .opcode(decode0_opcode_31),
    .rd(decode0_rd_32), .rs1(decode0_rs1_33), .rs2(decode0_rs2_34), .imm(decode0_imm_35), .rw(decode0_rw_36),
    .mem(decode0_mem_37), .store(decode0_store_38), .branch(decode0_branch_39), .jump(decode0_jump_40),
    .halt(decode0_halt_41), .packet(decode0_packet_42));
  Comparator #(.width(3), .mode("unsigned")) comparator_1 (
    .a(decode0_rd_32), .b(3'b000), .gt(gt_44), .eq(eq_45), .lt(lt_46));
  not not_4 (not_47, eq_45);
  and u_and_4 (and_48, decode0_rw_36, not_47);
  DecodeOne decode1 (
    .instr(fetch_instr1_20), .pc(fetch_pc1_22), .pred(fetch_pred1_24), .opcode(decode1_opcode_49),
    .rd(decode1_rd_50), .rs1(decode1_rs1_51), .rs2(decode1_rs2_52), .imm(decode1_imm_53), .rw(decode1_rw_54),
    .mem(decode1_mem_55), .store(decode1_store_56), .branch(decode1_branch_57), .jump(decode1_jump_58),
    .halt(decode1_halt_59), .packet(decode1_packet_60));
  Comparator #(.width(3), .mode("unsigned")) comparator_2 (
    .a(decode1_rd_50), .b(3'b000), .gt(gt_61), .eq(eq_62), .lt(lt_63));
  not not_5 (not_64, eq_62);
  and u_and_5 (and_65, decode1_rw_54, not_64);
  Rename_PRF rename (
    .clk(clk), .rst(rst), .enable(and_6), .clear(flush), .accept0(accept0), .accept1(accept1),
    .commit_v(commit_valid), .commit_rw(mux_343), .commit_rd(mux_341), .commit_new(mux_337),
    .commit_old(mux_339), .commit_data(commit_result), .c0_v(cdb0_valid), .c0_tag(c0_rd),
    .c0_data(c0_result), .c1_v(cdb1_valid), .c1_tag(c1_rd), .c1_data(c1_result), .rd0(decode0_rd_32),
    .rs10(decode0_rs1_33), .rs20(decode0_rs2_34), .rw0(and_48), .rd1(decode1_rd_50), .rs11(decode1_rs1_51),
    .rs21(decode1_rs2_52), .rw1(and_65), .available0(rename_available0_66),
    .available1(rename_available1_67), .new0(rename_new0_68), .new1(rename_new1_69), .old0(rename_old0_70),
    .old1(rename_old1_71), .qj0(rename_qj0_72), .dj0(rename_dj0_73), .vj0(rename_vj0_74),
    .qk0(rename_qk0_75), .dk0(rename_dk0_76), .vk0(rename_vk0_77), .qj1(rename_qj1_78), .dj1(rename_dj1_79),
    .vj1(rename_vj1_80), .qk1(rename_qk1_81), .dk1(rename_dk1_82), .vk1(rename_vk1_83), .r0(r0), .r1(r1),
    .r2(r2), .r3(r3), .r4(r4), .r5(r5), .r6(r6), .r7(r7));
  Adder #(.width(8)) adder_4 (.a(global_sn), .b(8'h1), .out(adder_92), .cin(1'b0));  // open: cout
  or or_3 (or_93, and_235, and_260);
  Multiplexer #(.width(4), .select(1), .enable("false")) multiplexer_2 (
    .in0(decode0_opcode_31), .in1(decode1_opcode_49), .out(mux_94), .sel(and_260));
  Multiplexer #(.width(6), .select(1), .enable("false")) multiplexer_3 (
    .in0(rename_new0_68), .in1(rename_new1_69), .out(mux_95), .sel(and_260));
  Multiplexer #(.width(6), .select(1), .enable("false")) multiplexer_4 (
    .in0(rename_qj0_72), .in1(rename_qj1_78), .out(mux_96), .sel(and_260));
  Multiplexer #(.width(6), .select(1), .enable("false")) multiplexer_5 (
    .in0(rename_qk0_75), .in1(rename_qk1_81), .out(mux_97), .sel(and_260));
  Multiplexer #(.width(16), .select(1), .enable("false")) multiplexer_6 (
    .in0(decode0_imm_35), .in1(decode1_imm_53), .out(mux_98), .sel(and_260));
  Multiplexer #(.width(16), .select(1), .enable("false")) multiplexer_7 (
    .in0(fetch_pc0_21), .in1(fetch_pc1_22), .out(mux_99), .sel(and_260));
  Multiplexer #(.width(8), .select(1), .enable("false")) multiplexer_8 (
    .in0(global_sn), .in1(adder_92), .out(mux_100), .sel(and_260));
  Multiplexer #(.width(1), .select(1), .enable("false")) multiplexer_9 (
    .in0(rename_vj0_74), .in1(rename_vj1_80), .out(mux_101), .sel(and_260));
  Multiplexer #(.width(1), .select(1), .enable("false")) multiplexer_10 (
    .in0(rename_vk0_77), .in1(rename_vk1_83), .out(mux_102), .sel(and_260));
  Multiplexer #(.width(16), .select(1), .enable("false")) multiplexer_11 (
    .in0(rename_dj0_73), .in1(rename_dj1_79), .out(mux_103), .sel(and_260));
  Multiplexer #(.width(16), .select(1), .enable("false")) multiplexer_12 (
    .in0(rename_dk0_76), .in1(rename_dk1_82), .out(mux_104), .sel(and_260));
  Multiplexer #(.width(6), .select(1), .enable("false")) multiplexer_13 (
    .in0(rename_old0_70), .in1(rename_old1_71), .out(mux_105), .sel(and_260));
  Multiplexer #(.width(3), .select(1), .enable("false")) multiplexer_14 (
    .in0(decode0_rd_32), .in1(decode1_rd_50), .out(mux_106), .sel(and_260));
  Multiplexer #(.width(1), .select(1), .enable("false")) multiplexer_15 (
    .in0(and_48), .in1(and_65), .out(mux_107), .sel(and_260));
  Multiplexer #(.width(16), .select(1), .enable("false")) multiplexer_16 (
    .in0(fetch_next0_25), .in1(fetch_next1_26), .out(mux_108), .sel(and_260));
  ALU_RS RS0 (
    .clk(clk), .rst(rst), .clear(or_7), .enable(and_6), .wr(or_93), .take(and_279), .op(mux_94), .rd(mux_95),
    .qj(mux_96), .qk(mux_97), .imm(mux_98), .pc(mux_99), .sn(mux_100), .vj(mux_101), .vk(mux_102),
    .dj(mux_103), .dk(mux_104), .c0_valid(cdb0_valid), .c0_rd(c0_rd), .c0_data(c0_result),
    .c1_valid(cdb1_valid), .c1_rd(c1_rd), .c1_data(c1_result), .full(RS0_full_109), .count(rs0_count),
    .ex_valid(RS0_ex_valid_111), .ex_op(RS0_ex_op_112), .ex_rd(RS0_ex_rd_113), .ex_imm(RS0_ex_imm_114),
    .ex_pc(RS0_ex_pc_115), .ex_sn(RS0_ex_sn_116), .ex_a(RS0_ex_a_117), .ex_b(RS0_ex_b_118));
  ROB ROB0 (
    .clk(clk), .rst(rst), .clear(or_7), .enable(and_6), .wr(or_93), .pop(and_319), .op(mux_94),
    .rd_new(mux_95), .rd_old(mux_105), .rd_logic(mux_106), .rw(mux_107), .pc(mux_99), .sn(mux_100),
    .pred_next(mux_108), .c0_valid(cdb0_valid), .c0_sn(c0_sn), .c0_result(c0_result), .c0_next(c0_next),
    .c0_taken(c0_taken), .c1_valid(cdb1_valid), .c1_sn(c1_sn), .c1_result(c1_result), .c1_next(adder_313),
    .c1_taken(1'b0), .full(ROB0_full_119), .count(rob0_count), .head_valid(ROB0_head_valid_121),
    .head_done(ROB0_head_done_122), .head_op(ROB0_head_op_123), .head_rd_new(ROB0_head_rd_new_124),
    .head_rd_old(ROB0_head_rd_old_125), .head_rd_logic(ROB0_head_rd_logic_126), .head_rw(ROB0_head_rw_127),
    .head_pc(ROB0_head_pc_128), .head_sn(ROB0_head_sn_129), .head_pred_next(ROB0_head_pred_next_130),
    .head_result(ROB0_head_result_131), .head_next(ROB0_head_next_132), .head_taken(ROB0_head_taken_133));
  or or_4 (or_134, and_241, and_264);
  Multiplexer #(.width(4), .select(1), .enable("false")) multiplexer_17 (
    .in0(decode0_opcode_31), .in1(decode1_opcode_49), .out(mux_135), .sel(and_264));
  Multiplexer #(.width(6), .select(1), .enable("false")) multiplexer_18 (
    .in0(rename_new0_68), .in1(rename_new1_69), .out(mux_136), .sel(and_264));
  Multiplexer #(.width(6), .select(1), .enable("false")) multiplexer_19 (
    .in0(rename_qj0_72), .in1(rename_qj1_78), .out(mux_137), .sel(and_264));
  Multiplexer #(.width(6), .select(1), .enable("false")) multiplexer_20 (
    .in0(rename_qk0_75), .in1(rename_qk1_81), .out(mux_138), .sel(and_264));
  Multiplexer #(.width(16), .select(1), .enable("false")) multiplexer_21 (
    .in0(decode0_imm_35), .in1(decode1_imm_53), .out(mux_139), .sel(and_264));
  Multiplexer #(.width(16), .select(1), .enable("false")) multiplexer_22 (
    .in0(fetch_pc0_21), .in1(fetch_pc1_22), .out(mux_140), .sel(and_264));
  Multiplexer #(.width(8), .select(1), .enable("false")) multiplexer_23 (
    .in0(global_sn), .in1(adder_92), .out(mux_141), .sel(and_264));
  Multiplexer #(.width(1), .select(1), .enable("false")) multiplexer_24 (
    .in0(rename_vj0_74), .in1(rename_vj1_80), .out(mux_142), .sel(and_264));
  Multiplexer #(.width(1), .select(1), .enable("false")) multiplexer_25 (
    .in0(rename_vk0_77), .in1(rename_vk1_83), .out(mux_143), .sel(and_264));
  Multiplexer #(.width(16), .select(1), .enable("false")) multiplexer_26 (
    .in0(rename_dj0_73), .in1(rename_dj1_79), .out(mux_144), .sel(and_264));
  Multiplexer #(.width(16), .select(1), .enable("false")) multiplexer_27 (
    .in0(rename_dk0_76), .in1(rename_dk1_82), .out(mux_145), .sel(and_264));
  Multiplexer #(.width(6), .select(1), .enable("false")) multiplexer_28 (
    .in0(rename_old0_70), .in1(rename_old1_71), .out(mux_146), .sel(and_264));
  Multiplexer #(.width(3), .select(1), .enable("false")) multiplexer_29 (
    .in0(decode0_rd_32), .in1(decode1_rd_50), .out(mux_147), .sel(and_264));
  Multiplexer #(.width(1), .select(1), .enable("false")) multiplexer_30 (
    .in0(and_48), .in1(and_65), .out(mux_148), .sel(and_264));
  Multiplexer #(.width(16), .select(1), .enable("false")) multiplexer_31 (
    .in0(fetch_next0_25), .in1(fetch_next1_26), .out(mux_149), .sel(and_264));
  ALU_RS RS1 (
    .clk(clk), .rst(rst), .clear(or_7), .enable(and_6), .wr(or_134), .take(and_282), .op(mux_135),
    .rd(mux_136), .qj(mux_137), .qk(mux_138), .imm(mux_139), .pc(mux_140), .sn(mux_141), .vj(mux_142),
    .vk(mux_143), .dj(mux_144), .dk(mux_145), .c0_valid(cdb0_valid), .c0_rd(c0_rd), .c0_data(c0_result),
    .c1_valid(cdb1_valid), .c1_rd(c1_rd), .c1_data(c1_result), .full(RS1_full_150), .count(rs1_count),
    .ex_valid(RS1_ex_valid_152), .ex_op(RS1_ex_op_153), .ex_rd(RS1_ex_rd_154), .ex_imm(RS1_ex_imm_155),
    .ex_pc(RS1_ex_pc_156), .ex_sn(RS1_ex_sn_157), .ex_a(RS1_ex_a_158), .ex_b(RS1_ex_b_159));
  ROB ROB1 (
    .clk(clk), .rst(rst), .clear(or_7), .enable(and_6), .wr(or_134), .pop(and_325), .op(mux_135),
    .rd_new(mux_136), .rd_old(mux_146), .rd_logic(mux_147), .rw(mux_148), .pc(mux_140), .sn(mux_141),
    .pred_next(mux_149), .c0_valid(cdb0_valid), .c0_sn(c0_sn), .c0_result(c0_result), .c0_next(c0_next),
    .c0_taken(c0_taken), .c1_valid(cdb1_valid), .c1_sn(c1_sn), .c1_result(c1_result), .c1_next(adder_313),
    .c1_taken(1'b0), .full(ROB1_full_160), .count(rob1_count), .head_valid(ROB1_head_valid_162),
    .head_done(ROB1_head_done_163), .head_op(ROB1_head_op_164), .head_rd_new(ROB1_head_rd_new_165),
    .head_rd_old(ROB1_head_rd_old_166), .head_rd_logic(ROB1_head_rd_logic_167), .head_rw(ROB1_head_rw_168),
    .head_pc(ROB1_head_pc_169), .head_sn(ROB1_head_sn_170), .head_pred_next(ROB1_head_pred_next_171),
    .head_result(ROB1_head_result_172), .head_next(ROB1_head_next_173), .head_taken(ROB1_head_taken_174));
  or or_5 (or_175, and_247, and_268);
  Multiplexer #(.width(4), .select(1), .enable("false")) multiplexer_32 (
    .in0(decode0_opcode_31), .in1(decode1_opcode_49), .out(mux_176), .sel(and_268));
  Multiplexer #(.width(6), .select(1), .enable("false")) multiplexer_33 (
    .in0(rename_new0_68), .in1(rename_new1_69), .out(mux_177), .sel(and_268));
  Multiplexer #(.width(6), .select(1), .enable("false")) multiplexer_34 (
    .in0(rename_qj0_72), .in1(rename_qj1_78), .out(mux_178), .sel(and_268));
  Multiplexer #(.width(6), .select(1), .enable("false")) multiplexer_35 (
    .in0(rename_qk0_75), .in1(rename_qk1_81), .out(mux_179), .sel(and_268));
  Multiplexer #(.width(16), .select(1), .enable("false")) multiplexer_36 (
    .in0(decode0_imm_35), .in1(decode1_imm_53), .out(mux_180), .sel(and_268));
  Multiplexer #(.width(16), .select(1), .enable("false")) multiplexer_37 (
    .in0(fetch_pc0_21), .in1(fetch_pc1_22), .out(mux_181), .sel(and_268));
  Multiplexer #(.width(8), .select(1), .enable("false")) multiplexer_38 (
    .in0(global_sn), .in1(adder_92), .out(mux_182), .sel(and_268));
  Multiplexer #(.width(1), .select(1), .enable("false")) multiplexer_39 (
    .in0(rename_vj0_74), .in1(rename_vj1_80), .out(mux_183), .sel(and_268));
  Multiplexer #(.width(1), .select(1), .enable("false")) multiplexer_40 (
    .in0(rename_vk0_77), .in1(rename_vk1_83), .out(mux_184), .sel(and_268));
  Multiplexer #(.width(16), .select(1), .enable("false")) multiplexer_41 (
    .in0(rename_dj0_73), .in1(rename_dj1_79), .out(mux_185), .sel(and_268));
  Multiplexer #(.width(16), .select(1), .enable("false")) multiplexer_42 (
    .in0(rename_dk0_76), .in1(rename_dk1_82), .out(mux_186), .sel(and_268));
  Multiplexer #(.width(6), .select(1), .enable("false")) multiplexer_43 (
    .in0(rename_old0_70), .in1(rename_old1_71), .out(mux_187), .sel(and_268));
  Multiplexer #(.width(3), .select(1), .enable("false")) multiplexer_44 (
    .in0(decode0_rd_32), .in1(decode1_rd_50), .out(mux_188), .sel(and_268));
  Multiplexer #(.width(1), .select(1), .enable("false")) multiplexer_45 (
    .in0(and_48), .in1(and_65), .out(mux_189), .sel(and_268));
  Multiplexer #(.width(16), .select(1), .enable("false")) multiplexer_46 (
    .in0(fetch_next0_25), .in1(fetch_next1_26), .out(mux_190), .sel(and_268));
  LS_RS RS2 (
    .clk(clk), .rst(rst), .clear(or_7), .enable(and_6), .wr(or_175), .take(cdb1_valid), .op(mux_176),
    .rd(mux_177), .qj(mux_178), .qk(mux_179), .imm(mux_180), .pc(mux_181), .sn(mux_182), .vj(mux_183),
    .vk(mux_184), .dj(mux_185), .dk(mux_186), .c0_valid(cdb0_valid), .c0_rd(c0_rd), .c0_data(c0_result),
    .c1_valid(cdb1_valid), .c1_rd(c1_rd), .c1_data(c1_result), .full(RS2_full_191), .count(rs2_count),
    .ex_valid(RS2_ex_valid_193), .ex_op(RS2_ex_op_194), .ex_rd(RS2_ex_rd_195), .ex_imm(RS2_ex_imm_196),
    .ex_pc(RS2_ex_pc_197), .ex_sn(c1_sn), .ex_a(RS2_ex_a_199), .ex_b(RS2_ex_b_200));
  ROB ROB2 (
    .clk(clk), .rst(rst), .clear(or_7), .enable(and_6), .wr(or_175), .pop(and_331), .op(mux_176),
    .rd_new(mux_177), .rd_old(mux_187), .rd_logic(mux_188), .rw(mux_189), .pc(mux_181), .sn(mux_182),
    .pred_next(mux_190), .c0_valid(cdb0_valid), .c0_sn(c0_sn), .c0_result(c0_result), .c0_next(c0_next),
    .c0_taken(c0_taken), .c1_valid(cdb1_valid), .c1_sn(c1_sn), .c1_result(c1_result), .c1_next(adder_313),
    .c1_taken(1'b0), .full(ROB2_full_201), .count(rob2_count), .head_valid(ROB2_head_valid_203),
    .head_done(ROB2_head_done_204), .head_op(ROB2_head_op_205), .head_rd_new(ROB2_head_rd_new_206),
    .head_rd_old(ROB2_head_rd_old_207), .head_rd_logic(ROB2_head_rd_logic_208), .head_rw(ROB2_head_rw_209),
    .head_pc(ROB2_head_pc_210), .head_sn(ROB2_head_sn_211), .head_pred_next(ROB2_head_pred_next_212),
    .head_result(ROB2_head_result_213), .head_next(ROB2_head_next_214), .head_taken(ROB2_head_taken_215));
  or or_6 (or_216, RS0_full_109, ROB0_full_119);
  not not_6 (not_217, or_216);
  or u_or_7 (or_218, RS1_full_150, ROB1_full_160);
  not not_7 (not_219, or_218);
  or or_8 (or_220, RS2_full_191, ROB2_full_201);
  not not_8 (not_221, or_220);
  Multiplexer #(.width(2), .select(1), .enable("false")) multiplexer_47 (
    .in0(2'b01), .in1(2'b00), .out(mux_224), .sel(not_217));
  Multiplexer #(.width(2), .select(1), .enable("false")) multiplexer_48 (
    .in0(mux_224), .in1(2'b10), .out(mux_226), .sel(decode0_mem_37));
  or or_9 (or_227, not_217, not_219);
  Multiplexer #(.width(1), .select(1), .enable("false")) multiplexer_49 (
    .in0(or_227), .in1(not_221), .out(mux_228), .sel(decode0_mem_37));
  and u_and_6 (and_229, and_6, fetch_valid0_27);
  and and_7 (and_230, and_229, rename_available0_66);
  and and_8 (accept0, and_230, mux_228);
  Comparator #(.width(2), .mode("unsigned")) comparator_3 (
    .a(mux_226), .b(2'b00), .gt(gt_232), .eq(eq_233), .lt(lt_234));
  and and_9 (and_235, accept0, eq_233);
  not not_9 (not_236, and_235);
  and and_10 (and_237, not_217, not_236);
  Comparator #(.width(2), .mode("unsigned")) comparator_4 (
    .a(mux_226), .b(2'b01), .gt(gt_238), .eq(eq_239), .lt(lt_240));
  and and_11 (and_241, accept0, eq_239);
  not not_10 (not_242, and_241);
  and and_12 (and_243, not_219, not_242);
  Comparator #(.width(2), .mode("unsigned")) comparator_5 (
    .a(mux_226), .b(2'b10), .gt(gt_244), .eq(eq_245), .lt(lt_246));
  and and_13 (and_247, accept0, eq_245);
  not not_11 (not_248, and_247);
  and and_14 (and_249, not_221, not_248);
  Multiplexer #(.width(2), .select(1), .enable("false")) multiplexer_50 (
    .in0(2'b00), .in1(2'b01), .out(mux_250), .sel(and_243));
  Multiplexer #(.width(2), .select(1), .enable("false")) multiplexer_51 (
    .in0(mux_250), .in1(2'b10), .out(mux_251), .sel(decode1_mem_55));
  or or_10 (or_252, and_237, and_243);
  Multiplexer #(.width(1), .select(1), .enable("false")) multiplexer_52 (
    .in0(or_252), .in1(and_249), .out(mux_253), .sel(decode1_mem_55));
  and and_15 (and_254, accept0, fetch_valid1_28);
  and and_16 (and_255, and_254, rename_available1_67);
  and and_17 (accept1, and_255, mux_253);
  Comparator #(.width(2), .mode("unsigned")) comparator_6 (
    .a(mux_251), .b(2'b00), .gt(gt_257), .eq(eq_258), .lt(lt_259));
  and and_18 (and_260, accept1, eq_258);
  Comparator #(.width(2), .mode("unsigned")) comparator_7 (
    .a(mux_251), .b(2'b01), .gt(gt_261), .eq(eq_262), .lt(lt_263));
  and and_19 (and_264, accept1, eq_262);
  Comparator #(.width(2), .mode("unsigned")) comparator_8 (
    .a(mux_251), .b(2'b10), .gt(gt_265), .eq(eq_266), .lt(lt_267));
  and and_20 (and_268, accept1, eq_266);
  ALU ALU0 (
    .op(RS0_ex_op_112), .a(RS0_ex_a_117), .b(RS0_ex_b_118), .imm(RS0_ex_imm_114), .pc(RS0_ex_pc_115),
    .result(ALU0_result_269), .next(ALU0_next_270), .target(ALU0_target_271), .taken(ALU0_taken_272),
    .addr(ALU0_addr_273));
  ALU ALU1 (
    .op(RS1_ex_op_153), .a(RS1_ex_a_158), .b(RS1_ex_b_159), .imm(RS1_ex_imm_155), .pc(RS1_ex_pc_156),
    .result(ALU1_result_274), .next(ALU1_next_275), .target(ALU1_target_276), .taken(ALU1_taken_277),
    .addr(ALU1_addr_278));
  and and_21 (and_279, and_6, RS0_ex_valid_111);
  not not_12 (not_280, and_279);
  and and_22 (and_281, and_6, RS1_ex_valid_152);
  and and_23 (and_282, and_281, not_280);
  or or_11 (cdb0_valid, and_279, and_282);
  Multiplexer #(.width(6), .select(1), .enable("false")) multiplexer_53 (
    .in0(RS1_ex_rd_154), .in1(RS0_ex_rd_113), .out(c0_rd), .sel(and_279));
  Multiplexer #(.width(8), .select(1), .enable("false")) multiplexer_54 (
    .in0(RS1_ex_sn_157), .in1(RS0_ex_sn_116), .out(c0_sn), .sel(and_279));
  Multiplexer #(.width(16), .select(1), .enable("false")) multiplexer_55 (
    .in0(ALU1_result_274), .in1(ALU0_result_269), .out(c0_result), .sel(and_279));
  Multiplexer #(.width(16), .select(1), .enable("false")) multiplexer_56 (
    .in0(ALU1_next_275), .in1(ALU0_next_270), .out(c0_next), .sel(and_279));
  Multiplexer #(.width(1), .select(1), .enable("false")) multiplexer_57 (
    .in0(ALU1_taken_277), .in1(ALU0_taken_272), .out(c0_taken), .sel(and_279));
  Adder #(.width(16)) adder_5 (.a(RS2_ex_a_199), .b(RS2_ex_imm_196), .out(adder_289), .cin(1'b0));  // open: cout
  Comparator #(.width(4), .mode("unsigned")) comparator_9 (
    .a(RS2_ex_op_194), .b(4'b1001), .gt(gt_291), .eq(eq_292), .lt(lt_293));
  and and_24 (and_294, cdb1_valid, eq_292);
  StoreBuffer stores (
    .clk(clk), .rst(rst), .enable(and_6), .clear(or_7), .push(and_294), .addr(adder_289),
    .data(RS2_ex_b_200), .sn(c1_sn), .load_addr(adder_289), .load_sn(c1_sn), .commit(and_389),
    .commit_sn(commit_sn), .full(stores_full_295), .count(sb_count), .forward(stores_forward_297),
    .forward_data(stores_forward_data_298), .commit_found(stores_commit_found_299),
    .commit_addr(stores_commit_addr_300), .commit_data(stores_commit_data_301));
  DataMemory memory (
    .clk(clk), .rst(rst), .read_addr(adder_289), .commit(and_389), .write_addr(stores_commit_addr_300),
    .write_data(stores_commit_data_301), .debug_addr(debug_addr), .data(memory_data_302),
    .debug_data(memory_debug));
  not not_13 (not_304, and_389);
  not not_14 (not_305, stores_full_295);
  Multiplexer #(.width(1), .select(1), .enable("false")) multiplexer_58 (
    .in0(not_304), .in1(not_305), .out(mux_306), .sel(eq_292));
  and and_25 (and_307, and_6, RS2_ex_valid_193);
  and and_26 (cdb1_valid, and_307, mux_306);
  Multiplexer #(.width(6), .select(1), .enable("false")) multiplexer_59 (
    .in0(RS2_ex_rd_195), .in1({6{1'b0}}), .out(c1_rd), .sel(eq_292));
  Multiplexer #(.width(16), .select(1), .enable("false")) multiplexer_60 (
    .in0(memory_data_302), .in1(stores_forward_data_298), .out(c1_result), .sel(stores_forward_297));
  Adder #(.width(16)) adder_6 (.a(RS2_ex_pc_197), .b(16'h1), .out(adder_313), .cin(1'b0));  // open: cout
  Comparator #(.width(8), .mode("unsigned")) comparator_10 (
    .a(ROB0_head_sn_129), .b(commit_sn), .gt(gt_314), .eq(eq_315), .lt(lt_316));
  and and_27 (and_317, and_6, ROB0_head_valid_121);
  and and_28 (and_318, and_317, ROB0_head_done_122);
  and and_29 (and_319, and_318, eq_315);
  Comparator #(.width(8), .mode("unsigned")) comparator_11 (
    .a(ROB1_head_sn_170), .b(commit_sn), .gt(gt_320), .eq(eq_321), .lt(lt_322));
  and and_30 (and_323, and_6, ROB1_head_valid_162);
  and and_31 (and_324, and_323, ROB1_head_done_163);
  and and_32 (and_325, and_324, eq_321);
  Comparator #(.width(8), .mode("unsigned")) comparator_12 (
    .a(ROB2_head_sn_211), .b(commit_sn), .gt(gt_326), .eq(eq_327), .lt(lt_328));
  and and_33 (and_329, and_6, ROB2_head_valid_203);
  and and_34 (and_330, and_329, ROB2_head_done_204);
  and and_35 (and_331, and_330, eq_327);
  or or_12 (or_332, and_319, and_325);
  or or_13 (commit_valid, or_332, and_331);
  Multiplexer #(.width(4), .select(1), .enable("false")) multiplexer_61 (
    .in0(ROB2_head_op_205), .in1(ROB1_head_op_164), .out(mux_334), .sel(and_325));
  Multiplexer #(.width(4), .select(1), .enable("false")) multiplexer_62 (
    .in0(mux_334), .in1(ROB0_head_op_123), .out(commit_op), .sel(and_319));
  Multiplexer #(.width(6), .select(1), .enable("false")) multiplexer_63 (
    .in0(ROB2_head_rd_new_206), .in1(ROB1_head_rd_new_165), .out(mux_336), .sel(and_325));
  Multiplexer #(.width(6), .select(1), .enable("false")) multiplexer_64 (
    .in0(mux_336), .in1(ROB0_head_rd_new_124), .out(mux_337), .sel(and_319));
  Multiplexer #(.width(6), .select(1), .enable("false")) multiplexer_65 (
    .in0(ROB2_head_rd_old_207), .in1(ROB1_head_rd_old_166), .out(mux_338), .sel(and_325));
  Multiplexer #(.width(6), .select(1), .enable("false")) multiplexer_66 (
    .in0(mux_338), .in1(ROB0_head_rd_old_125), .out(mux_339), .sel(and_319));
  Multiplexer #(.width(3), .select(1), .enable("false")) multiplexer_67 (
    .in0(ROB2_head_rd_logic_208), .in1(ROB1_head_rd_logic_167), .out(mux_340), .sel(and_325));
  Multiplexer #(.width(3), .select(1), .enable("false")) multiplexer_68 (
    .in0(mux_340), .in1(ROB0_head_rd_logic_126), .out(mux_341), .sel(and_319));
  Multiplexer #(.width(1), .select(1), .enable("false")) multiplexer_69 (
    .in0(ROB2_head_rw_209), .in1(ROB1_head_rw_168), .out(mux_342), .sel(and_325));
  Multiplexer #(.width(1), .select(1), .enable("false")) multiplexer_70 (
    .in0(mux_342), .in1(ROB0_head_rw_127), .out(mux_343), .sel(and_319));
  Multiplexer #(.width(16), .select(1), .enable("false")) multiplexer_71 (
    .in0(ROB2_head_pc_210), .in1(ROB1_head_pc_169), .out(mux_344), .sel(and_325));
  Multiplexer #(.width(16), .select(1), .enable("false")) multiplexer_72 (
    .in0(mux_344), .in1(ROB0_head_pc_128), .out(commit_pc), .sel(and_319));
  Multiplexer #(.width(8), .select(1), .enable("false")) multiplexer_73 (
    .in0(ROB2_head_sn_211), .in1(ROB1_head_sn_170), .out(mux_346), .sel(and_325));
  Multiplexer #(.width(8), .select(1), .enable("false")) multiplexer_74 (
    .in0(mux_346), .in1(ROB0_head_sn_129), .out(mux_347), .sel(and_319));
  Multiplexer #(.width(16), .select(1), .enable("false")) multiplexer_75 (
    .in0(ROB2_head_pred_next_212), .in1(ROB1_head_pred_next_171), .out(mux_348), .sel(and_325));
  Multiplexer #(.width(16), .select(1), .enable("false")) multiplexer_76 (
    .in0(mux_348), .in1(ROB0_head_pred_next_130), .out(mux_349), .sel(and_319));
  Multiplexer #(.width(16), .select(1), .enable("false")) multiplexer_77 (
    .in0(ROB2_head_result_213), .in1(ROB1_head_result_172), .out(mux_350), .sel(and_325));
  Multiplexer #(.width(16), .select(1), .enable("false")) multiplexer_78 (
    .in0(mux_350), .in1(ROB0_head_result_131), .out(commit_result), .sel(and_319));
  Multiplexer #(.width(16), .select(1), .enable("false")) multiplexer_79 (
    .in0(ROB2_head_next_214), .in1(ROB1_head_next_173), .out(mux_352), .sel(and_325));
  Multiplexer #(.width(16), .select(1), .enable("false")) multiplexer_80 (
    .in0(mux_352), .in1(ROB0_head_next_132), .out(mux_353), .sel(and_319));
  Multiplexer #(.width(1), .select(1), .enable("false")) multiplexer_81 (
    .in0(ROB2_head_taken_215), .in1(ROB1_head_taken_174), .out(mux_354), .sel(and_325));
  Multiplexer #(.width(1), .select(1), .enable("false")) multiplexer_82 (
    .in0(mux_354), .in1(ROB0_head_taken_133), .out(mux_355), .sel(and_319));
  Comparator #(.width(4), .mode("unsigned")) comparator_13 (
    .a(commit_op), .b(4'b1010), .gt(gt_357), .eq(eq_358), .lt(lt_359));
  Comparator #(.width(4), .mode("unsigned")) comparator_14 (
    .a(commit_op), .b(4'b1011), .gt(gt_361), .eq(eq_362), .lt(lt_363));
  Comparator #(.width(4), .mode("unsigned")) comparator_15 (
    .a(commit_op), .b(4'b1100), .gt(gt_365), .eq(eq_366), .lt(lt_367));
  Comparator #(.width(4), .mode("unsigned")) comparator_16 (
    .a(commit_op), .b(4'b1101), .gt(gt_369), .eq(eq_370), .lt(lt_371));
  or or_14 (or_372, eq_358, eq_362);
  or or_15 (or_373, or_372, eq_366);
  or or_16 (or_374, or_373, eq_370);
  Comparator #(.width(16), .mode("unsigned")) comparator_17 (
    .a(mux_349), .b(mux_353), .gt(gt_375), .eq(eq_376), .lt(lt_377));
  not not_15 (not_378, eq_376);
  and and_36 (and_379, commit_valid, or_374);
  and and_37 (and_380, and_379, not_378);
  Comparator #(.width(4), .mode("unsigned")) comparator_18 (
    .a(commit_op), .b(4'b1111), .gt(gt_382), .eq(eq_383), .lt(lt_384));
  and and_38 (and_385, commit_valid, eq_383);
  Comparator #(.width(4), .mode("unsigned")) comparator_19 (
    .a(commit_op), .b(4'b1001), .gt(gt_386), .eq(eq_387), .lt(lt_388));
  and and_39 (and_389, commit_valid, eq_387);
  and and_40 (and_390, cdb0_valid, cdb1_valid);
  Adder #(.width(32)) adder_7 (.a(cycles), .b(32'h1), .out(adder_392), .cin(1'b0));  // open: cout
  Register #(.width(32)) reg_cycles (.D(adder_392), .en(and_4), .Q(cycles), .clk(clk), .clr(rst));
  Adder #(.width(32)) adder_8 (.a(committed), .b(32'h1), .out(adder_393), .cin(1'b0));  // open: cout
  Register #(.width(32)) reg_committed (.D(adder_393), .en(commit_valid), .Q(committed), .clk(clk), .clr(rst));
  assign ext_394 = {{30{1'b0}}, issue_count};  // Bit_Extender bit_extender_4
  Adder #(.width(32)) adder_9 (.a(dispatched), .b(ext_394), .out(adder_395), .cin(1'b0));  // open: cout
  Register #(.width(32)) reg_dispatched (.D(adder_395), .en(and_6), .Q(dispatched), .clk(clk), .clr(rst));
  Adder #(.width(32)) u_adder_10 (.a(dual_issue), .b(32'h1), .out(adder_396), .cin(1'b0));  // open: cout
  Register #(.width(32)) reg_dual_issue (.D(adder_396), .en(accept1), .Q(dual_issue), .clk(clk), .clr(rst));
  Adder #(.width(32)) adder_11 (.a(recoveries), .b(32'h1), .out(adder_397), .cin(1'b0));  // open: cout
  Register #(.width(32)) reg_recoveries (.D(adder_397), .en(and_380), .Q(recoveries), .clk(clk), .clr(rst));
  Adder #(.width(32)) adder_12 (.a(dual_cdb), .b(32'h1), .out(adder_398), .cin(1'b0));  // open: cout
  Register #(.width(32)) reg_dual_cdb (.D(adder_398), .en(and_390), .Q(dual_cdb), .clk(clk), .clr(rst));
  not not_16 (not_399, accept0);
  and and_41 (stall, fetch_valid0_27, not_399);

  // Other names for the same wires on the sheet: adder_14[1:0] = issue_count; and_231 = accept0; and_256 = accept1;
  //   and_400 = stall; bp_we = and_379; branch_miss = and_380; c1_next[15:0] = adder_313; RS2_ex_sn_198[7:0] = c1_sn;
  //   commit_store = and_389; fetch_fetch_pc_29[15:0] = pc; halt_commit = and_385;
  //   memory_debug_data_303[15:0] = memory_debug; mux_284[5:0] = c0_rd; mux_285[7:0] = c0_sn;
  //   mux_286[15:0] = c0_result; mux_287[15:0] = c0_next; mux_288 = c0_taken; mux_310[5:0] = c1_rd;
  //   mux_311[15:0] = c1_result; c0_valid = cdb0_valid; or_283 = cdb0_valid; pop0 = and_319; pop1 = and_325;
  //   pop2 = and_331; recovery = flush; rename_r0_84[15:0] = r0; rename_r1_85[15:0] = r1; rename_r2_86[15:0] = r2;
  //   rename_r3_87[15:0] = r3; rename_r4_88[15:0] = r4; rename_r5_89[15:0] = r5; rename_r6_90[15:0] = r6;
  //   rename_r7_91[15:0] = r7; or_333 = commit_valid; retire = commit_valid; retire_next[15:0] = mux_353;
  //   mux_335[3:0] = commit_op; retire_op[3:0] = commit_op; mux_345[15:0] = commit_pc; retire_pc[15:0] = commit_pc;
  //   retire_pred_next[15:0] = mux_349; retire_rd_logic[2:0] = mux_341; retire_rd_new[5:0] = mux_337;
  //   retire_rd_old[5:0] = mux_339; mux_351[15:0] = commit_result; retire_result[15:0] = commit_result;
  //   retire_rw = mux_343; retire_sn[7:0] = mux_347; retire_taken = mux_355; retirement_sn[7:0] = commit_sn;
  //   ROB0_count_120[4:0] = rob0_count; ROB1_count_161[4:0] = rob1_count; ROB2_count_202[4:0] = rob2_count;
  //   RS0_count_110[4:0] = rs0_count; RS1_count_151[4:0] = rs1_count; RS2_count_192[4:0] = rs2_count;
  //   stores_count_296[3:0] = sb_count; take0 = and_279; take1 = and_282; and_308 = cdb1_valid; c1_valid = cdb1_valid;
  //   take2 = cdb1_valid; unit0_lane0 = and_235; unit0_lane1 = and_260; unit1_lane0 = and_241; unit1_lane1 = and_264;
  //   unit2_lane0 = and_247; unit2_lane1 = and_268

  // Notes on the sheet:
  //   Dual issue / out-of-order execute / precise ordered retirement
endmodule

module DecodeOne (
  input  [15:0] instr,
  input  [15:0] pc,
  input  pred,
  output [3:0] opcode,
  output [2:0] rd,
  output [2:0] rs1,
  output [2:0] rs2,
  output [15:0] imm,
  output rw,
  output mem,
  output store,
  output branch,
  output jump,
  output halt,
  output [56:0] packet
);

  wire eq_4, eq_8, eq_12, eq_16, eq_20, eq_24, eq_33, eq_37, eq_42, eq_46, eq_64, eq_68, gt_3, gt_7, gt_11,
       gt_15, gt_19, gt_23, gt_32, gt_36, gt_41, gt_45, gt_50, gt_54, gt_59, gt_63, gt_67, lt_5, lt_9, lt_13,
       lt_17, lt_21, lt_25, lt_34, lt_38, lt_43, lt_47, lt_52, lt_56, lt_61, lt_65, lt_69, or_26, or_27,
       or_28, or_29, or_30, or_70, or_71, or_72, or_73, or_75, or_76, or_77, or_87, or_88, or_89, or_90,
       or_91, or_92;
  wire [2:0] mux_82, mux_85, mux_111, mux_112, mux_113, mux_114, mux_115, mux_116, mux_117, mux_118, mux_119;
  wire [15:0] ext_95, ext_98, mux_96;

  Comparator #(.width(4), .mode("unsigned")) comparator_1 (
    .a(instr[15:12]), .b(4'b0001), .gt(gt_3), .eq(eq_4), .lt(lt_5));
  Comparator #(.width(4), .mode("unsigned")) comparator_2 (
    .a(instr[15:12]), .b(4'b0010), .gt(gt_7), .eq(eq_8), .lt(lt_9));
  Comparator #(.width(4), .mode("unsigned")) comparator_3 (
    .a(instr[15:12]), .b(4'b0011), .gt(gt_11), .eq(eq_12), .lt(lt_13));
  Comparator #(.width(4), .mode("unsigned")) comparator_4 (
    .a(instr[15:12]), .b(4'b0100), .gt(gt_15), .eq(eq_16), .lt(lt_17));
  Comparator #(.width(4), .mode("unsigned")) comparator_5 (
    .a(instr[15:12]), .b(4'b0101), .gt(gt_19), .eq(eq_20), .lt(lt_21));
  Comparator #(.width(4), .mode("unsigned")) comparator_6 (
    .a(instr[15:12]), .b(4'b0110), .gt(gt_23), .eq(eq_24), .lt(lt_25));
  or or_1 (or_26, eq_4, eq_8);
  or or_2 (or_27, or_26, eq_12);
  or or_3 (or_28, or_27, eq_16);
  or or_4 (or_29, or_28, eq_20);
  or or_5 (or_30, or_29, eq_24);
  Comparator #(.width(4), .mode("unsigned")) comparator_7 (
    .a(instr[15:12]), .b(4'b1010), .gt(gt_32), .eq(eq_33), .lt(lt_34));
  Comparator #(.width(4), .mode("unsigned")) comparator_8 (
    .a(instr[15:12]), .b(4'b1011), .gt(gt_36), .eq(eq_37), .lt(lt_38));
  or or_6 (branch, eq_33, eq_37);
  Comparator #(.width(4), .mode("unsigned")) comparator_9 (
    .a(instr[15:12]), .b(4'b1100), .gt(gt_41), .eq(eq_42), .lt(lt_43));
  Comparator #(.width(4), .mode("unsigned")) comparator_10 (
    .a(instr[15:12]), .b(4'b1101), .gt(gt_45), .eq(eq_46), .lt(lt_47));
  or or_7 (jump, eq_42, eq_46);
  Comparator #(.width(4), .mode("unsigned")) comparator_11 (
    .a(instr[15:12]), .b(4'b1001), .gt(gt_50), .eq(packet[31]), .lt(lt_52));
  Comparator #(.width(4), .mode("unsigned")) comparator_12 (
    .a(instr[15:12]), .b(4'b1000), .gt(gt_54), .eq(packet[38]), .lt(lt_56));
  or or_8 (mem, packet[38], packet[31]);
  Comparator #(.width(4), .mode("unsigned")) comparator_13 (
    .a(instr[15:12]), .b(4'b1111), .gt(gt_59), .eq(halt), .lt(lt_61));
  Comparator #(.width(4), .mode("unsigned")) comparator_14 (
    .a(instr[15:12]), .b(4'b0111), .gt(gt_63), .eq(eq_64), .lt(lt_65));
  Comparator #(.width(4), .mode("unsigned")) comparator_15 (
    .a(instr[15:12]), .b(4'b1110), .gt(gt_67), .eq(eq_68), .lt(lt_69));
  or or_9 (or_70, or_30, eq_64);
  or or_10 (or_71, or_70, packet[38]);
  or or_11 (or_72, or_71, eq_42);
  or or_12 (or_73, or_72, eq_46);
  or or_13 (packet[29], or_73, eq_68);
  or or_14 (or_75, branch, packet[31]);
  or or_15 (or_76, or_71, eq_46);
  or or_16 (or_77, or_76, eq_68);
  Multiplexer #(.width(3), .select(1), .enable("false")) multiplexer_1 (
    .in0(3'b000), .in1(instr[11:9]), .out(packet[6:4]), .sel(packet[29]));
  Multiplexer #(.width(3), .select(1), .enable("false")) multiplexer_2 (
    .in0(3'b000), .in1(instr[8:6]), .out(mux_82), .sel(or_77));
  Multiplexer #(.width(3), .select(1), .enable("false")) multiplexer_3 (
    .in0(mux_82), .in1(instr[11:9]), .out(packet[9:7]), .sel(or_75));
  Multiplexer #(.width(3), .select(1), .enable("false")) multiplexer_4 (
    .in0(3'b000), .in1(instr[5:3]), .out(mux_85), .sel(or_30));
  Multiplexer #(.width(3), .select(1), .enable("false")) multiplexer_5 (
    .in0(mux_85), .in1(instr[8:6]), .out(packet[12:10]), .sel(or_75));
  or or_17 (or_87, eq_64, packet[38]);
  or or_18 (or_88, or_87, packet[31]);
  or or_19 (or_89, or_88, eq_33);
  or or_20 (or_90, or_89, eq_37);
  or or_21 (or_91, or_90, eq_46);
  or or_22 (or_92, or_91, eq_68);
  assign ext_95 = {{10{instr[5]}}, instr[5:0]};  // Bit_Extender bit_extender_1
  Multiplexer #(.width(16), .select(1), .enable("false")) multiplexer_6 (
    .in0({16{1'b0}}), .in1(ext_95), .out(mux_96), .sel(or_92));
  assign ext_98 = {{7{instr[8]}}, instr[8:0]};  // Bit_Extender bit_extender_2
  Multiplexer #(.width(16), .select(1), .enable("false")) multiplexer_7 (
    .in0(mux_96), .in1(ext_98), .out(imm), .sel(eq_42));
  Multiplexer #(.width(3), .select(1), .enable("false")) multiplexer_8 (
    .in0(3'b001), .in1(3'b010), .out(mux_111), .sel(instr[12]));
  Multiplexer #(.width(3), .select(1), .enable("false")) multiplexer_9 (
    .in0(3'b000), .in1(mux_111), .out(mux_112), .sel(instr[13]));
  Multiplexer #(.width(3), .select(1), .enable("false")) multiplexer_10 (
    .in0(3'b011), .in1(3'b100), .out(mux_113), .sel(instr[12]));
  Multiplexer #(.width(3), .select(1), .enable("false")) multiplexer_11 (
    .in0(3'b101), .in1(3'b000), .out(mux_114), .sel(instr[12]));
  Multiplexer #(.width(3), .select(1), .enable("false")) multiplexer_12 (
    .in0(mux_113), .in1(mux_114), .out(mux_115), .sel(instr[13]));
  Multiplexer #(.width(3), .select(1), .enable("false")) multiplexer_13 (
    .in0(mux_112), .in1(mux_115), .out(mux_116), .sel(instr[14]));
  Multiplexer #(.width(3), .select(1), .enable("false")) multiplexer_14 (
    .in0(3'b000), .in1(3'b001), .out(mux_117), .sel(instr[13]));
  Multiplexer #(.width(3), .select(1), .enable("false")) multiplexer_15 (
    .in0(3'b000), .in1(mux_114), .out(mux_118), .sel(instr[13]));
  Multiplexer #(.width(3), .select(1), .enable("false")) multiplexer_16 (
    .in0(mux_117), .in1(mux_118), .out(mux_119), .sel(instr[14]));
  Multiplexer #(.width(3), .select(1), .enable("false")) multiplexer_17 (
    .in0(mux_116), .in1(mux_119), .out(packet[36:34]), .sel(instr[15]));
  or or_23 (packet[37], or_88, eq_68);

  assign opcode = instr[15:12];
  assign {packet[56:39], packet[33:32], packet[30], packet[28:13], packet[3:0]} = {pred, pc, halt, jump, branch, packet[38], imm, instr[15:12]};
  assign rd = packet[6:4];
  assign rs1 = packet[9:7];
  assign rs2 = packet[12:10];
  assign rw = packet[29];
  assign store = packet[31];

  // Other names for the same wires on the sheet: slice_94[5:0] = instr[5:0]; slice_97[8:0] = instr[8:0];
  //   slice_84[2:0] = instr[5:3]; slice_81[2:0] = instr[8:6]; slice_79[2:0] = instr[11:9]; or_57 = mem;
  //   pack_122[56:0] = {pred, pc, halt, packet[38:34], jump, branch, packet[31], packet[38], packet[29], imm, packet[12:4], instr[15:12]};
  //   slice_1[3:0] = instr[15:12]; slice_105[2:0] = instr[14:12]; slice_107[1:0] = instr[13:12];
  //   slice_109 = instr[12]; slice_110 = instr[13]; slice_108 = instr[14]; slice_106 = instr[15];
  //   mux_80[2:0] = packet[6:4]; mux_83[2:0] = packet[9:7]; mux_86[2:0] = packet[12:10]; mux_99[15:0] = imm;
  //   or_74 = packet[29]; eq_51 = packet[31]; or_39 = branch; or_48 = jump; mux_120[2:0] = packet[36:34];
  //   or_121 = packet[37]; eq_55 = packet[38]; eq_60 = halt

  // Notes on the sheet:
  //   16-bit ISA decode / 57-bit control packet
endmodule
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module ROB (
  input  clk,
  input  rst,
  input  clear,
  input  enable,
  input  wr,
  input  pop,
  input  [3:0] op,
  input  [5:0] rd_new,
  input  [5:0] rd_old,
  input  [2:0] rd_logic,
  input  rw,
  input  [15:0] pc,
  input  [7:0] sn,
  input  [15:0] pred_next,
  input  c0_valid,
  input  [7:0] c0_sn,
  input  [15:0] c0_result,
  input  [15:0] c0_next,
  input  c0_taken,
  input  c1_valid,
  input  [7:0] c1_sn,
  input  [15:0] c1_result,
  input  [15:0] c1_next,
  input  c1_taken,
  output full,
  output [4:0] count,
  output head_valid,
  output head_done,
  output [3:0] head_op,
  output [5:0] head_rd_new,
  output [5:0] head_rd_old,
  output [2:0] head_rd_logic,
  output head_rw,
  output [15:0] head_pc,
  output [7:0] head_sn,
  output [15:0] head_pred_next,
  output [15:0] head_result,
  output [15:0] head_next,
  output head_taken
);

  wire and_12, and_13, and_14, and_15, and_30, and_34, and_51, and_55, and_73, and_77, and_95, and_99,
       and_117, and_121, and_139, and_143, and_161, and_165, and_183, and_187, and_205, and_209, and_227,
       and_231, and_249, and_253, and_271, and_275, and_293, and_297, and_315, and_319, and_337, and_341,
       and_359, and_363, entry00_done_36, entry00_rw_41, entry00_taken_47, entry00_valid_35, entry01_done_57,
       entry01_rw_62, entry01_taken_68, entry01_valid_56, entry02_done_79, entry02_rw_84, entry02_taken_90,
       entry02_valid_78, entry03_done_101, entry03_rw_106, entry03_taken_112, entry03_valid_100,
       entry04_done_123, entry04_rw_128, entry04_taken_134, entry04_valid_122, entry05_done_145,
       entry05_rw_150, entry05_taken_156, entry05_valid_144, entry06_done_167, entry06_rw_172,
       entry06_taken_178, entry06_valid_166, entry07_done_189, entry07_rw_194, entry07_taken_200,
       entry07_valid_188, entry08_done_211, entry08_rw_216, entry08_taken_222, entry08_valid_210,
       entry09_done_233, entry09_rw_238, entry09_taken_244, entry09_valid_232, entry10_done_255,
       entry10_rw_260, entry10_taken_266, entry10_valid_254, entry11_done_277, entry11_rw_282,
       entry11_taken_288, entry11_valid_276, entry12_done_299, entry12_rw_304, entry12_taken_310,
       entry12_valid_298, entry13_done_321, entry13_rw_326, entry13_taken_332, entry13_valid_320,
       entry14_done_343, entry14_rw_348, entry14_taken_354, entry14_valid_342, entry15_done_365,
       entry15_rw_370, entry15_taken_376, entry15_valid_364, eq_8, eq_28, eq_32, eq_49, eq_53, eq_71, eq_75,
       eq_93, eq_97, eq_115, eq_119, eq_137, eq_141, eq_159, eq_163, eq_181, eq_185, eq_203, eq_207, eq_225,
       eq_229, eq_247, eq_251, eq_269, eq_273, eq_291, eq_295, eq_313, eq_317, eq_335, eq_339, eq_357,
       eq_361, gt_3, gt_7, gt_27, gt_31, gt_48, gt_52, gt_70, gt_74, gt_92, gt_96, gt_114, gt_118, gt_136,
       gt_140, gt_158, gt_162, gt_180, gt_184, gt_202, gt_206, gt_224, gt_228, gt_246, gt_250, gt_268,
       gt_272, gt_290, gt_294, gt_312, gt_316, gt_334, gt_338, gt_356, gt_360, lt_5, lt_9, lt_29, lt_33,
       lt_50, lt_54, lt_72, lt_76, lt_94, lt_98, lt_116, lt_120, lt_138, lt_142, lt_160, lt_164, lt_182,
       lt_186, lt_204, lt_208, lt_226, lt_230, lt_248, lt_252, lt_270, lt_274, lt_292, lt_296, lt_314,
       lt_318, lt_336, lt_340, lt_358, lt_362, mux_383, mux_384, mux_385, mux_386, mux_387, mux_388, mux_389,
       mux_390, mux_391, mux_392, mux_393, mux_394, mux_395, mux_396, mux_397, mux_399, mux_400, mux_401,
       mux_402, mux_403, mux_404, mux_405, mux_406, mux_407, mux_408, mux_409, mux_410, mux_411, mux_412,
       mux_474, mux_475, mux_476, mux_477, mux_478, mux_479, mux_480, mux_481, mux_482, mux_483, mux_484,
       mux_485, mux_486, mux_487, mux_564, mux_565, mux_566, mux_567, mux_568, mux_569, mux_570, mux_571,
       mux_572, mux_573, mux_574, mux_575, mux_576, mux_577, not_10, not_11, or_1, xor_25;
  wire [2:0] entry00_rd_logic_40, entry01_rd_logic_61, entry02_rd_logic_83, entry03_rd_logic_105,
       entry04_rd_logic_127, entry05_rd_logic_149, entry06_rd_logic_171, entry07_rd_logic_193,
       entry08_rd_logic_215, entry09_rd_logic_237, entry10_rd_logic_259, entry11_rd_logic_281,
       entry12_rd_logic_303, entry13_rd_logic_325, entry14_rd_logic_347, entry15_rd_logic_369, mux_459,
       mux_460, mux_461, mux_462, mux_463, mux_464, mux_465, mux_466, mux_467, mux_468, mux_469, mux_470,
       mux_471, mux_472;
  wire [3:0] adder_17, adder_19, entry00_op_37, entry01_op_58, entry02_op_80, entry03_op_102, entry04_op_124,
       entry05_op_146, entry06_op_168, entry07_op_190, entry08_op_212, entry09_op_234, entry10_op_256,
       entry11_op_278, entry12_op_300, entry13_op_322, entry14_op_344, entry15_op_366, mux_414, mux_415,
       mux_416, mux_417, mux_418, mux_419, mux_420, mux_421, mux_422, mux_423, mux_424, mux_425, mux_426,
       mux_427, Q_head, Q_tail;
  wire [4:0] adder_21, adder_23, mux_24;
  wire [5:0] entry00_rd_new_38, entry00_rd_old_39, entry01_rd_new_59, entry01_rd_old_60, entry02_rd_new_81,
       entry02_rd_old_82, entry03_rd_new_103, entry03_rd_old_104, entry04_rd_new_125, entry04_rd_old_126,
       entry05_rd_new_147, entry05_rd_old_148, entry06_rd_new_169, entry06_rd_old_170, entry07_rd_new_191,
       entry07_rd_old_192, entry08_rd_new_213, entry08_rd_old_214, entry09_rd_new_235, entry09_rd_old_236,
       entry10_rd_new_257, entry10_rd_old_258, entry11_rd_new_279, entry11_rd_old_280, entry12_rd_new_301,
       entry12_rd_old_302, entry13_rd_new_323, entry13_rd_old_324, entry14_rd_new_345, entry14_rd_old_346,
       entry15_rd_new_367, entry15_rd_old_368, mux_429, mux_430, mux_431, mux_432, mux_433, mux_434, mux_435,
       mux_436, mux_437, mux_438, mux_439, mux_440, mux_441, mux_442, mux_444, mux_445, mux_446, mux_447,
       mux_448, mux_449, mux_450, mux_451, mux_452, mux_453, mux_454, mux_455, mux_456, mux_457;
  wire [7:0] entry00_sn_43, entry01_sn_64, entry02_sn_86, entry03_sn_108, entry04_sn_130, entry05_sn_152,
       entry06_sn_174, entry07_sn_196, entry08_sn_218, entry09_sn_240, entry10_sn_262, entry11_sn_284,
       entry12_sn_306, entry13_sn_328, entry14_sn_350, entry15_sn_372, mux_504, mux_505, mux_506, mux_507,
       mux_508, mux_509, mux_510, mux_511, mux_512, mux_513, mux_514, mux_515, mux_516, mux_517;
  wire [15:0] entry00_next_46, entry00_pc_42, entry00_pred_next_44, entry00_result_45, entry01_next_67,
       entry01_pc_63, entry01_pred_next_65, entry01_result_66, entry02_next_89, entry02_pc_85,
       entry02_pred_next_87, entry02_result_88, entry03_next_111, entry03_pc_107, entry03_pred_next_109,
       entry03_result_110, entry04_next_133, entry04_pc_129, entry04_pred_next_131, entry04_result_132,
       entry05_next_155, entry05_pc_151, entry05_pred_next_153, entry05_result_154, entry06_next_177,
       entry06_pc_173, entry06_pred_next_175, entry06_result_176, entry07_next_199, entry07_pc_195,
       entry07_pred_next_197, entry07_result_198, entry08_next_221, entry08_pc_217, entry08_pred_next_219,
       entry08_result_220, entry09_next_243, entry09_pc_239, entry09_pred_next_241, entry09_result_242,
       entry10_next_265, entry10_pc_261, entry10_pred_next_263, entry10_result_264, entry11_next_287,
       entry11_pc_283, entry11_pred_next_285, entry11_result_286, entry12_next_309, entry12_pc_305,
       entry12_pred_next_307, entry12_result_308, entry13_next_331, entry13_pc_327, entry13_pred_next_329,
       entry13_result_330, entry14_next_353, entry14_pc_349, entry14_pred_next_351, entry14_result_352,
       entry15_next_375, entry15_pc_371, entry15_pred_next_373, entry15_result_374, mux_489, mux_490,
       mux_491, mux_492, mux_493, mux_494, mux_495, mux_496, mux_497, mux_498, mux_499, mux_500, mux_501,
       mux_502, mux_519, mux_520, mux_521, mux_522, mux_523, mux_524, mux_525, mux_526, mux_527, mux_528,
       mux_529, mux_530, mux_531, mux_532, mux_534, mux_535, mux_536, mux_537, mux_538, mux_539, mux_540,
       mux_541, mux_542, mux_543, mux_544, mux_545, mux_546, mux_547, mux_549, mux_550, mux_551, mux_552,
       mux_553, mux_554, mux_555, mux_556, mux_557, mux_558, mux_559, mux_560, mux_561, mux_562;

  or u_or_1 (or_1, rst, clear);
  Comparator #(.width(5), .mode("unsigned")) comparator_1 (.a(count), .b(5'b10000), .gt(gt_3), .eq(full), .lt(lt_5));
  Comparator #(.width(5), .mode("unsigned")) comparator_2 (.a(count), .b({5{1'b0}}), .gt(gt_7), .eq(eq_8), .lt(lt_9));
  not not_1 (not_10, eq_8);
  not not_2 (not_11, full);
  and and_1 (and_12, enable, wr);
  and and_2 (and_13, and_12, not_11);
  and and_3 (and_14, enable, pop);
  and and_4 (and_15, and_14, not_10);
  Adder #(.width(4)) adder_1 (.a(Q_head), .b(4'b0001), .out(adder_17), .cin(1'b0));  // open: cout
  Register #(.width(4)) reg_Q_head (.D(adder_17), .en(and_15), .Q(Q_head), .clk(clk), .clr(or_1));
  Adder #(.width(4)) adder_2 (.a(Q_tail), .b(4'b0001), .out(adder_19), .cin(1'b0));  // open: cout
  Register #(.width(4)) reg_Q_tail (.D(adder_19), .en(and_13), .Q(Q_tail), .clk(clk), .clr(or_1));
  Adder #(.width(5)) adder_3 (.a(count), .b({5{1'b1}}), .out(adder_21), .cin(1'b0));  // open: cout
  Adder #(.width(5)) adder_4 (.a(count), .b(5'b00001), .out(adder_23), .cin(1'b0));  // open: cout
  Multiplexer #(.width(5), .select(1), .enable("false")) multiplexer_1 (
    .in0(adder_21), .in1(adder_23), .out(mux_24), .sel(and_13));
  // XOR_Gate #(.width(1)) xor_1: pin names not known; wires that end beside it: and_13, and_15, xor_25
  Register #(.width(5)) reg_Q_count (.D(mux_24), .en(xor_25), .Q(count), .clk(clk), .clr(or_1));
  Comparator #(.width(4), .mode("unsigned")) comparator_3 (.a(Q_tail), .b(4'b0000), .gt(gt_27), .eq(eq_28), .lt(lt_29));
  and and_5 (and_30, and_13, eq_28);
  Comparator #(.width(4), .mode("unsigned")) comparator_4 (.a(Q_head), .b(4'b0000), .gt(gt_31), .eq(eq_32), .lt(lt_33));
  and and_6 (and_34, and_15, eq_32);
  ROB_Entry entry00 (
    .clk(clk), .rst(rst), .clear(clear), .enable(enable), .wr(and_30), .erase(and_34), .op(op),
    .rd_new(rd_new), .rd_old(rd_old), .rd_logic(rd_logic), .rw(rw), .pc(pc), .sn(sn), .pred_next(pred_next),
    .c0_valid(c0_valid), .c0_sn(c0_sn), .c0_result(c0_result), .c0_next(c0_next), .c0_taken(c0_taken),
    .c1_valid(c1_valid), .c1_sn(c1_sn), .c1_result(c1_result), .c1_next(c1_next), .c1_taken(c1_taken),
    .valid(entry00_valid_35), .done(entry00_done_36), .op_2(entry00_op_37), .rd_new_2(entry00_rd_new_38),
    .rd_old_2(entry00_rd_old_39), .rd_logic_2(entry00_rd_logic_40), .rw_2(entry00_rw_41),
    .pc_2(entry00_pc_42), .sn_2(entry00_sn_43), .pred_next_2(entry00_pred_next_44),
    .result(entry00_result_45), .next(entry00_next_46), .taken(entry00_taken_47));
  Comparator #(.width(4), .mode("unsigned")) comparator_5 (.a(Q_tail), .b(4'b0001), .gt(gt_48), .eq(eq_49), .lt(lt_50));
  and and_7 (and_51, and_13, eq_49);
  Comparator #(.width(4), .mode("unsigned")) comparator_6 (.a(Q_head), .b(4'b0001), .gt(gt_52), .eq(eq_53), .lt(lt_54));
  and and_8 (and_55, and_15, eq_53);
  ROB_Entry entry01 (
    .clk(clk), .rst(rst), .clear(clear), .enable(enable), .wr(and_51), .erase(and_55), .op(op),
    .rd_new(rd_new), .rd_old(rd_old), .rd_logic(rd_logic), .rw(rw), .pc(pc), .sn(sn), .pred_next(pred_next),
    .c0_valid(c0_valid), .c0_sn(c0_sn), .c0_result(c0_result), .c0_next(c0_next), .c0_taken(c0_taken),
    .c1_valid(c1_valid), .c1_sn(c1_sn), .c1_result(c1_result), .c1_next(c1_next), .c1_taken(c1_taken),
    .valid(entry01_valid_56), .done(entry01_done_57), .op_2(entry01_op_58), .rd_new_2(entry01_rd_new_59),
    .rd_old_2(entry01_rd_old_60), .rd_logic_2(entry01_rd_logic_61), .rw_2(entry01_rw_62),
    .pc_2(entry01_pc_63), .sn_2(entry01_sn_64), .pred_next_2(entry01_pred_next_65),
    .result(entry01_result_66), .next(entry01_next_67), .taken(entry01_taken_68));
  Comparator #(.width(4), .mode("unsigned")) comparator_7 (.a(Q_tail), .b(4'b0010), .gt(gt_70), .eq(eq_71), .lt(lt_72));
  and and_9 (and_73, and_13, eq_71);
  Comparator #(.width(4), .mode("unsigned")) comparator_8 (.a(Q_head), .b(4'b0010), .gt(gt_74), .eq(eq_75), .lt(lt_76));
  and and_10 (and_77, and_15, eq_75);
  ROB_Entry entry02 (
    .clk(clk), .rst(rst), .clear(clear), .enable(enable), .wr(and_73), .erase(and_77), .op(op),
    .rd_new(rd_new), .rd_old(rd_old), .rd_logic(rd_logic), .rw(rw), .pc(pc), .sn(sn), .pred_next(pred_next),
    .c0_valid(c0_valid), .c0_sn(c0_sn), .c0_result(c0_result), .c0_next(c0_next), .c0_taken(c0_taken),
    .c1_valid(c1_valid), .c1_sn(c1_sn), .c1_result(c1_result), .c1_next(c1_next), .c1_taken(c1_taken),
    .valid(entry02_valid_78), .done(entry02_done_79), .op_2(entry02_op_80), .rd_new_2(entry02_rd_new_81),
    .rd_old_2(entry02_rd_old_82), .rd_logic_2(entry02_rd_logic_83), .rw_2(entry02_rw_84),
    .pc_2(entry02_pc_85), .sn_2(entry02_sn_86), .pred_next_2(entry02_pred_next_87),
    .result(entry02_result_88), .next(entry02_next_89), .taken(entry02_taken_90));
  Comparator #(.width(4), .mode("unsigned")) comparator_9 (.a(Q_tail), .b(4'b0011), .gt(gt_92), .eq(eq_93), .lt(lt_94));
  and and_11 (and_95, and_13, eq_93);
  Comparator #(.width(4), .mode("unsigned")) comparator_10 (
    .a(Q_head), .b(4'b0011), .gt(gt_96), .eq(eq_97), .lt(lt_98));
  and u_and_12 (and_99, and_15, eq_97);
  ROB_Entry entry03 (
    .clk(clk), .rst(rst), .clear(clear), .enable(enable), .wr(and_95), .erase(and_99), .op(op),
    .rd_new(rd_new), .rd_old(rd_old), .rd_logic(rd_logic), .rw(rw), .pc(pc), .sn(sn), .pred_next(pred_next),
    .c0_valid(c0_valid), .c0_sn(c0_sn), .c0_result(c0_result), .c0_next(c0_next), .c0_taken(c0_taken),
    .c1_valid(c1_valid), .c1_sn(c1_sn), .c1_result(c1_result), .c1_next(c1_next), .c1_taken(c1_taken),
    .valid(entry03_valid_100), .done(entry03_done_101), .op_2(entry03_op_102), .rd_new_2(entry03_rd_new_103),
    .rd_old_2(entry03_rd_old_104), .rd_logic_2(entry03_rd_logic_105), .rw_2(entry03_rw_106),
    .pc_2(entry03_pc_107), .sn_2(entry03_sn_108), .pred_next_2(entry03_pred_next_109),
    .result(entry03_result_110), .next(entry03_next_111), .taken(entry03_taken_112));
  Comparator #(.width(4), .mode("unsigned")) comparator_11 (
    .a(Q_tail), .b(4'b0100), .gt(gt_114), .eq(eq_115), .lt(lt_116));
  and u_and_13 (and_117, and_13, eq_115);
  Comparator #(.width(4), .mode("unsigned")) comparator_12 (
    .a(Q_head), .b(4'b0100), .gt(gt_118), .eq(eq_119), .lt(lt_120));
  and u_and_14 (and_121, and_15, eq_119);
  ROB_Entry entry04 (
    .clk(clk), .rst(rst), .clear(clear), .enable(enable), .wr(and_117), .erase(and_121), .op(op),
    .rd_new(rd_new), .rd_old(rd_old), .rd_logic(rd_logic), .rw(rw), .pc(pc), .sn(sn), .pred_next(pred_next),
    .c0_valid(c0_valid), .c0_sn(c0_sn), .c0_result(c0_result), .c0_next(c0_next), .c0_taken(c0_taken),
    .c1_valid(c1_valid), .c1_sn(c1_sn), .c1_result(c1_result), .c1_next(c1_next), .c1_taken(c1_taken),
    .valid(entry04_valid_122), .done(entry04_done_123), .op_2(entry04_op_124), .rd_new_2(entry04_rd_new_125),
    .rd_old_2(entry04_rd_old_126), .rd_logic_2(entry04_rd_logic_127), .rw_2(entry04_rw_128),
    .pc_2(entry04_pc_129), .sn_2(entry04_sn_130), .pred_next_2(entry04_pred_next_131),
    .result(entry04_result_132), .next(entry04_next_133), .taken(entry04_taken_134));
  Comparator #(.width(4), .mode("unsigned")) comparator_13 (
    .a(Q_tail), .b(4'b0101), .gt(gt_136), .eq(eq_137), .lt(lt_138));
  and u_and_15 (and_139, and_13, eq_137);
  Comparator #(.width(4), .mode("unsigned")) comparator_14 (
    .a(Q_head), .b(4'b0101), .gt(gt_140), .eq(eq_141), .lt(lt_142));
  and and_16 (and_143, and_15, eq_141);
  ROB_Entry entry05 (
    .clk(clk), .rst(rst), .clear(clear), .enable(enable), .wr(and_139), .erase(and_143), .op(op),
    .rd_new(rd_new), .rd_old(rd_old), .rd_logic(rd_logic), .rw(rw), .pc(pc), .sn(sn), .pred_next(pred_next),
    .c0_valid(c0_valid), .c0_sn(c0_sn), .c0_result(c0_result), .c0_next(c0_next), .c0_taken(c0_taken),
    .c1_valid(c1_valid), .c1_sn(c1_sn), .c1_result(c1_result), .c1_next(c1_next), .c1_taken(c1_taken),
    .valid(entry05_valid_144), .done(entry05_done_145), .op_2(entry05_op_146), .rd_new_2(entry05_rd_new_147),
    .rd_old_2(entry05_rd_old_148), .rd_logic_2(entry05_rd_logic_149), .rw_2(entry05_rw_150),
    .pc_2(entry05_pc_151), .sn_2(entry05_sn_152), .pred_next_2(entry05_pred_next_153),
    .result(entry05_result_154), .next(entry05_next_155), .taken(entry05_taken_156));
  Comparator #(.width(4), .mode("unsigned")) comparator_15 (
    .a(Q_tail), .b(4'b0110), .gt(gt_158), .eq(eq_159), .lt(lt_160));
  and and_17 (and_161, and_13, eq_159);
  Comparator #(.width(4), .mode("unsigned")) comparator_16 (
    .a(Q_head), .b(4'b0110), .gt(gt_162), .eq(eq_163), .lt(lt_164));
  and and_18 (and_165, and_15, eq_163);
  ROB_Entry entry06 (
    .clk(clk), .rst(rst), .clear(clear), .enable(enable), .wr(and_161), .erase(and_165), .op(op),
    .rd_new(rd_new), .rd_old(rd_old), .rd_logic(rd_logic), .rw(rw), .pc(pc), .sn(sn), .pred_next(pred_next),
    .c0_valid(c0_valid), .c0_sn(c0_sn), .c0_result(c0_result), .c0_next(c0_next), .c0_taken(c0_taken),
    .c1_valid(c1_valid), .c1_sn(c1_sn), .c1_result(c1_result), .c1_next(c1_next), .c1_taken(c1_taken),
    .valid(entry06_valid_166), .done(entry06_done_167), .op_2(entry06_op_168), .rd_new_2(entry06_rd_new_169),
    .rd_old_2(entry06_rd_old_170), .rd_logic_2(entry06_rd_logic_171), .rw_2(entry06_rw_172),
    .pc_2(entry06_pc_173), .sn_2(entry06_sn_174), .pred_next_2(entry06_pred_next_175),
    .result(entry06_result_176), .next(entry06_next_177), .taken(entry06_taken_178));
  Comparator #(.width(4), .mode("unsigned")) comparator_17 (
    .a(Q_tail), .b(4'b0111), .gt(gt_180), .eq(eq_181), .lt(lt_182));
  and and_19 (and_183, and_13, eq_181);
  Comparator #(.width(4), .mode("unsigned")) comparator_18 (
    .a(Q_head), .b(4'b0111), .gt(gt_184), .eq(eq_185), .lt(lt_186));
  and and_20 (and_187, and_15, eq_185);
  ROB_Entry entry07 (
    .clk(clk), .rst(rst), .clear(clear), .enable(enable), .wr(and_183), .erase(and_187), .op(op),
    .rd_new(rd_new), .rd_old(rd_old), .rd_logic(rd_logic), .rw(rw), .pc(pc), .sn(sn), .pred_next(pred_next),
    .c0_valid(c0_valid), .c0_sn(c0_sn), .c0_result(c0_result), .c0_next(c0_next), .c0_taken(c0_taken),
    .c1_valid(c1_valid), .c1_sn(c1_sn), .c1_result(c1_result), .c1_next(c1_next), .c1_taken(c1_taken),
    .valid(entry07_valid_188), .done(entry07_done_189), .op_2(entry07_op_190), .rd_new_2(entry07_rd_new_191),
    .rd_old_2(entry07_rd_old_192), .rd_logic_2(entry07_rd_logic_193), .rw_2(entry07_rw_194),
    .pc_2(entry07_pc_195), .sn_2(entry07_sn_196), .pred_next_2(entry07_pred_next_197),
    .result(entry07_result_198), .next(entry07_next_199), .taken(entry07_taken_200));
  Comparator #(.width(4), .mode("unsigned")) comparator_19 (
    .a(Q_tail), .b(4'b1000), .gt(gt_202), .eq(eq_203), .lt(lt_204));
  and and_21 (and_205, and_13, eq_203);
  Comparator #(.width(4), .mode("unsigned")) comparator_20 (
    .a(Q_head), .b(4'b1000), .gt(gt_206), .eq(eq_207), .lt(lt_208));
  and and_22 (and_209, and_15, eq_207);
  ROB_Entry entry08 (
    .clk(clk), .rst(rst), .clear(clear), .enable(enable), .wr(and_205), .erase(and_209), .op(op),
    .rd_new(rd_new), .rd_old(rd_old), .rd_logic(rd_logic), .rw(rw), .pc(pc), .sn(sn), .pred_next(pred_next),
    .c0_valid(c0_valid), .c0_sn(c0_sn), .c0_result(c0_result), .c0_next(c0_next), .c0_taken(c0_taken),
    .c1_valid(c1_valid), .c1_sn(c1_sn), .c1_result(c1_result), .c1_next(c1_next), .c1_taken(c1_taken),
    .valid(entry08_valid_210), .done(entry08_done_211), .op_2(entry08_op_212), .rd_new_2(entry08_rd_new_213),
    .rd_old_2(entry08_rd_old_214), .rd_logic_2(entry08_rd_logic_215), .rw_2(entry08_rw_216),
    .pc_2(entry08_pc_217), .sn_2(entry08_sn_218), .pred_next_2(entry08_pred_next_219),
    .result(entry08_result_220), .next(entry08_next_221), .taken(entry08_taken_222));
  Comparator #(.width(4), .mode("unsigned")) comparator_21 (
    .a(Q_tail), .b(4'b1001), .gt(gt_224), .eq(eq_225), .lt(lt_226));
  and and_23 (and_227, and_13, eq_225);
  Comparator #(.width(4), .mode("unsigned")) comparator_22 (
    .a(Q_head), .b(4'b1001), .gt(gt_228), .eq(eq_229), .lt(lt_230));
  and and_24 (and_231, and_15, eq_229);
  ROB_Entry entry09 (
    .clk(clk), .rst(rst), .clear(clear), .enable(enable), .wr(and_227), .erase(and_231), .op(op),
    .rd_new(rd_new), .rd_old(rd_old), .rd_logic(rd_logic), .rw(rw), .pc(pc), .sn(sn), .pred_next(pred_next),
    .c0_valid(c0_valid), .c0_sn(c0_sn), .c0_result(c0_result), .c0_next(c0_next), .c0_taken(c0_taken),
    .c1_valid(c1_valid), .c1_sn(c1_sn), .c1_result(c1_result), .c1_next(c1_next), .c1_taken(c1_taken),
    .valid(entry09_valid_232), .done(entry09_done_233), .op_2(entry09_op_234), .rd_new_2(entry09_rd_new_235),
    .rd_old_2(entry09_rd_old_236), .rd_logic_2(entry09_rd_logic_237), .rw_2(entry09_rw_238),
    .pc_2(entry09_pc_239), .sn_2(entry09_sn_240), .pred_next_2(entry09_pred_next_241),
    .result(entry09_result_242), .next(entry09_next_243), .taken(entry09_taken_244));
  Comparator #(.width(4), .mode("unsigned")) comparator_23 (
    .a(Q_tail), .b(4'b1010), .gt(gt_246), .eq(eq_247), .lt(lt_248));
  and and_25 (and_249, and_13, eq_247);
  Comparator #(.width(4), .mode("unsigned")) comparator_24 (
    .a(Q_head), .b(4'b1010), .gt(gt_250), .eq(eq_251), .lt(lt_252));
  and and_26 (and_253, and_15, eq_251);
  ROB_Entry entry10 (
    .clk(clk), .rst(rst), .clear(clear), .enable(enable), .wr(and_249), .erase(and_253), .op(op),
    .rd_new(rd_new), .rd_old(rd_old), .rd_logic(rd_logic), .rw(rw), .pc(pc), .sn(sn), .pred_next(pred_next),
    .c0_valid(c0_valid), .c0_sn(c0_sn), .c0_result(c0_result), .c0_next(c0_next), .c0_taken(c0_taken),
    .c1_valid(c1_valid), .c1_sn(c1_sn), .c1_result(c1_result), .c1_next(c1_next), .c1_taken(c1_taken),
    .valid(entry10_valid_254), .done(entry10_done_255), .op_2(entry10_op_256), .rd_new_2(entry10_rd_new_257),
    .rd_old_2(entry10_rd_old_258), .rd_logic_2(entry10_rd_logic_259), .rw_2(entry10_rw_260),
    .pc_2(entry10_pc_261), .sn_2(entry10_sn_262), .pred_next_2(entry10_pred_next_263),
    .result(entry10_result_264), .next(entry10_next_265), .taken(entry10_taken_266));
  Comparator #(.width(4), .mode("unsigned")) comparator_25 (
    .a(Q_tail), .b(4'b1011), .gt(gt_268), .eq(eq_269), .lt(lt_270));
  and and_27 (and_271, and_13, eq_269);
  Comparator #(.width(4), .mode("unsigned")) comparator_26 (
    .a(Q_head), .b(4'b1011), .gt(gt_272), .eq(eq_273), .lt(lt_274));
  and and_28 (and_275, and_15, eq_273);
  ROB_Entry entry11 (
    .clk(clk), .rst(rst), .clear(clear), .enable(enable), .wr(and_271), .erase(and_275), .op(op),
    .rd_new(rd_new), .rd_old(rd_old), .rd_logic(rd_logic), .rw(rw), .pc(pc), .sn(sn), .pred_next(pred_next),
    .c0_valid(c0_valid), .c0_sn(c0_sn), .c0_result(c0_result), .c0_next(c0_next), .c0_taken(c0_taken),
    .c1_valid(c1_valid), .c1_sn(c1_sn), .c1_result(c1_result), .c1_next(c1_next), .c1_taken(c1_taken),
    .valid(entry11_valid_276), .done(entry11_done_277), .op_2(entry11_op_278), .rd_new_2(entry11_rd_new_279),
    .rd_old_2(entry11_rd_old_280), .rd_logic_2(entry11_rd_logic_281), .rw_2(entry11_rw_282),
    .pc_2(entry11_pc_283), .sn_2(entry11_sn_284), .pred_next_2(entry11_pred_next_285),
    .result(entry11_result_286), .next(entry11_next_287), .taken(entry11_taken_288));
  Comparator #(.width(4), .mode("unsigned")) comparator_27 (
    .a(Q_tail), .b(4'b1100), .gt(gt_290), .eq(eq_291), .lt(lt_292));
  and and_29 (and_293, and_13, eq_291);
  Comparator #(.width(4), .mode("unsigned")) comparator_28 (
    .a(Q_head), .b(4'b1100), .gt(gt_294), .eq(eq_295), .lt(lt_296));
  and u_and_30 (and_297, and_15, eq_295);
  ROB_Entry entry12 (
    .clk(clk), .rst(rst), .clear(clear), .enable(enable), .wr(and_293), .erase(and_297), .op(op),
    .rd_new(rd_new), .rd_old(rd_old), .rd_logic(rd_logic), .rw(rw), .pc(pc), .sn(sn), .pred_next(pred_next),
    .c0_valid(c0_valid), .c0_sn(c0_sn), .c0_result(c0_result), .c0_next(c0_next), .c0_taken(c0_taken),
    .c1_valid(c1_valid), .c1_sn(c1_sn), .c1_result(c1_result), .c1_next(c1_next), .c1_taken(c1_taken),
    .valid(entry12_valid_298), .done(entry12_done_299), .op_2(entry12_op_300), .rd_new_2(entry12_rd_new_301),
    .rd_old_2(entry12_rd_old_302), .rd_logic_2(entry12_rd_logic_303), .rw_2(entry12_rw_304),
    .pc_2(entry12_pc_305), .sn_2(entry12_sn_306), .pred_next_2(entry12_pred_next_307),
    .result(entry12_result_308), .next(entry12_next_309), .taken(entry12_taken_310));
  Comparator #(.width(4), .mode("unsigned")) comparator_29 (
    .a(Q_tail), .b(4'b1101), .gt(gt_312), .eq(eq_313), .lt(lt_314));
  and and_31 (and_315, and_13, eq_313);
  Comparator #(.width(4), .mode("unsigned")) comparator_30 (
    .a(Q_head), .b(4'b1101), .gt(gt_316), .eq(eq_317), .lt(lt_318));
  and and_32 (and_319, and_15, eq_317);
  ROB_Entry entry13 (
    .clk(clk), .rst(rst), .clear(clear), .enable(enable), .wr(and_315), .erase(and_319), .op(op),
    .rd_new(rd_new), .rd_old(rd_old), .rd_logic(rd_logic), .rw(rw), .pc(pc), .sn(sn), .pred_next(pred_next),
    .c0_valid(c0_valid), .c0_sn(c0_sn), .c0_result(c0_result), .c0_next(c0_next), .c0_taken(c0_taken),
    .c1_valid(c1_valid), .c1_sn(c1_sn), .c1_result(c1_result), .c1_next(c1_next), .c1_taken(c1_taken),
    .valid(entry13_valid_320), .done(entry13_done_321), .op_2(entry13_op_322), .rd_new_2(entry13_rd_new_323),
    .rd_old_2(entry13_rd_old_324), .rd_logic_2(entry13_rd_logic_325), .rw_2(entry13_rw_326),
    .pc_2(entry13_pc_327), .sn_2(entry13_sn_328), .pred_next_2(entry13_pred_next_329),
    .result(entry13_result_330), .next(entry13_next_331), .taken(entry13_taken_332));
  Comparator #(.width(4), .mode("unsigned")) comparator_31 (
    .a(Q_tail), .b(4'b1110), .gt(gt_334), .eq(eq_335), .lt(lt_336));
  and and_33 (and_337, and_13, eq_335);
  Comparator #(.width(4), .mode("unsigned")) comparator_32 (
    .a(Q_head), .b(4'b1110), .gt(gt_338), .eq(eq_339), .lt(lt_340));
  and u_and_34 (and_341, and_15, eq_339);
  ROB_Entry entry14 (
    .clk(clk), .rst(rst), .clear(clear), .enable(enable), .wr(and_337), .erase(and_341), .op(op),
    .rd_new(rd_new), .rd_old(rd_old), .rd_logic(rd_logic), .rw(rw), .pc(pc), .sn(sn), .pred_next(pred_next),
    .c0_valid(c0_valid), .c0_sn(c0_sn), .c0_result(c0_result), .c0_next(c0_next), .c0_taken(c0_taken),
    .c1_valid(c1_valid), .c1_sn(c1_sn), .c1_result(c1_result), .c1_next(c1_next), .c1_taken(c1_taken),
    .valid(entry14_valid_342), .done(entry14_done_343), .op_2(entry14_op_344), .rd_new_2(entry14_rd_new_345),
    .rd_old_2(entry14_rd_old_346), .rd_logic_2(entry14_rd_logic_347), .rw_2(entry14_rw_348),
    .pc_2(entry14_pc_349), .sn_2(entry14_sn_350), .pred_next_2(entry14_pred_next_351),
    .result(entry14_result_352), .next(entry14_next_353), .taken(entry14_taken_354));
  Comparator #(.width(4), .mode("unsigned")) comparator_33 (
    .a(Q_tail), .b(4'b1111), .gt(gt_356), .eq(eq_357), .lt(lt_358));
  and and_35 (and_359, and_13, eq_357);
  Comparator #(.width(4), .mode("unsigned")) comparator_34 (
    .a(Q_head), .b(4'b1111), .gt(gt_360), .eq(eq_361), .lt(lt_362));
  and and_36 (and_363, and_15, eq_361);
  ROB_Entry entry15 (
    .clk(clk), .rst(rst), .clear(clear), .enable(enable), .wr(and_359), .erase(and_363), .op(op),
    .rd_new(rd_new), .rd_old(rd_old), .rd_logic(rd_logic), .rw(rw), .pc(pc), .sn(sn), .pred_next(pred_next),
    .c0_valid(c0_valid), .c0_sn(c0_sn), .c0_result(c0_result), .c0_next(c0_next), .c0_taken(c0_taken),
    .c1_valid(c1_valid), .c1_sn(c1_sn), .c1_result(c1_result), .c1_next(c1_next), .c1_taken(c1_taken),
    .valid(entry15_valid_364), .done(entry15_done_365), .op_2(entry15_op_366), .rd_new_2(entry15_rd_new_367),
    .rd_old_2(entry15_rd_old_368), .rd_logic_2(entry15_rd_logic_369), .rw_2(entry15_rw_370),
    .pc_2(entry15_pc_371), .sn_2(entry15_sn_372), .pred_next_2(entry15_pred_next_373),
    .result(entry15_result_374), .next(entry15_next_375), .taken(entry15_taken_376));
  Multiplexer #(.width(1), .select(1), .enable("false")) multiplexer_2 (
    .in0(entry00_valid_35), .in1(entry01_valid_56), .out(mux_383), .sel(Q_head[0]));
  Multiplexer #(.width(1), .select(1), .enable("false")) multiplexer_3 (
    .in0(entry02_valid_78), .in1(entry03_valid_100), .out(mux_384), .sel(Q_head[0]));
  Multiplexer #(.width(1), .select(1), .enable("false")) multiplexer_4 (
    .in0(mux_383), .in1(mux_384), .out(mux_385), .sel(Q_head[1]));
  Multiplexer #(.width(1), .select(1), .enable("false")) multiplexer_5 (
    .in0(entry04_valid_122), .in1(entry05_valid_144), .out(mux_386), .sel(Q_head[0]));
  Multiplexer #(.width(1), .select(1), .enable("false")) multiplexer_6 (
    .in0(entry06_valid_166), .in1(entry07_valid_188), .out(mux_387), .sel(Q_head[0]));
  Multiplexer #(.width(1), .select(1), .enable("false")) multiplexer_7 (
    .in0(mux_386), .in1(mux_387), .out(mux_388), .sel(Q_head[1]));
  Multiplexer #(.width(1), .select(1), .enable("false")) multiplexer_8 (
    .in0(mux_385), .in1(mux_388), .out(mux_389), .sel(Q_head[2]));
  Multiplexer #(.width(1), .select(1), .enable("false")) multiplexer_9 (
    .in0(entry08_valid_210), .in1(entry09_valid_232), .out(mux_390), .sel(Q_head[0]));
  Multiplexer #(.width(1), .select(1), .enable("false")) multiplexer_10 (
    .in0(entry10_valid_254), .in1(entry11_valid_276), .out(mux_391), .sel(Q_head[0]));
  Multiplexer #(.width(1), .select(1), .enable("false")) multiplexer_11 (
    .in0(mux_390), .in1(mux_391), .out(mux_392), .sel(Q_head[1]));
  Multiplexer #(.width(1), .select(1), .enable("false")) multiplexer_12 (
    .in0(entry12_valid_298), .in1(entry13_valid_320), .out(mux_393), .sel(Q_head[0]));
  Multiplexer #(.width(1), .select(1), .enable("false")) multiplexer_13 (
    .in0(entry14_valid_342), .in1(entry15_valid_364), .out(mux_394), .sel(Q_head[0]));
  Multiplexer #(.width(1), .select(1), .enable("false")) multiplexer_14 (
    .in0(mux_393), .in1(mux_394), .out(mux_395), .sel(Q_head[1]));
  Multiplexer #(.width(1), .select(1), .enable("false")) multiplexer_15 (
    .in0(mux_392), .in1(mux_395), .out(mux_396), .sel(Q_head[2]));
  Multiplexer #(.width(1), .select(1), .enable("false")) multiplexer_16 (
    .in0(mux_389), .in1(mux_396), .out(mux_397), .sel(Q_head[3]));
  and and_37 (head_valid, not_10, mux_397);
  Multiplexer #(.width(1), .select(1), .enable("false")) multiplexer_17 (
    .in0(entry00_done_36), .in1(entry01_done_57), .out(mux_399), .sel(Q_head[0]));
  Multiplexer #(.width(1), .select(1), .enable("false")) multiplexer_18 (
    .in0(entry02_done_79), .in1(entry03_done_101), .out(mux_400), .sel(Q_head[0]));
  Multiplexer #(.width(1), .select(1), .enable("false")) multiplexer_19 (
    .in0(mux_399), .in1(mux_400), .out(mux_401), .sel(Q_head[1]));
  Multiplexer #(.width(1), .select(1), .enable("false")) multiplexer_20 (
    .in0(entry04_done_123), .in1(entry05_done_145), .out(mux_402), .sel(Q_head[0]));
  Multiplexer #(.width(1), .select(1), .enable("false")) multiplexer_21 (
    .in0(entry06_done_167), .in1(entry07_done_189), .out(mux_403), .sel(Q_head[0]));
  Multiplexer #(.width(1), .select(1), .enable("false")) multiplexer_22 (
    .in0(mux_402), .in1(mux_403), .out(mux_404), .sel(Q_head[1]));
  Multiplexer #(.width(1), .select(1), .enable("false")) multiplexer_23 (
    .in0(mux_401), .in1(mux_404), .out(mux_405), .sel(Q_head[2]));
  Multiplexer #(.width(1), .select(1), .enable("false")) multiplexer_24 (
    .in0(entry08_done_211), .in1(entry09_done_233), .out(mux_406), .sel(Q_head[0]));
  Multiplexer #(.width(1), .select(1), .enable("false")) multiplexer_25 (
    .in0(entry10_done_255), .in1(entry11_done_277), .out(mux_407), .sel(Q_head[0]));
  Multiplexer #(.width(1), .select(1), .enable("false")) multiplexer_26 (
    .in0(mux_406), .in1(mux_407), .out(mux_408), .sel(Q_head[1]));
  Multiplexer #(.width(1), .select(1), .enable("false")) multiplexer_27 (
    .in0(entry12_done_299), .in1(entry13_done_321), .out(mux_409), .sel(Q_head[0]));
  Multiplexer #(.width(1), .select(1), .enable("false")) multiplexer_28 (
    .in0(entry14_done_343), .in1(entry15_done_365), .out(mux_410), .sel(Q_head[0]));
  Multiplexer #(.width(1), .select(1), .enable("false")) multiplexer_29 (
    .in0(mux_409), .in1(mux_410), .out(mux_411), .sel(Q_head[1]));
  Multiplexer #(.width(1), .select(1), .enable("false")) multiplexer_30 (
    .in0(mux_408), .in1(mux_411), .out(mux_412), .sel(Q_head[2]));
  Multiplexer #(.width(1), .select(1), .enable("false")) multiplexer_31 (
    .in0(mux_405), .in1(mux_412), .out(head_done), .sel(Q_head[3]));
  Multiplexer #(.width(4), .select(1), .enable("false")) multiplexer_32 (
    .in0(entry00_op_37), .in1(entry01_op_58), .out(mux_414), .sel(Q_head[0]));
  Multiplexer #(.width(4), .select(1), .enable("false")) multiplexer_33 (
    .in0(entry02_op_80), .in1(entry03_op_102), .out(mux_415), .sel(Q_head[0]));
  Multiplexer #(.width(4), .select(1), .enable("false")) multiplexer_34 (
    .in0(mux_414), .in1(mux_415), .out(mux_416), .sel(Q_head[1]));
  Multiplexer #(.width(4), .select(1), .enable("false")) multiplexer_35 (
    .in0(entry04_op_124), .in1(entry05_op_146), .out(mux_417), .sel(Q_head[0]));
  Multiplexer #(.width(4), .select(1), .enable("false")) multiplexer_36 (
    .in0(entry06_op_168), .in1(entry07_op_190), .out(mux_418), .sel(Q_head[0]));
  Multiplexer #(.width(4), .select(1), .enable("false")) multiplexer_37 (
    .in0(mux_417), .in1(mux_418), .out(mux_419), .sel(Q_head[1]));
  Multiplexer #(.width(4), .select(1), .enable("false")) multiplexer_38 (
    .in0(mux_416), .in1(mux_419), .out(mux_420), .sel(Q_head[2]));
  Multiplexer #(.width(4), .select(1), .enable("false")) multiplexer_39 (
    .in0(entry08_op_212), .in1(entry09_op_234), .out(mux_421), .sel(Q_head[0]));
  Multiplexer #(.width(4), .select(1), .enable("false")) multiplexer_40 (
    .in0(entry10_op_256), .in1(entry11_op_278), .out(mux_422), .sel(Q_head[0]));
  Multiplexer #(.width(4), .select(1), .enable("false")) multiplexer_41 (
    .in0(mux_421), .in1(mux_422), .out(mux_423), .sel(Q_head[1]));
  Multiplexer #(.width(4), .select(1), .enable("false")) multiplexer_42 (
    .in0(entry12_op_300), .in1(entry13_op_322), .out(mux_424), .sel(Q_head[0]));
  Multiplexer #(.width(4), .select(1), .enable("false")) multiplexer_43 (
    .in0(entry14_op_344), .in1(entry15_op_366), .out(mux_425), .sel(Q_head[0]));
  Multiplexer #(.width(4), .select(1), .enable("false")) multiplexer_44 (
    .in0(mux_424), .in1(mux_425), .out(mux_426), .sel(Q_head[1]));
  Multiplexer #(.width(4), .select(1), .enable("false")) multiplexer_45 (
    .in0(mux_423), .in1(mux_426), .out(mux_427), .sel(Q_head[2]));
  Multiplexer #(.width(4), .select(1), .enable("false")) multiplexer_46 (
    .in0(mux_420), .in1(mux_427), .out(head_op), .sel(Q_head[3]));
  Multiplexer #(.width(6), .select(1), .enable("false")) multiplexer_47 (
    .in0(entry00_rd_new_38), .in1(entry01_rd_new_59), .out(mux_429), .sel(Q_head[0]));
  Multiplexer #(.width(6), .select(1), .enable("false")) multiplexer_48 (
    .in0(entry02_rd_new_81), .in1(entry03_rd_new_103), .out(mux_430), .sel(Q_head[0]));
  Multiplexer #(.width(6), .select(1), .enable("false")) multiplexer_49 (
    .in0(mux_429), .in1(mux_430), .out(mux_431), .sel(Q_head[1]));
  Multiplexer #(.width(6), .select(1), .enable("false")) multiplexer_50 (
    .in0(entry04_rd_new_125), .in1(entry05_rd_new_147), .out(mux_432), .sel(Q_head[0]));
  Multiplexer #(.width(6), .select(1), .enable("false")) multiplexer_51 (
    .in0(entry06_rd_new_169), .in1(entry07_rd_new_191), .out(mux_433), .sel(Q_head[0]));
  Multiplexer #(.width(6), .select(1), .enable("false")) multiplexer_52 (
    .in0(mux_432), .in1(mux_433), .out(mux_434), .sel(Q_head[1]));
  Multiplexer #(.width(6), .select(1), .enable("false")) multiplexer_53 (
    .in0(mux_431), .in1(mux_434), .out(mux_435), .sel(Q_head[2]));
  Multiplexer #(.width(6), .select(1), .enable("false")) multiplexer_54 (
    .in0(entry08_rd_new_213), .in1(entry09_rd_new_235), .out(mux_436), .sel(Q_head[0]));
  Multiplexer #(.width(6), .select(1), .enable("false")) multiplexer_55 (
    .in0(entry10_rd_new_257), .in1(entry11_rd_new_279), .out(mux_437), .sel(Q_head[0]));
  Multiplexer #(.width(6), .select(1), .enable("false")) multiplexer_56 (
    .in0(mux_436), .in1(mux_437), .out(mux_438), .sel(Q_head[1]));
  Multiplexer #(.width(6), .select(1), .enable("false")) multiplexer_57 (
    .in0(entry12_rd_new_301), .in1(entry13_rd_new_323), .out(mux_439), .sel(Q_head[0]));
  Multiplexer #(.width(6), .select(1), .enable("false")) multiplexer_58 (
    .in0(entry14_rd_new_345), .in1(entry15_rd_new_367), .out(mux_440), .sel(Q_head[0]));
  Multiplexer #(.width(6), .select(1), .enable("false")) multiplexer_59 (
    .in0(mux_439), .in1(mux_440), .out(mux_441), .sel(Q_head[1]));
  Multiplexer #(.width(6), .select(1), .enable("false")) multiplexer_60 (
    .in0(mux_438), .in1(mux_441), .out(mux_442), .sel(Q_head[2]));
  Multiplexer #(.width(6), .select(1), .enable("false")) multiplexer_61 (
    .in0(mux_435), .in1(mux_442), .out(head_rd_new), .sel(Q_head[3]));
  Multiplexer #(.width(6), .select(1), .enable("false")) multiplexer_62 (
    .in0(entry00_rd_old_39), .in1(entry01_rd_old_60), .out(mux_444), .sel(Q_head[0]));
  Multiplexer #(.width(6), .select(1), .enable("false")) multiplexer_63 (
    .in0(entry02_rd_old_82), .in1(entry03_rd_old_104), .out(mux_445), .sel(Q_head[0]));
  Multiplexer #(.width(6), .select(1), .enable("false")) multiplexer_64 (
    .in0(mux_444), .in1(mux_445), .out(mux_446), .sel(Q_head[1]));
  Multiplexer #(.width(6), .select(1), .enable("false")) multiplexer_65 (
    .in0(entry04_rd_old_126), .in1(entry05_rd_old_148), .out(mux_447), .sel(Q_head[0]));
  Multiplexer #(.width(6), .select(1), .enable("false")) multiplexer_66 (
    .in0(entry06_rd_old_170), .in1(entry07_rd_old_192), .out(mux_448), .sel(Q_head[0]));
  Multiplexer #(.width(6), .select(1), .enable("false")) multiplexer_67 (
    .in0(mux_447), .in1(mux_448), .out(mux_449), .sel(Q_head[1]));
  Multiplexer #(.width(6), .select(1), .enable("false")) multiplexer_68 (
    .in0(mux_446), .in1(mux_449), .out(mux_450), .sel(Q_head[2]));
  Multiplexer #(.width(6), .select(1), .enable("false")) multiplexer_69 (
    .in0(entry08_rd_old_214), .in1(entry09_rd_old_236), .out(mux_451), .sel(Q_head[0]));
  Multiplexer #(.width(6), .select(1), .enable("false")) multiplexer_70 (
    .in0(entry10_rd_old_258), .in1(entry11_rd_old_280), .out(mux_452), .sel(Q_head[0]));
  Multiplexer #(.width(6), .select(1), .enable("false")) multiplexer_71 (
    .in0(mux_451), .in1(mux_452), .out(mux_453), .sel(Q_head[1]));
  Multiplexer #(.width(6), .select(1), .enable("false")) multiplexer_72 (
    .in0(entry12_rd_old_302), .in1(entry13_rd_old_324), .out(mux_454), .sel(Q_head[0]));
  Multiplexer #(.width(6), .select(1), .enable("false")) multiplexer_73 (
    .in0(entry14_rd_old_346), .in1(entry15_rd_old_368), .out(mux_455), .sel(Q_head[0]));
  Multiplexer #(.width(6), .select(1), .enable("false")) multiplexer_74 (
    .in0(mux_454), .in1(mux_455), .out(mux_456), .sel(Q_head[1]));
  Multiplexer #(.width(6), .select(1), .enable("false")) multiplexer_75 (
    .in0(mux_453), .in1(mux_456), .out(mux_457), .sel(Q_head[2]));
  Multiplexer #(.width(6), .select(1), .enable("false")) multiplexer_76 (
    .in0(mux_450), .in1(mux_457), .out(head_rd_old), .sel(Q_head[3]));
  Multiplexer #(.width(3), .select(1), .enable("false")) multiplexer_77 (
    .in0(entry00_rd_logic_40), .in1(entry01_rd_logic_61), .out(mux_459), .sel(Q_head[0]));
  Multiplexer #(.width(3), .select(1), .enable("false")) multiplexer_78 (
    .in0(entry02_rd_logic_83), .in1(entry03_rd_logic_105), .out(mux_460), .sel(Q_head[0]));
  Multiplexer #(.width(3), .select(1), .enable("false")) multiplexer_79 (
    .in0(mux_459), .in1(mux_460), .out(mux_461), .sel(Q_head[1]));
  Multiplexer #(.width(3), .select(1), .enable("false")) multiplexer_80 (
    .in0(entry04_rd_logic_127), .in1(entry05_rd_logic_149), .out(mux_462), .sel(Q_head[0]));
  Multiplexer #(.width(3), .select(1), .enable("false")) multiplexer_81 (
    .in0(entry06_rd_logic_171), .in1(entry07_rd_logic_193), .out(mux_463), .sel(Q_head[0]));
  Multiplexer #(.width(3), .select(1), .enable("false")) multiplexer_82 (
    .in0(mux_462), .in1(mux_463), .out(mux_464), .sel(Q_head[1]));
  Multiplexer #(.width(3), .select(1), .enable("false")) multiplexer_83 (
    .in0(mux_461), .in1(mux_464), .out(mux_465), .sel(Q_head[2]));
  Multiplexer #(.width(3), .select(1), .enable("false")) multiplexer_84 (
    .in0(entry08_rd_logic_215), .in1(entry09_rd_logic_237), .out(mux_466), .sel(Q_head[0]));
  Multiplexer #(.width(3), .select(1), .enable("false")) multiplexer_85 (
    .in0(entry10_rd_logic_259), .in1(entry11_rd_logic_281), .out(mux_467), .sel(Q_head[0]));
  Multiplexer #(.width(3), .select(1), .enable("false")) multiplexer_86 (
    .in0(mux_466), .in1(mux_467), .out(mux_468), .sel(Q_head[1]));
  Multiplexer #(.width(3), .select(1), .enable("false")) multiplexer_87 (
    .in0(entry12_rd_logic_303), .in1(entry13_rd_logic_325), .out(mux_469), .sel(Q_head[0]));
  Multiplexer #(.width(3), .select(1), .enable("false")) multiplexer_88 (
    .in0(entry14_rd_logic_347), .in1(entry15_rd_logic_369), .out(mux_470), .sel(Q_head[0]));
  Multiplexer #(.width(3), .select(1), .enable("false")) multiplexer_89 (
    .in0(mux_469), .in1(mux_470), .out(mux_471), .sel(Q_head[1]));
  Multiplexer #(.width(3), .select(1), .enable("false")) multiplexer_90 (
    .in0(mux_468), .in1(mux_471), .out(mux_472), .sel(Q_head[2]));
  Multiplexer #(.width(3), .select(1), .enable("false")) multiplexer_91 (
    .in0(mux_465), .in1(mux_472), .out(head_rd_logic), .sel(Q_head[3]));
  Multiplexer #(.width(1), .select(1), .enable("false")) multiplexer_92 (
    .in0(entry00_rw_41), .in1(entry01_rw_62), .out(mux_474), .sel(Q_head[0]));
  Multiplexer #(.width(1), .select(1), .enable("false")) multiplexer_93 (
    .in0(entry02_rw_84), .in1(entry03_rw_106), .out(mux_475), .sel(Q_head[0]));
  Multiplexer #(.width(1), .select(1), .enable("false")) multiplexer_94 (
    .in0(mux_474), .in1(mux_475), .out(mux_476), .sel(Q_head[1]));
  Multiplexer #(.width(1), .select(1), .enable("false")) multiplexer_95 (
    .in0(entry04_rw_128), .in1(entry05_rw_150), .out(mux_477), .sel(Q_head[0]));
  Multiplexer #(.width(1), .select(1), .enable("false")) multiplexer_96 (
    .in0(entry06_rw_172), .in1(entry07_rw_194), .out(mux_478), .sel(Q_head[0]));
  Multiplexer #(.width(1), .select(1), .enable("false")) multiplexer_97 (
    .in0(mux_477), .in1(mux_478), .out(mux_479), .sel(Q_head[1]));
  Multiplexer #(.width(1), .select(1), .enable("false")) multiplexer_98 (
    .in0(mux_476), .in1(mux_479), .out(mux_480), .sel(Q_head[2]));
  Multiplexer #(.width(1), .select(1), .enable("false")) multiplexer_99 (
    .in0(entry08_rw_216), .in1(entry09_rw_238), .out(mux_481), .sel(Q_head[0]));
  Multiplexer #(.width(1), .select(1), .enable("false")) multiplexer_100 (
    .in0(entry10_rw_260), .in1(entry11_rw_282), .out(mux_482), .sel(Q_head[0]));
  Multiplexer #(.width(1), .select(1), .enable("false")) multiplexer_101 (
    .in0(mux_481), .in1(mux_482), .out(mux_483), .sel(Q_head[1]));
  Multiplexer #(.width(1), .select(1), .enable("false")) multiplexer_102 (
    .in0(entry12_rw_304), .in1(entry13_rw_326), .out(mux_484), .sel(Q_head[0]));
  Multiplexer #(.width(1), .select(1), .enable("false")) multiplexer_103 (
    .in0(entry14_rw_348), .in1(entry15_rw_370), .out(mux_485), .sel(Q_head[0]));
  Multiplexer #(.width(1), .select(1), .enable("false")) multiplexer_104 (
    .in0(mux_484), .in1(mux_485), .out(mux_486), .sel(Q_head[1]));
  Multiplexer #(.width(1), .select(1), .enable("false")) multiplexer_105 (
    .in0(mux_483), .in1(mux_486), .out(mux_487), .sel(Q_head[2]));
  Multiplexer #(.width(1), .select(1), .enable("false")) multiplexer_106 (
    .in0(mux_480), .in1(mux_487), .out(head_rw), .sel(Q_head[3]));
  Multiplexer #(.width(16), .select(1), .enable("false")) multiplexer_107 (
    .in0(entry00_pc_42), .in1(entry01_pc_63), .out(mux_489), .sel(Q_head[0]));
  Multiplexer #(.width(16), .select(1), .enable("false")) multiplexer_108 (
    .in0(entry02_pc_85), .in1(entry03_pc_107), .out(mux_490), .sel(Q_head[0]));
  Multiplexer #(.width(16), .select(1), .enable("false")) multiplexer_109 (
    .in0(mux_489), .in1(mux_490), .out(mux_491), .sel(Q_head[1]));
  Multiplexer #(.width(16), .select(1), .enable("false")) multiplexer_110 (
    .in0(entry04_pc_129), .in1(entry05_pc_151), .out(mux_492), .sel(Q_head[0]));
  Multiplexer #(.width(16), .select(1), .enable("false")) multiplexer_111 (
    .in0(entry06_pc_173), .in1(entry07_pc_195), .out(mux_493), .sel(Q_head[0]));
  Multiplexer #(.width(16), .select(1), .enable("false")) multiplexer_112 (
    .in0(mux_492), .in1(mux_493), .out(mux_494), .sel(Q_head[1]));
  Multiplexer #(.width(16), .select(1), .enable("false")) multiplexer_113 (
    .in0(mux_491), .in1(mux_494), .out(mux_495), .sel(Q_head[2]));
  Multiplexer #(.width(16), .select(1), .enable("false")) multiplexer_114 (
    .in0(entry08_pc_217), .in1(entry09_pc_239), .out(mux_496), .sel(Q_head[0]));
  Multiplexer #(.width(16), .select(1), .enable("false")) multiplexer_115 (
    .in0(entry10_pc_261), .in1(entry11_pc_283), .out(mux_497), .sel(Q_head[0]));
  Multiplexer #(.width(16), .select(1), .enable("false")) multiplexer_116 (
    .in0(mux_496), .in1(mux_497), .out(mux_498), .sel(Q_head[1]));
  Multiplexer #(.width(16), .select(1), .enable("false")) multiplexer_117 (
    .in0(entry12_pc_305), .in1(entry13_pc_327), .out(mux_499), .sel(Q_head[0]));
  Multiplexer #(.width(16), .select(1), .enable("false")) multiplexer_118 (
    .in0(entry14_pc_349), .in1(entry15_pc_371), .out(mux_500), .sel(Q_head[0]));
  Multiplexer #(.width(16), .select(1), .enable("false")) multiplexer_119 (
    .in0(mux_499), .in1(mux_500), .out(mux_501), .sel(Q_head[1]));
  Multiplexer #(.width(16), .select(1), .enable("false")) multiplexer_120 (
    .in0(mux_498), .in1(mux_501), .out(mux_502), .sel(Q_head[2]));
  Multiplexer #(.width(16), .select(1), .enable("false")) multiplexer_121 (
    .in0(mux_495), .in1(mux_502), .out(head_pc), .sel(Q_head[3]));
  Multiplexer #(.width(8), .select(1), .enable("false")) multiplexer_122 (
    .in0(entry00_sn_43), .in1(entry01_sn_64), .out(mux_504), .sel(Q_head[0]));
  Multiplexer #(.width(8), .select(1), .enable("false")) multiplexer_123 (
    .in0(entry02_sn_86), .in1(entry03_sn_108), .out(mux_505), .sel(Q_head[0]));
  Multiplexer #(.width(8), .select(1), .enable("false")) multiplexer_124 (
    .in0(mux_504), .in1(mux_505), .out(mux_506), .sel(Q_head[1]));
  Multiplexer #(.width(8), .select(1), .enable("false")) multiplexer_125 (
    .in0(entry04_sn_130), .in1(entry05_sn_152), .out(mux_507), .sel(Q_head[0]));
  Multiplexer #(.width(8), .select(1), .enable("false")) multiplexer_126 (
    .in0(entry06_sn_174), .in1(entry07_sn_196), .out(mux_508), .sel(Q_head[0]));
  Multiplexer #(.width(8), .select(1), .enable("false")) multiplexer_127 (
    .in0(mux_507), .in1(mux_508), .out(mux_509), .sel(Q_head[1]));
  Multiplexer #(.width(8), .select(1), .enable("false")) multiplexer_128 (
    .in0(mux_506), .in1(mux_509), .out(mux_510), .sel(Q_head[2]));
  Multiplexer #(.width(8), .select(1), .enable("false")) multiplexer_129 (
    .in0(entry08_sn_218), .in1(entry09_sn_240), .out(mux_511), .sel(Q_head[0]));
  Multiplexer #(.width(8), .select(1), .enable("false")) multiplexer_130 (
    .in0(entry10_sn_262), .in1(entry11_sn_284), .out(mux_512), .sel(Q_head[0]));
  Multiplexer #(.width(8), .select(1), .enable("false")) multiplexer_131 (
    .in0(mux_511), .in1(mux_512), .out(mux_513), .sel(Q_head[1]));
  Multiplexer #(.width(8), .select(1), .enable("false")) multiplexer_132 (
    .in0(entry12_sn_306), .in1(entry13_sn_328), .out(mux_514), .sel(Q_head[0]));
  Multiplexer #(.width(8), .select(1), .enable("false")) multiplexer_133 (
    .in0(entry14_sn_350), .in1(entry15_sn_372), .out(mux_515), .sel(Q_head[0]));
  Multiplexer #(.width(8), .select(1), .enable("false")) multiplexer_134 (
    .in0(mux_514), .in1(mux_515), .out(mux_516), .sel(Q_head[1]));
  Multiplexer #(.width(8), .select(1), .enable("false")) multiplexer_135 (
    .in0(mux_513), .in1(mux_516), .out(mux_517), .sel(Q_head[2]));
  Multiplexer #(.width(8), .select(1), .enable("false")) multiplexer_136 (
    .in0(mux_510), .in1(mux_517), .out(head_sn), .sel(Q_head[3]));
  Multiplexer #(.width(16), .select(1), .enable("false")) multiplexer_137 (
    .in0(entry00_pred_next_44), .in1(entry01_pred_next_65), .out(mux_519), .sel(Q_head[0]));
  Multiplexer #(.width(16), .select(1), .enable("false")) multiplexer_138 (
    .in0(entry02_pred_next_87), .in1(entry03_pred_next_109), .out(mux_520), .sel(Q_head[0]));
  Multiplexer #(.width(16), .select(1), .enable("false")) multiplexer_139 (
    .in0(mux_519), .in1(mux_520), .out(mux_521), .sel(Q_head[1]));
  Multiplexer #(.width(16), .select(1), .enable("false")) multiplexer_140 (
    .in0(entry04_pred_next_131), .in1(entry05_pred_next_153), .out(mux_522), .sel(Q_head[0]));
  Multiplexer #(.width(16), .select(1), .enable("false")) multiplexer_141 (
    .in0(entry06_pred_next_175), .in1(entry07_pred_next_197), .out(mux_523), .sel(Q_head[0]));
  Multiplexer #(.width(16), .select(1), .enable("false")) multiplexer_142 (
    .in0(mux_522), .in1(mux_523), .out(mux_524), .sel(Q_head[1]));
  Multiplexer #(.width(16), .select(1), .enable("false")) multiplexer_143 (
    .in0(mux_521), .in1(mux_524), .out(mux_525), .sel(Q_head[2]));
  Multiplexer #(.width(16), .select(1), .enable("false")) multiplexer_144 (
    .in0(entry08_pred_next_219), .in1(entry09_pred_next_241), .out(mux_526), .sel(Q_head[0]));
  Multiplexer #(.width(16), .select(1), .enable("false")) multiplexer_145 (
    .in0(entry10_pred_next_263), .in1(entry11_pred_next_285), .out(mux_527), .sel(Q_head[0]));
  Multiplexer #(.width(16), .select(1), .enable("false")) multiplexer_146 (
    .in0(mux_526), .in1(mux_527), .out(mux_528), .sel(Q_head[1]));
  Multiplexer #(.width(16), .select(1), .enable("false")) multiplexer_147 (
    .in0(entry12_pred_next_307), .in1(entry13_pred_next_329), .out(mux_529), .sel(Q_head[0]));
  Multiplexer #(.width(16), .select(1), .enable("false")) multiplexer_148 (
    .in0(entry14_pred_next_351), .in1(entry15_pred_next_373), .out(mux_530), .sel(Q_head[0]));
  Multiplexer #(.width(16), .select(1), .enable("false")) multiplexer_149 (
    .in0(mux_529), .in1(mux_530), .out(mux_531), .sel(Q_head[1]));
  Multiplexer #(.width(16), .select(1), .enable("false")) multiplexer_150 (
    .in0(mux_528), .in1(mux_531), .out(mux_532), .sel(Q_head[2]));
  Multiplexer #(.width(16), .select(1), .enable("false")) multiplexer_151 (
    .in0(mux_525), .in1(mux_532), .out(head_pred_next), .sel(Q_head[3]));
  Multiplexer #(.width(16), .select(1), .enable("false")) multiplexer_152 (
    .in0(entry00_result_45), .in1(entry01_result_66), .out(mux_534), .sel(Q_head[0]));
  Multiplexer #(.width(16), .select(1), .enable("false")) multiplexer_153 (
    .in0(entry02_result_88), .in1(entry03_result_110), .out(mux_535), .sel(Q_head[0]));
  Multiplexer #(.width(16), .select(1), .enable("false")) multiplexer_154 (
    .in0(mux_534), .in1(mux_535), .out(mux_536), .sel(Q_head[1]));
  Multiplexer #(.width(16), .select(1), .enable("false")) multiplexer_155 (
    .in0(entry04_result_132), .in1(entry05_result_154), .out(mux_537), .sel(Q_head[0]));
  Multiplexer #(.width(16), .select(1), .enable("false")) multiplexer_156 (
    .in0(entry06_result_176), .in1(entry07_result_198), .out(mux_538), .sel(Q_head[0]));
  Multiplexer #(.width(16), .select(1), .enable("false")) multiplexer_157 (
    .in0(mux_537), .in1(mux_538), .out(mux_539), .sel(Q_head[1]));
  Multiplexer #(.width(16), .select(1), .enable("false")) multiplexer_158 (
    .in0(mux_536), .in1(mux_539), .out(mux_540), .sel(Q_head[2]));
  Multiplexer #(.width(16), .select(1), .enable("false")) multiplexer_159 (
    .in0(entry08_result_220), .in1(entry09_result_242), .out(mux_541), .sel(Q_head[0]));
  Multiplexer #(.width(16), .select(1), .enable("false")) multiplexer_160 (
    .in0(entry10_result_264), .in1(entry11_result_286), .out(mux_542), .sel(Q_head[0]));
  Multiplexer #(.width(16), .select(1), .enable("false")) multiplexer_161 (
    .in0(mux_541), .in1(mux_542), .out(mux_543), .sel(Q_head[1]));
  Multiplexer #(.width(16), .select(1), .enable("false")) multiplexer_162 (
    .in0(entry12_result_308), .in1(entry13_result_330), .out(mux_544), .sel(Q_head[0]));
  Multiplexer #(.width(16), .select(1), .enable("false")) multiplexer_163 (
    .in0(entry14_result_352), .in1(entry15_result_374), .out(mux_545), .sel(Q_head[0]));
  Multiplexer #(.width(16), .select(1), .enable("false")) multiplexer_164 (
    .in0(mux_544), .in1(mux_545), .out(mux_546), .sel(Q_head[1]));
  Multiplexer #(.width(16), .select(1), .enable("false")) multiplexer_165 (
    .in0(mux_543), .in1(mux_546), .out(mux_547), .sel(Q_head[2]));
  Multiplexer #(.width(16), .select(1), .enable("false")) multiplexer_166 (
    .in0(mux_540), .in1(mux_547), .out(head_result), .sel(Q_head[3]));
  Multiplexer #(.width(16), .select(1), .enable("false")) multiplexer_167 (
    .in0(entry00_next_46), .in1(entry01_next_67), .out(mux_549), .sel(Q_head[0]));
  Multiplexer #(.width(16), .select(1), .enable("false")) multiplexer_168 (
    .in0(entry02_next_89), .in1(entry03_next_111), .out(mux_550), .sel(Q_head[0]));
  Multiplexer #(.width(16), .select(1), .enable("false")) multiplexer_169 (
    .in0(mux_549), .in1(mux_550), .out(mux_551), .sel(Q_head[1]));
  Multiplexer #(.width(16), .select(1), .enable("false")) multiplexer_170 (
    .in0(entry04_next_133), .in1(entry05_next_155), .out(mux_552), .sel(Q_head[0]));
  Multiplexer #(.width(16), .select(1), .enable("false")) multiplexer_171 (
    .in0(entry06_next_177), .in1(entry07_next_199), .out(mux_553), .sel(Q_head[0]));
  Multiplexer #(.width(16), .select(1), .enable("false")) multiplexer_172 (
    .in0(mux_552), .in1(mux_553), .out(mux_554), .sel(Q_head[1]));
  Multiplexer #(.width(16), .select(1), .enable("false")) multiplexer_173 (
    .in0(mux_551), .in1(mux_554), .out(mux_555), .sel(Q_head[2]));
  Multiplexer #(.width(16), .select(1), .enable("false")) multiplexer_174 (
    .in0(entry08_next_221), .in1(entry09_next_243), .out(mux_556), .sel(Q_head[0]));
  Multiplexer #(.width(16), .select(1), .enable("false")) multiplexer_175 (
    .in0(entry10_next_265), .in1(entry11_next_287), .out(mux_557), .sel(Q_head[0]));
  Multiplexer #(.width(16), .select(1), .enable("false")) multiplexer_176 (
    .in0(mux_556), .in1(mux_557), .out(mux_558), .sel(Q_head[1]));
  Multiplexer #(.width(16), .select(1), .enable("false")) multiplexer_177 (
    .in0(entry12_next_309), .in1(entry13_next_331), .out(mux_559), .sel(Q_head[0]));
  Multiplexer #(.width(16), .select(1), .enable("false")) multiplexer_178 (
    .in0(entry14_next_353), .in1(entry15_next_375), .out(mux_560), .sel(Q_head[0]));
  Multiplexer #(.width(16), .select(1), .enable("false")) multiplexer_179 (
    .in0(mux_559), .in1(mux_560), .out(mux_561), .sel(Q_head[1]));
  Multiplexer #(.width(16), .select(1), .enable("false")) multiplexer_180 (
    .in0(mux_558), .in1(mux_561), .out(mux_562), .sel(Q_head[2]));
  Multiplexer #(.width(16), .select(1), .enable("false")) multiplexer_181 (
    .in0(mux_555), .in1(mux_562), .out(head_next), .sel(Q_head[3]));
  Multiplexer #(.width(1), .select(1), .enable("false")) multiplexer_182 (
    .in0(entry00_taken_47), .in1(entry01_taken_68), .out(mux_564), .sel(Q_head[0]));
  Multiplexer #(.width(1), .select(1), .enable("false")) multiplexer_183 (
    .in0(entry02_taken_90), .in1(entry03_taken_112), .out(mux_565), .sel(Q_head[0]));
  Multiplexer #(.width(1), .select(1), .enable("false")) multiplexer_184 (
    .in0(mux_564), .in1(mux_565), .out(mux_566), .sel(Q_head[1]));
  Multiplexer #(.width(1), .select(1), .enable("false")) multiplexer_185 (
    .in0(entry04_taken_134), .in1(entry05_taken_156), .out(mux_567), .sel(Q_head[0]));
  Multiplexer #(.width(1), .select(1), .enable("false")) multiplexer_186 (
    .in0(entry06_taken_178), .in1(entry07_taken_200), .out(mux_568), .sel(Q_head[0]));
  Multiplexer #(.width(1), .select(1), .enable("false")) multiplexer_187 (
    .in0(mux_567), .in1(mux_568), .out(mux_569), .sel(Q_head[1]));
  Multiplexer #(.width(1), .select(1), .enable("false")) multiplexer_188 (
    .in0(mux_566), .in1(mux_569), .out(mux_570), .sel(Q_head[2]));
  Multiplexer #(.width(1), .select(1), .enable("false")) multiplexer_189 (
    .in0(entry08_taken_222), .in1(entry09_taken_244), .out(mux_571), .sel(Q_head[0]));
  Multiplexer #(.width(1), .select(1), .enable("false")) multiplexer_190 (
    .in0(entry10_taken_266), .in1(entry11_taken_288), .out(mux_572), .sel(Q_head[0]));
  Multiplexer #(.width(1), .select(1), .enable("false")) multiplexer_191 (
    .in0(mux_571), .in1(mux_572), .out(mux_573), .sel(Q_head[1]));
  Multiplexer #(.width(1), .select(1), .enable("false")) multiplexer_192 (
    .in0(entry12_taken_310), .in1(entry13_taken_332), .out(mux_574), .sel(Q_head[0]));
  Multiplexer #(.width(1), .select(1), .enable("false")) multiplexer_193 (
    .in0(entry14_taken_354), .in1(entry15_taken_376), .out(mux_575), .sel(Q_head[0]));
  Multiplexer #(.width(1), .select(1), .enable("false")) multiplexer_194 (
    .in0(mux_574), .in1(mux_575), .out(mux_576), .sel(Q_head[1]));
  Multiplexer #(.width(1), .select(1), .enable("false")) multiplexer_195 (
    .in0(mux_573), .in1(mux_576), .out(mux_577), .sel(Q_head[2]));
  Multiplexer #(.width(1), .select(1), .enable("false")) multiplexer_196 (
    .in0(mux_570), .in1(mux_577), .out(head_taken), .sel(Q_head[3]));

  // Other names for the same wires on the sheet: and_398 = head_valid; eq_4 = full; mux_413 = head_done;
  //   mux_428[3:0] = head_op; mux_443[5:0] = head_rd_new; mux_458[5:0] = head_rd_old; mux_473[2:0] = head_rd_logic;
  //   mux_488 = head_rw; mux_503[15:0] = head_pc; mux_518[7:0] = head_sn; mux_533[15:0] = head_pred_next;
  //   mux_548[15:0] = head_result; mux_563[15:0] = head_next; mux_578 = head_taken; Q_count[4:0] = count;
  //   slice_377[2:0] = Q_head[2:0]; slice_379[1:0] = Q_head[1:0]; slice_381 = Q_head[0]; slice_382 = Q_head[1];
  //   slice_380 = Q_head[2]; slice_378 = Q_head[3]

  // Notes on the sheet:
  //   16-entry distributed ROB | stable head, single retire
endmodule
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