// Logisim project primitive-tests.circ as structural Verilog: 3 circuits, main circuit PrimitiveCombinational
module PrimitiveCombinational (
  input  [15:0] a,
  input  [15:0] b,
  input  sel,
  output [15:0] add,
  output [15:0] sub,
  output [15:0] \and ,
  output [15:0] \or ,
  output [15:0] \xor ,
  output [15:0] \not ,
  output [15:0] mux,
  output eq,
  output lt,
  output signed_lt,
  output [3:0] low,
  output [7:0] middle,
  output [3:0] high,
  output [15:0] pack,
  output [15:0] extend,
  output [15:0] sign_extend,
  output [15:0] \const ,
  output [16:0] packed17,
  output [15:0] after_pack17
);

  wire eq_13, gt_9, gt_12;

  Adder #(.width(16)) adder_1 (.a(a), .b(b), .out(add), .cin(1'b0));  // open: cout
  assign \or  = a | b;  // OR_Gate or_1, 16 bits wide
  Comparator #(.width(16), .mode("unsigned")) comparator_1 (.a(a), .b(b), .gt(gt_9), .eq(eq), .lt(lt));
  // XOR_Gate #(.width(16)) xor_1: pin names not known; wires that end beside it: a, b, \xor 
  Comparator #(.width(16), .mode("twosComplement")) comparator_2 (.a(a), .b(b), .gt(gt_12), .eq(eq_13), .lt(signed_lt));
  Subtractor #(.width(16)) subtractor_1 (.a(a), .b(b), .out(sub), .bin(1'b0));  // open: bout
  assign \not  = ~a;  // NOT_Gate not_1, 16 bits wide
  assign extend = {{12{1'b0}}, a[15:12]};  // Bit_Extender bit_extender_1
  Adder #(.width(16)) adder_2 (.a(a), .b(b), .out(after_pack17), .cin(1'b0));  // open: cout
  assign \and  = a & b;  // AND_Gate and_1, 16 bits wide
  Multiplexer #(.width(16), .select(1), .enable("false")) multiplexer_1 (.in0(a), .in1(b), .out(mux), .sel(sel));
  assign sign_extend = {{12{a[15]}}, a[15:12]};  // Bit_Extender bit_extender_2

  assign \const  = 16'h1234;
  assign high = a[15:12];
  assign low = a[3:0];
  assign middle = a[11:4];
  assign pack = a;
  assign packed17 = {sel, a};

  // Other names for the same wires on the sheet: pack_18[15:0] = a; pack_38[16:0] = {sel, a}; slice_15[3:0] = a[3:0];
  //   slice_23 = a[1]; slice_24 = a[2]; slice_16[7:0] = a[11:4]; slice_27 = a[5]; slice_28 = a[6]; slice_31 = a[9];
  //   slice_32 = a[10]; adder_1[15:0] = add; adder_39[15:0] = after_pack17; and_4[15:0] = \and ; eq_10 = eq;
  //   ext_19[15:0] = extend; ext_20[15:0] = sign_extend; lt_11 = lt; lt_14 = signed_lt; mux_8[15:0] = mux;
  //   not_7[15:0] = \not ; or_5[15:0] = \or ; slice_17[3:0] = a[15:12]; slice_35 = a[13]; slice_36 = a[14];
  //   slice_22 = a[0]; slice_25 = a[3]; slice_26 = a[4]; slice_29 = a[7]; slice_30 = a[8]; slice_33 = a[11];
  //   slice_34 = a[12]; slice_37 = a[15]; subtractor_3[15:0] = sub; xor_6[15:0] = \xor 

  // Notes on the sheet:
  //   PrimitiveCombinational
endmodule

module PrimitiveSequential (
  input  clk,
  input  rst,
  input  en,
  input  [15:0] data,
  output [15:0] q,
  output [15:0] init_q
);

  wire or_3;
  wire [15:0] mux_2;

  Register #(.width(16)) reg_state (.D(data), .en(en), .Q(q), .clk(clk), .clr(rst));
  or or_1 (or_3, en, rst);
  Register #(.width(16)) reg_init_state (.D(mux_2), .en(or_3), .Q(init_q), .clk(clk), .clr(1'b0));
  Multiplexer #(.width(16), .select(1), .enable("false")) multiplexer_1 (
    .in0(data), .in1(16'h1234), .out(mux_2), .sel(rst));

  // Other names for the same wires on the sheet: init_state[15:0] = init_q; state[15:0] = q

  // Notes on the sheet:
  //   PrimitiveSequential
endmodule

module PrimitiveWrapper (
  input  [15:0] a,
  input  [15:0] b,
  input  sel,
  output [15:0] add,
  output [15:0] sub,
  output [15:0] \and ,
  output [15:0] \or ,
  output [15:0] \xor ,
  output [15:0] \not ,
  output [15:0] mux,
  output eq,
  output lt,
  output signed_lt,
  output [3:0] low,
  output [7:0] middle,
  output [3:0] high,
  output [15:0] pack,
  output [15:0] extend,
  output [15:0] sign_extend,
  output [15:0] \const ,
  output [16:0] packed17,
  output [15:0] after_pack17
);

  PrimitiveCombinational PrimitiveCombinational_inst1 (
    .a(a), .b(b), .sel(sel), .add(add), .sub(sub), .\and (\and ), .\or (\or ), .\xor (\xor ), .\not (\not ),
    .mux(mux), .eq(eq), .lt(lt), .signed_lt(signed_lt), .low(low), .middle(middle), .high(high), .pack(pack),
    .extend(extend), .sign_extend(sign_extend), .\const (\const ), .packed17(packed17),
    .after_pack17(after_pack17));

  // Other names for the same wires on the sheet: PrimitiveCombinational_add_1[15:0] = add;
  //   PrimitiveCombinational_after_pack17_19[15:0] = after_pack17; PrimitiveCombinational_and_3[15:0] = \and ;
  //   PrimitiveCombinational_const_17[15:0] = \const ; PrimitiveCombinational_eq_8 = eq;
  //   PrimitiveCombinational_extend_15[15:0] = extend; PrimitiveCombinational_high_13[3:0] = high;
  //   PrimitiveCombinational_low_11[3:0] = low; PrimitiveCombinational_lt_9 = lt;
  //   PrimitiveCombinational_middle_12[7:0] = middle; PrimitiveCombinational_mux_7[15:0] = mux;
  //   PrimitiveCombinational_not_6[15:0] = \not ; PrimitiveCombinational_or_4[15:0] = \or ;
  //   PrimitiveCombinational_pack_14[15:0] = pack; PrimitiveCombinational_packed17_18[16:0] = packed17;
  //   PrimitiveCombinational_sign_extend_16[15:0] = sign_extend; PrimitiveCombinational_signed_lt_10 = signed_lt;
  //   PrimitiveCombinational_sub_2[15:0] = sub; PrimitiveCombinational_xor_5[15:0] = \xor 

  // Notes on the sheet:
  //   PrimitiveWrapper
endmodule
